// Logisim project 14강_Clock.circ as structural Verilog: 21 circuits, main circuit main
module main (
  output out_1,
  output out_2,
  output out_3
);

  Clk clk_1 (.clk_e(out_2), .clk_s(out_3), .clk(out_1));
endmodule

module _1M (
  input  i,
  input  s,
  output o
);

  wire _1_out, _2_out, _4_out;

  nand _1 (_1_out, i, s);
  nand _2 (_2_out, _1_out, s);
  nand _3 (o, _1_out, _4_out);
  nand _4 (_4_out, o, _2_out);
endmodule

module _8M (
  input  in_1,
  input  [7:0] in_2,
  output [7:0] out_3
);

  _1M u_1m_1 (.o(out_3[0]), .s(in_1), .i(in_2[0]));
  _1M u_1m_2 (.o(out_3[1]), .s(in_1), .i(in_2[1]));
  _1M u_1m_3 (.o(out_3[2]), .s(in_1), .i(in_2[2]));
  _1M u_1m_4 (.o(out_3[3]), .s(in_1), .i(in_2[3]));
  _1M u_1m_5 (.o(out_3[4]), .s(in_1), .i(in_2[4]));
  _1M u_1m_6 (.o(out_3[5]), .s(in_1), .i(in_2[5]));
  _1M u_1m_7 (.o(out_3[6]), .s(in_1), .i(in_2[6]));
  _1M u_1m_8 (.o(out_3[7]), .s(in_1), .i(in_2[7]));
endmodule

module _8Register (
  input  set,
  input  [7:0] i,
  input  en,
  output [7:0] o
);

  wire [7:0] controlled_buffer_1_out, n8m_1_out_3;

  assign controlled_buffer_1_out = set ? i : 8'bz;  // Controlled_Buffer controlled_buffer_1
  _8M u_8m_1 (.in_1(set), .in_2(controlled_buffer_1_out), .out_3(n8m_1_out_3));
  Enabler enabler_1 (.out_3(o), .in_2(en), .in_1(n8m_1_out_3));
endmodule

module Enabler (
  input  [7:0] in_1,
  input  in_2,
  output [7:0] out_3
);

  assign out_3 = in_2 ? in_1 : 8'bz;  // Controlled_Buffer controlled_buffer_1
endmodule

module _3x8Decoder (
  input  in_1,
  input  in_2,
  input  in_3,
  output out_4,
  output out_5,
  output out_6,
  output out_7,
  output out_8,
  output out_9,
  output out_10,
  output out_11
);

  wire not_1_out, not_2_out, not_3_out;

  not not_1 (not_1_out, in_1);
  not not_2 (not_2_out, in_2);
  not not_3 (not_3_out, in_3);
  and and_1 (out_4, not_1_out, not_2_out, not_3_out);
  and and_2 (out_5, not_1_out, not_2_out, in_3);
  and and_3 (out_6, not_1_out, in_2, not_3_out);
  and and_4 (out_7, not_1_out, in_2, in_3);
  and and_5 (out_8, in_1, not_2_out, not_3_out);
  and and_6 (out_9, in_1, not_2_out, in_3);
  and and_7 (out_10, in_1, in_2, not_3_out);
  and and_8 (out_11, in_1, in_2, in_3);
endmodule

module RAM256 (
  input  sa,
  input  [7:0] a,
  input  [7:0] b_i,
  input  b_s,
  input  b_e,
  output [7:0] b_o
);

  wire decoder_1_out0, decoder_1_out1, decoder_1_out2, decoder_1_out3, decoder_1_out4, decoder_1_out5,
       decoder_1_out6, decoder_1_out7, decoder_1_out8, decoder_1_out9, decoder_1_out10, decoder_1_out11,
       decoder_1_out12, decoder_1_out13, decoder_1_out14, decoder_1_out15, decoder_2_out0, decoder_2_out1,
       decoder_2_out2, decoder_2_out3, decoder_2_out4, decoder_2_out5, decoder_2_out6, decoder_2_out7,
       decoder_2_out8, decoder_2_out9, decoder_2_out10, decoder_2_out11, decoder_2_out12, decoder_2_out13,
       decoder_2_out14, decoder_2_out15;
  wire [7:0] controlled_buffer_1_out, n8register_1_o;

  _8Register u_8register_1 (.o(n8register_1_o), .i(a), .en(1'b1), .set(sa));
  Decoder #(.enable("false"), .select(4)) decoder_1 (
    .out0(decoder_1_out0), .out1(decoder_1_out1), .out2(decoder_1_out2), .out3(decoder_1_out3),
    .out4(decoder_1_out4), .out5(decoder_1_out5), .out6(decoder_1_out6), .out7(decoder_1_out7),
    .out8(decoder_1_out8), .out9(decoder_1_out9), .out10(decoder_1_out10), .out11(decoder_1_out11),
    .out12(decoder_1_out12), .out13(decoder_1_out13), .out14(decoder_1_out14), .out15(decoder_1_out15),
    .sel(n8register_1_o[7:4]));
  assign controlled_buffer_1_out = b_s ? b_i : 8'bz;  // Controlled_Buffer controlled_buffer_1
  RAM1 ram1_1 (
    .b_o(controlled_buffer_1_out), .b_i(controlled_buffer_1_out), .x(decoder_2_out0), .b_s(b_s), .b_e(b_e),
    .y(decoder_1_out0));
  RAM1 ram1_2 (
    .b_o(controlled_buffer_1_out), .b_i(controlled_buffer_1_out), .x(decoder_2_out0), .b_s(b_s), .b_e(b_e),
    .y(decoder_1_out1));
  RAM1 ram1_3 (
    .b_o(controlled_buffer_1_out), .b_i(controlled_buffer_1_out), .x(decoder_2_out0), .b_s(b_s), .b_e(b_e),
    .y(decoder_1_out2));
  RAM1 ram1_4 (
    .b_o(controlled_buffer_1_out), .b_i(controlled_buffer_1_out), .x(decoder_2_out0), .b_s(b_s), .b_e(b_e),
    .y(decoder_1_out3));
  RAM1 ram1_5 (
    .b_o(controlled_buffer_1_out), .b_i(controlled_buffer_1_out), .x(decoder_2_out0), .b_s(b_s), .b_e(b_e),
    .y(decoder_1_out4));
  RAM1 ram1_6 (
    .b_o(controlled_buffer_1_out), .b_i(controlled_buffer_1_out), .x(decoder_2_out0), .b_s(b_s), .b_e(b_e),
    .y(decoder_1_out5));
  RAM1 ram1_7 (
    .b_o(controlled_buffer_1_out), .b_i(controlled_buffer_1_out), .x(decoder_2_out0), .b_s(b_s), .b_e(b_e),
    .y(decoder_1_out6));
  RAM1 ram1_8 (
    .b_o(controlled_buffer_1_out), .b_i(controlled_buffer_1_out), .x(decoder_2_out0), .b_s(b_s), .b_e(b_e),
    .y(decoder_1_out7));
  RAM1 ram1_9 (
    .b_o(controlled_buffer_1_out), .b_i(controlled_buffer_1_out), .x(decoder_2_out0), .b_s(b_s), .b_e(b_e),
    .y(decoder_1_out8));
  RAM1 ram1_10 (
    .b_o(controlled_buffer_1_out), .b_i(controlled_buffer_1_out), .x(decoder_2_out0), .b_s(b_s), .b_e(b_e),
    .y(decoder_1_out9));
  RAM1 ram1_11 (
    .b_o(controlled_buffer_1_out), .b_i(controlled_buffer_1_out), .x(decoder_2_out0), .b_s(b_s), .b_e(b_e),
    .y(decoder_1_out10));
  RAM1 ram1_12 (
    .b_o(controlled_buffer_1_out), .b_i(controlled_buffer_1_out), .x(decoder_2_out0), .b_s(b_s), .b_e(b_e),
    .y(decoder_1_out11));
  RAM1 ram1_13 (
    .b_o(controlled_buffer_1_out), .b_i(controlled_buffer_1_out), .x(decoder_2_out0), .b_s(b_s), .b_e(b_e),
    .y(decoder_1_out12));
  RAM1 ram1_14 (
    .b_o(controlled_buffer_1_out), .b_i(controlled_buffer_1_out), .x(decoder_2_out0), .b_s(b_s), .b_e(b_e),
    .y(decoder_1_out13));
  RAM1 ram1_15 (
    .b_o(controlled_buffer_1_out), .b_i(controlled_buffer_1_out), .x(decoder_2_out0), .b_s(b_s), .b_e(b_e),
    .y(decoder_1_out14));
  RAM1 ram1_16 (
    .b_o(controlled_buffer_1_out), .b_i(controlled_buffer_1_out), .x(decoder_2_out0), .b_s(b_s), .b_e(b_e),
    .y(decoder_1_out15));
  RAM1 ram1_17 (
    .b_o(controlled_buffer_1_out), .b_i(controlled_buffer_1_out), .x(decoder_2_out1), .b_s(b_s), .b_e(b_e),
    .y(decoder_1_out0));
  RAM1 ram1_18 (
    .b_o(controlled_buffer_1_out), .b_i(controlled_buffer_1_out), .x(decoder_2_out1), .b_s(b_s), .b_e(b_e),
    .y(decoder_1_out1));
  RAM1 ram1_19 (
    .b_o(controlled_buffer_1_out), .b_i(controlled_buffer_1_out), .x(decoder_2_out1), .b_s(b_s), .b_e(b_e),
    .y(decoder_1_out2));
  RAM1 ram1_20 (
    .b_o(controlled_buffer_1_out), .b_i(controlled_buffer_1_out), .x(decoder_2_out1), .b_s(b_s), .b_e(b_e),
    .y(decoder_1_out3));
  RAM1 ram1_21 (
    .b_o(controlled_buffer_1_out), .b_i(controlled_buffer_1_out), .x(decoder_2_out1), .b_s(b_s), .b_e(b_e),
    .y(decoder_1_out4));
  RAM1 ram1_22 (
    .b_o(controlled_buffer_1_out), .b_i(controlled_buffer_1_out), .x(decoder_2_out1), .b_s(b_s), .b_e(b_e),
    .y(decoder_1_out5));
  RAM1 ram1_23 (
    .b_o(controlled_buffer_1_out), .b_i(controlled_buffer_1_out), .x(decoder_2_out1), .b_s(b_s), .b_e(b_e),
    .y(decoder_1_out6));
  RAM1 ram1_24 (
    .b_o(controlled_buffer_1_out), .b_i(controlled_buffer_1_out), .x(decoder_2_out1), .b_s(b_s), .b_e(b_e),
    .y(decoder_1_out7));
  RAM1 ram1_25 (
    .b_o(controlled_buffer_1_out), .b_i(controlled_buffer_1_out), .x(decoder_2_out1), .b_s(b_s), .b_e(b_e),
    .y(decoder_1_out8));
  RAM1 ram1_26 (
    .b_o(controlled_buffer_1_out), .b_i(controlled_buffer_1_out), .x(decoder_2_out1), .b_s(b_s), .b_e(b_e),
    .y(decoder_1_out9));
  RAM1 ram1_27 (
    .b_o(controlled_buffer_1_out), .b_i(controlled_buffer_1_out), .x(decoder_2_out1), .b_s(b_s), .b_e(b_e),
    .y(decoder_1_out10));
  RAM1 ram1_28 (
    .b_o(controlled_buffer_1_out), .b_i(controlled_buffer_1_out), .x(decoder_2_out1), .b_s(b_s), .b_e(b_e),
    .y(decoder_1_out11));
  RAM1 ram1_29 (
    .b_o(controlled_buffer_1_out), .b_i(controlled_buffer_1_out), .x(decoder_2_out1), .b_s(b_s), .b_e(b_e),
    .y(decoder_1_out12));
  RAM1 ram1_30 (
    .b_o(controlled_buffer_1_out), .b_i(controlled_buffer_1_out), .x(decoder_2_out1), .b_s(b_s), .b_e(b_e),
    .y(decoder_1_out13));
  RAM1 ram1_31 (
    .b_o(controlled_buffer_1_out), .b_i(controlled_buffer_1_out), .x(decoder_2_out1), .b_s(b_s), .b_e(b_e),
    .y(decoder_1_out14));
  RAM1 ram1_32 (
    .b_o(controlled_buffer_1_out), .b_i(controlled_buffer_1_out), .x(decoder_2_out1), .b_s(b_s), .b_e(b_e),
    .y(decoder_1_out15));
  RAM1 ram1_33 (
    .b_o(controlled_buffer_1_out), .b_i(controlled_buffer_1_out), .x(decoder_2_out2), .b_s(b_s), .b_e(b_e),
    .y(decoder_1_out0));
  RAM1 ram1_34 (
    .b_o(controlled_buffer_1_out), .b_i(controlled_buffer_1_out), .x(decoder_2_out2), .b_s(b_s), .b_e(b_e),
    .y(decoder_1_out1));
  RAM1 ram1_35 (
    .b_o(controlled_buffer_1_out), .b_i(controlled_buffer_1_out), .x(decoder_2_out2), .b_s(b_s), .b_e(b_e),
    .y(decoder_1_out2));
  RAM1 ram1_36 (
    .b_o(controlled_buffer_1_out), .b_i(controlled_buffer_1_out), .x(decoder_2_out2), .b_s(b_s), .b_e(b_e),
    .y(decoder_1_out3));
  RAM1 ram1_37 (
    .b_o(controlled_buffer_1_out), .b_i(controlled_buffer_1_out), .x(decoder_2_out2), .b_s(b_s), .b_e(b_e),
    .y(decoder_1_out4));
  RAM1 ram1_38 (
    .b_o(controlled_buffer_1_out), .b_i(controlled_buffer_1_out), .x(decoder_2_out2), .b_s(b_s), .b_e(b_e),
    .y(decoder_1_out5));
  RAM1 ram1_39 (
    .b_o(controlled_buffer_1_out), .b_i(controlled_buffer_1_out), .x(decoder_2_out2), .b_s(b_s), .b_e(b_e),
    .y(decoder_1_out6));
  RAM1 ram1_40 (
    .b_o(controlled_buffer_1_out), .b_i(controlled_buffer_1_out), .x(decoder_2_out2), .b_s(b_s), .b_e(b_e),
    .y(decoder_1_out7));
  RAM1 ram1_41 (
    .b_o(controlled_buffer_1_out), .b_i(controlled_buffer_1_out), .x(decoder_2_out2), .b_s(b_s), .b_e(b_e),
    .y(decoder_1_out8));
  RAM1 ram1_42 (
    .b_o(controlled_buffer_1_out), .b_i(controlled_buffer_1_out), .x(decoder_2_out2), .b_s(b_s), .b_e(b_e),
    .y(decoder_1_out9));
  RAM1 ram1_43 (
    .b_o(controlled_buffer_1_out), .b_i(controlled_buffer_1_out), .x(decoder_2_out2), .b_s(b_s), .b_e(b_e),
    .y(decoder_1_out10));
  RAM1 ram1_44 (
    .b_o(controlled_buffer_1_out), .b_i(controlled_buffer_1_out), .x(decoder_2_out2), .b_s(b_s), .b_e(b_e),
    .y(decoder_1_out11));
  RAM1 ram1_45 (
    .b_o(controlled_buffer_1_out), .b_i(controlled_buffer_1_out), .x(decoder_2_out2), .b_s(b_s), .b_e(b_e),
    .y(decoder_1_out12));
  RAM1 ram1_46 (
    .b_o(controlled_buffer_1_out), .b_i(controlled_buffer_1_out), .x(decoder_2_out2), .b_s(b_s), .b_e(b_e),
    .y(decoder_1_out13));
  RAM1 ram1_47 (
    .b_o(controlled_buffer_1_out), .b_i(controlled_buffer_1_out), .x(decoder_2_out2), .b_s(b_s), .b_e(b_e),
    .y(decoder_1_out14));
  RAM1 ram1_48 (
    .b_o(controlled_buffer_1_out), .b_i(controlled_buffer_1_out), .x(decoder_2_out2), .b_s(b_s), .b_e(b_e),
    .y(decoder_1_out15));
  RAM1 ram1_49 (
    .b_o(controlled_buffer_1_out), .b_i(controlled_buffer_1_out), .x(decoder_2_out3), .b_s(b_s), .b_e(b_e),
    .y(decoder_1_out0));
  RAM1 ram1_50 (
    .b_o(controlled_buffer_1_out), .b_i(controlled_buffer_1_out), .x(decoder_2_out3), .b_s(b_s), .b_e(b_e),
    .y(decoder_1_out1));
  RAM1 ram1_51 (
    .b_o(controlled_buffer_1_out), .b_i(controlled_buffer_1_out), .x(decoder_2_out3), .b_s(b_s), .b_e(b_e),
    .y(decoder_1_out2));
  RAM1 ram1_52 (
    .b_o(controlled_buffer_1_out), .b_i(controlled_buffer_1_out), .x(decoder_2_out3), .b_s(b_s), .b_e(b_e),
    .y(decoder_1_out3));
  RAM1 ram1_53 (
    .b_o(controlled_buffer_1_out), .b_i(controlled_buffer_1_out), .x(decoder_2_out3), .b_s(b_s), .b_e(b_e),
    .y(decoder_1_out4));
  RAM1 ram1_54 (
    .b_o(controlled_buffer_1_out), .b_i(controlled_buffer_1_out), .x(decoder_2_out3), .b_s(b_s), .b_e(b_e),
    .y(decoder_1_out5));
  RAM1 ram1_55 (
    .b_o(controlled_buffer_1_out), .b_i(controlled_buffer_1_out), .x(decoder_2_out3), .b_s(b_s), .b_e(b_e),
    .y(decoder_1_out6));
  RAM1 ram1_56 (
    .b_o(controlled_buffer_1_out), .b_i(controlled_buffer_1_out), .x(decoder_2_out3), .b_s(b_s), .b_e(b_e),
    .y(decoder_1_out7));
  RAM1 ram1_57 (
    .b_o(controlled_buffer_1_out), .b_i(controlled_buffer_1_out), .x(decoder_2_out3), .b_s(b_s), .b_e(b_e),
    .y(decoder_1_out8));
  RAM1 ram1_58 (
    .b_o(controlled_buffer_1_out), .b_i(controlled_buffer_1_out), .x(decoder_2_out3), .b_s(b_s), .b_e(b_e),
    .y(decoder_1_out9));
  RAM1 ram1_59 (
    .b_o(controlled_buffer_1_out), .b_i(controlled_buffer_1_out), .x(decoder_2_out3), .b_s(b_s), .b_e(b_e),
    .y(decoder_1_out10));
  RAM1 ram1_60 (
    .b_o(controlled_buffer_1_out), .b_i(controlled_buffer_1_out), .x(decoder_2_out3), .b_s(b_s), .b_e(b_e),
    .y(decoder_1_out11));
  RAM1 ram1_61 (
    .b_o(controlled_buffer_1_out), .b_i(controlled_buffer_1_out), .x(decoder_2_out3), .b_s(b_s), .b_e(b_e),
    .y(decoder_1_out12));
  RAM1 ram1_62 (
    .b_o(controlled_buffer_1_out), .b_i(controlled_buffer_1_out), .x(decoder_2_out3), .b_s(b_s), .b_e(b_e),
    .y(decoder_1_out13));
  RAM1 ram1_63 (
    .b_o(controlled_buffer_1_out), .b_i(controlled_buffer_1_out), .x(decoder_2_out3), .b_s(b_s), .b_e(b_e),
    .y(decoder_1_out14));
  RAM1 ram1_64 (
    .b_o(controlled_buffer_1_out), .b_i(controlled_buffer_1_out), .x(decoder_2_out3), .b_s(b_s), .b_e(b_e),
    .y(decoder_1_out15));
  RAM1 ram1_65 (
    .b_o(controlled_buffer_1_out), .b_i(controlled_buffer_1_out), .x(decoder_2_out4), .b_s(b_s), .b_e(b_e),
    .y(decoder_1_out0));
  RAM1 ram1_66 (
    .b_o(controlled_buffer_1_out), .b_i(controlled_buffer_1_out), .x(decoder_2_out4), .b_s(b_s), .b_e(b_e),
    .y(decoder_1_out1));
  RAM1 ram1_67 (
    .b_o(controlled_buffer_1_out), .b_i(controlled_buffer_1_out), .x(decoder_2_out4), .b_s(b_s), .b_e(b_e),
    .y(decoder_1_out2));
  RAM1 ram1_68 (
    .b_o(controlled_buffer_1_out), .b_i(controlled_buffer_1_out), .x(decoder_2_out4), .b_s(b_s), .b_e(b_e),
    .y(decoder_1_out3));
  RAM1 ram1_69 (
    .b_o(controlled_buffer_1_out), .b_i(controlled_buffer_1_out), .x(decoder_2_out4), .b_s(b_s), .b_e(b_e),
    .y(decoder_1_out4));
  RAM1 ram1_70 (
    .b_o(controlled_buffer_1_out), .b_i(controlled_buffer_1_out), .x(decoder_2_out4), .b_s(b_s), .b_e(b_e),
    .y(decoder_1_out5));
  RAM1 ram1_71 (
    .b_o(controlled_buffer_1_out), .b_i(controlled_buffer_1_out), .x(decoder_2_out4), .b_s(b_s), .b_e(b_e),
    .y(decoder_1_out6));
  RAM1 ram1_72 (
    .b_o(controlled_buffer_1_out), .b_i(controlled_buffer_1_out), .x(decoder_2_out4), .b_s(b_s), .b_e(b_e),
    .y(decoder_1_out7));
  RAM1 ram1_73 (
    .b_o(controlled_buffer_1_out), .b_i(controlled_buffer_1_out), .x(decoder_2_out4), .b_s(b_s), .b_e(b_e),
    .y(decoder_1_out8));
  RAM1 ram1_74 (
    .b_o(controlled_buffer_1_out), .b_i(controlled_buffer_1_out), .x(decoder_2_out4), .b_s(b_s), .b_e(b_e),
    .y(decoder_1_out9));
  RAM1 ram1_75 (
    .b_o(controlled_buffer_1_out), .b_i(controlled_buffer_1_out), .x(decoder_2_out4), .b_s(b_s), .b_e(b_e),
    .y(decoder_1_out10));
  RAM1 ram1_76 (
    .b_o(controlled_buffer_1_out), .b_i(controlled_buffer_1_out), .x(decoder_2_out4), .b_s(b_s), .b_e(b_e),
    .y(decoder_1_out11));
  RAM1 ram1_77 (
    .b_o(controlled_buffer_1_out), .b_i(controlled_buffer_1_out), .x(decoder_2_out4), .b_s(b_s), .b_e(b_e),
    .y(decoder_1_out12));
  RAM1 ram1_78 (
    .b_o(controlled_buffer_1_out), .b_i(controlled_buffer_1_out), .x(decoder_2_out4), .b_s(b_s), .b_e(b_e),
    .y(decoder_1_out13));
  RAM1 ram1_79 (
    .b_o(controlled_buffer_1_out), .b_i(controlled_buffer_1_out), .x(decoder_2_out4), .b_s(b_s), .b_e(b_e),
    .y(decoder_1_out14));
  RAM1 ram1_80 (
    .b_o(controlled_buffer_1_out), .b_i(controlled_buffer_1_out), .x(decoder_2_out4), .b_s(b_s), .b_e(b_e),
    .y(decoder_1_out15));
  RAM1 ram1_81 (
    .b_o(controlled_buffer_1_out), .b_i(controlled_buffer_1_out), .x(decoder_2_out5), .b_s(b_s), .b_e(b_e),
    .y(decoder_1_out0));
  RAM1 ram1_82 (
    .b_o(controlled_buffer_1_out), .b_i(controlled_buffer_1_out), .x(decoder_2_out5), .b_s(b_s), .b_e(b_e),
    .y(decoder_1_out1));
  RAM1 ram1_83 (
    .b_o(controlled_buffer_1_out), .b_i(controlled_buffer_1_out), .x(decoder_2_out5), .b_s(b_s), .b_e(b_e),
    .y(decoder_1_out2));
  RAM1 ram1_84 (
    .b_o(controlled_buffer_1_out), .b_i(controlled_buffer_1_out), .x(decoder_2_out5), .b_s(b_s), .b_e(b_e),
    .y(decoder_1_out3));
  RAM1 ram1_85 (
    .b_o(controlled_buffer_1_out), .b_i(controlled_buffer_1_out), .x(decoder_2_out5), .b_s(b_s), .b_e(b_e),
    .y(decoder_1_out4));
  RAM1 ram1_86 (
    .b_o(controlled_buffer_1_out), .b_i(controlled_buffer_1_out), .x(decoder_2_out5), .b_s(b_s), .b_e(b_e),
    .y(decoder_1_out5));
  RAM1 ram1_87 (
    .b_o(controlled_buffer_1_out), .b_i(controlled_buffer_1_out), .x(decoder_2_out5), .b_s(b_s), .b_e(b_e),
    .y(decoder_1_out6));
  RAM1 ram1_88 (
    .b_o(controlled_buffer_1_out), .b_i(controlled_buffer_1_out), .x(decoder_2_out5), .b_s(b_s), .b_e(b_e),
    .y(decoder_1_out7));
  RAM1 ram1_89 (
    .b_o(controlled_buffer_1_out), .b_i(controlled_buffer_1_out), .x(decoder_2_out5), .b_s(b_s), .b_e(b_e),
    .y(decoder_1_out8));
  RAM1 ram1_90 (
    .b_o(controlled_buffer_1_out), .b_i(controlled_buffer_1_out), .x(decoder_2_out5), .b_s(b_s), .b_e(b_e),
    .y(decoder_1_out9));
  RAM1 ram1_91 (
    .b_o(controlled_buffer_1_out), .b_i(controlled_buffer_1_out), .x(decoder_2_out5), .b_s(b_s), .b_e(b_e),
    .y(decoder_1_out10));
  RAM1 ram1_92 (
    .b_o(controlled_buffer_1_out), .b_i(controlled_buffer_1_out), .x(decoder_2_out5), .b_s(b_s), .b_e(b_e),
    .y(decoder_1_out11));
  RAM1 ram1_93 (
    .b_o(controlled_buffer_1_out), .b_i(controlled_buffer_1_out), .x(decoder_2_out5), .b_s(b_s), .b_e(b_e),
    .y(decoder_1_out12));
  RAM1 ram1_94 (
    .b_o(controlled_buffer_1_out), .b_i(controlled_buffer_1_out), .x(decoder_2_out5), .b_s(b_s), .b_e(b_e),
    .y(decoder_1_out13));
  RAM1 ram1_95 (
    .b_o(controlled_buffer_1_out), .b_i(controlled_buffer_1_out), .x(decoder_2_out5), .b_s(b_s), .b_e(b_e),
    .y(decoder_1_out14));
  RAM1 ram1_96 (
    .b_o(controlled_buffer_1_out), .b_i(controlled_buffer_1_out), .x(decoder_2_out5), .b_s(b_s), .b_e(b_e),
    .y(decoder_1_out15));
  Decoder #(.enable("false"), .select(4)) decoder_2 (
    .out0(decoder_2_out0), .out1(decoder_2_out1), .out2(decoder_2_out2), .out3(decoder_2_out3),
    .out4(decoder_2_out4), .out5(decoder_2_out5), .out6(decoder_2_out6), .out7(decoder_2_out7),
    .out8(decoder_2_out8), .out9(decoder_2_out9), .out10(decoder_2_out10), .out11(decoder_2_out11),
    .out12(decoder_2_out12), .out13(decoder_2_out13), .out14(decoder_2_out14), .out15(decoder_2_out15),
    .sel(n8register_1_o[3:0]));
  RAM1 ram1_97 (
    .b_o(controlled_buffer_1_out), .b_i(controlled_buffer_1_out), .x(decoder_2_out6), .b_s(b_s), .b_e(b_e),
    .y(decoder_1_out0));
  RAM1 ram1_98 (
    .b_o(controlled_buffer_1_out), .b_i(controlled_buffer_1_out), .x(decoder_2_out6), .b_s(b_s), .b_e(b_e),
    .y(decoder_1_out1));
  RAM1 ram1_99 (
    .b_o(controlled_buffer_1_out), .b_i(controlled_buffer_1_out), .x(decoder_2_out6), .b_s(b_s), .b_e(b_e),
    .y(decoder_1_out2));
  RAM1 ram1_100 (
    .b_o(controlled_buffer_1_out), .b_i(controlled_buffer_1_out), .x(decoder_2_out6), .b_s(b_s), .b_e(b_e),
    .y(decoder_1_out3));
  RAM1 ram1_101 (
    .b_o(controlled_buffer_1_out), .b_i(controlled_buffer_1_out), .x(decoder_2_out6), .b_s(b_s), .b_e(b_e),
    .y(decoder_1_out4));
  RAM1 ram1_102 (
    .b_o(controlled_buffer_1_out), .b_i(controlled_buffer_1_out), .x(decoder_2_out6), .b_s(b_s), .b_e(b_e),
    .y(decoder_1_out5));
  RAM1 ram1_103 (
    .b_o(controlled_buffer_1_out), .b_i(controlled_buffer_1_out), .x(decoder_2_out6), .b_s(b_s), .b_e(b_e),
    .y(decoder_1_out6));
  RAM1 ram1_104 (
    .b_o(controlled_buffer_1_out), .b_i(controlled_buffer_1_out), .x(decoder_2_out6), .b_s(b_s), .b_e(b_e),
    .y(decoder_1_out7));
  RAM1 ram1_105 (
    .b_o(controlled_buffer_1_out), .b_i(controlled_buffer_1_out), .x(decoder_2_out6), .b_s(b_s), .b_e(b_e),
    .y(decoder_1_out8));
  RAM1 ram1_106 (
    .b_o(controlled_buffer_1_out), .b_i(controlled_buffer_1_out), .x(decoder_2_out6), .b_s(b_s), .b_e(b_e),
    .y(decoder_1_out9));
  RAM1 ram1_107 (
    .b_o(controlled_buffer_1_out), .b_i(controlled_buffer_1_out), .x(decoder_2_out6), .b_s(b_s), .b_e(b_e),
    .y(decoder_1_out10));
  RAM1 ram1_108 (
    .b_o(controlled_buffer_1_out), .b_i(controlled_buffer_1_out), .x(decoder_2_out6), .b_s(b_s), .b_e(b_e),
    .y(decoder_1_out11));
  RAM1 ram1_109 (
    .b_o(controlled_buffer_1_out), .b_i(controlled_buffer_1_out), .x(decoder_2_out6), .b_s(b_s), .b_e(b_e),
    .y(decoder_1_out12));
  RAM1 ram1_110 (
    .b_o(controlled_buffer_1_out), .b_i(controlled_buffer_1_out), .x(decoder_2_out6), .b_s(b_s), .b_e(b_e),
    .y(decoder_1_out13));
  RAM1 ram1_111 (
    .b_o(controlled_buffer_1_out), .b_i(controlled_buffer_1_out), .x(decoder_2_out6), .b_s(b_s), .b_e(b_e),
    .y(decoder_1_out14));
  RAM1 ram1_112 (
    .b_o(controlled_buffer_1_out), .b_i(controlled_buffer_1_out), .x(decoder_2_out6), .b_s(b_s), .b_e(b_e),
    .y(decoder_1_out15));
  RAM1 ram1_113 (
    .b_o(controlled_buffer_1_out), .b_i(controlled_buffer_1_out), .x(decoder_2_out7), .b_s(b_s), .b_e(b_e),
    .y(decoder_1_out0));
  RAM1 ram1_114 (
    .b_o(controlled_buffer_1_out), .b_i(controlled_buffer_1_out), .x(decoder_2_out7), .b_s(b_s), .b_e(b_e),
    .y(decoder_1_out1));
  RAM1 ram1_115 (
    .b_o(controlled_buffer_1_out), .b_i(controlled_buffer_1_out), .x(decoder_2_out7), .b_s(b_s), .b_e(b_e),
    .y(decoder_1_out2));
  RAM1 ram1_116 (
    .b_o(controlled_buffer_1_out), .b_i(controlled_buffer_1_out), .x(decoder_2_out7), .b_s(b_s), .b_e(b_e),
    .y(decoder_1_out3));
  RAM1 ram1_117 (
    .b_o(controlled_buffer_1_out), .b_i(controlled_buffer_1_out), .x(decoder_2_out7), .b_s(b_s), .b_e(b_e),
    .y(decoder_1_out4));
  RAM1 ram1_118 (
    .b_o(controlled_buffer_1_out), .b_i(controlled_buffer_1_out), .x(decoder_2_out7), .b_s(b_s), .b_e(b_e),
    .y(decoder_1_out5));
  RAM1 ram1_119 (
    .b_o(controlled_buffer_1_out), .b_i(controlled_buffer_1_out), .x(decoder_2_out7), .b_s(b_s), .b_e(b_e),
    .y(decoder_1_out6));
  RAM1 ram1_120 (
    .b_o(controlled_buffer_1_out), .b_i(controlled_buffer_1_out), .x(decoder_2_out7), .b_s(b_s), .b_e(b_e),
    .y(decoder_1_out7));
  RAM1 ram1_121 (
    .b_o(controlled_buffer_1_out), .b_i(controlled_buffer_1_out), .x(decoder_2_out7), .b_s(b_s), .b_e(b_e),
    .y(decoder_1_out8));
  RAM1 ram1_122 (
    .b_o(controlled_buffer_1_out), .b_i(controlled_buffer_1_out), .x(decoder_2_out7), .b_s(b_s), .b_e(b_e),
    .y(decoder_1_out9));
  RAM1 ram1_123 (
    .b_o(controlled_buffer_1_out), .b_i(controlled_buffer_1_out), .x(decoder_2_out7), .b_s(b_s), .b_e(b_e),
    .y(decoder_1_out10));
  RAM1 ram1_124 (
    .b_o(controlled_buffer_1_out), .b_i(controlled_buffer_1_out), .x(decoder_2_out7), .b_s(b_s), .b_e(b_e),
    .y(decoder_1_out11));
  RAM1 ram1_125 (
    .b_o(controlled_buffer_1_out), .b_i(controlled_buffer_1_out), .x(decoder_2_out7), .b_s(b_s), .b_e(b_e),
    .y(decoder_1_out12));
  RAM1 ram1_126 (
    .b_o(controlled_buffer_1_out), .b_i(controlled_buffer_1_out), .x(decoder_2_out7), .b_s(b_s), .b_e(b_e),
    .y(decoder_1_out13));
  RAM1 ram1_127 (
    .b_o(controlled_buffer_1_out), .b_i(controlled_buffer_1_out), .x(decoder_2_out7), .b_s(b_s), .b_e(b_e),
    .y(decoder_1_out14));
  RAM1 ram1_128 (
    .b_o(controlled_buffer_1_out), .b_i(controlled_buffer_1_out), .x(decoder_2_out7), .b_s(b_s), .b_e(b_e),
    .y(decoder_1_out15));
  RAM1 ram1_129 (
    .b_o(controlled_buffer_1_out), .b_i(controlled_buffer_1_out), .x(decoder_2_out8), .b_s(b_s), .b_e(b_e),
    .y(decoder_1_out0));
  RAM1 ram1_130 (
    .b_o(controlled_buffer_1_out), .b_i(controlled_buffer_1_out), .x(decoder_2_out8), .b_s(b_s), .b_e(b_e),
    .y(decoder_1_out1));
  RAM1 ram1_131 (
    .b_o(controlled_buffer_1_out), .b_i(controlled_buffer_1_out), .x(decoder_2_out8), .b_s(b_s), .b_e(b_e),
    .y(decoder_1_out2));
  RAM1 ram1_132 (
    .b_o(controlled_buffer_1_out), .b_i(controlled_buffer_1_out), .x(decoder_2_out8), .b_s(b_s), .b_e(b_e),
    .y(decoder_1_out3));
  RAM1 ram1_133 (
    .b_o(controlled_buffer_1_out), .b_i(controlled_buffer_1_out), .x(decoder_2_out8), .b_s(b_s), .b_e(b_e),
    .y(decoder_1_out4));
  RAM1 ram1_134 (
    .b_o(controlled_buffer_1_out), .b_i(controlled_buffer_1_out), .x(decoder_2_out8), .b_s(b_s), .b_e(b_e),
    .y(decoder_1_out5));
  RAM1 ram1_135 (
    .b_o(controlled_buffer_1_out), .b_i(controlled_buffer_1_out), .x(decoder_2_out8), .b_s(b_s), .b_e(b_e),
    .y(decoder_1_out6));
  RAM1 ram1_136 (
    .b_o(controlled_buffer_1_out), .b_i(controlled_buffer_1_out), .x(decoder_2_out8), .b_s(b_s), .b_e(b_e),
    .y(decoder_1_out7));
  RAM1 ram1_137 (
    .b_o(controlled_buffer_1_out), .b_i(controlled_buffer_1_out), .x(decoder_2_out8), .b_s(b_s), .b_e(b_e),
    .y(decoder_1_out8));
  RAM1 ram1_138 (
    .b_o(controlled_buffer_1_out), .b_i(controlled_buffer_1_out), .x(decoder_2_out8), .b_s(b_s), .b_e(b_e),
    .y(decoder_1_out9));
  RAM1 ram1_139 (
    .b_o(controlled_buffer_1_out), .b_i(controlled_buffer_1_out), .x(decoder_2_out8), .b_s(b_s), .b_e(b_e),
    .y(decoder_1_out10));
  RAM1 ram1_140 (
    .b_o(controlled_buffer_1_out), .b_i(controlled_buffer_1_out), .x(decoder_2_out8), .b_s(b_s), .b_e(b_e),
    .y(decoder_1_out11));
  RAM1 ram1_141 (
    .b_o(controlled_buffer_1_out), .b_i(controlled_buffer_1_out), .x(decoder_2_out8), .b_s(b_s), .b_e(b_e),
    .y(decoder_1_out12));
  RAM1 ram1_142 (
    .b_o(controlled_buffer_1_out), .b_i(controlled_buffer_1_out), .x(decoder_2_out8), .b_s(b_s), .b_e(b_e),
    .y(decoder_1_out13));
  RAM1 ram1_143 (
    .b_o(controlled_buffer_1_out), .b_i(controlled_buffer_1_out), .x(decoder_2_out8), .b_s(b_s), .b_e(b_e),
    .y(decoder_1_out14));
  RAM1 ram1_144 (
    .b_o(controlled_buffer_1_out), .b_i(controlled_buffer_1_out), .x(decoder_2_out8), .b_s(b_s), .b_e(b_e),
    .y(decoder_1_out15));
  RAM1 ram1_145 (
    .b_o(controlled_buffer_1_out), .b_i(controlled_buffer_1_out), .x(decoder_2_out9), .b_s(b_s), .b_e(b_e),
    .y(decoder_1_out0));
  RAM1 ram1_146 (
    .b_o(controlled_buffer_1_out), .b_i(controlled_buffer_1_out), .x(decoder_2_out9), .b_s(b_s), .b_e(b_e),
    .y(decoder_1_out1));
  RAM1 ram1_147 (
    .b_o(controlled_buffer_1_out), .b_i(controlled_buffer_1_out), .x(decoder_2_out9), .b_s(b_s), .b_e(b_e),
    .y(decoder_1_out2));
  RAM1 ram1_148 (
    .b_o(controlled_buffer_1_out), .b_i(controlled_buffer_1_out), .x(decoder_2_out9), .b_s(b_s), .b_e(b_e),
    .y(decoder_1_out3));
  RAM1 ram1_149 (
    .b_o(controlled_buffer_1_out), .b_i(controlled_buffer_1_out), .x(decoder_2_out9), .b_s(b_s), .b_e(b_e),
    .y(decoder_1_out4));
  RAM1 ram1_150 (
    .b_o(controlled_buffer_1_out), .b_i(controlled_buffer_1_out), .x(decoder_2_out9), .b_s(b_s), .b_e(b_e),
    .y(decoder_1_out5));
  RAM1 ram1_151 (
    .b_o(controlled_buffer_1_out), .b_i(controlled_buffer_1_out), .x(decoder_2_out9), .b_s(b_s), .b_e(b_e),
    .y(decoder_1_out6));
  RAM1 ram1_152 (
    .b_o(controlled_buffer_1_out), .b_i(controlled_buffer_1_out), .x(decoder_2_out9), .b_s(b_s), .b_e(b_e),
    .y(decoder_1_out7));
  RAM1 ram1_153 (
    .b_o(controlled_buffer_1_out), .b_i(controlled_buffer_1_out), .x(decoder_2_out9), .b_s(b_s), .b_e(b_e),
    .y(decoder_1_out8));
  RAM1 ram1_154 (
    .b_o(controlled_buffer_1_out), .b_i(controlled_buffer_1_out), .x(decoder_2_out9), .b_s(b_s), .b_e(b_e),
    .y(decoder_1_out9));
  RAM1 ram1_155 (
    .b_o(controlled_buffer_1_out), .b_i(controlled_buffer_1_out), .x(decoder_2_out9), .b_s(b_s), .b_e(b_e),
    .y(decoder_1_out10));
  RAM1 ram1_156 (
    .b_o(controlled_buffer_1_out), .b_i(controlled_buffer_1_out), .x(decoder_2_out9), .b_s(b_s), .b_e(b_e),
    .y(decoder_1_out11));
  RAM1 ram1_157 (
    .b_o(controlled_buffer_1_out), .b_i(controlled_buffer_1_out), .x(decoder_2_out9), .b_s(b_s), .b_e(b_e),
    .y(decoder_1_out12));
  RAM1 ram1_158 (
    .b_o(controlled_buffer_1_out), .b_i(controlled_buffer_1_out), .x(decoder_2_out9), .b_s(b_s), .b_e(b_e),
    .y(decoder_1_out13));
  RAM1 ram1_159 (
    .b_o(controlled_buffer_1_out), .b_i(controlled_buffer_1_out), .x(decoder_2_out9), .b_s(b_s), .b_e(b_e),
    .y(decoder_1_out14));
  RAM1 ram1_160 (
    .b_o(controlled_buffer_1_out), .b_i(controlled_buffer_1_out), .x(decoder_2_out9), .b_s(b_s), .b_e(b_e),
    .y(decoder_1_out15));
  RAM1 ram1_161 (
    .b_o(controlled_buffer_1_out), .b_i(controlled_buffer_1_out), .x(decoder_2_out10), .b_s(b_s), .b_e(b_e),
    .y(decoder_1_out0));
  RAM1 ram1_162 (
    .b_o(controlled_buffer_1_out), .b_i(controlled_buffer_1_out), .x(decoder_2_out10), .b_s(b_s), .b_e(b_e),
    .y(decoder_1_out1));
  RAM1 ram1_163 (
    .b_o(controlled_buffer_1_out), .b_i(controlled_buffer_1_out), .x(decoder_2_out10), .b_s(b_s), .b_e(b_e),
    .y(decoder_1_out2));
  RAM1 ram1_164 (
    .b_o(controlled_buffer_1_out), .b_i(controlled_buffer_1_out), .x(decoder_2_out10), .b_s(b_s), .b_e(b_e),
    .y(decoder_1_out3));
  RAM1 ram1_165 (
    .b_o(controlled_buffer_1_out), .b_i(controlled_buffer_1_out), .x(decoder_2_out10), .b_s(b_s), .b_e(b_e),
    .y(decoder_1_out4));
  RAM1 ram1_166 (
    .b_o(controlled_buffer_1_out), .b_i(controlled_buffer_1_out), .x(decoder_2_out10), .b_s(b_s), .b_e(b_e),
    .y(decoder_1_out5));
  RAM1 ram1_167 (
    .b_o(controlled_buffer_1_out), .b_i(controlled_buffer_1_out), .x(decoder_2_out10), .b_s(b_s), .b_e(b_e),
    .y(decoder_1_out6));
  RAM1 ram1_168 (
    .b_o(controlled_buffer_1_out), .b_i(controlled_buffer_1_out), .x(decoder_2_out10), .b_s(b_s), .b_e(b_e),
    .y(decoder_1_out7));
  RAM1 ram1_169 (
    .b_o(controlled_buffer_1_out), .b_i(controlled_buffer_1_out), .x(decoder_2_out10), .b_s(b_s), .b_e(b_e),
    .y(decoder_1_out8));
  RAM1 ram1_170 (
    .b_o(controlled_buffer_1_out), .b_i(controlled_buffer_1_out), .x(decoder_2_out10), .b_s(b_s), .b_e(b_e),
    .y(decoder_1_out9));
  RAM1 ram1_171 (
    .b_o(controlled_buffer_1_out), .b_i(controlled_buffer_1_out), .x(decoder_2_out10), .b_s(b_s), .b_e(b_e),
    .y(decoder_1_out10));
  RAM1 ram1_172 (
    .b_o(controlled_buffer_1_out), .b_i(controlled_buffer_1_out), .x(decoder_2_out10), .b_s(b_s), .b_e(b_e),
    .y(decoder_1_out11));
  RAM1 ram1_173 (
    .b_o(controlled_buffer_1_out), .b_i(controlled_buffer_1_out), .x(decoder_2_out10), .b_s(b_s), .b_e(b_e),
    .y(decoder_1_out12));
  RAM1 ram1_174 (
    .b_o(controlled_buffer_1_out), .b_i(controlled_buffer_1_out), .x(decoder_2_out10), .b_s(b_s), .b_e(b_e),
    .y(decoder_1_out13));
  RAM1 ram1_175 (
    .b_o(controlled_buffer_1_out), .b_i(controlled_buffer_1_out), .x(decoder_2_out10), .b_s(b_s), .b_e(b_e),
    .y(decoder_1_out14));
  RAM1 ram1_176 (
    .b_o(controlled_buffer_1_out), .b_i(controlled_buffer_1_out), .x(decoder_2_out10), .b_s(b_s), .b_e(b_e),
    .y(decoder_1_out15));
  RAM1 ram1_177 (
    .b_o(controlled_buffer_1_out), .b_i(controlled_buffer_1_out), .x(decoder_2_out11), .b_s(b_s), .b_e(b_e),
    .y(decoder_1_out0));
  RAM1 ram1_178 (
    .b_o(controlled_buffer_1_out), .b_i(controlled_buffer_1_out), .x(decoder_2_out11), .b_s(b_s), .b_e(b_e),
    .y(decoder_1_out1));
  RAM1 ram1_179 (
    .b_o(controlled_buffer_1_out), .b_i(controlled_buffer_1_out), .x(decoder_2_out11), .b_s(b_s), .b_e(b_e),
    .y(decoder_1_out2));
  RAM1 ram1_180 (
    .b_o(controlled_buffer_1_out), .b_i(controlled_buffer_1_out), .x(decoder_2_out11), .b_s(b_s), .b_e(b_e),
    .y(decoder_1_out3));
  RAM1 ram1_181 (
    .b_o(controlled_buffer_1_out), .b_i(controlled_buffer_1_out), .x(decoder_2_out11), .b_s(b_s), .b_e(b_e),
    .y(decoder_1_out4));
  RAM1 ram1_182 (
    .b_o(controlled_buffer_1_out), .b_i(controlled_buffer_1_out), .x(decoder_2_out11), .b_s(b_s), .b_e(b_e),
    .y(decoder_1_out5));
  RAM1 ram1_183 (
    .b_o(controlled_buffer_1_out), .b_i(controlled_buffer_1_out), .x(decoder_2_out11), .b_s(b_s), .b_e(b_e),
    .y(decoder_1_out6));
  RAM1 ram1_184 (
    .b_o(controlled_buffer_1_out), .b_i(controlled_buffer_1_out), .x(decoder_2_out11), .b_s(b_s), .b_e(b_e),
    .y(decoder_1_out7));
  RAM1 ram1_185 (
    .b_o(controlled_buffer_1_out), .b_i(controlled_buffer_1_out), .x(decoder_2_out11), .b_s(b_s), .b_e(b_e),
    .y(decoder_1_out8));
  RAM1 ram1_186 (
    .b_o(controlled_buffer_1_out), .b_i(controlled_buffer_1_out), .x(decoder_2_out11), .b_s(b_s), .b_e(b_e),
    .y(decoder_1_out9));
  RAM1 ram1_187 (
    .b_o(controlled_buffer_1_out), .b_i(controlled_buffer_1_out), .x(decoder_2_out11), .b_s(b_s), .b_e(b_e),
    .y(decoder_1_out10));
  RAM1 ram1_188 (
    .b_o(controlled_buffer_1_out), .b_i(controlled_buffer_1_out), .x(decoder_2_out11), .b_s(b_s), .b_e(b_e),
    .y(decoder_1_out11));
  RAM1 ram1_189 (
    .b_o(controlled_buffer_1_out), .b_i(controlled_buffer_1_out), .x(decoder_2_out11), .b_s(b_s), .b_e(b_e),
    .y(decoder_1_out12));
  RAM1 ram1_190 (
    .b_o(controlled_buffer_1_out), .b_i(controlled_buffer_1_out), .x(decoder_2_out11), .b_s(b_s), .b_e(b_e),
    .y(decoder_1_out13));
  RAM1 ram1_191 (
    .b_o(controlled_buffer_1_out), .b_i(controlled_buffer_1_out), .x(decoder_2_out11), .b_s(b_s), .b_e(b_e),
    .y(decoder_1_out14));
  RAM1 ram1_192 (
    .b_o(controlled_buffer_1_out), .b_i(controlled_buffer_1_out), .x(decoder_2_out11), .b_s(b_s), .b_e(b_e),
    .y(decoder_1_out15));
  RAM1 ram1_193 (
    .b_o(controlled_buffer_1_out), .b_i(controlled_buffer_1_out), .x(decoder_2_out12), .b_s(b_s), .b_e(b_e),
    .y(decoder_1_out0));
  RAM1 ram1_194 (
    .b_o(controlled_buffer_1_out), .b_i(controlled_buffer_1_out), .x(decoder_2_out12), .b_s(b_s), .b_e(b_e),
    .y(decoder_1_out1));
  RAM1 ram1_195 (
    .b_o(controlled_buffer_1_out), .b_i(controlled_buffer_1_out), .x(decoder_2_out12), .b_s(b_s), .b_e(b_e),
    .y(decoder_1_out2));
  RAM1 ram1_196 (
    .b_o(controlled_buffer_1_out), .b_i(controlled_buffer_1_out), .x(decoder_2_out12), .b_s(b_s), .b_e(b_e),
    .y(decoder_1_out3));
  RAM1 ram1_197 (
    .b_o(controlled_buffer_1_out), .b_i(controlled_buffer_1_out), .x(decoder_2_out12), .b_s(b_s), .b_e(b_e),
    .y(decoder_1_out4));
  RAM1 ram1_198 (
    .b_o(controlled_buffer_1_out), .b_i(controlled_buffer_1_out), .x(decoder_2_out12), .b_s(b_s), .b_e(b_e),
    .y(decoder_1_out5));
  RAM1 ram1_199 (
    .b_o(controlled_buffer_1_out), .b_i(controlled_buffer_1_out), .x(decoder_2_out12), .b_s(b_s), .b_e(b_e),
    .y(decoder_1_out6));
  RAM1 ram1_200 (
    .b_o(controlled_buffer_1_out), .b_i(controlled_buffer_1_out), .x(decoder_2_out12), .b_s(b_s), .b_e(b_e),
    .y(decoder_1_out7));
  RAM1 ram1_201 (
    .b_o(controlled_buffer_1_out), .b_i(controlled_buffer_1_out), .x(decoder_2_out12), .b_s(b_s), .b_e(b_e),
    .y(decoder_1_out8));
  RAM1 ram1_202 (
    .b_o(controlled_buffer_1_out), .b_i(controlled_buffer_1_out), .x(decoder_2_out12), .b_s(b_s), .b_e(b_e),
    .y(decoder_1_out9));
  RAM1 ram1_203 (
    .b_o(controlled_buffer_1_out), .b_i(controlled_buffer_1_out), .x(decoder_2_out12), .b_s(b_s), .b_e(b_e),
    .y(decoder_1_out10));
  RAM1 ram1_204 (
    .b_o(controlled_buffer_1_out), .b_i(controlled_buffer_1_out), .x(decoder_2_out12), .b_s(b_s), .b_e(b_e),
    .y(decoder_1_out11));
  RAM1 ram1_205 (
    .b_o(controlled_buffer_1_out), .b_i(controlled_buffer_1_out), .x(decoder_2_out12), .b_s(b_s), .b_e(b_e),
    .y(decoder_1_out12));
  RAM1 ram1_206 (
    .b_o(controlled_buffer_1_out), .b_i(controlled_buffer_1_out), .x(decoder_2_out12), .b_s(b_s), .b_e(b_e),
    .y(decoder_1_out13));
  RAM1 ram1_207 (
    .b_o(controlled_buffer_1_out), .b_i(controlled_buffer_1_out), .x(decoder_2_out12), .b_s(b_s), .b_e(b_e),
    .y(decoder_1_out14));
  RAM1 ram1_208 (
    .b_o(controlled_buffer_1_out), .b_i(controlled_buffer_1_out), .x(decoder_2_out12), .b_s(b_s), .b_e(b_e),
    .y(decoder_1_out15));
  RAM1 ram1_209 (
    .b_o(controlled_buffer_1_out), .b_i(controlled_buffer_1_out), .x(decoder_2_out13), .b_s(b_s), .b_e(b_e),
    .y(decoder_1_out0));
  RAM1 ram1_210 (
    .b_o(controlled_buffer_1_out), .b_i(controlled_buffer_1_out), .x(decoder_2_out13), .b_s(b_s), .b_e(b_e),
    .y(decoder_1_out1));
  RAM1 ram1_211 (
    .b_o(controlled_buffer_1_out), .b_i(controlled_buffer_1_out), .x(decoder_2_out13), .b_s(b_s), .b_e(b_e),
    .y(decoder_1_out2));
  RAM1 ram1_212 (
    .b_o(controlled_buffer_1_out), .b_i(controlled_buffer_1_out), .x(decoder_2_out13), .b_s(b_s), .b_e(b_e),
    .y(decoder_1_out3));
  RAM1 ram1_213 (
    .b_o(controlled_buffer_1_out), .b_i(controlled_buffer_1_out), .x(decoder_2_out13), .b_s(b_s), .b_e(b_e),
    .y(decoder_1_out4));
  RAM1 ram1_214 (
    .b_o(controlled_buffer_1_out), .b_i(controlled_buffer_1_out), .x(decoder_2_out13), .b_s(b_s), .b_e(b_e),
    .y(decoder_1_out5));
  RAM1 ram1_215 (
    .b_o(controlled_buffer_1_out), .b_i(controlled_buffer_1_out), .x(decoder_2_out13), .b_s(b_s), .b_e(b_e),
    .y(decoder_1_out6));
  RAM1 ram1_216 (
    .b_o(controlled_buffer_1_out), .b_i(controlled_buffer_1_out), .x(decoder_2_out13), .b_s(b_s), .b_e(b_e),
    .y(decoder_1_out7));
  RAM1 ram1_217 (
    .b_o(controlled_buffer_1_out), .b_i(controlled_buffer_1_out), .x(decoder_2_out13), .b_s(b_s), .b_e(b_e),
    .y(decoder_1_out8));
  RAM1 ram1_218 (
    .b_o(controlled_buffer_1_out), .b_i(controlled_buffer_1_out), .x(decoder_2_out13), .b_s(b_s), .b_e(b_e),
    .y(decoder_1_out9));
  RAM1 ram1_219 (
    .b_o(controlled_buffer_1_out), .b_i(controlled_buffer_1_out), .x(decoder_2_out13), .b_s(b_s), .b_e(b_e),
    .y(decoder_1_out10));
  RAM1 ram1_220 (
    .b_o(controlled_buffer_1_out), .b_i(controlled_buffer_1_out), .x(decoder_2_out13), .b_s(b_s), .b_e(b_e),
    .y(decoder_1_out11));
  RAM1 ram1_221 (
    .b_o(controlled_buffer_1_out), .b_i(controlled_buffer_1_out), .x(decoder_2_out13), .b_s(b_s), .b_e(b_e),
    .y(decoder_1_out12));
  RAM1 ram1_222 (
    .b_o(controlled_buffer_1_out), .b_i(controlled_buffer_1_out), .x(decoder_2_out13), .b_s(b_s), .b_e(b_e),
    .y(decoder_1_out13));
  RAM1 ram1_223 (
    .b_o(controlled_buffer_1_out), .b_i(controlled_buffer_1_out), .x(decoder_2_out13), .b_s(b_s), .b_e(b_e),
    .y(decoder_1_out14));
  RAM1 ram1_224 (
    .b_o(controlled_buffer_1_out), .b_i(controlled_buffer_1_out), .x(decoder_2_out13), .b_s(b_s), .b_e(b_e),
    .y(decoder_1_out15));
  RAM1 ram1_225 (
    .b_o(controlled_buffer_1_out), .b_i(controlled_buffer_1_out), .x(decoder_2_out14), .b_s(b_s), .b_e(b_e),
    .y(decoder_1_out0));
  RAM1 ram1_226 (
    .b_o(controlled_buffer_1_out), .b_i(controlled_buffer_1_out), .x(decoder_2_out14), .b_s(b_s), .b_e(b_e),
    .y(decoder_1_out1));
  RAM1 ram1_227 (
    .b_o(controlled_buffer_1_out), .b_i(controlled_buffer_1_out), .x(decoder_2_out14), .b_s(b_s), .b_e(b_e),
    .y(decoder_1_out2));
  RAM1 ram1_228 (
    .b_o(controlled_buffer_1_out), .b_i(controlled_buffer_1_out), .x(decoder_2_out14), .b_s(b_s), .b_e(b_e),
    .y(decoder_1_out3));
  RAM1 ram1_229 (
    .b_o(controlled_buffer_1_out), .b_i(controlled_buffer_1_out), .x(decoder_2_out14), .b_s(b_s), .b_e(b_e),
    .y(decoder_1_out4));
  RAM1 ram1_230 (
    .b_o(controlled_buffer_1_out), .b_i(controlled_buffer_1_out), .x(decoder_2_out14), .b_s(b_s), .b_e(b_e),
    .y(decoder_1_out5));
  RAM1 ram1_231 (
    .b_o(controlled_buffer_1_out), .b_i(controlled_buffer_1_out), .x(decoder_2_out14), .b_s(b_s), .b_e(b_e),
    .y(decoder_1_out6));
  RAM1 ram1_232 (
    .b_o(controlled_buffer_1_out), .b_i(controlled_buffer_1_out), .x(decoder_2_out14), .b_s(b_s), .b_e(b_e),
    .y(decoder_1_out7));
  RAM1 ram1_233 (
    .b_o(controlled_buffer_1_out), .b_i(controlled_buffer_1_out), .x(decoder_2_out14), .b_s(b_s), .b_e(b_e),
    .y(decoder_1_out8));
  RAM1 ram1_234 (
    .b_o(controlled_buffer_1_out), .b_i(controlled_buffer_1_out), .x(decoder_2_out14), .b_s(b_s), .b_e(b_e),
    .y(decoder_1_out9));
  RAM1 ram1_235 (
    .b_o(controlled_buffer_1_out), .b_i(controlled_buffer_1_out), .x(decoder_2_out14), .b_s(b_s), .b_e(b_e),
    .y(decoder_1_out10));
  RAM1 ram1_236 (
    .b_o(controlled_buffer_1_out), .b_i(controlled_buffer_1_out), .x(decoder_2_out14), .b_s(b_s), .b_e(b_e),
    .y(decoder_1_out11));
  RAM1 ram1_237 (
    .b_o(controlled_buffer_1_out), .b_i(controlled_buffer_1_out), .x(decoder_2_out14), .b_s(b_s), .b_e(b_e),
    .y(decoder_1_out12));
  RAM1 ram1_238 (
    .b_o(controlled_buffer_1_out), .b_i(controlled_buffer_1_out), .x(decoder_2_out14), .b_s(b_s), .b_e(b_e),
    .y(decoder_1_out13));
  RAM1 ram1_239 (
    .b_o(controlled_buffer_1_out), .b_i(controlled_buffer_1_out), .x(decoder_2_out14), .b_s(b_s), .b_e(b_e),
    .y(decoder_1_out14));
  RAM1 ram1_240 (
    .b_o(controlled_buffer_1_out), .b_i(controlled_buffer_1_out), .x(decoder_2_out14), .b_s(b_s), .b_e(b_e),
    .y(decoder_1_out15));
  RAM1 ram1_241 (
    .b_o(controlled_buffer_1_out), .b_i(controlled_buffer_1_out), .x(decoder_2_out15), .b_s(b_s), .b_e(b_e),
    .y(decoder_1_out0));
  RAM1 ram1_242 (
    .b_o(controlled_buffer_1_out), .b_i(controlled_buffer_1_out), .x(decoder_2_out15), .b_s(b_s), .b_e(b_e),
    .y(decoder_1_out1));
  RAM1 ram1_243 (
    .b_o(controlled_buffer_1_out), .b_i(controlled_buffer_1_out), .x(decoder_2_out15), .b_s(b_s), .b_e(b_e),
    .y(decoder_1_out2));
  RAM1 ram1_244 (
    .b_o(controlled_buffer_1_out), .b_i(controlled_buffer_1_out), .x(decoder_2_out15), .b_s(b_s), .b_e(b_e),
    .y(decoder_1_out3));
  RAM1 ram1_245 (
    .b_o(controlled_buffer_1_out), .b_i(controlled_buffer_1_out), .x(decoder_2_out15), .b_s(b_s), .b_e(b_e),
    .y(decoder_1_out4));
  RAM1 ram1_246 (
    .b_o(controlled_buffer_1_out), .b_i(controlled_buffer_1_out), .x(decoder_2_out15), .b_s(b_s), .b_e(b_e),
    .y(decoder_1_out5));
  RAM1 ram1_247 (
    .b_o(controlled_buffer_1_out), .b_i(controlled_buffer_1_out), .x(decoder_2_out15), .b_s(b_s), .b_e(b_e),
    .y(decoder_1_out6));
  RAM1 ram1_248 (
    .b_o(controlled_buffer_1_out), .b_i(controlled_buffer_1_out), .x(decoder_2_out15), .b_s(b_s), .b_e(b_e),
    .y(decoder_1_out7));
  RAM1 ram1_249 (
    .b_o(controlled_buffer_1_out), .b_i(controlled_buffer_1_out), .x(decoder_2_out15), .b_s(b_s), .b_e(b_e),
    .y(decoder_1_out8));
  RAM1 ram1_250 (
    .b_o(controlled_buffer_1_out), .b_i(controlled_buffer_1_out), .x(decoder_2_out15), .b_s(b_s), .b_e(b_e),
    .y(decoder_1_out9));
  RAM1 ram1_251 (
    .b_o(controlled_buffer_1_out), .b_i(controlled_buffer_1_out), .x(decoder_2_out15), .b_s(b_s), .b_e(b_e),
    .y(decoder_1_out10));
  RAM1 ram1_252 (
    .b_o(controlled_buffer_1_out), .b_i(controlled_buffer_1_out), .x(decoder_2_out15), .b_s(b_s), .b_e(b_e),
    .y(decoder_1_out11));
  RAM1 ram1_253 (
    .b_o(controlled_buffer_1_out), .b_i(controlled_buffer_1_out), .x(decoder_2_out15), .b_s(b_s), .b_e(b_e),
    .y(decoder_1_out12));
  RAM1 ram1_254 (
    .b_o(controlled_buffer_1_out), .b_i(controlled_buffer_1_out), .x(decoder_2_out15), .b_s(b_s), .b_e(b_e),
    .y(decoder_1_out13));
  RAM1 ram1_255 (
    .b_o(controlled_buffer_1_out), .b_i(controlled_buffer_1_out), .x(decoder_2_out15), .b_s(b_s), .b_e(b_e),
    .y(decoder_1_out14));
  RAM1 ram1_256 (
    .b_o(controlled_buffer_1_out), .b_i(controlled_buffer_1_out), .x(decoder_2_out15), .b_s(b_s), .b_e(b_e),
    .y(decoder_1_out15));
  assign b_o = b_e ? controlled_buffer_1_out : 8'bz;  // Controlled_Buffer controlled_buffer_2
endmodule

module RAM1 (
  input  y,
  input  x,
  input  b_s,
  input  b_e,
  input  [7:0] b_i,
  output [7:0] b_o
);

  wire and_1_out, and_2_out, and_3_out;
  wire [7:0] _00_o, controlled_buffer_1_out;

  and and_1 (and_1_out, y, x);
  and and_2 (and_2_out, and_1_out, b_s);
  and and_3 (and_3_out, and_1_out, b_e);
  assign controlled_buffer_1_out = and_2_out ? b_i : 8'bz;  // Controlled_Buffer controlled_buffer_1
  assign b_o = and_3_out ? _00_o : 8'bz;  // Controlled_Buffer controlled_buffer_2
  _8Register _00 (.o(_00_o), .i(controlled_buffer_1_out), .en(and_3_out), .set(and_2_out));
endmodule

module Adder_8 (
  input  ci,
  input  [7:0] a,
  input  [7:0] b,
  output [7:0] o,
  output co
);

  wire adder1_1_co, adder1_2_co, adder1_3_co, adder1_4_co, adder1_5_co, adder1_6_co, adder1_7_co;

  Adder1 adder1_1 (.co(adder1_1_co), .sum(o[0]), .ci(ci), .a(a[0]), .b(b[0]));
  Adder1 adder1_2 (.co(adder1_2_co), .sum(o[1]), .ci(adder1_1_co), .a(a[1]), .b(b[1]));
  Adder1 adder1_3 (.co(adder1_3_co), .sum(o[2]), .ci(adder1_2_co), .a(a[2]), .b(b[2]));
  Adder1 adder1_4 (.co(adder1_4_co), .sum(o[3]), .ci(adder1_3_co), .a(a[3]), .b(b[3]));
  Adder1 adder1_5 (.co(adder1_5_co), .sum(o[4]), .ci(adder1_4_co), .a(a[4]), .b(b[4]));
  Adder1 adder1_6 (.co(adder1_6_co), .sum(o[5]), .ci(adder1_5_co), .a(a[5]), .b(b[5]));
  Adder1 adder1_7 (.co(adder1_7_co), .sum(o[6]), .ci(adder1_6_co), .a(a[6]), .b(b[6]));
  Adder1 adder1_8 (.co(co), .sum(o[7]), .ci(adder1_7_co), .a(a[7]), .b(b[7]));
endmodule

module Adder1 (
  input  a,
  input  b,
  input  ci,
  output sum,
  output co
);

  wire co1_out, co2_out, sum1_out;

  xor sum1 (sum1_out, a, b);
  xor sum2 (sum, sum1_out, ci);
  and co2 (co2_out, sum1_out, ci);
  and co1 (co1_out, a, b);
  or or_1 (co, co2_out, co1_out);
endmodule

module SHR (
  input  [7:0] i,
  input  si,
  output so,
  output [7:0] o
);

  wire [7:1] \출발지_레지스터_o ;

  _8Register \u_출발지_레지스터  (.o({\출발지_레지스터_o , so}), .i(i), .en(1'b1), .set(1'b1));
  _8Register \u_목적지_레지스터  (.o(o), .i({si, \출발지_레지스터_o }), .en(1'b1), .set(1'b1));
endmodule

module SHL (
  input  si,
  input  [7:0] i,
  output [7:0] o,
  output so
);

  wire [6:0] \출발지_레지스터_o ;

  _8Register \u_출발지_레지스터  (.o({so, \출발지_레지스터_o }), .i(i), .en(1'b1), .set(1'b1));
  _8Register \u_목적지_레지스터  (.o(o), .i({\출발지_레지스터_o , si}), .en(1'b1), .set(1'b1));
endmodule

module Inverter (
  input  [7:0] in_1,
  output [7:0] out_2
);

  assign out_2 = ~in_1;  // NOT_Gate not_1, 8 bits wide
endmodule

module ANDer (
  input  [7:0] a,
  input  [7:0] b,
  output [7:0] o
);

  and and_1 (o[0], a[0], b[0]);
  and and_2 (o[1], a[1], b[1]);
  and and_3 (o[2], a[2], b[2]);
  and and_4 (o[3], a[3], b[3]);
  and and_5 (o[4], a[4], b[4]);
  and and_6 (o[5], a[5], b[5]);
  and and_7 (o[6], a[6], b[6]);
  and and_8 (o[7], a[7], b[7]);
endmodule

module ORer (
  input  [7:0] a,
  input  [7:0] b,
  output [7:0] o
);

  or or_1 (o[0], a[0], b[0]);
  or or_2 (o[1], a[1], b[1]);
  or or_3 (o[2], a[2], b[2]);
  or or_4 (o[3], a[3], b[3]);
  or or_5 (o[4], a[4], b[4]);
  or or_6 (o[5], a[5], b[5]);
  or or_7 (o[6], a[6], b[6]);
  or or_8 (o[7], a[7], b[7]);
endmodule

module xor_1 (
  input  s_i,
  input  l_i,
  input  a,
  input  b,
  output o,
  output s_o,
  output l_o
);

  wire and_2_out, not_1_out;

  xor xor_1 (o, a, b);
  not not_1 (not_1_out, o);
  and and_1 (s_o, not_1_out, s_i);
  and and_2 (and_2_out, s_i, a, o);
  or or_1 (l_o, and_2_out, l_i);
endmodule

module XORer (
  input  [7:0] a,
  input  [7:0] b,
  output [7:0] out_3,
  output s_o,
  output l_o
);

  wire xor_1_1_l_o, xor_1_1_s_o, xor_1_2_l_o, xor_1_2_s_o, xor_1_3_l_o, xor_1_3_s_o, xor_1_4_l_o,
       xor_1_4_s_o, xor_1_5_l_o, xor_1_5_s_o, xor_1_6_l_o, xor_1_6_s_o, xor_1_7_l_o, xor_1_7_s_o;

  xor_1 xor_1_1 (.s_o(xor_1_1_s_o), .l_o(xor_1_1_l_o), .o(out_3[7]), .s_i(1'b1), .l_i(1'b0), .a(a[7]), .b(b[7]));
  xor_1 xor_1_2 (
    .s_o(xor_1_2_s_o), .l_o(xor_1_2_l_o), .o(out_3[6]), .s_i(xor_1_1_s_o), .l_i(xor_1_1_l_o), .a(a[6]),
    .b(b[6]));
  xor_1 xor_1_3 (
    .s_o(xor_1_3_s_o), .l_o(xor_1_3_l_o), .o(out_3[5]), .s_i(xor_1_2_s_o), .l_i(xor_1_2_l_o), .a(a[5]),
    .b(b[5]));
  xor_1 xor_1_4 (
    .s_o(xor_1_4_s_o), .l_o(xor_1_4_l_o), .o(out_3[4]), .s_i(xor_1_3_s_o), .l_i(xor_1_3_l_o), .a(a[4]),
    .b(b[4]));
  xor_1 xor_1_5 (
    .s_o(xor_1_5_s_o), .l_o(xor_1_5_l_o), .o(out_3[3]), .s_i(xor_1_4_s_o), .l_i(xor_1_4_l_o), .a(a[3]),
    .b(b[3]));
  xor_1 xor_1_6 (
    .s_o(xor_1_6_s_o), .l_o(xor_1_6_l_o), .o(out_3[2]), .s_i(xor_1_5_s_o), .l_i(xor_1_5_l_o), .a(a[2]),
    .b(b[2]));
  xor_1 xor_1_7 (
    .s_o(xor_1_7_s_o), .l_o(xor_1_7_l_o), .o(out_3[1]), .s_i(xor_1_6_s_o), .l_i(xor_1_6_l_o), .a(a[1]),
    .b(b[1]));
  xor_1 xor_1_8 (.s_o(s_o), .l_o(l_o), .o(out_3[0]), .s_i(xor_1_7_s_o), .l_i(xor_1_7_l_o), .a(a[0]), .b(b[0]));
endmodule

module ZEROer (
  input  [7:0] in,
  output out
);

  wire or_1_out;

  or or_1 (or_1_out, in[0], in[1], in[2], in[3], in[4], in[5], in[6], in[7]);
  not not_1 (out, or_1_out);
endmodule

module Enabler_old (
  input  [7:0] in_1,
  input  in_2,
  output [7:0] out_3
);

  Controlled_Buffer controlled_buffer_1 ();  // open: in, out, en
  and and_1 (out_3[0], in_2, in_1[0]);
  and and_2 (out_3[1], in_2, in_1[1]);
  and and_3 (out_3[2], in_2, in_1[2]);
  and and_4 (out_3[3], in_2, in_1[3]);
  and and_5 (out_3[4], in_2, in_1[4]);
  and and_6 (out_3[5], in_2, in_1[5]);
  and and_7 (out_3[6], in_2, in_1[6]);
  and and_8 (out_3[7], in_2, in_1[7]);
endmodule

module ALU (
  input  [7:0] a,
  input  [7:0] b,
  input  \자리올림_입력 ,
  input  [2:0] op,
  output a_b,
  output a_b_2,
  output zero,
  output [7:0] o,
  output \자리올림_출력 
);

  wire adder_8_1_co, and_1_out, and_2_out, and_3_out, decoder_1_out0, decoder_1_out1, decoder_1_out2,
       decoder_1_out3, decoder_1_out4, decoder_1_out5, decoder_1_out6, decoder_1_out7, shl_1_so, shr_1_so;
  wire [7:0] adder_8_1_o, ander_1_o, inverter_1_out_2, orer_1_o, shl_1_o, shr_1_o, xorer_1_out_3;

  XORer xorer_1 (.s_o(a_b_2), .l_o(a_b), .out_3(xorer_1_out_3), .a(a), .b(b));
  ORer orer_1 (.o(orer_1_o), .a(a), .b(b));
  ANDer ander_1 (.o(ander_1_o), .a(a), .b(b));
  Inverter inverter_1 (.out_2(inverter_1_out_2), .in_1(a));
  SHL shl_1 (.so(shl_1_so), .o(shl_1_o), .i(a), .si(\자리올림_입력 ));
  SHR shr_1 (.so(shr_1_so), .o(shr_1_o), .i(a), .si(\자리올림_입력 ));
  Adder_8 adder_8_1 (.o(adder_8_1_o), .co(adder_8_1_co), .a(a), .b(b), .ci(\자리올림_입력 ));
  Decoder #(.enable("false"), .select(3)) decoder_1 (
    .out0(decoder_1_out0), .out1(decoder_1_out1), .out2(decoder_1_out2), .out3(decoder_1_out3),
    .out4(decoder_1_out4), .out5(decoder_1_out5), .out6(decoder_1_out6), .out7(decoder_1_out7), .sel(op));
  and and_1 (and_1_out, shl_1_so, decoder_1_out2);
  and and_2 (and_2_out, adder_8_1_co, decoder_1_out0);
  assign o = decoder_1_out7 ? {8{1'b0}} : 8'bz;  // Controlled_Buffer controlled_buffer_1
  Enabler enabler_1 (.out_3(o), .in_2(decoder_1_out6), .in_1(xorer_1_out_3));
  Enabler enabler_2 (.out_3(o), .in_2(decoder_1_out5), .in_1(orer_1_o));
  Enabler enabler_3 (.out_3(o), .in_2(decoder_1_out4), .in_1(ander_1_o));
  Enabler enabler_4 (.out_3(o), .in_2(decoder_1_out3), .in_1(inverter_1_out_2));
  Enabler enabler_5 (.out_3(o), .in_2(decoder_1_out2), .in_1(shl_1_o));
  and and_3 (and_3_out, shr_1_so, decoder_1_out1);
  Enabler enabler_6 (.out_3(o), .in_2(decoder_1_out1), .in_1(shr_1_o));
  Enabler enabler_7 (.out_3(o), .in_2(decoder_1_out0), .in_1(adder_8_1_o));
  ZEROer zeroer_1 (.out(zero), .in(o));
  or or_1 (\자리올림_출력 , and_1_out, and_3_out, and_2_out);
endmodule

module Clk (
  output clk,
  output clk_e,
  output clk_s
);

  wire clk_raw_out, j_k_ff_1_qn;

  Clock clk_raw (.out(clk_raw_out));
  J_K_Flip_Flop j_k_ff_1 (.J(1'b1), .clk(clk_raw_out), .K(1'b1), .Q(clk), .Qn(j_k_ff_1_qn));  // open: preset, reset
  nand nand_1 (clk_e, clk_raw_out, j_k_ff_1_qn);
  and and_1 (clk_s, clk_raw_out, clk);
endmodule
