// Logisim project 30_Conditional_Jump.circ as structural Verilog
module M (
  input  i,
  input  s,
  output o
);

  wire nand_1_out, nand_2_out, nand_4_out;

  nand nand_1 (nand_1_out, i, s);
  nand nand_2 (nand_2_out, nand_1_out, s);
  nand nand_3 (o, nand_1_out, nand_4_out);
  nand nand_4 (nand_4_out, o, nand_2_out);
endmodule

module M8 (
  input  in_1,
  input  [7:0] in_2,
  output [7:0] out_3
);

  M m_1 (.o(out_3[0]), .i(in_2[0]), .s(in_1));
  M m_2 (.o(out_3[1]), .i(in_2[1]), .s(in_1));
  M m_3 (.o(out_3[2]), .i(in_2[2]), .s(in_1));
  M m_4 (.o(out_3[3]), .i(in_2[3]), .s(in_1));
  M m_5 (.o(out_3[4]), .i(in_2[4]), .s(in_1));
  M m_6 (.o(out_3[5]), .i(in_2[5]), .s(in_1));
  M m_7 (.o(out_3[6]), .i(in_2[6]), .s(in_1));
  M m_8 (.o(out_3[7]), .i(in_2[7]), .s(in_1));
endmodule

module Reg (
  input  set,
  input  [7:0] i,
  input  en,
  output [7:0] o
);

  wire [7:0] controlled_buffer_1_out, m8_1_out_3;

  assign controlled_buffer_1_out = set ? i : 8'bz;  // Controlled_Buffer controlled_buffer_1
  M8 m8_1 (.in_1(set), .in_2(controlled_buffer_1_out), .out_3(m8_1_out_3));
  Enabler enabler_1 (.out_3(o), .in_2(en), .in_1(m8_1_out_3));
endmodule

module Enabler (
  input  [7:0] in_1,
  input  in_2,
  output [7:0] out_3
);

  assign out_3 = in_2 ? in_1 : 8'bz;  // Controlled_Buffer controlled_buffer_1
endmodule

module Decoder3x8 (
  input  in_1,
  input  in_2,
  input  in_3,
  output out_4,
  output out_5,
  output out_6,
  output out_7,
  output out_8,
  output out_9,
  output out_10,
  output out_11
);

  wire not_1_out, not_2_out, not_3_out;

  not not_1 (not_1_out, in_1);
  not not_2 (not_2_out, in_2);
  not not_3 (not_3_out, in_3);
  and and_1 (out_4, not_1_out, not_2_out, not_3_out);
  and and_2 (out_5, not_1_out, not_2_out, in_3);
  and and_3 (out_6, not_1_out, in_2, not_3_out);
  and and_4 (out_7, not_1_out, in_2, in_3);
  and and_5 (out_8, in_1, not_2_out, not_3_out);
  and and_6 (out_9, in_1, not_2_out, in_3);
  and and_7 (out_10, in_1, in_2, not_3_out);
  and and_8 (out_11, in_1, in_2, in_3);
endmodule

module RAM256 (
  input  [7:0] a,
  input  sa,
  input  [7:0] b_i_b1862039,
  input  b_s_28718816,
  input  b_e_394dcd69,
  output [7:0] b_o_c2cd5d60
);

  wire decoder_1_out0, decoder_1_out1, decoder_1_out2, decoder_1_out3, decoder_1_out4, decoder_1_out5,
       decoder_1_out6, decoder_1_out7, decoder_1_out8, decoder_1_out9, decoder_1_out10, decoder_1_out11,
       decoder_1_out12, decoder_1_out13, decoder_1_out14, decoder_1_out15, decoder_2_out0, decoder_2_out1,
       decoder_2_out2, decoder_2_out3, decoder_2_out4, decoder_2_out5, decoder_2_out6, decoder_2_out7,
       decoder_2_out8, decoder_2_out9, decoder_2_out10, decoder_2_out11, decoder_2_out12, decoder_2_out13,
       decoder_2_out14, decoder_2_out15;
  wire [7:0] controlled_buffer_1_out, reg_1_o;

  Reg reg_1 (.o(reg_1_o), .i(a), .en(1'b1), .set(sa));
  Decoder #(.enable("false"), .select(4)) decoder_1 (
    .out0(decoder_1_out0), .out1(decoder_1_out1), .out2(decoder_1_out2), .out3(decoder_1_out3),
    .out4(decoder_1_out4), .out5(decoder_1_out5), .out6(decoder_1_out6), .out7(decoder_1_out7),
    .out8(decoder_1_out8), .out9(decoder_1_out9), .out10(decoder_1_out10), .out11(decoder_1_out11),
    .out12(decoder_1_out12), .out13(decoder_1_out13), .out14(decoder_1_out14), .out15(decoder_1_out15),
    .sel(reg_1_o[7:4]));
  assign controlled_buffer_1_out = b_s_28718816 ? b_i_b1862039 : 8'bz;  // Controlled_Buffer controlled_buffer_1
  RAM1 ram1_1 (
    .b_o(controlled_buffer_1_out), .x(decoder_2_out0), .b_s(b_s_28718816), .b_e(b_e_394dcd69),
    .y(decoder_1_out0), .b_i(controlled_buffer_1_out));
  RAM1 ram1_2 (
    .b_o(controlled_buffer_1_out), .x(decoder_2_out0), .b_s(b_s_28718816), .b_e(b_e_394dcd69),
    .y(decoder_1_out1), .b_i(controlled_buffer_1_out));
  RAM1 ram1_3 (
    .b_o(controlled_buffer_1_out), .x(decoder_2_out0), .b_s(b_s_28718816), .b_e(b_e_394dcd69),
    .y(decoder_1_out2), .b_i(controlled_buffer_1_out));
  RAM1 ram1_4 (
    .b_o(controlled_buffer_1_out), .x(decoder_2_out0), .b_s(b_s_28718816), .b_e(b_e_394dcd69),
    .y(decoder_1_out3), .b_i(controlled_buffer_1_out));
  RAM1 ram1_5 (
    .b_o(controlled_buffer_1_out), .x(decoder_2_out0), .b_s(b_s_28718816), .b_e(b_e_394dcd69),
    .y(decoder_1_out4), .b_i(controlled_buffer_1_out));
  RAM1 ram1_6 (
    .b_o(controlled_buffer_1_out), .x(decoder_2_out0), .b_s(b_s_28718816), .b_e(b_e_394dcd69),
    .y(decoder_1_out5), .b_i(controlled_buffer_1_out));
  RAM1 ram1_7 (
    .b_o(controlled_buffer_1_out), .x(decoder_2_out0), .b_s(b_s_28718816), .b_e(b_e_394dcd69),
    .y(decoder_1_out6), .b_i(controlled_buffer_1_out));
  RAM1 ram1_8 (
    .b_o(controlled_buffer_1_out), .x(decoder_2_out0), .b_s(b_s_28718816), .b_e(b_e_394dcd69),
    .y(decoder_1_out7), .b_i(controlled_buffer_1_out));
  RAM1 ram1_9 (
    .b_o(controlled_buffer_1_out), .x(decoder_2_out0), .b_s(b_s_28718816), .b_e(b_e_394dcd69),
    .y(decoder_1_out8), .b_i(controlled_buffer_1_out));
  RAM1 ram1_10 (
    .b_o(controlled_buffer_1_out), .x(decoder_2_out0), .b_s(b_s_28718816), .b_e(b_e_394dcd69),
    .y(decoder_1_out9), .b_i(controlled_buffer_1_out));
  RAM1 ram1_11 (
    .b_o(controlled_buffer_1_out), .x(decoder_2_out0), .b_s(b_s_28718816), .b_e(b_e_394dcd69),
    .y(decoder_1_out10), .b_i(controlled_buffer_1_out));
  RAM1 ram1_12 (
    .b_o(controlled_buffer_1_out), .x(decoder_2_out0), .b_s(b_s_28718816), .b_e(b_e_394dcd69),
    .y(decoder_1_out11), .b_i(controlled_buffer_1_out));
  RAM1 ram1_13 (
    .b_o(controlled_buffer_1_out), .x(decoder_2_out0), .b_s(b_s_28718816), .b_e(b_e_394dcd69),
    .y(decoder_1_out12), .b_i(controlled_buffer_1_out));
  RAM1 ram1_14 (
    .b_o(controlled_buffer_1_out), .x(decoder_2_out0), .b_s(b_s_28718816), .b_e(b_e_394dcd69),
    .y(decoder_1_out13), .b_i(controlled_buffer_1_out));
  RAM1 ram1_15 (
    .b_o(controlled_buffer_1_out), .x(decoder_2_out0), .b_s(b_s_28718816), .b_e(b_e_394dcd69),
    .y(decoder_1_out14), .b_i(controlled_buffer_1_out));
  RAM1 ram1_16 (
    .b_o(controlled_buffer_1_out), .x(decoder_2_out0), .b_s(b_s_28718816), .b_e(b_e_394dcd69),
    .y(decoder_1_out15), .b_i(controlled_buffer_1_out));
  RAM1 ram1_17 (
    .b_o(controlled_buffer_1_out), .x(decoder_2_out1), .b_s(b_s_28718816), .b_e(b_e_394dcd69),
    .y(decoder_1_out0), .b_i(controlled_buffer_1_out));
  RAM1 ram1_18 (
    .b_o(controlled_buffer_1_out), .x(decoder_2_out1), .b_s(b_s_28718816), .b_e(b_e_394dcd69),
    .y(decoder_1_out1), .b_i(controlled_buffer_1_out));
  RAM1 ram1_19 (
    .b_o(controlled_buffer_1_out), .x(decoder_2_out1), .b_s(b_s_28718816), .b_e(b_e_394dcd69),
    .y(decoder_1_out2), .b_i(controlled_buffer_1_out));
  RAM1 ram1_20 (
    .b_o(controlled_buffer_1_out), .x(decoder_2_out1), .b_s(b_s_28718816), .b_e(b_e_394dcd69),
    .y(decoder_1_out3), .b_i(controlled_buffer_1_out));
  RAM1 ram1_21 (
    .b_o(controlled_buffer_1_out), .x(decoder_2_out1), .b_s(b_s_28718816), .b_e(b_e_394dcd69),
    .y(decoder_1_out4), .b_i(controlled_buffer_1_out));
  RAM1 ram1_22 (
    .b_o(controlled_buffer_1_out), .x(decoder_2_out1), .b_s(b_s_28718816), .b_e(b_e_394dcd69),
    .y(decoder_1_out5), .b_i(controlled_buffer_1_out));
  RAM1 ram1_23 (
    .b_o(controlled_buffer_1_out), .x(decoder_2_out1), .b_s(b_s_28718816), .b_e(b_e_394dcd69),
    .y(decoder_1_out6), .b_i(controlled_buffer_1_out));
  RAM1 ram1_24 (
    .b_o(controlled_buffer_1_out), .x(decoder_2_out1), .b_s(b_s_28718816), .b_e(b_e_394dcd69),
    .y(decoder_1_out7), .b_i(controlled_buffer_1_out));
  RAM1 ram1_25 (
    .b_o(controlled_buffer_1_out), .x(decoder_2_out1), .b_s(b_s_28718816), .b_e(b_e_394dcd69),
    .y(decoder_1_out8), .b_i(controlled_buffer_1_out));
  RAM1 ram1_26 (
    .b_o(controlled_buffer_1_out), .x(decoder_2_out1), .b_s(b_s_28718816), .b_e(b_e_394dcd69),
    .y(decoder_1_out9), .b_i(controlled_buffer_1_out));
  RAM1 ram1_27 (
    .b_o(controlled_buffer_1_out), .x(decoder_2_out1), .b_s(b_s_28718816), .b_e(b_e_394dcd69),
    .y(decoder_1_out10), .b_i(controlled_buffer_1_out));
  RAM1 ram1_28 (
    .b_o(controlled_buffer_1_out), .x(decoder_2_out1), .b_s(b_s_28718816), .b_e(b_e_394dcd69),
    .y(decoder_1_out11), .b_i(controlled_buffer_1_out));
  RAM1 ram1_29 (
    .b_o(controlled_buffer_1_out), .x(decoder_2_out1), .b_s(b_s_28718816), .b_e(b_e_394dcd69),
    .y(decoder_1_out12), .b_i(controlled_buffer_1_out));
  RAM1 ram1_30 (
    .b_o(controlled_buffer_1_out), .x(decoder_2_out1), .b_s(b_s_28718816), .b_e(b_e_394dcd69),
    .y(decoder_1_out13), .b_i(controlled_buffer_1_out));
  RAM1 ram1_31 (
    .b_o(controlled_buffer_1_out), .x(decoder_2_out1), .b_s(b_s_28718816), .b_e(b_e_394dcd69),
    .y(decoder_1_out14), .b_i(controlled_buffer_1_out));
  RAM1 ram1_32 (
    .b_o(controlled_buffer_1_out), .x(decoder_2_out1), .b_s(b_s_28718816), .b_e(b_e_394dcd69),
    .y(decoder_1_out15), .b_i(controlled_buffer_1_out));
  RAM1 ram1_33 (
    .b_o(controlled_buffer_1_out), .x(decoder_2_out2), .b_s(b_s_28718816), .b_e(b_e_394dcd69),
    .y(decoder_1_out0), .b_i(controlled_buffer_1_out));
  RAM1 ram1_34 (
    .b_o(controlled_buffer_1_out), .x(decoder_2_out2), .b_s(b_s_28718816), .b_e(b_e_394dcd69),
    .y(decoder_1_out1), .b_i(controlled_buffer_1_out));
  RAM1 ram1_35 (
    .b_o(controlled_buffer_1_out), .x(decoder_2_out2), .b_s(b_s_28718816), .b_e(b_e_394dcd69),
    .y(decoder_1_out2), .b_i(controlled_buffer_1_out));
  RAM1 ram1_36 (
    .b_o(controlled_buffer_1_out), .x(decoder_2_out2), .b_s(b_s_28718816), .b_e(b_e_394dcd69),
    .y(decoder_1_out3), .b_i(controlled_buffer_1_out));
  RAM1 ram1_37 (
    .b_o(controlled_buffer_1_out), .x(decoder_2_out2), .b_s(b_s_28718816), .b_e(b_e_394dcd69),
    .y(decoder_1_out4), .b_i(controlled_buffer_1_out));
  RAM1 ram1_38 (
    .b_o(controlled_buffer_1_out), .x(decoder_2_out2), .b_s(b_s_28718816), .b_e(b_e_394dcd69),
    .y(decoder_1_out5), .b_i(controlled_buffer_1_out));
  RAM1 ram1_39 (
    .b_o(controlled_buffer_1_out), .x(decoder_2_out2), .b_s(b_s_28718816), .b_e(b_e_394dcd69),
    .y(decoder_1_out6), .b_i(controlled_buffer_1_out));
  RAM1 ram1_40 (
    .b_o(controlled_buffer_1_out), .x(decoder_2_out2), .b_s(b_s_28718816), .b_e(b_e_394dcd69),
    .y(decoder_1_out7), .b_i(controlled_buffer_1_out));
  RAM1 ram1_41 (
    .b_o(controlled_buffer_1_out), .x(decoder_2_out2), .b_s(b_s_28718816), .b_e(b_e_394dcd69),
    .y(decoder_1_out8), .b_i(controlled_buffer_1_out));
  RAM1 ram1_42 (
    .b_o(controlled_buffer_1_out), .x(decoder_2_out2), .b_s(b_s_28718816), .b_e(b_e_394dcd69),
    .y(decoder_1_out9), .b_i(controlled_buffer_1_out));
  RAM1 ram1_43 (
    .b_o(controlled_buffer_1_out), .x(decoder_2_out2), .b_s(b_s_28718816), .b_e(b_e_394dcd69),
    .y(decoder_1_out10), .b_i(controlled_buffer_1_out));
  RAM1 ram1_44 (
    .b_o(controlled_buffer_1_out), .x(decoder_2_out2), .b_s(b_s_28718816), .b_e(b_e_394dcd69),
    .y(decoder_1_out11), .b_i(controlled_buffer_1_out));
  RAM1 ram1_45 (
    .b_o(controlled_buffer_1_out), .x(decoder_2_out2), .b_s(b_s_28718816), .b_e(b_e_394dcd69),
    .y(decoder_1_out12), .b_i(controlled_buffer_1_out));
  RAM1 ram1_46 (
    .b_o(controlled_buffer_1_out), .x(decoder_2_out2), .b_s(b_s_28718816), .b_e(b_e_394dcd69),
    .y(decoder_1_out13), .b_i(controlled_buffer_1_out));
  RAM1 ram1_47 (
    .b_o(controlled_buffer_1_out), .x(decoder_2_out2), .b_s(b_s_28718816), .b_e(b_e_394dcd69),
    .y(decoder_1_out14), .b_i(controlled_buffer_1_out));
  RAM1 ram1_48 (
    .b_o(controlled_buffer_1_out), .x(decoder_2_out2), .b_s(b_s_28718816), .b_e(b_e_394dcd69),
    .y(decoder_1_out15), .b_i(controlled_buffer_1_out));
  RAM1 ram1_49 (
    .b_o(controlled_buffer_1_out), .x(decoder_2_out3), .b_s(b_s_28718816), .b_e(b_e_394dcd69),
    .y(decoder_1_out0), .b_i(controlled_buffer_1_out));
  RAM1 ram1_50 (
    .b_o(controlled_buffer_1_out), .x(decoder_2_out3), .b_s(b_s_28718816), .b_e(b_e_394dcd69),
    .y(decoder_1_out1), .b_i(controlled_buffer_1_out));
  RAM1 ram1_51 (
    .b_o(controlled_buffer_1_out), .x(decoder_2_out3), .b_s(b_s_28718816), .b_e(b_e_394dcd69),
    .y(decoder_1_out2), .b_i(controlled_buffer_1_out));
  RAM1 ram1_52 (
    .b_o(controlled_buffer_1_out), .x(decoder_2_out3), .b_s(b_s_28718816), .b_e(b_e_394dcd69),
    .y(decoder_1_out3), .b_i(controlled_buffer_1_out));
  RAM1 ram1_53 (
    .b_o(controlled_buffer_1_out), .x(decoder_2_out3), .b_s(b_s_28718816), .b_e(b_e_394dcd69),
    .y(decoder_1_out4), .b_i(controlled_buffer_1_out));
  RAM1 ram1_54 (
    .b_o(controlled_buffer_1_out), .x(decoder_2_out3), .b_s(b_s_28718816), .b_e(b_e_394dcd69),
    .y(decoder_1_out5), .b_i(controlled_buffer_1_out));
  RAM1 ram1_55 (
    .b_o(controlled_buffer_1_out), .x(decoder_2_out3), .b_s(b_s_28718816), .b_e(b_e_394dcd69),
    .y(decoder_1_out6), .b_i(controlled_buffer_1_out));
  RAM1 ram1_56 (
    .b_o(controlled_buffer_1_out), .x(decoder_2_out3), .b_s(b_s_28718816), .b_e(b_e_394dcd69),
    .y(decoder_1_out7), .b_i(controlled_buffer_1_out));
  RAM1 ram1_57 (
    .b_o(controlled_buffer_1_out), .x(decoder_2_out3), .b_s(b_s_28718816), .b_e(b_e_394dcd69),
    .y(decoder_1_out8), .b_i(controlled_buffer_1_out));
  RAM1 ram1_58 (
    .b_o(controlled_buffer_1_out), .x(decoder_2_out3), .b_s(b_s_28718816), .b_e(b_e_394dcd69),
    .y(decoder_1_out9), .b_i(controlled_buffer_1_out));
  RAM1 ram1_59 (
    .b_o(controlled_buffer_1_out), .x(decoder_2_out3), .b_s(b_s_28718816), .b_e(b_e_394dcd69),
    .y(decoder_1_out10), .b_i(controlled_buffer_1_out));
  RAM1 ram1_60 (
    .b_o(controlled_buffer_1_out), .x(decoder_2_out3), .b_s(b_s_28718816), .b_e(b_e_394dcd69),
    .y(decoder_1_out11), .b_i(controlled_buffer_1_out));
  RAM1 ram1_61 (
    .b_o(controlled_buffer_1_out), .x(decoder_2_out3), .b_s(b_s_28718816), .b_e(b_e_394dcd69),
    .y(decoder_1_out12), .b_i(controlled_buffer_1_out));
  RAM1 ram1_62 (
    .b_o(controlled_buffer_1_out), .x(decoder_2_out3), .b_s(b_s_28718816), .b_e(b_e_394dcd69),
    .y(decoder_1_out13), .b_i(controlled_buffer_1_out));
  RAM1 ram1_63 (
    .b_o(controlled_buffer_1_out), .x(decoder_2_out3), .b_s(b_s_28718816), .b_e(b_e_394dcd69),
    .y(decoder_1_out14), .b_i(controlled_buffer_1_out));
  RAM1 ram1_64 (
    .b_o(controlled_buffer_1_out), .x(decoder_2_out3), .b_s(b_s_28718816), .b_e(b_e_394dcd69),
    .y(decoder_1_out15), .b_i(controlled_buffer_1_out));
  RAM1 ram1_65 (
    .b_o(controlled_buffer_1_out), .x(decoder_2_out4), .b_s(b_s_28718816), .b_e(b_e_394dcd69),
    .y(decoder_1_out0), .b_i(controlled_buffer_1_out));
  RAM1 ram1_66 (
    .b_o(controlled_buffer_1_out), .x(decoder_2_out4), .b_s(b_s_28718816), .b_e(b_e_394dcd69),
    .y(decoder_1_out1), .b_i(controlled_buffer_1_out));
  RAM1 ram1_67 (
    .b_o(controlled_buffer_1_out), .x(decoder_2_out4), .b_s(b_s_28718816), .b_e(b_e_394dcd69),
    .y(decoder_1_out2), .b_i(controlled_buffer_1_out));
  RAM1 ram1_68 (
    .b_o(controlled_buffer_1_out), .x(decoder_2_out4), .b_s(b_s_28718816), .b_e(b_e_394dcd69),
    .y(decoder_1_out3), .b_i(controlled_buffer_1_out));
  RAM1 ram1_69 (
    .b_o(controlled_buffer_1_out), .x(decoder_2_out4), .b_s(b_s_28718816), .b_e(b_e_394dcd69),
    .y(decoder_1_out4), .b_i(controlled_buffer_1_out));
  RAM1 ram1_70 (
    .b_o(controlled_buffer_1_out), .x(decoder_2_out4), .b_s(b_s_28718816), .b_e(b_e_394dcd69),
    .y(decoder_1_out5), .b_i(controlled_buffer_1_out));
  RAM1 ram1_71 (
    .b_o(controlled_buffer_1_out), .x(decoder_2_out4), .b_s(b_s_28718816), .b_e(b_e_394dcd69),
    .y(decoder_1_out6), .b_i(controlled_buffer_1_out));
  RAM1 ram1_72 (
    .b_o(controlled_buffer_1_out), .x(decoder_2_out4), .b_s(b_s_28718816), .b_e(b_e_394dcd69),
    .y(decoder_1_out7), .b_i(controlled_buffer_1_out));
  RAM1 ram1_73 (
    .b_o(controlled_buffer_1_out), .x(decoder_2_out4), .b_s(b_s_28718816), .b_e(b_e_394dcd69),
    .y(decoder_1_out8), .b_i(controlled_buffer_1_out));
  RAM1 ram1_74 (
    .b_o(controlled_buffer_1_out), .x(decoder_2_out4), .b_s(b_s_28718816), .b_e(b_e_394dcd69),
    .y(decoder_1_out9), .b_i(controlled_buffer_1_out));
  RAM1 ram1_75 (
    .b_o(controlled_buffer_1_out), .x(decoder_2_out4), .b_s(b_s_28718816), .b_e(b_e_394dcd69),
    .y(decoder_1_out10), .b_i(controlled_buffer_1_out));
  RAM1 ram1_76 (
    .b_o(controlled_buffer_1_out), .x(decoder_2_out4), .b_s(b_s_28718816), .b_e(b_e_394dcd69),
    .y(decoder_1_out11), .b_i(controlled_buffer_1_out));
  RAM1 ram1_77 (
    .b_o(controlled_buffer_1_out), .x(decoder_2_out4), .b_s(b_s_28718816), .b_e(b_e_394dcd69),
    .y(decoder_1_out12), .b_i(controlled_buffer_1_out));
  RAM1 ram1_78 (
    .b_o(controlled_buffer_1_out), .x(decoder_2_out4), .b_s(b_s_28718816), .b_e(b_e_394dcd69),
    .y(decoder_1_out13), .b_i(controlled_buffer_1_out));
  RAM1 ram1_79 (
    .b_o(controlled_buffer_1_out), .x(decoder_2_out4), .b_s(b_s_28718816), .b_e(b_e_394dcd69),
    .y(decoder_1_out14), .b_i(controlled_buffer_1_out));
  RAM1 ram1_80 (
    .b_o(controlled_buffer_1_out), .x(decoder_2_out4), .b_s(b_s_28718816), .b_e(b_e_394dcd69),
    .y(decoder_1_out15), .b_i(controlled_buffer_1_out));
  RAM1 ram1_81 (
    .b_o(controlled_buffer_1_out), .x(decoder_2_out5), .b_s(b_s_28718816), .b_e(b_e_394dcd69),
    .y(decoder_1_out0), .b_i(controlled_buffer_1_out));
  RAM1 ram1_82 (
    .b_o(controlled_buffer_1_out), .x(decoder_2_out5), .b_s(b_s_28718816), .b_e(b_e_394dcd69),
    .y(decoder_1_out1), .b_i(controlled_buffer_1_out));
  RAM1 ram1_83 (
    .b_o(controlled_buffer_1_out), .x(decoder_2_out5), .b_s(b_s_28718816), .b_e(b_e_394dcd69),
    .y(decoder_1_out2), .b_i(controlled_buffer_1_out));
  RAM1 ram1_84 (
    .b_o(controlled_buffer_1_out), .x(decoder_2_out5), .b_s(b_s_28718816), .b_e(b_e_394dcd69),
    .y(decoder_1_out3), .b_i(controlled_buffer_1_out));
  RAM1 ram1_85 (
    .b_o(controlled_buffer_1_out), .x(decoder_2_out5), .b_s(b_s_28718816), .b_e(b_e_394dcd69),
    .y(decoder_1_out4), .b_i(controlled_buffer_1_out));
  RAM1 ram1_86 (
    .b_o(controlled_buffer_1_out), .x(decoder_2_out5), .b_s(b_s_28718816), .b_e(b_e_394dcd69),
    .y(decoder_1_out5), .b_i(controlled_buffer_1_out));
  RAM1 ram1_87 (
    .b_o(controlled_buffer_1_out), .x(decoder_2_out5), .b_s(b_s_28718816), .b_e(b_e_394dcd69),
    .y(decoder_1_out6), .b_i(controlled_buffer_1_out));
  RAM1 ram1_88 (
    .b_o(controlled_buffer_1_out), .x(decoder_2_out5), .b_s(b_s_28718816), .b_e(b_e_394dcd69),
    .y(decoder_1_out7), .b_i(controlled_buffer_1_out));
  RAM1 ram1_89 (
    .b_o(controlled_buffer_1_out), .x(decoder_2_out5), .b_s(b_s_28718816), .b_e(b_e_394dcd69),
    .y(decoder_1_out8), .b_i(controlled_buffer_1_out));
  RAM1 ram1_90 (
    .b_o(controlled_buffer_1_out), .x(decoder_2_out5), .b_s(b_s_28718816), .b_e(b_e_394dcd69),
    .y(decoder_1_out9), .b_i(controlled_buffer_1_out));
  RAM1 ram1_91 (
    .b_o(controlled_buffer_1_out), .x(decoder_2_out5), .b_s(b_s_28718816), .b_e(b_e_394dcd69),
    .y(decoder_1_out10), .b_i(controlled_buffer_1_out));
  RAM1 ram1_92 (
    .b_o(controlled_buffer_1_out), .x(decoder_2_out5), .b_s(b_s_28718816), .b_e(b_e_394dcd69),
    .y(decoder_1_out11), .b_i(controlled_buffer_1_out));
  RAM1 ram1_93 (
    .b_o(controlled_buffer_1_out), .x(decoder_2_out5), .b_s(b_s_28718816), .b_e(b_e_394dcd69),
    .y(decoder_1_out12), .b_i(controlled_buffer_1_out));
  RAM1 ram1_94 (
    .b_o(controlled_buffer_1_out), .x(decoder_2_out5), .b_s(b_s_28718816), .b_e(b_e_394dcd69),
    .y(decoder_1_out13), .b_i(controlled_buffer_1_out));
  RAM1 ram1_95 (
    .b_o(controlled_buffer_1_out), .x(decoder_2_out5), .b_s(b_s_28718816), .b_e(b_e_394dcd69),
    .y(decoder_1_out14), .b_i(controlled_buffer_1_out));
  RAM1 ram1_96 (
    .b_o(controlled_buffer_1_out), .x(decoder_2_out5), .b_s(b_s_28718816), .b_e(b_e_394dcd69),
    .y(decoder_1_out15), .b_i(controlled_buffer_1_out));
  Decoder #(.enable("false"), .select(4)) decoder_2 (
    .out0(decoder_2_out0), .out1(decoder_2_out1), .out2(decoder_2_out2), .out3(decoder_2_out3),
    .out4(decoder_2_out4), .out5(decoder_2_out5), .out6(decoder_2_out6), .out7(decoder_2_out7),
    .out8(decoder_2_out8), .out9(decoder_2_out9), .out10(decoder_2_out10), .out11(decoder_2_out11),
    .out12(decoder_2_out12), .out13(decoder_2_out13), .out14(decoder_2_out14), .out15(decoder_2_out15),
    .sel(reg_1_o[3:0]));
  RAM1 ram1_97 (
    .b_o(controlled_buffer_1_out), .x(decoder_2_out6), .b_s(b_s_28718816), .b_e(b_e_394dcd69),
    .y(decoder_1_out0), .b_i(controlled_buffer_1_out));
  RAM1 ram1_98 (
    .b_o(controlled_buffer_1_out), .x(decoder_2_out6), .b_s(b_s_28718816), .b_e(b_e_394dcd69),
    .y(decoder_1_out1), .b_i(controlled_buffer_1_out));
  RAM1 ram1_99 (
    .b_o(controlled_buffer_1_out), .x(decoder_2_out6), .b_s(b_s_28718816), .b_e(b_e_394dcd69),
    .y(decoder_1_out2), .b_i(controlled_buffer_1_out));
  RAM1 ram1_100 (
    .b_o(controlled_buffer_1_out), .x(decoder_2_out6), .b_s(b_s_28718816), .b_e(b_e_394dcd69),
    .y(decoder_1_out3), .b_i(controlled_buffer_1_out));
  RAM1 ram1_101 (
    .b_o(controlled_buffer_1_out), .x(decoder_2_out6), .b_s(b_s_28718816), .b_e(b_e_394dcd69),
    .y(decoder_1_out4), .b_i(controlled_buffer_1_out));
  RAM1 ram1_102 (
    .b_o(controlled_buffer_1_out), .x(decoder_2_out6), .b_s(b_s_28718816), .b_e(b_e_394dcd69),
    .y(decoder_1_out5), .b_i(controlled_buffer_1_out));
  RAM1 ram1_103 (
    .b_o(controlled_buffer_1_out), .x(decoder_2_out6), .b_s(b_s_28718816), .b_e(b_e_394dcd69),
    .y(decoder_1_out6), .b_i(controlled_buffer_1_out));
  RAM1 ram1_104 (
    .b_o(controlled_buffer_1_out), .x(decoder_2_out6), .b_s(b_s_28718816), .b_e(b_e_394dcd69),
    .y(decoder_1_out7), .b_i(controlled_buffer_1_out));
  RAM1 ram1_105 (
    .b_o(controlled_buffer_1_out), .x(decoder_2_out6), .b_s(b_s_28718816), .b_e(b_e_394dcd69),
    .y(decoder_1_out8), .b_i(controlled_buffer_1_out));
  RAM1 ram1_106 (
    .b_o(controlled_buffer_1_out), .x(decoder_2_out6), .b_s(b_s_28718816), .b_e(b_e_394dcd69),
    .y(decoder_1_out9), .b_i(controlled_buffer_1_out));
  RAM1 ram1_107 (
    .b_o(controlled_buffer_1_out), .x(decoder_2_out6), .b_s(b_s_28718816), .b_e(b_e_394dcd69),
    .y(decoder_1_out10), .b_i(controlled_buffer_1_out));
  RAM1 ram1_108 (
    .b_o(controlled_buffer_1_out), .x(decoder_2_out6), .b_s(b_s_28718816), .b_e(b_e_394dcd69),
    .y(decoder_1_out11), .b_i(controlled_buffer_1_out));
  RAM1 ram1_109 (
    .b_o(controlled_buffer_1_out), .x(decoder_2_out6), .b_s(b_s_28718816), .b_e(b_e_394dcd69),
    .y(decoder_1_out12), .b_i(controlled_buffer_1_out));
  RAM1 ram1_110 (
    .b_o(controlled_buffer_1_out), .x(decoder_2_out6), .b_s(b_s_28718816), .b_e(b_e_394dcd69),
    .y(decoder_1_out13), .b_i(controlled_buffer_1_out));
  RAM1 ram1_111 (
    .b_o(controlled_buffer_1_out), .x(decoder_2_out6), .b_s(b_s_28718816), .b_e(b_e_394dcd69),
    .y(decoder_1_out14), .b_i(controlled_buffer_1_out));
  RAM1 ram1_112 (
    .b_o(controlled_buffer_1_out), .x(decoder_2_out6), .b_s(b_s_28718816), .b_e(b_e_394dcd69),
    .y(decoder_1_out15), .b_i(controlled_buffer_1_out));
  RAM1 ram1_113 (
    .b_o(controlled_buffer_1_out), .x(decoder_2_out7), .b_s(b_s_28718816), .b_e(b_e_394dcd69),
    .y(decoder_1_out0), .b_i(controlled_buffer_1_out));
  RAM1 ram1_114 (
    .b_o(controlled_buffer_1_out), .x(decoder_2_out7), .b_s(b_s_28718816), .b_e(b_e_394dcd69),
    .y(decoder_1_out1), .b_i(controlled_buffer_1_out));
  RAM1 ram1_115 (
    .b_o(controlled_buffer_1_out), .x(decoder_2_out7), .b_s(b_s_28718816), .b_e(b_e_394dcd69),
    .y(decoder_1_out2), .b_i(controlled_buffer_1_out));
  RAM1 ram1_116 (
    .b_o(controlled_buffer_1_out), .x(decoder_2_out7), .b_s(b_s_28718816), .b_e(b_e_394dcd69),
    .y(decoder_1_out3), .b_i(controlled_buffer_1_out));
  RAM1 ram1_117 (
    .b_o(controlled_buffer_1_out), .x(decoder_2_out7), .b_s(b_s_28718816), .b_e(b_e_394dcd69),
    .y(decoder_1_out4), .b_i(controlled_buffer_1_out));
  RAM1 ram1_118 (
    .b_o(controlled_buffer_1_out), .x(decoder_2_out7), .b_s(b_s_28718816), .b_e(b_e_394dcd69),
    .y(decoder_1_out5), .b_i(controlled_buffer_1_out));
  RAM1 ram1_119 (
    .b_o(controlled_buffer_1_out), .x(decoder_2_out7), .b_s(b_s_28718816), .b_e(b_e_394dcd69),
    .y(decoder_1_out6), .b_i(controlled_buffer_1_out));
  RAM1 ram1_120 (
    .b_o(controlled_buffer_1_out), .x(decoder_2_out7), .b_s(b_s_28718816), .b_e(b_e_394dcd69),
    .y(decoder_1_out7), .b_i(controlled_buffer_1_out));
  RAM1 ram1_121 (
    .b_o(controlled_buffer_1_out), .x(decoder_2_out7), .b_s(b_s_28718816), .b_e(b_e_394dcd69),
    .y(decoder_1_out8), .b_i(controlled_buffer_1_out));
  RAM1 ram1_122 (
    .b_o(controlled_buffer_1_out), .x(decoder_2_out7), .b_s(b_s_28718816), .b_e(b_e_394dcd69),
    .y(decoder_1_out9), .b_i(controlled_buffer_1_out));
  RAM1 ram1_123 (
    .b_o(controlled_buffer_1_out), .x(decoder_2_out7), .b_s(b_s_28718816), .b_e(b_e_394dcd69),
    .y(decoder_1_out10), .b_i(controlled_buffer_1_out));
  RAM1 ram1_124 (
    .b_o(controlled_buffer_1_out), .x(decoder_2_out7), .b_s(b_s_28718816), .b_e(b_e_394dcd69),
    .y(decoder_1_out11), .b_i(controlled_buffer_1_out));
  RAM1 ram1_125 (
    .b_o(controlled_buffer_1_out), .x(decoder_2_out7), .b_s(b_s_28718816), .b_e(b_e_394dcd69),
    .y(decoder_1_out12), .b_i(controlled_buffer_1_out));
  RAM1 ram1_126 (
    .b_o(controlled_buffer_1_out), .x(decoder_2_out7), .b_s(b_s_28718816), .b_e(b_e_394dcd69),
    .y(decoder_1_out13), .b_i(controlled_buffer_1_out));
  RAM1 ram1_127 (
    .b_o(controlled_buffer_1_out), .x(decoder_2_out7), .b_s(b_s_28718816), .b_e(b_e_394dcd69),
    .y(decoder_1_out14), .b_i(controlled_buffer_1_out));
  RAM1 ram1_128 (
    .b_o(controlled_buffer_1_out), .x(decoder_2_out7), .b_s(b_s_28718816), .b_e(b_e_394dcd69),
    .y(decoder_1_out15), .b_i(controlled_buffer_1_out));
  RAM1 ram1_129 (
    .b_o(controlled_buffer_1_out), .x(decoder_2_out8), .b_s(b_s_28718816), .b_e(b_e_394dcd69),
    .y(decoder_1_out0), .b_i(controlled_buffer_1_out));
  RAM1 ram1_130 (
    .b_o(controlled_buffer_1_out), .x(decoder_2_out8), .b_s(b_s_28718816), .b_e(b_e_394dcd69),
    .y(decoder_1_out1), .b_i(controlled_buffer_1_out));
  RAM1 ram1_131 (
    .b_o(controlled_buffer_1_out), .x(decoder_2_out8), .b_s(b_s_28718816), .b_e(b_e_394dcd69),
    .y(decoder_1_out2), .b_i(controlled_buffer_1_out));
  RAM1 ram1_132 (
    .b_o(controlled_buffer_1_out), .x(decoder_2_out8), .b_s(b_s_28718816), .b_e(b_e_394dcd69),
    .y(decoder_1_out3), .b_i(controlled_buffer_1_out));
  RAM1 ram1_133 (
    .b_o(controlled_buffer_1_out), .x(decoder_2_out8), .b_s(b_s_28718816), .b_e(b_e_394dcd69),
    .y(decoder_1_out4), .b_i(controlled_buffer_1_out));
  RAM1 ram1_134 (
    .b_o(controlled_buffer_1_out), .x(decoder_2_out8), .b_s(b_s_28718816), .b_e(b_e_394dcd69),
    .y(decoder_1_out5), .b_i(controlled_buffer_1_out));
  RAM1 ram1_135 (
    .b_o(controlled_buffer_1_out), .x(decoder_2_out8), .b_s(b_s_28718816), .b_e(b_e_394dcd69),
    .y(decoder_1_out6), .b_i(controlled_buffer_1_out));
  RAM1 ram1_136 (
    .b_o(controlled_buffer_1_out), .x(decoder_2_out8), .b_s(b_s_28718816), .b_e(b_e_394dcd69),
    .y(decoder_1_out7), .b_i(controlled_buffer_1_out));
  RAM1 ram1_137 (
    .b_o(controlled_buffer_1_out), .x(decoder_2_out8), .b_s(b_s_28718816), .b_e(b_e_394dcd69),
    .y(decoder_1_out8), .b_i(controlled_buffer_1_out));
  RAM1 ram1_138 (
    .b_o(controlled_buffer_1_out), .x(decoder_2_out8), .b_s(b_s_28718816), .b_e(b_e_394dcd69),
    .y(decoder_1_out9), .b_i(controlled_buffer_1_out));
  RAM1 ram1_139 (
    .b_o(controlled_buffer_1_out), .x(decoder_2_out8), .b_s(b_s_28718816), .b_e(b_e_394dcd69),
    .y(decoder_1_out10), .b_i(controlled_buffer_1_out));
  RAM1 ram1_140 (
    .b_o(controlled_buffer_1_out), .x(decoder_2_out8), .b_s(b_s_28718816), .b_e(b_e_394dcd69),
    .y(decoder_1_out11), .b_i(controlled_buffer_1_out));
  RAM1 ram1_141 (
    .b_o(controlled_buffer_1_out), .x(decoder_2_out8), .b_s(b_s_28718816), .b_e(b_e_394dcd69),
    .y(decoder_1_out12), .b_i(controlled_buffer_1_out));
  RAM1 ram1_142 (
    .b_o(controlled_buffer_1_out), .x(decoder_2_out8), .b_s(b_s_28718816), .b_e(b_e_394dcd69),
    .y(decoder_1_out13), .b_i(controlled_buffer_1_out));
  RAM1 ram1_143 (
    .b_o(controlled_buffer_1_out), .x(decoder_2_out8), .b_s(b_s_28718816), .b_e(b_e_394dcd69),
    .y(decoder_1_out14), .b_i(controlled_buffer_1_out));
  RAM1 ram1_144 (
    .b_o(controlled_buffer_1_out), .x(decoder_2_out8), .b_s(b_s_28718816), .b_e(b_e_394dcd69),
    .y(decoder_1_out15), .b_i(controlled_buffer_1_out));
  RAM1 ram1_145 (
    .b_o(controlled_buffer_1_out), .x(decoder_2_out9), .b_s(b_s_28718816), .b_e(b_e_394dcd69),
    .y(decoder_1_out0), .b_i(controlled_buffer_1_out));
  RAM1 ram1_146 (
    .b_o(controlled_buffer_1_out), .x(decoder_2_out9), .b_s(b_s_28718816), .b_e(b_e_394dcd69),
    .y(decoder_1_out1), .b_i(controlled_buffer_1_out));
  RAM1 ram1_147 (
    .b_o(controlled_buffer_1_out), .x(decoder_2_out9), .b_s(b_s_28718816), .b_e(b_e_394dcd69),
    .y(decoder_1_out2), .b_i(controlled_buffer_1_out));
  RAM1 ram1_148 (
    .b_o(controlled_buffer_1_out), .x(decoder_2_out9), .b_s(b_s_28718816), .b_e(b_e_394dcd69),
    .y(decoder_1_out3), .b_i(controlled_buffer_1_out));
  RAM1 ram1_149 (
    .b_o(controlled_buffer_1_out), .x(decoder_2_out9), .b_s(b_s_28718816), .b_e(b_e_394dcd69),
    .y(decoder_1_out4), .b_i(controlled_buffer_1_out));
  RAM1 ram1_150 (
    .b_o(controlled_buffer_1_out), .x(decoder_2_out9), .b_s(b_s_28718816), .b_e(b_e_394dcd69),
    .y(decoder_1_out5), .b_i(controlled_buffer_1_out));
  RAM1 ram1_151 (
    .b_o(controlled_buffer_1_out), .x(decoder_2_out9), .b_s(b_s_28718816), .b_e(b_e_394dcd69),
    .y(decoder_1_out6), .b_i(controlled_buffer_1_out));
  RAM1 ram1_152 (
    .b_o(controlled_buffer_1_out), .x(decoder_2_out9), .b_s(b_s_28718816), .b_e(b_e_394dcd69),
    .y(decoder_1_out7), .b_i(controlled_buffer_1_out));
  RAM1 ram1_153 (
    .b_o(controlled_buffer_1_out), .x(decoder_2_out9), .b_s(b_s_28718816), .b_e(b_e_394dcd69),
    .y(decoder_1_out8), .b_i(controlled_buffer_1_out));
  RAM1 ram1_154 (
    .b_o(controlled_buffer_1_out), .x(decoder_2_out9), .b_s(b_s_28718816), .b_e(b_e_394dcd69),
    .y(decoder_1_out9), .b_i(controlled_buffer_1_out));
  RAM1 ram1_155 (
    .b_o(controlled_buffer_1_out), .x(decoder_2_out9), .b_s(b_s_28718816), .b_e(b_e_394dcd69),
    .y(decoder_1_out10), .b_i(controlled_buffer_1_out));
  RAM1 ram1_156 (
    .b_o(controlled_buffer_1_out), .x(decoder_2_out9), .b_s(b_s_28718816), .b_e(b_e_394dcd69),
    .y(decoder_1_out11), .b_i(controlled_buffer_1_out));
  RAM1 ram1_157 (
    .b_o(controlled_buffer_1_out), .x(decoder_2_out9), .b_s(b_s_28718816), .b_e(b_e_394dcd69),
    .y(decoder_1_out12), .b_i(controlled_buffer_1_out));
  RAM1 ram1_158 (
    .b_o(controlled_buffer_1_out), .x(decoder_2_out9), .b_s(b_s_28718816), .b_e(b_e_394dcd69),
    .y(decoder_1_out13), .b_i(controlled_buffer_1_out));
  RAM1 ram1_159 (
    .b_o(controlled_buffer_1_out), .x(decoder_2_out9), .b_s(b_s_28718816), .b_e(b_e_394dcd69),
    .y(decoder_1_out14), .b_i(controlled_buffer_1_out));
  RAM1 ram1_160 (
    .b_o(controlled_buffer_1_out), .x(decoder_2_out9), .b_s(b_s_28718816), .b_e(b_e_394dcd69),
    .y(decoder_1_out15), .b_i(controlled_buffer_1_out));
  RAM1 ram1_161 (
    .b_o(controlled_buffer_1_out), .x(decoder_2_out10), .b_s(b_s_28718816), .b_e(b_e_394dcd69),
    .y(decoder_1_out0), .b_i(controlled_buffer_1_out));
  RAM1 ram1_162 (
    .b_o(controlled_buffer_1_out), .x(decoder_2_out10), .b_s(b_s_28718816), .b_e(b_e_394dcd69),
    .y(decoder_1_out1), .b_i(controlled_buffer_1_out));
  RAM1 ram1_163 (
    .b_o(controlled_buffer_1_out), .x(decoder_2_out10), .b_s(b_s_28718816), .b_e(b_e_394dcd69),
    .y(decoder_1_out2), .b_i(controlled_buffer_1_out));
  RAM1 ram1_164 (
    .b_o(controlled_buffer_1_out), .x(decoder_2_out10), .b_s(b_s_28718816), .b_e(b_e_394dcd69),
    .y(decoder_1_out3), .b_i(controlled_buffer_1_out));
  RAM1 ram1_165 (
    .b_o(controlled_buffer_1_out), .x(decoder_2_out10), .b_s(b_s_28718816), .b_e(b_e_394dcd69),
    .y(decoder_1_out4), .b_i(controlled_buffer_1_out));
  RAM1 ram1_166 (
    .b_o(controlled_buffer_1_out), .x(decoder_2_out10), .b_s(b_s_28718816), .b_e(b_e_394dcd69),
    .y(decoder_1_out5), .b_i(controlled_buffer_1_out));
  RAM1 ram1_167 (
    .b_o(controlled_buffer_1_out), .x(decoder_2_out10), .b_s(b_s_28718816), .b_e(b_e_394dcd69),
    .y(decoder_1_out6), .b_i(controlled_buffer_1_out));
  RAM1 ram1_168 (
    .b_o(controlled_buffer_1_out), .x(decoder_2_out10), .b_s(b_s_28718816), .b_e(b_e_394dcd69),
    .y(decoder_1_out7), .b_i(controlled_buffer_1_out));
  RAM1 ram1_169 (
    .b_o(controlled_buffer_1_out), .x(decoder_2_out10), .b_s(b_s_28718816), .b_e(b_e_394dcd69),
    .y(decoder_1_out8), .b_i(controlled_buffer_1_out));
  RAM1 ram1_170 (
    .b_o(controlled_buffer_1_out), .x(decoder_2_out10), .b_s(b_s_28718816), .b_e(b_e_394dcd69),
    .y(decoder_1_out9), .b_i(controlled_buffer_1_out));
  RAM1 ram1_171 (
    .b_o(controlled_buffer_1_out), .x(decoder_2_out10), .b_s(b_s_28718816), .b_e(b_e_394dcd69),
    .y(decoder_1_out10), .b_i(controlled_buffer_1_out));
  RAM1 ram1_172 (
    .b_o(controlled_buffer_1_out), .x(decoder_2_out10), .b_s(b_s_28718816), .b_e(b_e_394dcd69),
    .y(decoder_1_out11), .b_i(controlled_buffer_1_out));
  RAM1 ram1_173 (
    .b_o(controlled_buffer_1_out), .x(decoder_2_out10), .b_s(b_s_28718816), .b_e(b_e_394dcd69),
    .y(decoder_1_out12), .b_i(controlled_buffer_1_out));
  RAM1 ram1_174 (
    .b_o(controlled_buffer_1_out), .x(decoder_2_out10), .b_s(b_s_28718816), .b_e(b_e_394dcd69),
    .y(decoder_1_out13), .b_i(controlled_buffer_1_out));
  RAM1 ram1_175 (
    .b_o(controlled_buffer_1_out), .x(decoder_2_out10), .b_s(b_s_28718816), .b_e(b_e_394dcd69),
    .y(decoder_1_out14), .b_i(controlled_buffer_1_out));
  RAM1 ram1_176 (
    .b_o(controlled_buffer_1_out), .x(decoder_2_out10), .b_s(b_s_28718816), .b_e(b_e_394dcd69),
    .y(decoder_1_out15), .b_i(controlled_buffer_1_out));
  RAM1 ram1_177 (
    .b_o(controlled_buffer_1_out), .x(decoder_2_out11), .b_s(b_s_28718816), .b_e(b_e_394dcd69),
    .y(decoder_1_out0), .b_i(controlled_buffer_1_out));
  RAM1 ram1_178 (
    .b_o(controlled_buffer_1_out), .x(decoder_2_out11), .b_s(b_s_28718816), .b_e(b_e_394dcd69),
    .y(decoder_1_out1), .b_i(controlled_buffer_1_out));
  RAM1 ram1_179 (
    .b_o(controlled_buffer_1_out), .x(decoder_2_out11), .b_s(b_s_28718816), .b_e(b_e_394dcd69),
    .y(decoder_1_out2), .b_i(controlled_buffer_1_out));
  RAM1 ram1_180 (
    .b_o(controlled_buffer_1_out), .x(decoder_2_out11), .b_s(b_s_28718816), .b_e(b_e_394dcd69),
    .y(decoder_1_out3), .b_i(controlled_buffer_1_out));
  RAM1 ram1_181 (
    .b_o(controlled_buffer_1_out), .x(decoder_2_out11), .b_s(b_s_28718816), .b_e(b_e_394dcd69),
    .y(decoder_1_out4), .b_i(controlled_buffer_1_out));
  RAM1 ram1_182 (
    .b_o(controlled_buffer_1_out), .x(decoder_2_out11), .b_s(b_s_28718816), .b_e(b_e_394dcd69),
    .y(decoder_1_out5), .b_i(controlled_buffer_1_out));
  RAM1 ram1_183 (
    .b_o(controlled_buffer_1_out), .x(decoder_2_out11), .b_s(b_s_28718816), .b_e(b_e_394dcd69),
    .y(decoder_1_out6), .b_i(controlled_buffer_1_out));
  RAM1 ram1_184 (
    .b_o(controlled_buffer_1_out), .x(decoder_2_out11), .b_s(b_s_28718816), .b_e(b_e_394dcd69),
    .y(decoder_1_out7), .b_i(controlled_buffer_1_out));
  RAM1 ram1_185 (
    .b_o(controlled_buffer_1_out), .x(decoder_2_out11), .b_s(b_s_28718816), .b_e(b_e_394dcd69),
    .y(decoder_1_out8), .b_i(controlled_buffer_1_out));
  RAM1 ram1_186 (
    .b_o(controlled_buffer_1_out), .x(decoder_2_out11), .b_s(b_s_28718816), .b_e(b_e_394dcd69),
    .y(decoder_1_out9), .b_i(controlled_buffer_1_out));
  RAM1 ram1_187 (
    .b_o(controlled_buffer_1_out), .x(decoder_2_out11), .b_s(b_s_28718816), .b_e(b_e_394dcd69),
    .y(decoder_1_out10), .b_i(controlled_buffer_1_out));
  RAM1 ram1_188 (
    .b_o(controlled_buffer_1_out), .x(decoder_2_out11), .b_s(b_s_28718816), .b_e(b_e_394dcd69),
    .y(decoder_1_out11), .b_i(controlled_buffer_1_out));
  RAM1 ram1_189 (
    .b_o(controlled_buffer_1_out), .x(decoder_2_out11), .b_s(b_s_28718816), .b_e(b_e_394dcd69),
    .y(decoder_1_out12), .b_i(controlled_buffer_1_out));
  RAM1 ram1_190 (
    .b_o(controlled_buffer_1_out), .x(decoder_2_out11), .b_s(b_s_28718816), .b_e(b_e_394dcd69),
    .y(decoder_1_out13), .b_i(controlled_buffer_1_out));
  RAM1 ram1_191 (
    .b_o(controlled_buffer_1_out), .x(decoder_2_out11), .b_s(b_s_28718816), .b_e(b_e_394dcd69),
    .y(decoder_1_out14), .b_i(controlled_buffer_1_out));
  RAM1 ram1_192 (
    .b_o(controlled_buffer_1_out), .x(decoder_2_out11), .b_s(b_s_28718816), .b_e(b_e_394dcd69),
    .y(decoder_1_out15), .b_i(controlled_buffer_1_out));
  RAM1 ram1_193 (
    .b_o(controlled_buffer_1_out), .x(decoder_2_out12), .b_s(b_s_28718816), .b_e(b_e_394dcd69),
    .y(decoder_1_out0), .b_i(controlled_buffer_1_out));
  RAM1 ram1_194 (
    .b_o(controlled_buffer_1_out), .x(decoder_2_out12), .b_s(b_s_28718816), .b_e(b_e_394dcd69),
    .y(decoder_1_out1), .b_i(controlled_buffer_1_out));
  RAM1 ram1_195 (
    .b_o(controlled_buffer_1_out), .x(decoder_2_out12), .b_s(b_s_28718816), .b_e(b_e_394dcd69),
    .y(decoder_1_out2), .b_i(controlled_buffer_1_out));
  RAM1 ram1_196 (
    .b_o(controlled_buffer_1_out), .x(decoder_2_out12), .b_s(b_s_28718816), .b_e(b_e_394dcd69),
    .y(decoder_1_out3), .b_i(controlled_buffer_1_out));
  RAM1 ram1_197 (
    .b_o(controlled_buffer_1_out), .x(decoder_2_out12), .b_s(b_s_28718816), .b_e(b_e_394dcd69),
    .y(decoder_1_out4), .b_i(controlled_buffer_1_out));
  RAM1 ram1_198 (
    .b_o(controlled_buffer_1_out), .x(decoder_2_out12), .b_s(b_s_28718816), .b_e(b_e_394dcd69),
    .y(decoder_1_out5), .b_i(controlled_buffer_1_out));
  RAM1 ram1_199 (
    .b_o(controlled_buffer_1_out), .x(decoder_2_out12), .b_s(b_s_28718816), .b_e(b_e_394dcd69),
    .y(decoder_1_out6), .b_i(controlled_buffer_1_out));
  RAM1 ram1_200 (
    .b_o(controlled_buffer_1_out), .x(decoder_2_out12), .b_s(b_s_28718816), .b_e(b_e_394dcd69),
    .y(decoder_1_out7), .b_i(controlled_buffer_1_out));
  RAM1 ram1_201 (
    .b_o(controlled_buffer_1_out), .x(decoder_2_out12), .b_s(b_s_28718816), .b_e(b_e_394dcd69),
    .y(decoder_1_out8), .b_i(controlled_buffer_1_out));
  RAM1 ram1_202 (
    .b_o(controlled_buffer_1_out), .x(decoder_2_out12), .b_s(b_s_28718816), .b_e(b_e_394dcd69),
    .y(decoder_1_out9), .b_i(controlled_buffer_1_out));
  RAM1 ram1_203 (
    .b_o(controlled_buffer_1_out), .x(decoder_2_out12), .b_s(b_s_28718816), .b_e(b_e_394dcd69),
    .y(decoder_1_out10), .b_i(controlled_buffer_1_out));
  RAM1 ram1_204 (
    .b_o(controlled_buffer_1_out), .x(decoder_2_out12), .b_s(b_s_28718816), .b_e(b_e_394dcd69),
    .y(decoder_1_out11), .b_i(controlled_buffer_1_out));
  RAM1 ram1_205 (
    .b_o(controlled_buffer_1_out), .x(decoder_2_out12), .b_s(b_s_28718816), .b_e(b_e_394dcd69),
    .y(decoder_1_out12), .b_i(controlled_buffer_1_out));
  RAM1 ram1_206 (
    .b_o(controlled_buffer_1_out), .x(decoder_2_out12), .b_s(b_s_28718816), .b_e(b_e_394dcd69),
    .y(decoder_1_out13), .b_i(controlled_buffer_1_out));
  RAM1 ram1_207 (
    .b_o(controlled_buffer_1_out), .x(decoder_2_out12), .b_s(b_s_28718816), .b_e(b_e_394dcd69),
    .y(decoder_1_out14), .b_i(controlled_buffer_1_out));
  RAM1 ram1_208 (
    .b_o(controlled_buffer_1_out), .x(decoder_2_out12), .b_s(b_s_28718816), .b_e(b_e_394dcd69),
    .y(decoder_1_out15), .b_i(controlled_buffer_1_out));
  RAM1 ram1_209 (
    .b_o(controlled_buffer_1_out), .x(decoder_2_out13), .b_s(b_s_28718816), .b_e(b_e_394dcd69),
    .y(decoder_1_out0), .b_i(controlled_buffer_1_out));
  RAM1 ram1_210 (
    .b_o(controlled_buffer_1_out), .x(decoder_2_out13), .b_s(b_s_28718816), .b_e(b_e_394dcd69),
    .y(decoder_1_out1), .b_i(controlled_buffer_1_out));
  RAM1 ram1_211 (
    .b_o(controlled_buffer_1_out), .x(decoder_2_out13), .b_s(b_s_28718816), .b_e(b_e_394dcd69),
    .y(decoder_1_out2), .b_i(controlled_buffer_1_out));
  RAM1 ram1_212 (
    .b_o(controlled_buffer_1_out), .x(decoder_2_out13), .b_s(b_s_28718816), .b_e(b_e_394dcd69),
    .y(decoder_1_out3), .b_i(controlled_buffer_1_out));
  RAM1 ram1_213 (
    .b_o(controlled_buffer_1_out), .x(decoder_2_out13), .b_s(b_s_28718816), .b_e(b_e_394dcd69),
    .y(decoder_1_out4), .b_i(controlled_buffer_1_out));
  RAM1 ram1_214 (
    .b_o(controlled_buffer_1_out), .x(decoder_2_out13), .b_s(b_s_28718816), .b_e(b_e_394dcd69),
    .y(decoder_1_out5), .b_i(controlled_buffer_1_out));
  RAM1 ram1_215 (
    .b_o(controlled_buffer_1_out), .x(decoder_2_out13), .b_s(b_s_28718816), .b_e(b_e_394dcd69),
    .y(decoder_1_out6), .b_i(controlled_buffer_1_out));
  RAM1 ram1_216 (
    .b_o(controlled_buffer_1_out), .x(decoder_2_out13), .b_s(b_s_28718816), .b_e(b_e_394dcd69),
    .y(decoder_1_out7), .b_i(controlled_buffer_1_out));
  RAM1 ram1_217 (
    .b_o(controlled_buffer_1_out), .x(decoder_2_out13), .b_s(b_s_28718816), .b_e(b_e_394dcd69),
    .y(decoder_1_out8), .b_i(controlled_buffer_1_out));
  RAM1 ram1_218 (
    .b_o(controlled_buffer_1_out), .x(decoder_2_out13), .b_s(b_s_28718816), .b_e(b_e_394dcd69),
    .y(decoder_1_out9), .b_i(controlled_buffer_1_out));
  RAM1 ram1_219 (
    .b_o(controlled_buffer_1_out), .x(decoder_2_out13), .b_s(b_s_28718816), .b_e(b_e_394dcd69),
    .y(decoder_1_out10), .b_i(controlled_buffer_1_out));
  RAM1 ram1_220 (
    .b_o(controlled_buffer_1_out), .x(decoder_2_out13), .b_s(b_s_28718816), .b_e(b_e_394dcd69),
    .y(decoder_1_out11), .b_i(controlled_buffer_1_out));
  RAM1 ram1_221 (
    .b_o(controlled_buffer_1_out), .x(decoder_2_out13), .b_s(b_s_28718816), .b_e(b_e_394dcd69),
    .y(decoder_1_out12), .b_i(controlled_buffer_1_out));
  RAM1 ram1_222 (
    .b_o(controlled_buffer_1_out), .x(decoder_2_out13), .b_s(b_s_28718816), .b_e(b_e_394dcd69),
    .y(decoder_1_out13), .b_i(controlled_buffer_1_out));
  RAM1 ram1_223 (
    .b_o(controlled_buffer_1_out), .x(decoder_2_out13), .b_s(b_s_28718816), .b_e(b_e_394dcd69),
    .y(decoder_1_out14), .b_i(controlled_buffer_1_out));
  RAM1 ram1_224 (
    .b_o(controlled_buffer_1_out), .x(decoder_2_out13), .b_s(b_s_28718816), .b_e(b_e_394dcd69),
    .y(decoder_1_out15), .b_i(controlled_buffer_1_out));
  RAM1 ram1_225 (
    .b_o(controlled_buffer_1_out), .x(decoder_2_out14), .b_s(b_s_28718816), .b_e(b_e_394dcd69),
    .y(decoder_1_out0), .b_i(controlled_buffer_1_out));
  RAM1 ram1_226 (
    .b_o(controlled_buffer_1_out), .x(decoder_2_out14), .b_s(b_s_28718816), .b_e(b_e_394dcd69),
    .y(decoder_1_out1), .b_i(controlled_buffer_1_out));
  RAM1 ram1_227 (
    .b_o(controlled_buffer_1_out), .x(decoder_2_out14), .b_s(b_s_28718816), .b_e(b_e_394dcd69),
    .y(decoder_1_out2), .b_i(controlled_buffer_1_out));
  RAM1 ram1_228 (
    .b_o(controlled_buffer_1_out), .x(decoder_2_out14), .b_s(b_s_28718816), .b_e(b_e_394dcd69),
    .y(decoder_1_out3), .b_i(controlled_buffer_1_out));
  RAM1 ram1_229 (
    .b_o(controlled_buffer_1_out), .x(decoder_2_out14), .b_s(b_s_28718816), .b_e(b_e_394dcd69),
    .y(decoder_1_out4), .b_i(controlled_buffer_1_out));
  RAM1 ram1_230 (
    .b_o(controlled_buffer_1_out), .x(decoder_2_out14), .b_s(b_s_28718816), .b_e(b_e_394dcd69),
    .y(decoder_1_out5), .b_i(controlled_buffer_1_out));
  RAM1 ram1_231 (
    .b_o(controlled_buffer_1_out), .x(decoder_2_out14), .b_s(b_s_28718816), .b_e(b_e_394dcd69),
    .y(decoder_1_out6), .b_i(controlled_buffer_1_out));
  RAM1 ram1_232 (
    .b_o(controlled_buffer_1_out), .x(decoder_2_out14), .b_s(b_s_28718816), .b_e(b_e_394dcd69),
    .y(decoder_1_out7), .b_i(controlled_buffer_1_out));
  RAM1 ram1_233 (
    .b_o(controlled_buffer_1_out), .x(decoder_2_out14), .b_s(b_s_28718816), .b_e(b_e_394dcd69),
    .y(decoder_1_out8), .b_i(controlled_buffer_1_out));
  RAM1 ram1_234 (
    .b_o(controlled_buffer_1_out), .x(decoder_2_out14), .b_s(b_s_28718816), .b_e(b_e_394dcd69),
    .y(decoder_1_out9), .b_i(controlled_buffer_1_out));
  RAM1 ram1_235 (
    .b_o(controlled_buffer_1_out), .x(decoder_2_out14), .b_s(b_s_28718816), .b_e(b_e_394dcd69),
    .y(decoder_1_out10), .b_i(controlled_buffer_1_out));
  RAM1 ram1_236 (
    .b_o(controlled_buffer_1_out), .x(decoder_2_out14), .b_s(b_s_28718816), .b_e(b_e_394dcd69),
    .y(decoder_1_out11), .b_i(controlled_buffer_1_out));
  RAM1 ram1_237 (
    .b_o(controlled_buffer_1_out), .x(decoder_2_out14), .b_s(b_s_28718816), .b_e(b_e_394dcd69),
    .y(decoder_1_out12), .b_i(controlled_buffer_1_out));
  RAM1 ram1_238 (
    .b_o(controlled_buffer_1_out), .x(decoder_2_out14), .b_s(b_s_28718816), .b_e(b_e_394dcd69),
    .y(decoder_1_out13), .b_i(controlled_buffer_1_out));
  RAM1 ram1_239 (
    .b_o(controlled_buffer_1_out), .x(decoder_2_out14), .b_s(b_s_28718816), .b_e(b_e_394dcd69),
    .y(decoder_1_out14), .b_i(controlled_buffer_1_out));
  RAM1 ram1_240 (
    .b_o(controlled_buffer_1_out), .x(decoder_2_out14), .b_s(b_s_28718816), .b_e(b_e_394dcd69),
    .y(decoder_1_out15), .b_i(controlled_buffer_1_out));
  RAM1 ram1_241 (
    .b_o(controlled_buffer_1_out), .x(decoder_2_out15), .b_s(b_s_28718816), .b_e(b_e_394dcd69),
    .y(decoder_1_out0), .b_i(controlled_buffer_1_out));
  RAM1 ram1_242 (
    .b_o(controlled_buffer_1_out), .x(decoder_2_out15), .b_s(b_s_28718816), .b_e(b_e_394dcd69),
    .y(decoder_1_out1), .b_i(controlled_buffer_1_out));
  RAM1 ram1_243 (
    .b_o(controlled_buffer_1_out), .x(decoder_2_out15), .b_s(b_s_28718816), .b_e(b_e_394dcd69),
    .y(decoder_1_out2), .b_i(controlled_buffer_1_out));
  RAM1 ram1_244 (
    .b_o(controlled_buffer_1_out), .x(decoder_2_out15), .b_s(b_s_28718816), .b_e(b_e_394dcd69),
    .y(decoder_1_out3), .b_i(controlled_buffer_1_out));
  RAM1 ram1_245 (
    .b_o(controlled_buffer_1_out), .x(decoder_2_out15), .b_s(b_s_28718816), .b_e(b_e_394dcd69),
    .y(decoder_1_out4), .b_i(controlled_buffer_1_out));
  RAM1 ram1_246 (
    .b_o(controlled_buffer_1_out), .x(decoder_2_out15), .b_s(b_s_28718816), .b_e(b_e_394dcd69),
    .y(decoder_1_out5), .b_i(controlled_buffer_1_out));
  RAM1 ram1_247 (
    .b_o(controlled_buffer_1_out), .x(decoder_2_out15), .b_s(b_s_28718816), .b_e(b_e_394dcd69),
    .y(decoder_1_out6), .b_i(controlled_buffer_1_out));
  RAM1 ram1_248 (
    .b_o(controlled_buffer_1_out), .x(decoder_2_out15), .b_s(b_s_28718816), .b_e(b_e_394dcd69),
    .y(decoder_1_out7), .b_i(controlled_buffer_1_out));
  RAM1 ram1_249 (
    .b_o(controlled_buffer_1_out), .x(decoder_2_out15), .b_s(b_s_28718816), .b_e(b_e_394dcd69),
    .y(decoder_1_out8), .b_i(controlled_buffer_1_out));
  RAM1 ram1_250 (
    .b_o(controlled_buffer_1_out), .x(decoder_2_out15), .b_s(b_s_28718816), .b_e(b_e_394dcd69),
    .y(decoder_1_out9), .b_i(controlled_buffer_1_out));
  RAM1 ram1_251 (
    .b_o(controlled_buffer_1_out), .x(decoder_2_out15), .b_s(b_s_28718816), .b_e(b_e_394dcd69),
    .y(decoder_1_out10), .b_i(controlled_buffer_1_out));
  RAM1 ram1_252 (
    .b_o(controlled_buffer_1_out), .x(decoder_2_out15), .b_s(b_s_28718816), .b_e(b_e_394dcd69),
    .y(decoder_1_out11), .b_i(controlled_buffer_1_out));
  RAM1 ram1_253 (
    .b_o(controlled_buffer_1_out), .x(decoder_2_out15), .b_s(b_s_28718816), .b_e(b_e_394dcd69),
    .y(decoder_1_out12), .b_i(controlled_buffer_1_out));
  RAM1 ram1_254 (
    .b_o(controlled_buffer_1_out), .x(decoder_2_out15), .b_s(b_s_28718816), .b_e(b_e_394dcd69),
    .y(decoder_1_out13), .b_i(controlled_buffer_1_out));
  RAM1 ram1_255 (
    .b_o(controlled_buffer_1_out), .x(decoder_2_out15), .b_s(b_s_28718816), .b_e(b_e_394dcd69),
    .y(decoder_1_out14), .b_i(controlled_buffer_1_out));
  RAM1 ram1_256 (
    .b_o(controlled_buffer_1_out), .x(decoder_2_out15), .b_s(b_s_28718816), .b_e(b_e_394dcd69),
    .y(decoder_1_out15), .b_i(controlled_buffer_1_out));
  assign b_o_c2cd5d60 = b_e_394dcd69 ? controlled_buffer_1_out : 8'bz;  // Controlled_Buffer controlled_buffer_2
endmodule

module RAM1 (
  input  y,
  input  x,
  input  b_s,
  input  b_e,
  input  [7:0] b_i,
  output [7:0] b_o
);

  wire and_1_out, and_2_out, and_3_out;
  wire [7:0] controlled_buffer_1_out, reg_1_o;

  and and_1 (and_1_out, y, x);
  and and_2 (and_2_out, and_1_out, b_s);
  and and_3 (and_3_out, and_1_out, b_e);
  assign controlled_buffer_1_out = and_2_out ? b_i : 8'bz;  // Controlled_Buffer controlled_buffer_1
  assign b_o = and_3_out ? reg_1_o : 8'bz;  // Controlled_Buffer controlled_buffer_2
  Reg reg_1 (.o(reg_1_o), .i(controlled_buffer_1_out), .en(and_3_out), .set(and_2_out));
endmodule

module Adder (
  input  ci,
  input  [7:0] a,
  input  [7:0] b,
  output [7:0] o,
  output co
);

  wire adder1_1_co, adder1_2_co, adder1_3_co, adder1_4_co, adder1_5_co, adder1_6_co, adder1_7_co;

  Adder1 adder1_1 (.co(adder1_1_co), .sum(o[0]), .ci(ci), .a(a[0]), .b(b[0]));
  Adder1 adder1_2 (.co(adder1_2_co), .sum(o[1]), .ci(adder1_1_co), .a(a[1]), .b(b[1]));
  Adder1 adder1_3 (.co(adder1_3_co), .sum(o[2]), .ci(adder1_2_co), .a(a[2]), .b(b[2]));
  Adder1 adder1_4 (.co(adder1_4_co), .sum(o[3]), .ci(adder1_3_co), .a(a[3]), .b(b[3]));
  Adder1 adder1_5 (.co(adder1_5_co), .sum(o[4]), .ci(adder1_4_co), .a(a[4]), .b(b[4]));
  Adder1 adder1_6 (.co(adder1_6_co), .sum(o[5]), .ci(adder1_5_co), .a(a[5]), .b(b[5]));
  Adder1 adder1_7 (.co(adder1_7_co), .sum(o[6]), .ci(adder1_6_co), .a(a[6]), .b(b[6]));
  Adder1 adder1_8 (.co(co), .sum(o[7]), .ci(adder1_7_co), .a(a[7]), .b(b[7]));
endmodule

module Adder1 (
  input  a,
  input  b,
  input  ci,
  output sum,
  output co
);

  wire co1_out, co2_out, sum1_out;

  xor sum1 (sum1_out, a, b);
  xor sum2 (sum, sum1_out, ci);
  and co2 (co2_out, sum1_out, ci);
  and co1 (co1_out, a, b);
  or or_1 (co, co2_out, co1_out);
endmodule

module SHR (
  input  [7:0] i,
  input  si,
  output so,
  output [7:0] o
);

  wire [7:1] \출발지_레지스터_o ;

  Reg \u_출발지_레지스터  (.o({\출발지_레지스터_o , so}), .i(i), .en(1'b1), .set(1'b1));
  Reg \u_목적지_레지스터  (.o(o), .i({si, \출발지_레지스터_o }), .en(1'b1), .set(1'b1));
endmodule

module SHL (
  input  si,
  input  [7:0] i,
  output [7:0] o,
  output so
);

  wire [6:0] \출발지_레지스터_o ;

  Reg \u_출발지_레지스터  (.o({so, \출발지_레지스터_o }), .i(i), .en(1'b1), .set(1'b1));
  Reg \u_목적지_레지스터  (.o(o), .i({\출발지_레지스터_o , si}), .en(1'b1), .set(1'b1));
endmodule

module Inverter (
  input  [7:0] in_1,
  output [7:0] out_2
);

  assign out_2 = ~in_1;  // NOT_Gate not_1, 8 bits wide
endmodule

module ANDer (
  input  [7:0] a,
  input  [7:0] b,
  output [7:0] o
);

  and and_1 (o[0], a[0], b[0]);
  and and_2 (o[1], a[1], b[1]);
  and and_3 (o[2], a[2], b[2]);
  and and_4 (o[3], a[3], b[3]);
  and and_5 (o[4], a[4], b[4]);
  and and_6 (o[5], a[5], b[5]);
  and and_7 (o[6], a[6], b[6]);
  and and_8 (o[7], a[7], b[7]);
endmodule

module ORer (
  input  [7:0] a,
  input  [7:0] b,
  output [7:0] o
);

  or or_1 (o[0], a[0], b[0]);
  or or_2 (o[1], a[1], b[1]);
  or or_3 (o[2], a[2], b[2]);
  or or_4 (o[3], a[3], b[3]);
  or or_5 (o[4], a[4], b[4]);
  or or_6 (o[5], a[5], b[5]);
  or or_7 (o[6], a[6], b[6]);
  or or_8 (o[7], a[7], b[7]);
endmodule

module XOR1 (
  input  s_i,
  input  l_i,
  input  a,
  input  b,
  output o,
  output s_o,
  output l_o
);

  wire and_2_out, not_1_out;

  xor xor_1 (o, a, b);
  not not_1 (not_1_out, o);
  and and_1 (s_o, not_1_out, s_i);
  and and_2 (and_2_out, s_i, a, o);
  or or_1 (l_o, and_2_out, l_i);
endmodule

module XORer (
  input  [7:0] a,
  input  [7:0] b,
  output [7:0] out_3,
  output s_o,
  output l_o
);

  wire xor1_1_l_o, xor1_1_s_o, xor1_2_l_o, xor1_2_s_o, xor1_3_l_o, xor1_3_s_o, xor1_4_l_o, xor1_4_s_o,
       xor1_5_l_o, xor1_5_s_o, xor1_6_l_o, xor1_6_s_o, xor1_7_l_o, xor1_7_s_o;

  XOR1 xor1_1 (.s_o(xor1_1_s_o), .l_o(xor1_1_l_o), .o(out_3[7]), .s_i(1'b1), .l_i(1'b0), .a(a[7]), .b(b[7]));
  XOR1 xor1_2 (
    .s_o(xor1_2_s_o), .l_o(xor1_2_l_o), .o(out_3[6]), .s_i(xor1_1_s_o), .l_i(xor1_1_l_o), .a(a[6]), .b(b[6]));
  XOR1 xor1_3 (
    .s_o(xor1_3_s_o), .l_o(xor1_3_l_o), .o(out_3[5]), .s_i(xor1_2_s_o), .l_i(xor1_2_l_o), .a(a[5]), .b(b[5]));
  XOR1 xor1_4 (
    .s_o(xor1_4_s_o), .l_o(xor1_4_l_o), .o(out_3[4]), .s_i(xor1_3_s_o), .l_i(xor1_3_l_o), .a(a[4]), .b(b[4]));
  XOR1 xor1_5 (
    .s_o(xor1_5_s_o), .l_o(xor1_5_l_o), .o(out_3[3]), .s_i(xor1_4_s_o), .l_i(xor1_4_l_o), .a(a[3]), .b(b[3]));
  XOR1 xor1_6 (
    .s_o(xor1_6_s_o), .l_o(xor1_6_l_o), .o(out_3[2]), .s_i(xor1_5_s_o), .l_i(xor1_5_l_o), .a(a[2]), .b(b[2]));
  XOR1 xor1_7 (
    .s_o(xor1_7_s_o), .l_o(xor1_7_l_o), .o(out_3[1]), .s_i(xor1_6_s_o), .l_i(xor1_6_l_o), .a(a[1]), .b(b[1]));
  XOR1 xor1_8 (.s_o(s_o), .l_o(l_o), .o(out_3[0]), .s_i(xor1_7_s_o), .l_i(xor1_7_l_o), .a(a[0]), .b(b[0]));
endmodule

module ZEROer (
  input  [7:0] in,
  output out
);

  wire or_1_out;

  or or_1 (or_1_out, in[0], in[1], in[2], in[3], in[4], in[5], in[6], in[7]);
  not not_1 (out, or_1_out);
endmodule

module Enabler_old (
  input  [7:0] in_1,
  input  in_2,
  output [7:0] out_3
);

  Controlled_Buffer controlled_buffer_1 ();  // open: in, out, en
  and and_1 (out_3[0], in_2, in_1[0]);
  and and_2 (out_3[1], in_2, in_1[1]);
  and and_3 (out_3[2], in_2, in_1[2]);
  and and_4 (out_3[3], in_2, in_1[3]);
  and and_5 (out_3[4], in_2, in_1[4]);
  and and_6 (out_3[5], in_2, in_1[5]);
  and and_7 (out_3[6], in_2, in_1[6]);
  and and_8 (out_3[7], in_2, in_1[7]);
endmodule

module ALU (
  input  [7:0] a,
  input  [7:0] b,
  input  ci,
  input  [2:0] op,
  output a_b,
  output a_b_2,
  output zero,
  output [7:0] o,
  output co
);

  wire adder_1_co, and_1_out, and_2_out, and_3_out, decoder_1_out0, decoder_1_out1, decoder_1_out2,
       decoder_1_out3, decoder_1_out4, decoder_1_out5, decoder_1_out6, decoder_1_out7, shl_1_so, shr_1_so;
  wire [7:0] adder_1_o, ander_1_o, inverter_1_out_2, orer_1_o, shl_1_o, shr_1_o, xorer_1_out_3;

  XORer xorer_1 (.s_o(a_b_2), .l_o(a_b), .out_3(xorer_1_out_3), .a(a), .b(b));
  ORer orer_1 (.o(orer_1_o), .a(a), .b(b));
  ANDer ander_1 (.o(ander_1_o), .a(a), .b(b));
  Inverter inverter_1 (.out_2(inverter_1_out_2), .in_1(a));
  SHL shl_1 (.so(shl_1_so), .o(shl_1_o), .i(a), .si(ci));
  SHR shr_1 (.so(shr_1_so), .o(shr_1_o), .i(a), .si(ci));
  Adder adder_1 (.o(adder_1_o), .co(adder_1_co), .a(a), .b(b), .ci(ci));
  Decoder #(.enable("false"), .select(3)) decoder_1 (
    .out0(decoder_1_out0), .out1(decoder_1_out1), .out2(decoder_1_out2), .out3(decoder_1_out3),
    .out4(decoder_1_out4), .out5(decoder_1_out5), .out6(decoder_1_out6), .out7(decoder_1_out7), .sel(op));
  and and_1 (and_1_out, shl_1_so, decoder_1_out2);
  and and_2 (and_2_out, adder_1_co, decoder_1_out0);
  assign o = decoder_1_out7 ? {8{1'b0}} : 8'bz;  // Controlled_Buffer controlled_buffer_1
  Enabler enabler_1 (.out_3(o), .in_2(decoder_1_out6), .in_1(xorer_1_out_3));
  Enabler enabler_2 (.out_3(o), .in_2(decoder_1_out5), .in_1(orer_1_o));
  Enabler enabler_3 (.out_3(o), .in_2(decoder_1_out4), .in_1(ander_1_o));
  Enabler enabler_4 (.out_3(o), .in_2(decoder_1_out3), .in_1(inverter_1_out_2));
  Enabler enabler_5 (.out_3(o), .in_2(decoder_1_out2), .in_1(shl_1_o));
  and and_3 (and_3_out, shr_1_so, decoder_1_out1);
  Enabler enabler_6 (.out_3(o), .in_2(decoder_1_out1), .in_1(shr_1_o));
  Enabler enabler_7 (.out_3(o), .in_2(decoder_1_out0), .in_1(adder_1_o));
  ZEROer zeroer_1 (.out(zero), .in(o));
  or or_1 (co, and_1_out, and_3_out, and_2_out);
endmodule

module Clk (
  output clk,
  output clk_e,
  output clk_s
);

  wire clk_raw_out, j_k_ff_1_qn;

  Clock clk_raw (.out(clk_raw_out));
  J_K_Flip_Flop j_k_ff_1 (.J(1'b1), .clk(clk_raw_out), .K(1'b1), .Q(clk), .Qn(j_k_ff_1_qn));  // open: preset, reset
  nand nand_1 (clk_e, clk_raw_out, j_k_ff_1_qn);
  and and_1 (clk_s, clk_raw_out, clk);
endmodule

module Stepper_book (
  input  reset,
  input  clk,
  output _1,
  output _2,
  output _3,
  output _4,
  output _5,
  output _6,
  output _7
);

  wire m_1_o, m_2_o, m_3_o, m_4_o, m_5_o, m_6_o, m_7_o, m_8_o, m_9_o, m_10_o, m_11_o, not_1_out, not_2_out,
       not_3_out, not_4_out, not_5_out, not_6_out, not_7_out, not_8_out, or_1_out, or_2_out;

  not not_1 (not_1_out, clk);
  not not_2 (not_2_out, reset);
  or or_1 (or_1_out, reset, clk);
  or or_2 (or_2_out, reset, not_1_out);
  or or_3 (_1, reset, not_3_out);
  not not_3 (not_3_out, m_2_o);
  M m_1 (.o(m_1_o), .i(not_2_out), .s(or_1_out));
  M m_2 (.o(m_2_o), .i(m_1_o), .s(or_2_out));
  and and_1 (_2, m_2_o, not_4_out);
  M m_3 (.o(m_3_o), .i(m_2_o), .s(or_1_out));
  not not_4 (not_4_out, m_4_o);
  M m_4 (.o(m_4_o), .i(m_3_o), .s(or_2_out));
  and and_2 (_3, m_4_o, not_5_out);
  M m_5 (.o(m_5_o), .i(m_4_o), .s(or_1_out));
  not not_5 (not_5_out, m_6_o);
  M m_6 (.o(m_6_o), .i(m_5_o), .s(or_2_out));
  M m_7 (.o(m_7_o), .i(m_6_o), .s(or_1_out));
  and and_3 (_4, m_6_o, not_6_out);
  not not_6 (not_6_out, m_8_o);
  M m_8 (.o(m_8_o), .i(m_7_o), .s(or_2_out));
  and and_4 (_5, m_8_o, not_7_out);
  not not_7 (not_7_out, m_10_o);
  M m_9 (.o(m_9_o), .i(m_8_o), .s(or_1_out));
  M m_10 (.o(m_10_o), .i(m_9_o), .s(or_2_out));
  and and_5 (_6, m_10_o, not_8_out);
  M m_11 (.o(m_11_o), .i(m_10_o), .s(or_1_out));
  not not_8 (not_8_out, _7);
  M m_12 (.o(_7), .i(m_11_o), .s(or_2_out));
endmodule

module Stepper (
  input  clk,
  input  reset,
  output _1,
  output _2,
  output _3,
  output _4,
  output _5,
  output _6,
  output _7
);

  wire d_ff_1_q, d_ff_2_q, d_ff_3_q, d_ff_4_q, d_ff_5_q, d_ff_6_q, d_ff_7_q, d_ff_8_q, d_ff_9_q, d_ff_10_q,
       d_ff_11_q, not_1_out, not_2_out, not_3_out, not_4_out, not_5_out, not_6_out, not_7_out, not_8_out,
       or_1_out, or_2_out;

  not not_1 (not_1_out, clk);
  not not_2 (not_2_out, _7);
  or or_1 (or_1_out, _7, clk);
  or or_2 (or_2_out, _7, not_1_out);
  D_Flip_Flop d_ff_1 (.clk(or_1_out), .D(not_2_out), .Q(d_ff_1_q), .reset(reset));  // open: Qn, preset
  or or_3 (_1, _7, not_3_out);
  not not_3 (not_3_out, d_ff_2_q);
  D_Flip_Flop d_ff_2 (.clk(or_2_out), .D(d_ff_1_q), .Q(d_ff_2_q), .reset(reset));  // open: Qn, preset
  and and_1 (_2, d_ff_2_q, not_4_out);
  not not_4 (not_4_out, d_ff_4_q);
  D_Flip_Flop d_ff_3 (.clk(or_1_out), .D(d_ff_2_q), .Q(d_ff_3_q), .reset(reset));  // open: Qn, preset
  D_Flip_Flop d_ff_4 (.clk(or_2_out), .D(d_ff_3_q), .Q(d_ff_4_q), .reset(reset));  // open: Qn, preset
  and and_2 (_3, d_ff_4_q, not_5_out);
  D_Flip_Flop d_ff_5 (.clk(or_1_out), .D(d_ff_4_q), .Q(d_ff_5_q), .reset(reset));  // open: Qn, preset
  not not_5 (not_5_out, d_ff_6_q);
  D_Flip_Flop d_ff_6 (.clk(or_2_out), .D(d_ff_5_q), .Q(d_ff_6_q), .reset(reset));  // open: Qn, preset
  and and_3 (_4, d_ff_6_q, not_6_out);
  D_Flip_Flop d_ff_7 (.clk(or_1_out), .D(d_ff_6_q), .Q(d_ff_7_q), .reset(reset));  // open: Qn, preset
  not not_6 (not_6_out, d_ff_8_q);
  D_Flip_Flop d_ff_8 (.clk(or_2_out), .D(d_ff_7_q), .Q(d_ff_8_q), .reset(reset));  // open: Qn, preset
  D_Flip_Flop d_ff_9 (.clk(or_1_out), .D(d_ff_8_q), .Q(d_ff_9_q), .reset(reset));  // open: Qn, preset
  and and_4 (_5, d_ff_8_q, not_7_out);
  not not_7 (not_7_out, d_ff_10_q);
  D_Flip_Flop d_ff_10 (.clk(or_2_out), .D(d_ff_9_q), .Q(d_ff_10_q), .reset(reset));  // open: Qn, preset
  and and_5 (_6, d_ff_10_q, not_8_out);
  not not_8 (not_8_out, _7);
  D_Flip_Flop d_ff_11 (.clk(or_1_out), .D(d_ff_10_q), .Q(d_ff_11_q), .reset(reset));  // open: Qn, preset
  D_Flip_Flop d_ff_12 (.clk(or_2_out), .D(d_ff_11_q), .Q(_7), .reset(reset));  // open: Qn, preset
endmodule

module SR_LATCH (
  input  r,
  input  s,
  output q,
  output not_q
);

  nor nor_1 (q, r, not_q);
  nor nor_2 (not_q, q, s);
endmodule

module SR_LATCH_single_input (
  input  i,
  output q,
  output not_q
);

  wire not_1_out;

  not not_1 (not_1_out, i);
  nor nor_1 (q, not_1_out, not_q);
  nor nor_2 (not_q, q, i);
endmodule

module SR_LATCH_enable (
  input  r,
  input  en,
  input  s,
  output q,
  output not_q
);

  wire and_1_out, and_2_out;

  and and_1 (and_1_out, r, en);
  and and_2 (and_2_out, en, s);
  nor nor_1 (q, and_1_out, not_q);
  nor nor_2 (not_q, q, and_2_out);
endmodule

module D_LATCH (
  input  s,
  input  i,
  output o,
  output out_4
);

  wire and_1_out, and_2_out, not_1_out;

  not not_1 (not_1_out, i);
  and and_1 (and_1_out, not_1_out, s);
  and and_2 (and_2_out, s, i);
  nor nor_1 (o, and_1_out, out_4);
  nor nor_2 (out_4, o, and_2_out);
endmodule

module D_flipflop (
  input  clk,
  input  i,
  output o,
  output out_4
);

  wire and_1_out, and_2_out, and_3_out, not_1_out, not_2_out;

  not not_1 (not_1_out, clk);
  and and_1 (and_1_out, clk, not_1_out);
  not not_2 (not_2_out, i);
  and and_2 (and_2_out, not_2_out, and_1_out);
  and and_3 (and_3_out, and_1_out, i);
  nor nor_1 (o, and_2_out, out_4);
  nor nor_2 (out_4, o, and_3_out);
endmodule

module ControlUnit (
  input  F4,
  input  F5,
  input  F6,
  input  _0,
  input  _1,
  input  _2,
  input  _3,
  input  _4,
  input  _5,
  input  _6,
  input  _7,
  input  F7,
  output R0_S,
  output R0_E,
  output R1_S,
  output R1_E,
  output R2_S,
  output R2_E,
  output R3_S,
  output R3_E,
  output Bus1_E,
  output MAR_S,
  output IAR_E,
  output IR_S,
  output RAM_E,
  output IAR_S,
  output ACC_E,
  output ACC_S,
  output TMP_S,
  output RAM_S,
  output CI_E,
  output FLAGS_S,
  output [2:0] op_out
);

  wire A_out, ACC_ALU_E, ACC_ALU_S, ACC_DATA_E, ACC_DATA_S, ACC_IF_E, ACC_IF_S, ACC_NJ_E, ACC_NJ_S,
       and_12_out, and_24_out, and_25_out, and_26_out, and_27_out, and_28_out, and_29_out, and_30_out,
       and_31_out, BUS1_CLF_E, BUS1_DATA_E, BUS1_IF_E, BUS1_JC_E, C_out, CI_ALU_E, CLF_E, clk_1_clk, clk_e,
       clk_s, DATA_E, decoder3x8_1_out_4, decoder3x8_1_out_5, decoder3x8_1_out_6, decoder3x8_1_out_7,
       decoder3x8_1_out_8, decoder3x8_1_out_9, decoder3x8_1_out_10, decoder3x8_1_out_11, decoder_2x4_1__01,
       decoder_2x4_1_o2, decoder_2x4_1_o3, decoder_2x4_1_o4, decoder_2x4_2__01, decoder_2x4_2_o2,
       decoder_2x4_2_o3, decoder_2x4_2_o4, decoder_2x4_inverted_1__01, decoder_2x4_inverted_1_o2,
       decoder_2x4_inverted_1_o3, decoder_2x4_inverted_1_o4, E_2_out, FLAGS_CLF_S, IAR_DATA_E, IAR_DATA_S,
       IAR_IF_E, IAR_IF_S, IAR_JC_E, IAR_JC_S, IAR_JMP_E, IAR_JMP_S, IAR_JMPR_S, IAR_NJ_S, IR_IF_S, JC_E,
       JMP_E, JMPR_E, LD_E, MAR_DATA_S, MAR_IF_S, MAR_JMP_S, MAR_LD_S, MAR_ST_S, NOP_E, not_1_out, not_3_out,
       not_4_out, not_5_out, RA_E, RA_LD_E, RA_ST_E, RAM_DATA_E, RAM_IF_E, RAM_JC_E, RAM_JMP_E, RAM_LD_E,
       RAM_ST_S, RB_ALU_E, RB_ALU_S, RB_DATA_S, RB_E, RB_JMPR_E, RB_LD_S, RB_S, RB_ST_E, S1, S2, S2_IF, S3,
       S3_IF, S4, S4_ALU, S4_CLF, S4_JMP, S4_JMPR, S4_LD, S4_ST, S5, S5_ALU, S5_DATA, S5_JC, S5_JMP, S5_LD,
       S5_ST, S6, S6_ALU, S6_DATA, S6_JC, ST_E, stepper_1__7, TMP_ALU_S, UPDATE_IAR, UPDATE_RB, Z_out;

  LED e (.in(clk_e));
  or or_1 (Bus1_E, BUS1_IF_E, BUS1_DATA_E, BUS1_CLF_E, BUS1_JC_E, 1'b0, 1'b0, 1'b0, 1'b0);
  or or_2 (IAR_E, IAR_IF_E, IAR_DATA_E, IAR_JMP_E, IAR_JC_E, 1'b0, 1'b0, 1'b0, 1'b0);
  or or_3 (RAM_E, RAM_IF_E, RAM_LD_E, RAM_DATA_E, RAM_JMP_E, RAM_JC_E, 1'b0, 1'b0, 1'b0);
  or or_4 (ACC_E, ACC_IF_E, ACC_ALU_E, ACC_DATA_E, ACC_NJ_E, 1'b0, 1'b0, 1'b0, 1'b0);
  or or_5 (RA_E, CI_ALU_E, RA_LD_E, RA_ST_E, 1'b0, 1'b0, 1'b0, 1'b0, 1'b0);
  or or_6 (RB_E, RB_ALU_E, RB_ST_E, RB_JMPR_E, 1'b0, 1'b0, 1'b0, 1'b0, 1'b0);
  or or_7 (CI_E, CI_ALU_E, 1'b0);
  and and_1 (op_out[0], S5_ALU, _0, _3);
  and and_2 (op_out[1], S5_ALU, _0, _2);
  and and_3 (op_out[2], S5_ALU, _0, _1);
  LED u__1 (.in(S1));
  Clk clk_1 (.clk_e(clk_e), .clk_s(clk_s), .clk(clk_1_clk));
  LED u__2 (.in(S2));
  not not_1 (not_1_out, _0);
  Stepper stepper_1 (
    ._5(S5), ._6(S6), ._7(stepper_1__7), ._1(S1), ._2(S2), ._3(S3), ._4(S4), .clk(clk_1_clk),
    .reset(stepper_1__7));
  LED u__3 (.in(S3));
  and and_4 (LD_E, not_1_out, decoder3x8_1_out_4);
  Decoder3x8 decoder3x8_1 (
    .out_6(decoder3x8_1_out_6), .out_7(decoder3x8_1_out_7), .out_8(decoder3x8_1_out_8),
    .out_9(decoder3x8_1_out_9), .out_10(decoder3x8_1_out_10), .out_11(decoder3x8_1_out_11),
    .out_4(decoder3x8_1_out_4), .out_5(decoder3x8_1_out_5), .in_1(_1), .in_2(_2), .in_3(_3));
  and and_5 (ST_E, not_1_out, decoder3x8_1_out_5);
  and and_6 (DATA_E, not_1_out, decoder3x8_1_out_6);
  and and_7 (JMPR_E, not_1_out, decoder3x8_1_out_7);
  and and_8 (JMP_E, not_1_out, decoder3x8_1_out_8);
  and and_9 (JC_E, not_1_out, decoder3x8_1_out_9);
  and and_10 (CLF_E, not_1_out, decoder3x8_1_out_10);
  and and_11 (NOP_E, not_1_out, decoder3x8_1_out_11);
  LED u__4 (.in(S4));
  LED u__5 (.in(S5));
  and and_12 (and_12_out, _3, _2, _1);
  LED u__6 (.in(S6));
  not not_2 (UPDATE_RB, and_12_out);
  LED s (.in(clk_s));
  or or_8 (MAR_S, MAR_IF_S, MAR_LD_S, MAR_ST_S, MAR_DATA_S, MAR_JMP_S, ACC_NJ_S, 1'b0, 1'b0);
  or or_9 (IR_S, IR_IF_S, 1'b0, 1'b0, 1'b0, 1'b0, 1'b0, 1'b0, 1'b0);
  or or_10 (IAR_S, IAR_IF_S, IAR_DATA_S, IAR_JMPR_S, IAR_JMP_S, IAR_NJ_S, IAR_JC_S, 1'b0, 1'b0);
  or or_11 (ACC_S, ACC_IF_S, ACC_ALU_S, ACC_DATA_S, ACC_NJ_S, 1'b0, 1'b0, 1'b0, 1'b0);
  or or_12 (TMP_S, TMP_ALU_S, 1'b0, 1'b0, 1'b0, 1'b0, 1'b0, 1'b0, 1'b0);
  or or_13 (RAM_S, RAM_ST_S, 1'b0, 1'b0, 1'b0, 1'b0, 1'b0, 1'b0, 1'b0);
  or or_14 (RB_S, RB_ALU_S, RB_LD_S, RB_DATA_S, 1'b0, 1'b0, 1'b0, 1'b0, 1'b0);
  or or_15 (FLAGS_S, ACC_ALU_S, FLAGS_CLF_S);
  and and_13 (IAR_JC_E, clk_e, BUS1_JC_E);
  and and_14 (ACC_NJ_E, clk_e, S5_JC);
  and and_15 (RAM_JC_E, clk_e, S6_JC);
  and and_16 (BUS1_CLF_E, clk_e, S4_CLF);
  or or_16 (R0_E, and_24_out, and_28_out);
  or or_17 (R1_E, and_25_out, and_29_out);
  or or_18 (R2_E, and_26_out, and_30_out);
  or or_19 (R3_E, and_27_out, and_31_out);
  and and_17 (RB_ALU_E, clk_e, S4_ALU);
  and and_18 (CI_ALU_E, clk_e, S5_ALU);
  and and_19 (ACC_ALU_E, clk_e, S6_ALU);
  and and_20 (RA_LD_E, clk_e, S4_LD);
  and and_21 (RAM_LD_E, clk_e, S5_LD);
  and and_22 (RA_ST_E, clk_e, S4_ST);
  and and_23 (RB_ST_E, clk_e, S5_ST);
  and and_24 (and_24_out, clk_e, RB_E, decoder_2x4_1__01);
  and and_25 (and_25_out, clk_e, RB_E, decoder_2x4_1_o2);
  and and_26 (and_26_out, clk_e, RB_E, decoder_2x4_1_o3);
  and and_27 (and_27_out, clk_e, RB_E, decoder_2x4_1_o4);
  and and_28 (and_28_out, clk_e, RA_E, decoder_2x4_2__01);
  and and_29 (and_29_out, clk_e, RA_E, decoder_2x4_2_o2);
  and and_30 (and_30_out, clk_e, RA_E, decoder_2x4_2_o3);
  and and_31 (and_31_out, clk_e, RA_E, decoder_2x4_2_o4);
  and and_32 (ACC_NJ_S, clk_s, BUS1_JC_E);
  and and_33 (IAR_NJ_S, clk_s, S5_JC);
  and and_34 (IAR_JC_S, clk_s, S6_JC);
  and and_35 (FLAGS_CLF_S, clk_s, S4_CLF);
  Decoder_2x4 decoder_2x4_1 (
    .o3(decoder_2x4_1_o3), .o4(decoder_2x4_1_o4), ._01(decoder_2x4_1__01), .o2(decoder_2x4_1_o2), .a(_7),
    .b(_6));
  Decoder_2x4 decoder_2x4_2 (
    .o3(decoder_2x4_2_o3), .o4(decoder_2x4_2_o4), ._01(decoder_2x4_2__01), .o2(decoder_2x4_2_o2), .a(_5),
    .b(_4));
  Decoder_2x4_inverted decoder_2x4_inverted_1 (
    .o3(decoder_2x4_inverted_1_o3), .o4(decoder_2x4_inverted_1_o4), ._01(decoder_2x4_inverted_1__01),
    .o2(decoder_2x4_inverted_1_o2), .a(_7), .b(_6));
  and and_36 (TMP_ALU_S, clk_s, S4_ALU);
  and and_37 (ACC_ALU_S, clk_s, S5_ALU);
  and and_38 (RB_ALU_S, clk_s, S6_ALU);
  and and_39 (MAR_LD_S, clk_s, S4_LD);
  and and_40 (RB_LD_S, clk_s, S5_LD);
  and and_41 (MAR_ST_S, clk_s, S4_ST);
  and and_42 (RAM_ST_S, clk_s, S5_ST);
  and and_43 (R0_S, clk_s, RB_S, decoder_2x4_inverted_1__01);
  and and_44 (R1_S, clk_s, RB_S, decoder_2x4_inverted_1_o2);
  and and_45 (R2_S, clk_s, RB_S, decoder_2x4_inverted_1_o3);
  and and_46 (R3_S, clk_s, RB_S, decoder_2x4_inverted_1_o4);
  and and_47 (S4_CLF, S4, CLF_E);
  and and_48 (BUS1_JC_E, S4, JC_E);
  and and_49 (S5_JC, S5, JC_E);
  and and_50 (S6_JC, S6, JC_E, UPDATE_IAR);
  and and_51 (S4_ALU, S4, _0);
  and and_52 (S5_ALU, S5, _0);
  and and_53 (S6_ALU, S6, _0, UPDATE_RB);
  and and_54 (S4_LD, S4, LD_E);
  and and_55 (S5_LD, S5, LD_E);
  and and_56 (S4_ST, S4, ST_E);
  and and_57 (S5_ST, S5, ST_E);
  and C (C_out, _4, F4);
  and A (A_out, _5, F5);
  and E_2 (E_2_out, _6, F6);
  and Z (Z_out, _7, F7);
  and and_58 (IAR_IF_E, clk_e, BUS1_IF_E);
  and and_59 (RAM_IF_E, clk_e, S2_IF);
  and and_60 (ACC_IF_E, clk_e, S3_IF);
  and and_61 (IAR_DATA_E, clk_e, BUS1_DATA_E);
  and and_62 (RAM_DATA_E, clk_e, S5_DATA);
  and and_63 (ACC_DATA_E, clk_e, S6_DATA);
  or or_20 (UPDATE_IAR, C_out, A_out, E_2_out, Z_out);
  and and_64 (RB_JMPR_E, clk_e, S4_JMPR);
  and and_65 (IAR_JMP_E, clk_e, S4_JMP);
  and and_66 (RAM_JMP_E, clk_e, S5_JMP);
  and and_67 (ACC_IF_S, clk_s, BUS1_IF_E);
  and and_68 (MAR_IF_S, clk_s, BUS1_IF_E);
  and and_69 (IR_IF_S, clk_s, S2_IF);
  and and_70 (IAR_IF_S, clk_s, S3_IF);
  and and_71 (ACC_DATA_S, clk_s, BUS1_DATA_E);
  and and_72 (MAR_DATA_S, clk_s, BUS1_DATA_E);
  and and_73 (RB_DATA_S, clk_s, S5_DATA);
  and and_74 (IAR_DATA_S, clk_s, S6_DATA);
  and and_75 (IAR_JMPR_S, clk_s, S4_JMPR);
  and and_76 (MAR_JMP_S, clk_s, S4_JMP);
  and and_77 (IAR_JMP_S, clk_s, S5_JMP);
  and and_78 (BUS1_IF_E, S1, not_3_out);
  not not_3 (not_3_out, NOP_E);
  and and_79 (S2_IF, S2, not_4_out);
  not not_4 (not_4_out, NOP_E);
  and and_80 (S3_IF, S3, not_5_out);
  not not_5 (not_5_out, NOP_E);
  and and_81 (BUS1_DATA_E, S4, DATA_E);
  and and_82 (S5_DATA, S5, DATA_E);
  and and_83 (S6_DATA, S6, DATA_E);
  and and_84 (S4_JMPR, S4, JMPR_E);
  and and_85 (S4_JMP, S4, JMP_E);
  and and_86 (S5_JMP, S5, JMP_E);

  // Other names for the same wires on the sheet: FLAGS_ALU_S = ACC_ALU_S; IR_0 = _0; IR_1 = _1; IR_2 = _2; IR_3 = _3;
  //   IR_4 = _4; IR_5 = _5; IR_6 = _6; IR_7 = _7; MAR_JC_S = ACC_NJ_S; RA_ALU_E = CI_ALU_E; S1_IF = BUS1_IF_E;
  //   S4_DATA = BUS1_DATA_E; S4_JC = BUS1_JC_E

  // Notes on the sheet:
  //   IR_IN
  //   Stepper Module
  //   Non-ALU Instruction Condition
  //   IR Code Module
  //   JC Instructions Module
  //   Clear Flag Instruction Module
  //   ALU Instruction Module
  //   LOAD Instruction Module
  //   STORE Instruction Module
  //   Register Selection Module
  //   Clear Flag Instruction Condition
  //   JC  Instructions Condition
  //   ALU Instruction Condition
  //   LOAD Instruction Condition
  //   STORE Instruction Condition
  //   IAR Update Condition
  //   Instruction Fetch Module
  //   DATA
  //    Instruction Module
  //   JMPR Instruction Module
  //   JMP Instruction Module
  //   Instruction Fetch Condition
  //   DATA Instruction Condition
  //   JMPR Instruction Condition
  //   JMP Instruction Condition
endmodule

module CPU (
);

  wire alu_1_a_b, alu_1_a_b_2, alu_1_co, alu_1_zero, controlunit_1_acc_e, controlunit_1_acc_s,
       controlunit_1_bus1_e, controlunit_1_ci_e, controlunit_1_flags_s, controlunit_1_iar_e,
       controlunit_1_iar_s, controlunit_1_ir_s, controlunit_1_mar_s, controlunit_1_r0_e, controlunit_1_r0_s,
       controlunit_1_r1_e, controlunit_1_r1_s, controlunit_1_r2_e, controlunit_1_r2_s, controlunit_1_r3_e,
       controlunit_1_r3_s, controlunit_1_ram_e, controlunit_1_ram_s, controlunit_1_tmp_s, ctmp_1_o,
       flags_1_o_4, flags_1_o_5, flags_1_o_6, flags_1_o_7, ir_1__0, ir_1__1, ir_1__2, ir_1__3, ir_1__4,
       ir_1__5, ir_1__6, ir_1__7;
  wire [2:0] controlunit_1_op_out;
  wire [7:0] acc_1_o, alu_1_o, bus1_1_out_3, tmp_1_o;

  ALU alu_1 (
    .a_b_2(alu_1_a_b_2), .a_b(alu_1_a_b), .zero(alu_1_zero), .o(alu_1_o), .co(alu_1_co), .ci(ctmp_1_o),
    .op(controlunit_1_op_out), .a(acc_1_o), .b(bus1_1_out_3));
  TMP tmp_1 (.o(tmp_1_o), .set(controlunit_1_tmp_s), .i(acc_1_o));
  Bus1 bus1_1 (.out_3(bus1_1_out_3), .bus1_e(controlunit_1_bus1_e), .in_1(tmp_1_o));
  ACC acc_1 (.o(acc_1_o), .set(controlunit_1_acc_s), .i(alu_1_o), .en(controlunit_1_acc_e));
  CTMP ctmp_1 (.o(ctmp_1_o), .set(controlunit_1_tmp_s), .en(controlunit_1_ci_e), .i(flags_1_o_4));
  Flags flags_1 (
    .o_4(flags_1_o_4), .o_5(flags_1_o_5), .o_6(flags_1_o_6), .o_7(flags_1_o_7), .set(controlunit_1_flags_s),
    .i_4(alu_1_co), .i_5(alu_1_a_b), .i_6(alu_1_a_b_2), .i_7(alu_1_zero));
  R0 r0_1 (.o(acc_1_o), .set(controlunit_1_r0_s), .i(acc_1_o), .en(controlunit_1_r0_e));
  IAR iar_1 (.o(acc_1_o), .i(acc_1_o), .set(controlunit_1_iar_s), .en(controlunit_1_iar_e));
  R1 r1_1 (.o(acc_1_o), .set(controlunit_1_r1_s), .i(acc_1_o), .en(controlunit_1_r1_e));
  R2 r2_1 (.o(acc_1_o), .set(controlunit_1_r2_s), .i(acc_1_o), .en(controlunit_1_r2_e));
  ControlUnit controlunit_1 (
    .R0_E(controlunit_1_r0_e), .R1_E(controlunit_1_r1_e), .R2_E(controlunit_1_r2_e),
    .R3_E(controlunit_1_r3_e), .CI_E(controlunit_1_ci_e), .op_out(controlunit_1_op_out),
    .Bus1_E(controlunit_1_bus1_e), .IAR_E(controlunit_1_iar_e), .RAM_E(controlunit_1_ram_e),
    .ACC_E(controlunit_1_acc_e), .R0_S(controlunit_1_r0_s), .R1_S(controlunit_1_r1_s),
    .R2_S(controlunit_1_r2_s), .R3_S(controlunit_1_r3_s), .MAR_S(controlunit_1_mar_s),
    .IR_S(controlunit_1_ir_s), .IAR_S(controlunit_1_iar_s), .TMP_S(controlunit_1_tmp_s),
    .RAM_S(controlunit_1_ram_s), .FLAGS_S(controlunit_1_flags_s), .ACC_S(controlunit_1_acc_s),
    .F4(flags_1_o_4), .F5(flags_1_o_5), .F6(flags_1_o_6), .F7(flags_1_o_7), ._0(ir_1__0), ._1(ir_1__1),
    ._2(ir_1__2), ._3(ir_1__3), ._4(ir_1__4), ._5(ir_1__5), ._6(ir_1__6), ._7(ir_1__7));
  IR ir_1 (
    ._0(ir_1__0), ._1(ir_1__1), ._2(ir_1__2), ._3(ir_1__3), ._4(ir_1__4), ._5(ir_1__5), ._6(ir_1__6),
    ._7(ir_1__7), .i(acc_1_o), .set(controlunit_1_ir_s));
  R3 r3_1 (.o(acc_1_o), .set(controlunit_1_r3_s), .i(acc_1_o), .en(controlunit_1_r3_e));
  RAM ram_1 (
    .out_6(acc_1_o), .a(acc_1_o), .i(acc_1_o), .sa(controlunit_1_mar_s), .in_3(controlunit_1_ram_s),
    .e(controlunit_1_ram_e));
endmodule

module R0 (
  input  [7:0] i,
  input  set,
  input  en,
  output [7:0] o
);

  wire [7:0] register_1_q;

  Register #(.trigger("high")) register_1 (.D(i), .en(set), .Q(register_1_q), .clk(1'b1));  // open: clr
  Enabler enabler_1 (.out_3(o), .in_2(en), .in_1(register_1_q));
endmodule

module R1 (
  input  [7:0] i,
  input  set,
  input  en,
  output [7:0] o
);

  wire [7:0] register_1_q;

  Register #(.trigger("high")) register_1 (.D(i), .en(set), .Q(register_1_q), .clk(1'b1));  // open: clr
  Enabler enabler_1 (.out_3(o), .in_2(en), .in_1(register_1_q));
endmodule

module R2 (
  input  [7:0] i,
  input  set,
  input  en,
  output [7:0] o
);

  wire [7:0] register_1_q;

  Register #(.trigger("high")) register_1 (.D(i), .en(set), .Q(register_1_q), .clk(1'b1));  // open: clr
  Enabler enabler_1 (.out_3(o), .in_2(en), .in_1(register_1_q));
endmodule

module R3 (
  input  [7:0] i,
  input  set,
  input  en,
  output [7:0] o
);

  wire [7:0] register_1_q;

  Register #(.trigger("high")) register_1 (.D(i), .en(set), .Q(register_1_q), .clk(1'b1));  // open: clr
  Enabler enabler_1 (.out_3(o), .in_2(en), .in_1(register_1_q));
endmodule

module TMP (
  input  [7:0] i,
  input  set,
  output [7:0] o
);

  Register #(.trigger("high")) register_1 (.D(i), .en(set), .Q(o), .clk(1'b1));  // open: clr
endmodule

module ACC (
  input  [7:0] i,
  input  set,
  input  en,
  output [7:0] o
);

  wire [7:0] register_1_q;

  Register #(.trigger("high")) register_1 (.D(i), .en(set), .Q(register_1_q), .clk(1'b1));  // open: clr
  Enabler enabler_1 (.out_3(o), .in_2(en), .in_1(register_1_q));
endmodule

module IAR (
  input  [7:0] i,
  input  set,
  input  en,
  output [7:0] o
);

  wire [7:0] register_1_q;

  Register #(.trigger("high")) register_1 (.D(i), .en(set), .Q(register_1_q), .clk(1'b1));  // open: clr
  Enabler enabler_1 (.out_3(o), .in_2(en), .in_1(register_1_q));
endmodule

module Bus1 (
  input  [7:0] in_1,
  input  bus1_e,
  output [7:0] out_3
);

  wire not_1_out;

  not not_1 (not_1_out, bus1_e);
  assign out_3 = not_1_out ? in_1 : 8'bz;  // Controlled_Buffer controlled_buffer_1
  assign out_3 = bus1_e ? 8'h1 : 8'bz;  // Controlled_Buffer controlled_buffer_2
endmodule

module IR (
  input  [7:0] i,
  input  set,
  output _0,
  output _1,
  output _2,
  output _3,
  output _4,
  output _5,
  output _6,
  output _7
);

  Register #(.trigger("high")) register_1 (
    .D(i), .en(set), .Q({_0, _1, _2, _3, _4, _5, _6, _7}), .clk(1'b1));  // open: clr
endmodule

module Decoder_2x4 (
  input  a,
  input  b,
  output _01,
  output o2,
  output o3,
  output o4
);

  wire not_1_out, not_2_out;

  not not_1 (not_1_out, a);
  not not_2 (not_2_out, b);
  and and_1 (_01, not_1_out, not_2_out);
  and and_2 (o2, a, not_2_out);
  and and_3 (o3, not_1_out, b);
  and and_4 (o4, a, b);
endmodule

module Decoder_2x4_inverted (
  input  a,
  input  b,
  output _01,
  output o2,
  output o3,
  output o4
);

  wire not_1_out, not_2_out;

  not not_1 (not_1_out, a);
  not not_2 (not_2_out, b);
  and and_1 (_01, not_1_out, not_2_out);
  and and_2 (o2, a, not_2_out);
  and and_3 (o3, not_1_out, b);
  and and_4 (o4, a, b);
endmodule

module RAM (
  input  [7:0] a,
  input  sa,
  input  in_3,
  input  [7:0] i,
  input  e,
  output [7:0] out_6
);

  wire [7:0] controlled_buffer_1_out, mar_1_o, ram_1_dout;

  assign controlled_buffer_1_out = in_3 ? i : 8'bz;  // Controlled_Buffer controlled_buffer_1
  MAR mar_1 (.o(mar_1_o), .i(a), .set(sa));
  RAM_part #(.trigger("high"), .\type ("nonvolatile")) ram_1 (
    .addr(mar_1_o), .we(in_3), .clk(1'b1), .din(controlled_buffer_1_out), .dout(ram_1_dout));
  Hex_Digit_Display a1 (.value(mar_1_o[7:4]));  // open: dp
  Hex_Digit_Display a0 (.value(mar_1_o[3:0]));  // open: dp
  Hex_Digit_Display d1 (.value(ram_1_dout[7:4]));  // open: dp
  assign out_6 = e ? ram_1_dout : 8'bz;  // Controlled_Buffer controlled_buffer_2
  Hex_Digit_Display d0 (.value(ram_1_dout[3:0]));  // open: dp
endmodule

module MAR (
  input  [7:0] i,
  input  set,
  output [7:0] o
);

  Register #(.trigger("high")) register_1 (.D(i), .en(set), .Q(o), .clk(1'b1));  // open: clr
endmodule

module Flags (
  input  i_4,
  input  i_5,
  input  i_6,
  input  i_7,
  input  set,
  output o_4,
  output o_5,
  output o_6,
  output o_7
);

  wire [3:0] register_1_q;

  Register #(.trigger("high")) register_1 (
    .D({i_7, i_6, i_5, i_4, 4'b0000}), .en(set), .Q({o_7, o_6, o_5, o_4, register_1_q}), .clk(1'b1));  // open: clr
endmodule

module CTMP (
  input  i,
  input  set,
  input  en,
  output o
);

  wire register_1_q;

  Register #(.trigger("high"), .width(1)) register_1 (.D(i), .en(set), .Q(register_1_q), .clk(1'b1));  // open: clr
  and and_1 (o, register_1_q, en);
endmodule

module CPU_old (
);

  wire alu_1_a_b, alu_1_a_b_2, alu_1_co, alu_1_zero, controlunit_1_acc_e, controlunit_1_acc_s,
       controlunit_1_bus1_e, controlunit_1_ci_e, controlunit_1_flags_s, controlunit_1_iar_e,
       controlunit_1_iar_s, controlunit_1_ir_s, controlunit_1_mar_s, controlunit_1_r0_e, controlunit_1_r0_s,
       controlunit_1_r1_e, controlunit_1_r1_s, controlunit_1_r2_e, controlunit_1_r2_s, controlunit_1_r3_e,
       controlunit_1_r3_s, controlunit_1_ram_e, controlunit_1_ram_s, controlunit_1_tmp_s, flags_1_o_4,
       flags_1_o_5, flags_1_o_6, flags_1_o_7, ir_1__0, ir_1__1, ir_1__2, ir_1__3, ir_1__4, ir_1__5, ir_1__6,
       ir_1__7;
  wire [2:0] controlunit_1_op_out;
  wire [7:0] acc_1_o, alu_1_o, bus1_1_out_3, tmp_1_o;

  ALU alu_1 (
    .a_b_2(alu_1_a_b_2), .a_b(alu_1_a_b), .zero(alu_1_zero), .o(alu_1_o), .co(alu_1_co),
    .ci(controlunit_1_ci_e), .op(controlunit_1_op_out), .a(acc_1_o), .b(bus1_1_out_3));
  TMP tmp_1 (.o(tmp_1_o), .set(controlunit_1_tmp_s), .i(acc_1_o));
  Bus1 bus1_1 (.out_3(bus1_1_out_3), .bus1_e(controlunit_1_bus1_e), .in_1(tmp_1_o));
  ACC acc_1 (.o(acc_1_o), .set(controlunit_1_acc_s), .i(alu_1_o), .en(controlunit_1_acc_e));
  Flags flags_1 (
    .o_4(flags_1_o_4), .o_5(flags_1_o_5), .o_6(flags_1_o_6), .o_7(flags_1_o_7), .set(controlunit_1_flags_s),
    .i_4(alu_1_co), .i_5(alu_1_a_b), .i_6(alu_1_a_b_2), .i_7(alu_1_zero));
  R0 r0_1 (.o(acc_1_o), .set(controlunit_1_r0_s), .i(acc_1_o), .en(controlunit_1_r0_e));
  IAR iar_1 (.o(acc_1_o), .i(acc_1_o), .set(controlunit_1_iar_s), .en(controlunit_1_iar_e));
  R1 r1_1 (.o(acc_1_o), .set(controlunit_1_r1_s), .i(acc_1_o), .en(controlunit_1_r1_e));
  R2 r2_1 (.o(acc_1_o), .set(controlunit_1_r2_s), .i(acc_1_o), .en(controlunit_1_r2_e));
  ControlUnit controlunit_1 (
    .R0_E(controlunit_1_r0_e), .R1_E(controlunit_1_r1_e), .R2_E(controlunit_1_r2_e),
    .R3_E(controlunit_1_r3_e), .CI_E(controlunit_1_ci_e), .op_out(controlunit_1_op_out),
    .Bus1_E(controlunit_1_bus1_e), .IAR_E(controlunit_1_iar_e), .RAM_E(controlunit_1_ram_e),
    .ACC_E(controlunit_1_acc_e), .R0_S(controlunit_1_r0_s), .R1_S(controlunit_1_r1_s),
    .R2_S(controlunit_1_r2_s), .R3_S(controlunit_1_r3_s), .MAR_S(controlunit_1_mar_s),
    .IR_S(controlunit_1_ir_s), .IAR_S(controlunit_1_iar_s), .TMP_S(controlunit_1_tmp_s),
    .RAM_S(controlunit_1_ram_s), .FLAGS_S(controlunit_1_flags_s), .ACC_S(controlunit_1_acc_s),
    .F4(flags_1_o_4), .F5(flags_1_o_5), .F6(flags_1_o_6), .F7(flags_1_o_7), ._0(ir_1__0), ._1(ir_1__1),
    ._2(ir_1__2), ._3(ir_1__3), ._4(ir_1__4), ._5(ir_1__5), ._6(ir_1__6), ._7(ir_1__7));
  IR ir_1 (
    ._0(ir_1__0), ._1(ir_1__1), ._2(ir_1__2), ._3(ir_1__3), ._4(ir_1__4), ._5(ir_1__5), ._6(ir_1__6),
    ._7(ir_1__7), .i(acc_1_o), .set(controlunit_1_ir_s));
  R3 r3_1 (.o(acc_1_o), .set(controlunit_1_r3_s), .i(acc_1_o), .en(controlunit_1_r3_e));
  RAM ram_1 (
    .out_6(acc_1_o), .a(acc_1_o), .i(acc_1_o), .sa(controlunit_1_mar_s), .in_3(controlunit_1_ram_s),
    .e(controlunit_1_ram_e));
endmodule
