// Logisim project 32_framebuffer.circ as structural Verilog
module \프레임버퍼  (
  input  reset,
  input  wrt
);

  wire clk_out, xcnt_carry;
  wire [9:0] xcnt_q;
  wire [23:0] rgb_video_1_p6;

  Counter #(.max('h1f), .trigger("falling"), .width(5)) ycnt (
    .Q(xcnt_q[9:5]), .clk(xcnt_carry));  // open: load, D, count, carry, clr
  Counter #(.max('h1f), .width(5)) xcnt (
    .Q(xcnt_q[4:0]), .carry(xcnt_carry), .clk(clk_out));  // open: load, D, count, clr
  Clock clk (.out(clk_out));
  // RGB_Video #(.height(32), .scale(8), .width(32)) rgb_video_1: pin names not known; wires that end beside it: reset, clk_out, wrt, xcnt_q[4:0], xcnt_q[9:5], rgb_video_1_p6
  ROM #(.addrWidth(10), .dataWidth(24)) rom_1 (.addr(xcnt_q), .data(rgb_video_1_p6));

  // Notes on the sheet:
  //   contents of rom_1 (hex, n*v repeats v):
  //   compressed eJx1mEmSJLcORPc8Bdd/FcGZx+F4/yPoOZlZJX3rlsyaFWPC6Q4HEKv3Xoadqc3ibAyuv8XG4paW
  //   5v07bYwsW0twzz25TYo+cdRnrdnZvZfvXgvPn6Vtlrlbs7vP0oLdbnCrWa2XkixLLsWuyNGyc/dc
  //   H8vDqza78vB12zl7rcHO0VN9DUe5OvtdVi/V36OzcKudubcKlNhnc3aktmswO43Jy8ZoRfgeV95s
  //   k/Pv223yB0OsPjquZe8vPo5Men0AdG6huGp3AUP5wddmbqB9xkvwq/ZUohDV0gw3hNLtegkw2BX6
  //   rhzF4ViIM5V9o34vhi8U80W0wJDsbCw8kAC27Fg9ctQbwVRbV8lp2rJzjMMQS2jRjtDe3G2YLr/J
  //   puzdO7QkEbcgztvYweeE1rlH+JoLNjXfuTZS3Zlw93jKvIiClippbBANkdPFXxovmwy+UeN/ED32
  //   F8NZ9uVP5BQDORVup2MB0dPEe6vV5Wzrm0scF1Gz1XO0bO3lSdGgnsTO81TlzsNfEbDDX7swHYhe
  //   G6d/hU8wXwONwLTA5LLNM1QnAlD5q+AV9UGEFNN4FJmifsxBtHT0g8j9QPmQw77UIp3VOqWziT77
  //   Q4BEnfNKXlBChCrQAay2vFOwzZeUmiUBRiZznvpkZ0iS2R87ZhsFfM1NEEWSRTA7MMEX3RaNw23B
  //   rMAEX9FiYzrYP2rl1W96pLpVs2XjA2x+OTqIDFB+EEUlVxOUxMlGED3wHPdt6EdnChdyYqyGJYmc
  //   mie/0FyJqR4oadvuAOr1XMzJKheRIps68zZ7zdEgvN78KwDrNr7IVPkHWo4my5L3DMH0/nHewPSG
  //   zbDdEkyOuIUNaVLrbjnvS85rD6Jv5pgvOY5oqu27xdKks4cAibLEfnVWRFVHZ+0tPiUDlE5WAeXF
  //   z3hHQm64W/tCmXcZvLMOmCbjnuLF38EXWySkMNBns4gtAYwlvNUGdgsbDQPGgg3KxmJCBx9H3nXw
  //   +eEiTIcF2seWmWKIlqR/knIFOlDI2xL+0t9aCIl/FjyQK0lQUm4AIyAnnbULxQPltdqVHI2cNdcb
  //   fLMogrdxJ4/zQErJD9uKfNFWhO2dLTUGXw0mx5bogZXyDzAY0uLAd5YMPr+AuS0MpXcar51YFnfJ
  //   WhJ3DuuJTzCF/eTmdMVmH6LDkyfvqSYFtmTalEJWEFATJlI8aDvmJGCBfUF1gZCm5OYz+RdwxWRb
  //   oDCRCCF2B7cYCYj6G5eDuDe9mIBO8gu1kTvv9Wv8xaFkAiQGEMlWyD+ZDPz5551adI1btAXLsGTQ
  //   shMT/gj6RZjccUQbDo28P7tE3nJvVbFBDoYtbqCNmw06Wzekgobmi05O4kyL093mTOlpNg8tpjh2
  //   ifxzqEn0U40j2UgmAaWQJtjMiNq6ssLW1hUsYpuPkVFD2SWrfUefVHeVeddeJGIpaTqi7AVRVQTM
  //   eCWeFzDnog2Fq0kUCy3LEOiiTLXRAWxo8eDTb/MAmTp4AG49UWPNVUtjQ5r2RQ+EyQNDbUV03UBU
  //   g7GcAu2FBW3REgANosiRuwve2hEmtuZwzFNXXjKc/HvITaS6oOqDCKLwQ4utLECf4J0YI/GMV6oF
  //   JZ5OEsLRrj+iFXKY1hXlbYD5Lgl3Fw2QsxjTc9QVF3QtP7y1irizVLQrz/JYtRUetwxpj41fXQ+b
  //   i6Ihx0ioLbT0Hjht7MGpjUly4YZtTDOBq/xbx3uUb2LsRcrREl5m4f1RwaeLAZNR/unk1FG6iHTk
  //   mlNBgT2vk3eBrwoUP/ijGf5WMyTlynfFyuGPl6vQStCZri0g7ze8nrz1qHeY1MIOr/ChXptG6KQh
  //   se+A6VTylnpb6cIoGoPU2SovOK3pXa5l4anFx6JHXmoBSeCCmQ9/hwcZJbkJe0AxdxFH4YsItM9B
  //   exA53ZkEBQUepi++cfgD1pCulamRsgSwqiWxULrJHOlze9iMULcNJ3ugdgTM9FVFrzIkeWu1a07f
  //   aWbneia9sFt9RbsX7e8wQh5OVlXIkToR5gemvEYyjcdfPhikzn/xJ0RTGPIFpoZO2N1JZjXkREk5
  //   tSGSVduApwqYR7QUokeglZvlplrWQlpBXMwsXQvOJHyTOOnNJwWlLQomHSB901A/D5iuhf/+uxga
  //   nBWOFA+G5yJ6j38qi7QgS5nOvP7pr7+E45/fxOvfMjgkRcjQ0ZReaQG8ejeW6R8DnnINqZBAcDT8
  //   o+eAraPESRBFEVcjyYapokhvcoO4qm4mp1f9C2lmV1lEb8P/PpgoPggeQsAxPijMF1q+LvLhJVxC
  //   oFUUfFCke3RQmCMxL6VNBcxmkELkSrneRzenvagyk8pJGiA6IO9NSF6mF1+gkYHjglkRV7HpIetY
  //   8ITAcLIZPDJVHFRMHhn5tV8wIMPzrTSitHkuF+/XGafAfLhwN238heYOMyfBlvBmcfEck5AF6igK
  //   k0HDijtIXTxwnSPES4JHe6+6nfG7AIaRxBC+93RzmighiHqOZZBQLia1/ZHOi4b32c8vmKCuMBjC
  //   FxfSk2zw+c2fdmU27jVSbL6a9HTDm8ThAhpXdI1INfS4x73QxRW11/yt8cFTadzhl5Jq5NmSGUZH
  //   AYIZOXoMqE9uwf5WsZa8LDIoD+LDvUzHNBdB1QzCkqXSz/4vZtjoY8ruC+aTM6AwOqW4Pwizrv5w
  //   UfSHdn9hwxB73tJkYebdBwyOV2R9ZAIB8+IhQdJ7SG3Rv0oWBkB/WhYmeRMrJCTlDMWLJIO+k0FT
  //   YHLourYRnVqySG9lMYaFb+Nx/P9HT/hxMn95OcCseIAJwZKnZ52Gs5tp87YeTeVKu13ZdFhqx8Wl
  //   UoO2so7WMTRH1rPwqibQdPunQgNMpQuY4KMHVF1ik2hxY79aG9AFEzNkJMc/j5bOH1Q3GkDGlxzQ
  //   4WIeaJD4F3zvlVg/VVh5BSKdeolTzWJXSKqfyhbZfj+2r+wRzAGDp5+kY75idNQzZSF5pnKFNHg8
  //   aM9ki07FuB4aaROkUB9EFRzRL6eAB8QJMMTYgFmVLbil3H9cUheg00qa8bHFHLMpOQ9mmj/jS1d1
  //   7vLXnWZLqKJbEA9OqpuXjn5KLKDXhdn0AFfOIHDqEh3go7r7OA2q3HLuZPy7S7upp57xy1/lEcTn
  //   yKUi/h74Syq/Gg4DfojH4DngK/oDp+RORJvC5s4cIaUZuoxJF/VHfB9P+9g8R/W2CUMOE26LtD5y
  //   E2yZyZC14CE3b/dtn44XTpUkufa83Z6MDiiPOw9oyBNoVQLH6zQScfU4xQjMAw/SfISvggGqEoi4
  //   JVOaSYShIwpgQMKOa/SanUJGX+/HGOUv+GgalBbxVqxHWaZwodEcRU6V2I34jgazNKivJMcCX0W9
  //   hE+FY+kWtkder073dBlHwoEUBd0DcZCoSudUr0muhO66Ms4F5jn6A1yDnM9MqCQlnY8y7lWHxZ7p
  //   CJDXgtrtsDbzuArA+n9gX3zqAU5aPPKQ/M044VOVPVX3TFR+nVrKyaFUI6cOzGv4Ud+NPjRqnpvy
  //   HuVft8f3292QpELxKDfp4536QlRH+7suvnXKFkNTz4/qs5cUGQsocBR79cTqiMFHCR+a1VfpeZnd
  //   NmP9X/DRut1iGwRz3IxTX7hUkU43m+/g6C6+pLZWEp74xCnEQfz5m6JZ807QH9ISI+elv+vVmiad
  //   5rmlxMu+iJwAOTjKyb9O1ExiOcs8MDomLeGLF5hXs0/KIWFme3366rPtFg0dI///xV/20eftIoRW
  //   JYtuT3UsaBwct6M7XZPoCIPkYhjN4vP657rBH//kl40qnJ7bVLlHytqCohqg5gG5TWmi+NMTVyXX
  //   Fo34J+W8q5VS8EwmGI2lraoqGip8GsTJV9qsVJ/i6UzWWtP8FHPiVBhqovXD5dvvULY0Ij1aKkro  d0edoQnacq0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
endmodule
