// Logisim project 33_프레임버퍼 애니메이션.circ as structural Verilog: 1 circuit, main circuit framebufferAnime64x64
// 22
module framebufferAnime64x64 (
  input  reset,
  input  wrt
);

  wire clk_out, xcnt_carry, ycnt_carry;
  wire [7:0] zcnt_q;
  wire [11:0] xcnt_q;
  wire [23:0] rgb_video_1_p6;

  Counter zcnt (.Q(zcnt_q), .clk(ycnt_carry));  // open: load, D, count, carry, clr
  Counter #(.max('h3f), .trigger("falling"), .width(6)) ycnt (
    .Q(xcnt_q[11:6]), .carry(ycnt_carry), .clk(xcnt_carry));  // open: load, D, count, clr
  Counter #(.max('h3f), .width(6)) xcnt (
    .Q(xcnt_q[5:0]), .carry(xcnt_carry), .clk(clk_out));  // open: load, D, count, clr
  Clock clk (.out(clk_out));
  // RGB_Video #(.height(64), .scale(4), .width(64)) rgb_video_1: pin names not known; wires that end beside it: reset, clk_out, wrt, xcnt_q[5:0], xcnt_q[11:6], rgb_video_1_p6
  ROM #(.addrWidth(20), .dataWidth(24)) rom_1 (.addr({zcnt_q, xcnt_q}), .data(rgb_video_1_p6));
endmodule
