// Logisim project Matrix32_03_adding_assembly.circ as structural Verilog
module M (
  input  i,
  input  s,
  output o
);

  wire nand_1_out, nand_2_out, nand_4_out;

  nand nand_1 (nand_1_out, i, s);
  nand nand_2 (nand_2_out, nand_1_out, s);
  nand nand_3 (o, nand_1_out, nand_4_out);
  nand nand_4 (nand_4_out, o, nand_2_out);
endmodule

module M8 (
  input  in_1,
  input  [7:0] in_2,
  output [7:0] out_3
);

  M m_1 (.o(out_3[0]), .i(in_2[0]), .s(in_1));
  M m_2 (.o(out_3[1]), .i(in_2[1]), .s(in_1));
  M m_3 (.o(out_3[2]), .i(in_2[2]), .s(in_1));
  M m_4 (.o(out_3[3]), .i(in_2[3]), .s(in_1));
  M m_5 (.o(out_3[4]), .i(in_2[4]), .s(in_1));
  M m_6 (.o(out_3[5]), .i(in_2[5]), .s(in_1));
  M m_7 (.o(out_3[6]), .i(in_2[6]), .s(in_1));
  M m_8 (.o(out_3[7]), .i(in_2[7]), .s(in_1));
endmodule

module Enabler (
  input  [31:0] in_1,
  input  in_2,
  output [31:0] out_3
);

  assign out_3 = in_2 ? in_1 : 32'bz;  // Controlled_Buffer controlled_buffer_1
endmodule

module Decoder3x8 (
  input  in_1,
  input  in_2,
  input  in_3,
  output out_4,
  output out_5,
  output out_6,
  output out_7,
  output out_8,
  output out_9,
  output out_10,
  output out_11
);

  wire not_1_out, not_2_out, not_3_out;

  not not_1 (not_1_out, in_1);
  not not_2 (not_2_out, in_2);
  not not_3 (not_3_out, in_3);
  and and_1 (out_4, not_1_out, not_2_out, not_3_out);
  and and_2 (out_5, not_1_out, not_2_out, in_3);
  and and_3 (out_6, not_1_out, in_2, not_3_out);
  and and_4 (out_7, not_1_out, in_2, in_3);
  and and_5 (out_8, in_1, not_2_out, not_3_out);
  and and_6 (out_9, in_1, not_2_out, in_3);
  and and_7 (out_10, in_1, in_2, not_3_out);
  and and_8 (out_11, in_1, in_2, in_3);
endmodule

module ZEROer (
  input  [31:0] in,
  output out
);

  wire not_1_out, or_1_out;

  or or_1 (or_1_out, in[0], in[1], in[2], in[3], in[4], in[5], in[6], in[7], in[8], in[9], in[10], in[11], in[12], in[13], in[14], in[15], in[16], in[17], in[18], in[19], in[20], in[21], in[22], in[23], in[24], in[25], in[26], in[27], in[28], in[29], in[30], in[31]);
  not not_1 (not_1_out, or_1_out);
  not not_2 (out, not_1_out);
endmodule

module Clk (
  output clk,
  output clk_e,
  output clk_s
);

  wire clk_raw_out, j_k_ff_1_qn;

  Clock clk_raw (.out(clk_raw_out));
  J_K_Flip_Flop j_k_ff_1 (.J(1'b1), .clk(clk_raw_out), .K(1'b1), .Q(clk), .Qn(j_k_ff_1_qn));  // open: preset, reset
  nand nand_1 (clk_e, clk_raw_out, j_k_ff_1_qn);
  and and_1 (clk_s, clk_raw_out, clk);
endmodule

module Stepper (
  input  clk,
  input  reset,
  output _1,
  output _2,
  output _3,
  output _4,
  output _5,
  output _6,
  output _7
);

  wire d_ff_1_q, d_ff_2_q, d_ff_3_q, d_ff_4_q, d_ff_5_q, d_ff_6_q, d_ff_7_q, d_ff_8_q, d_ff_9_q, d_ff_10_q,
       d_ff_11_q, not_1_out, not_2_out, not_3_out, not_4_out, not_5_out, not_6_out, not_7_out, not_8_out,
       or_1_out, or_2_out;

  not not_1 (not_1_out, clk);
  not not_2 (not_2_out, _7);
  or or_1 (or_1_out, _7, clk);
  or or_2 (or_2_out, _7, not_1_out);
  D_Flip_Flop d_ff_1 (.clk(or_1_out), .D(not_2_out), .Q(d_ff_1_q), .reset(reset));  // open: Qn, preset
  or or_3 (_1, _7, not_3_out);
  not not_3 (not_3_out, d_ff_2_q);
  D_Flip_Flop d_ff_2 (.clk(or_2_out), .D(d_ff_1_q), .Q(d_ff_2_q), .reset(reset));  // open: Qn, preset
  and and_1 (_2, d_ff_2_q, not_4_out);
  not not_4 (not_4_out, d_ff_4_q);
  D_Flip_Flop d_ff_3 (.clk(or_1_out), .D(d_ff_2_q), .Q(d_ff_3_q), .reset(reset));  // open: Qn, preset
  D_Flip_Flop d_ff_4 (.clk(or_2_out), .D(d_ff_3_q), .Q(d_ff_4_q), .reset(reset));  // open: Qn, preset
  and and_2 (_3, d_ff_4_q, not_5_out);
  D_Flip_Flop d_ff_5 (.clk(or_1_out), .D(d_ff_4_q), .Q(d_ff_5_q), .reset(reset));  // open: Qn, preset
  not not_5 (not_5_out, d_ff_6_q);
  D_Flip_Flop d_ff_6 (.clk(or_2_out), .D(d_ff_5_q), .Q(d_ff_6_q), .reset(reset));  // open: Qn, preset
  and and_3 (_4, d_ff_6_q, not_6_out);
  D_Flip_Flop d_ff_7 (.clk(or_1_out), .D(d_ff_6_q), .Q(d_ff_7_q), .reset(reset));  // open: Qn, preset
  not not_6 (not_6_out, d_ff_8_q);
  D_Flip_Flop d_ff_8 (.clk(or_2_out), .D(d_ff_7_q), .Q(d_ff_8_q), .reset(reset));  // open: Qn, preset
  D_Flip_Flop d_ff_9 (.clk(or_1_out), .D(d_ff_8_q), .Q(d_ff_9_q), .reset(reset));  // open: Qn, preset
  and and_4 (_5, d_ff_8_q, not_7_out);
  not not_7 (not_7_out, d_ff_10_q);
  D_Flip_Flop d_ff_10 (.clk(or_2_out), .D(d_ff_9_q), .Q(d_ff_10_q), .reset(reset));  // open: Qn, preset
  and and_5 (_6, d_ff_10_q, not_8_out);
  not not_8 (not_8_out, _7);
  D_Flip_Flop d_ff_11 (.clk(or_1_out), .D(d_ff_10_q), .Q(d_ff_11_q), .reset(reset));  // open: Qn, preset
  D_Flip_Flop d_ff_12 (.clk(or_2_out), .D(d_ff_11_q), .Q(_7), .reset(reset));  // open: Qn, preset
endmodule

module ControlUnit (
  input  [31:0] IR_CODE,
  input  CLK_IN,
  input  F4,
  input  F5,
  input  F6,
  input  F7,
  output [3:0] RBbits,
  output BUS1_E,
  output ACC_E,
  output IOCLK_E,
  output MAR_S,
  output RA_S,
  output FLAGS_S,
  output PC_S,
  output RA_E,
  output IN_OUT,
  output [3:0] RAbits,
  output PC_E,
  output RB_S,
  output DATA_ADDR,
  output IR_S,
  output RB_E,
  output RAM_S,
  output TMP_S,
  output RAM_E,
  output CI_E,
  output ACC_S,
  output IOCLK_S,
  output [4:0] op_out
);

  wire A_out, and_1_out, and_8_out, C_out, comparator_1_eq, comparator_2_eq, E_out, END_INST, HLT, JA_E,
       JC_E, JE_E, JZ_E, NO_JC, not_1_out, not_2_out, OP_IN, RST_MCS, UPDATE_PC, UPDATE_RB, Z_out;
  wire [3:0] STEP;
  wire [7:2] Micro_code_ROM_data;

  ROM #(.addrWidth(12), .dataWidth(32)) Micro_code_ROM (
    .addr({IR_CODE[31:24], STEP}),
    .data({BUS1_E, MAR_S, PC_S, PC_E, IR_S, RAM_S, RAM_E, ACC_S, ACC_E, RA_S, RA_E, RB_S, RB_E, TMP_S, CI_E, IOCLK_S, IOCLK_E, FLAGS_S, IN_OUT, DATA_ADDR, JC_E, JA_E, JE_E, JZ_E, Micro_code_ROM_data, HLT, END_INST}));
  not not_1 (not_1_out, HLT);
  Counter #(.max('hf), .width(4)) counter_1 (
    .count(not_1_out), .Q(STEP), .clk(CLK_IN), .clr(RST_MCS));  // open: load, D, carry
  Comparator comparator_1 (.a(IR_CODE[31:24]), .b(8'h41), .eq(comparator_1_eq));  // open: gt, lt
  and and_1 (and_1_out, comparator_1_eq, NO_JC);
  Comparator #(.width(4)) comparator_2 (.a(STEP), .b(4'b0101), .eq(comparator_2_eq));  // open: gt, lt
  Comparator #(.width(4)) comparator_3 (.a(STEP), .b(4'b0100), .eq(OP_IN));  // open: gt, lt
  or or_1 (RST_MCS, and_1_out, END_INST);
  and and_2 (NO_JC, comparator_2_eq, not_2_out);
  not not_2 (not_2_out, UPDATE_PC);
  and and_3 (op_out[0], OP_IN, IR_CODE[31], IR_CODE[24]);
  and and_4 (op_out[1], OP_IN, IR_CODE[31], IR_CODE[25]);
  and and_5 (op_out[2], OP_IN, IR_CODE[31], IR_CODE[26]);
  and and_6 (op_out[3], OP_IN, IR_CODE[31], IR_CODE[27]);
  and and_7 (op_out[4], OP_IN, IR_CODE[31], IR_CODE[28]);
  and and_8 (and_8_out, IR_CODE[25], IR_CODE[26], IR_CODE[27], IR_CODE[28]);
  not not_3 (UPDATE_RB, and_8_out);
  and C (C_out, JC_E, F4);
  and A (A_out, JA_E, F5);
  and E (E_out, JE_E, F6);
  and Z (Z_out, JZ_E, F7);
  or or_2 (UPDATE_PC, C_out, A_out, E_out, Z_out);

  assign RAbits = IR_CODE[23:20];
  assign RBbits = IR_CODE[19:16];

  // Other names for the same wires on the sheet: DATA_CODE[15:0] = IR_CODE[15:0]; OPERAND_CODE[7:0] = IR_CODE[23:16];
  //   OPRB_00 = IR_CODE[16]; RB_bits[3:0] = IR_CODE[19:16]; OPRB_01 = IR_CODE[17]; OPRB_02 = IR_CODE[18];
  //   OPRB_03 = IR_CODE[19]; OPRA_00 = IR_CODE[20]; RA_bits[3:0] = IR_CODE[23:20]; OPRA_01 = IR_CODE[21];
  //   OPRA_02 = IR_CODE[22]; OPRA_03 = IR_CODE[23]; OP_00 = IR_CODE[24]; OP_CODE[7:0] = IR_CODE[31:24];
  //   OP_01 = IR_CODE[25]; OP_02 = IR_CODE[26]; OP_03 = IR_CODE[27]; OP_04 = IR_CODE[28]; OP_05 = IR_CODE[29];
  //   OP_06 = IR_CODE[30]; OP_07 = IR_CODE[31]

  // Notes on the sheet:
  //   contents of Micro_code_ROM (hex, n*v repeats v):
  //   compressed eJzt2EsOwiAQBuA9p2DtamZKIxzH2PufQYZXo/ZBjTFq/i4KYebrAGlC2okpXfZSWiGfO46kjOQU
  //   y5bpRHYqwqwLl0ceRa1hmmiRWqNF2IZNGSu1GryQOT9ppGqFFhfyTHjYXKc2rqe24dTZn2MMnPWm
  //   YnXxc3qQsgW6IR35MRBsGDR/6MrfXv9dGBoaGhoa+v06RXwd8fUU1xEcYtDQ0NDQ0N+orzlJRD+W
  //   TShm59gG+jj63TcM+mUthsf+Ggu/tg7MEBoaGhoaGhoaGhr6f/UNkCgxsA==
  //   Micro state Counter
  //   Control Signals
  //   OP Code bits
  //   IR Code bits
  //   OPERAND Code bits
  //   ALU OP OUT Module
  //   PC Update Condition
endmodule

module CPU (
  input  in_1
);

  wire arithmetic_logic_unit_1_a_b, arithmetic_logic_unit_1_a_b_2, arithmetic_logic_unit_1_co,
       arithmetic_logic_unit_1_zero, carry_temp_register_1_o, CLK, controlunit_1_acc_e, controlunit_1_acc_s,
       controlunit_1_bus1_e, controlunit_1_ci_e, controlunit_1_data_addr, controlunit_1_flags_s,
       controlunit_1_in_out, controlunit_1_ioclk_e, controlunit_1_ioclk_s, controlunit_1_ir_s,
       controlunit_1_mar_s, controlunit_1_pc_e, controlunit_1_pc_s, controlunit_1_ra_e, controlunit_1_ra_s,
       controlunit_1_ram_e, controlunit_1_ram_s, controlunit_1_rb_e, controlunit_1_rb_s, controlunit_1_tmp_s,
       flag_register_1_o_4, flag_register_1_o_5, flag_register_1_o_6, flag_register_1_o_7, rgb_video_1_p2,
       video_graphics_adaptor_1_p8, video_graphics_adaptor_1_p9, video_graphics_adaptor_1_p10;
  wire [3:0] controlunit_1_rabits, controlunit_1_rbbits;
  wire [4:0] controlunit_1_op_out;
  wire [31:0] accumulator_1_o, arithmetic_logic_unit_1_o, bus1_1_out_3, instruction_register_1_o,
       temp_register_1_o;

  Arithmetic_Logic_Unit arithmetic_logic_unit_1 (
    .o(arithmetic_logic_unit_1_o), .zero(arithmetic_logic_unit_1_zero), .co(arithmetic_logic_unit_1_co),
    .a_b(arithmetic_logic_unit_1_a_b), .a_b_2(arithmetic_logic_unit_1_a_b_2), .ci(carry_temp_register_1_o),
    .a(accumulator_1_o), .b(bus1_1_out_3), .op(controlunit_1_op_out));
  Accumulator accumulator_1 (
    .o(accumulator_1_o), .CLK(CLK), .set(controlunit_1_acc_s), .i(arithmetic_logic_unit_1_o),
    .en(controlunit_1_acc_e));
  Temp_Register temp_register_1 (.o(temp_register_1_o), .set(controlunit_1_tmp_s), .CLK(CLK), .i(accumulator_1_o));
  Bus1 bus1_1 (.out_3(bus1_1_out_3), .bus1_e(controlunit_1_bus1_e), .in_1(temp_register_1_o));
  Carry_Temp_Register carry_temp_register_1 (
    .o(carry_temp_register_1_o), .CLK(CLK), .set(controlunit_1_tmp_s), .en(controlunit_1_ci_e),
    .i(flag_register_1_o_4));
  Flag_Register flag_register_1 (
    .o_4(flag_register_1_o_4), .o_5(flag_register_1_o_5), .o_6(flag_register_1_o_6),
    .o_7(flag_register_1_o_7), .CLK(CLK), .set(controlunit_1_flags_s), .i_4(arithmetic_logic_unit_1_co),
    .i_5(arithmetic_logic_unit_1_a_b), .i_6(arithmetic_logic_unit_1_a_b_2), .i_7(arithmetic_logic_unit_1_zero));
  Clock MCLK (.out(CLK));
  Program_Counter program_counter_1 (
    .o(accumulator_1_o), .i(accumulator_1_o), .set(controlunit_1_pc_s), .CLK(CLK), .en(controlunit_1_pc_e));
  Register_Files register_files_1 (
    .o(accumulator_1_o), .RA_SEL(controlunit_1_rabits), .RB_SEL(controlunit_1_rbbits), .i(accumulator_1_o),
    .CLK(CLK), .AS(controlunit_1_ra_s), .BS(controlunit_1_rb_s), .BE(controlunit_1_rb_e),
    .AE(controlunit_1_ra_e));
  ControlUnit controlunit_1 (
    .RBbits(controlunit_1_rbbits), .RAbits(controlunit_1_rabits), .BUS1_E(controlunit_1_bus1_e),
    .MAR_S(controlunit_1_mar_s), .PC_S(controlunit_1_pc_s), .PC_E(controlunit_1_pc_e),
    .IR_S(controlunit_1_ir_s), .RAM_S(controlunit_1_ram_s), .RAM_E(controlunit_1_ram_e),
    .ACC_S(controlunit_1_acc_s), .ACC_E(controlunit_1_acc_e), .RA_S(controlunit_1_ra_s),
    .RA_E(controlunit_1_ra_e), .RB_S(controlunit_1_rb_s), .RB_E(controlunit_1_rb_e),
    .TMP_S(controlunit_1_tmp_s), .CI_E(controlunit_1_ci_e), .IOCLK_S(controlunit_1_ioclk_s),
    .IOCLK_E(controlunit_1_ioclk_e), .FLAGS_S(controlunit_1_flags_s), .IN_OUT(controlunit_1_in_out),
    .DATA_ADDR(controlunit_1_data_addr), .op_out(controlunit_1_op_out), .F4(flag_register_1_o_4),
    .F5(flag_register_1_o_5), .F6(flag_register_1_o_6), .F7(flag_register_1_o_7), .CLK_IN(CLK),
    .IR_CODE(instruction_register_1_o));
  Instruction_Register instruction_register_1 (
    .o(instruction_register_1_o), .i(accumulator_1_o), .set(controlunit_1_ir_s), .CLK(CLK));
  Random_Access_Memory random_access_memory_1 (
    .o(accumulator_1_o), .a(accumulator_1_o), .CLK(CLK), .i(accumulator_1_o), .sa(controlunit_1_mar_s),
    .sd(controlunit_1_ram_s), .e(controlunit_1_ram_e));
  // Video_Graphics_Adaptor video_graphics_adaptor_1: pin names not known; wires that end beside it: CLK, controlunit_1_in_out, controlunit_1_data_addr, controlunit_1_ioclk_s, controlunit_1_ioclk_e, accumulator_1_o, CLK, video_graphics_adaptor_1_p8, video_graphics_adaptor_1_p9, video_graphics_adaptor_1_p10
  // RGB_Video #(.height(256), .scale(1), .width(256)) rgb_video_1: pin names not known; wires that end beside it: in_1, rgb_video_1_p2, 1'b1, video_graphics_adaptor_1_p8, video_graphics_adaptor_1_p9, video_graphics_adaptor_1_p10
  Clock clock_1 (.out(rgb_video_1_p2));

  // Notes on the sheet:
  //   Monitor (256x256)
endmodule

module R0 (
  input  [31:0] i,
  input  set,
  input  en,
  output [31:0] o
);

  wire [31:0] register_1_q;

  Register #(.trigger("high"), .width(32)) register_1 (.D(i), .en(set), .Q(register_1_q), .clk(1'b1));  // open: clr
  Enabler enabler_1 (.out_3(o), .in_2(en), .in_1(register_1_q));
endmodule

module R1 (
  input  [31:0] i,
  input  set,
  input  en,
  output [31:0] o
);

  wire [31:0] register_1_q;

  Register #(.trigger("high"), .width(32)) register_1 (.D(i), .en(set), .Q(register_1_q), .clk(1'b1));  // open: clr
  Enabler enabler_1 (.out_3(o), .in_2(en), .in_1(register_1_q));
endmodule

module R2 (
  input  [31:0] i,
  input  set,
  input  en,
  output [31:0] o
);

  wire [31:0] register_1_q;

  Register #(.trigger("high"), .width(32)) register_1 (.D(i), .en(set), .Q(register_1_q), .clk(1'b1));  // open: clr
  Enabler enabler_1 (.out_3(o), .in_2(en), .in_1(register_1_q));
endmodule

module R3 (
  input  [31:0] i,
  input  set,
  input  en,
  output [31:0] o
);

  wire [31:0] register_1_q;

  Register #(.trigger("high"), .width(32)) register_1 (.D(i), .en(set), .Q(register_1_q), .clk(1'b1));  // open: clr
  Enabler enabler_1 (.out_3(o), .in_2(en), .in_1(register_1_q));
endmodule

module Bus1 (
  input  [31:0] in_1,
  input  bus1_e,
  output [31:0] out_3
);

  wire not_1_out;

  not not_1 (not_1_out, bus1_e);
  assign out_3 = not_1_out ? in_1 : 32'bz;  // Controlled_Buffer controlled_buffer_1
  assign out_3 = bus1_e ? 32'h1 : 32'bz;  // Controlled_Buffer controlled_buffer_2
endmodule

module Decoder_2x4 (
  input  a,
  input  b,
  output _01,
  output o2,
  output o3,
  output o4
);

  wire not_1_out, not_2_out;

  not not_1 (not_1_out, a);
  not not_2 (not_2_out, b);
  and and_1 (_01, not_1_out, not_2_out);
  and and_2 (o2, a, not_2_out);
  and and_3 (o3, not_1_out, b);
  and and_4 (o4, a, b);
endmodule

module Decoder_2x4_inverted (
  input  a,
  input  b,
  output _01,
  output o2,
  output o3,
  output o4
);

  wire not_1_out, not_2_out;

  not not_1 (not_1_out, a);
  not not_2 (not_2_out, b);
  and and_1 (_01, not_1_out, not_2_out);
  and and_2 (o2, a, not_2_out);
  and and_3 (o3, not_1_out, b);
  and and_4 (o4, a, b);
endmodule

module Flag_Register (
  input  i_4,
  input  i_5,
  input  i_6,
  input  i_7,
  input  CLK,
  input  set,
  output o_4,
  output o_5,
  output o_6,
  output o_7
);

  wire [3:0] register_1_q;

  Register register_1 (
    .D({i_7, i_6, i_5, i_4, 4'b0000}), .en(set), .Q({o_7, o_6, o_5, o_4, register_1_q}), .clk(CLK));  // open: clr
endmodule

module Carry_Temp_Register (
  input  i,
  input  CLK,
  input  set,
  input  en,
  output o
);

  wire register_1_q;

  Register #(.width(1)) register_1 (.D(i), .en(set), .Q(register_1_q), .clk(CLK));  // open: clr
  and and_1 (o, register_1_q, en);
endmodule

module IN_MAR16 (
  input  [15:0] i,
  input  set,
  output [15:0] o
);

  Register #(.trigger("high"), .width(16)) register_1 (.D(i), .en(set), .Q(o), .clk(1'b1));  // open: clr
endmodule

module OUT_MAR16 (
  input  [15:0] i,
  input  set,
  output [15:0] o
);

  Register #(.trigger("high"), .width(16)) register_1 (.D(i), .en(set), .Q(o), .clk(1'b1));  // open: clr
endmodule

module Memory_Address_Register (
  input  [23:0] i,
  input  set,
  input  in_3,
  output [23:0] o
);

  Register #(.trigger("high"), .width(24)) register_1 (.D(i), .en(set), .Q(o), .clk(in_3));  // open: clr
endmodule

module Random_Access_Memory (
  input  sa,
  input  [31:0] a,
  input  sd,
  input  CLK,
  input  [31:0] i,
  input  e,
  output [31:0] o
);

  wire [23:0] memory_address_register_1_o;
  wire [31:0] ram_1_dout;

  Memory_Address_Register memory_address_register_1 (
    .o(memory_address_register_1_o), .i(a[23:0]), .set(sa), .in_3(CLK));
  RAM #(.addrWidth(24), .dataWidth(32), .\type ("nonvolatile")) ram_1 (
    .addr(memory_address_register_1_o), .we(sd), .clk(CLK), .din(i), .dout(ram_1_dout));
  Hex_Digit_Display m5 (.value(memory_address_register_1_o[23:20]));  // open: dp
  Hex_Digit_Display m4 (.value(memory_address_register_1_o[19:16]));  // open: dp
  Hex_Digit_Display m3 (.value(memory_address_register_1_o[15:12]));  // open: dp
  Hex_Digit_Display m2 (.value(memory_address_register_1_o[11:8]));  // open: dp
  Hex_Digit_Display m1 (.value(memory_address_register_1_o[7:4]));  // open: dp
  Hex_Digit_Display m0 (.value(memory_address_register_1_o[3:0]));  // open: dp
  assign o = e ? ram_1_dout : 32'bz;  // Controlled_Buffer controlled_buffer_1
  Hex_Digit_Display d7 (.value(ram_1_dout[31:28]));  // open: dp
  Hex_Digit_Display d6 (.value(ram_1_dout[27:24]));  // open: dp
  Hex_Digit_Display d5 (.value(ram_1_dout[23:20]));  // open: dp
  Hex_Digit_Display d4 (.value(ram_1_dout[19:16]));  // open: dp
  Hex_Digit_Display d3 (.value(ram_1_dout[15:12]));  // open: dp
  Hex_Digit_Display d1 (.value(ram_1_dout[7:4]));  // open: dp
  Hex_Digit_Display d2 (.value(ram_1_dout[11:8]));  // open: dp
  Hex_Digit_Display d0 (.value(ram_1_dout[3:0]));  // open: dp
endmodule

module Video_Graphics_Adaptor (
  input  I_O,
  input  D_A,
  input  IO_clk_s,
  input  IO_clk_e,
  input  [31:0] fromBus,
  output [7:0] xpos,
  output [7:0] ypos,
  output wrt,
  output [15:0] color
);

  wire and_1_out, and_2_out, and_3_out, clk_out, not_1_out, x_counter_carry;
  wire [15:0] in_mar16_1_o, out_mar16_1_o, x_counter_q;

  not not_1 (not_1_out, D_A);
  and and_1 (and_1_out, I_O, D_A, IO_clk_s);
  and and_2 (and_2_out, I_O, not_1_out, IO_clk_s);
  not not_2 (wrt, I_O);
  assign {ypos, xpos} = I_O ? in_mar16_1_o : 16'bz;  // Controlled_Buffer controlled_buffer_1
  IN_MAR16 in_mar16_1 (.o(in_mar16_1_o), .i(fromBus[15:0]), .set(and_1_out));
  assign {ypos, xpos} = wrt ? out_mar16_1_o : 16'bz;  // Controlled_Buffer controlled_buffer_2
  RAM #(.addrWidth(16), .dataWidth(16), .trigger("high")) Video_RAM (
    .addr({ypos, xpos}), .we(I_O), .clk(and_2_out), .din(fromBus[15:0]), .dout(color));
  OUT_MAR16 out_mar16_1 (.o(out_mar16_1_o), .i(x_counter_q), .set(wrt));
  Clock #(.phaseOffset(1)) clk (.out(clk_out));
  Counter x_counter (.Q(x_counter_q[7:0]), .carry(x_counter_carry), .clk(and_3_out));  // open: load, D, count, clr
  and and_3 (and_3_out, wrt, clk_out);
  Counter #(.trigger("falling")) y_counter (
    .Q(x_counter_q[15:8]), .clk(x_counter_carry));  // open: load, D, count, carry, clr
endmodule

module Accumulator (
  input  [31:0] i,
  input  set,
  input  en,
  input  CLK,
  output [31:0] o
);

  wire [31:0] register_1_q;

  Register #(.width(32)) register_1 (.D(i), .en(set), .Q(register_1_q), .clk(CLK));  // open: clr
  Enabler enabler_1 (.out_3(o), .in_2(en), .in_1(register_1_q));
endmodule

module Program_Counter (
  input  [31:0] i,
  input  set,
  input  CLK,
  input  en,
  output [31:0] o
);

  wire [31:0] register_1_q;

  Register #(.width(32)) register_1 (.D(i), .en(set), .Q(register_1_q), .clk(CLK));  // open: clr
  Enabler enabler_1 (.out_3(o), .in_2(en), .in_1(register_1_q));
endmodule

module Instruction_Register (
  input  [31:0] i,
  input  set,
  input  CLK,
  output [31:0] o
);

  Register #(.width(32)) register_1 (.D(i), .en(set), .Q(o), .clk(CLK));  // open: clr
endmodule

module Temp_Register (
  input  [31:0] i,
  input  set,
  input  CLK,
  output [31:0] o
);

  Register #(.width(32)) register_1 (.D(i), .en(set), .Q(o), .clk(CLK));  // open: clr
endmodule

module Adder1 (
  input  a,
  input  b,
  input  ci,
  output sum,
  output co
);

  wire co1_out, co2_out, sum1_out;

  xor sum1 (sum1_out, a, b);
  xor sum2 (sum, sum1_out, ci);
  and co2 (co2_out, sum1_out, ci);
  and co1 (co1_out, a, b);
  or or_1 (co, co2_out, co1_out);
endmodule

module Adder8 (
  input  ci,
  input  [7:0] a,
  input  [7:0] b,
  output [7:0] o,
  output co
);

  wire adder1_1_co, adder1_2_co, adder1_3_co, adder1_4_co, adder1_5_co, adder1_6_co, adder1_7_co;

  Adder1 adder1_1 (.co(adder1_1_co), .sum(o[0]), .ci(ci), .a(a[0]), .b(b[0]));
  Adder1 adder1_2 (.co(adder1_2_co), .sum(o[1]), .ci(adder1_1_co), .a(a[1]), .b(b[1]));
  Adder1 adder1_3 (.co(adder1_3_co), .sum(o[2]), .ci(adder1_2_co), .a(a[2]), .b(b[2]));
  Adder1 adder1_4 (.co(adder1_4_co), .sum(o[3]), .ci(adder1_3_co), .a(a[3]), .b(b[3]));
  Adder1 adder1_5 (.co(adder1_5_co), .sum(o[4]), .ci(adder1_4_co), .a(a[4]), .b(b[4]));
  Adder1 adder1_6 (.co(adder1_6_co), .sum(o[5]), .ci(adder1_5_co), .a(a[5]), .b(b[5]));
  Adder1 adder1_7 (.co(adder1_7_co), .sum(o[6]), .ci(adder1_6_co), .a(a[6]), .b(b[6]));
  Adder1 adder1_8 (.co(co), .sum(o[7]), .ci(adder1_7_co), .a(a[7]), .b(b[7]));
endmodule

module Adder16 (
  input  ci,
  input  [15:0] a,
  input  [15:0] b,
  output [15:0] o,
  output co
);

  wire adder8_1_co;

  Adder8 adder8_1 (.co(adder8_1_co), .o(o[7:0]), .a(a[7:0]), .b(b[7:0]), .ci(ci));
  Adder8 adder8_2 (.co(co), .o(o[15:8]), .a(a[15:8]), .b(b[15:8]), .ci(adder8_1_co));
endmodule

module Adder (
  input  ci,
  input  [31:0] a,
  input  [31:0] b,
  output [31:0] o,
  output co
);

  wire adder16_1_co;

  Adder16 adder16_1 (.co(adder16_1_co), .o(o[15:0]), .a(a[15:0]), .b(b[15:0]), .ci(ci));
  Adder16 adder16_2 (.co(co), .o(o[31:16]), .a(a[31:16]), .b(b[31:16]), .ci(adder16_1_co));
endmodule

module XORer (
  input  [31:0] a,
  input  [31:0] b,
  output [31:0] o
);

  xor xor_1 (o[0], a[0], b[0]);
  xor xor_2 (o[1], a[1], b[1]);
  xor xor_3 (o[2], a[2], b[2]);
  xor xor_4 (o[3], a[3], b[3]);
  xor xor_5 (o[4], a[4], b[4]);
  xor xor_6 (o[5], a[5], b[5]);
  xor xor_7 (o[6], a[6], b[6]);
  xor xor_8 (o[7], a[7], b[7]);
  xor xor_9 (o[8], a[8], b[8]);
  xor xor_10 (o[9], a[9], b[9]);
  xor xor_11 (o[10], a[10], b[10]);
  xor xor_12 (o[11], a[11], b[11]);
  xor xor_13 (o[12], a[12], b[12]);
  xor xor_14 (o[13], a[13], b[13]);
  xor xor_15 (o[14], a[14], b[14]);
  xor xor_16 (o[15], a[15], b[15]);
  xor xor_17 (o[16], a[16], b[16]);
  xor xor_18 (o[17], a[17], b[17]);
  xor xor_19 (o[18], a[18], b[18]);
  xor xor_20 (o[19], a[19], b[19]);
  xor xor_21 (o[20], a[20], b[20]);
  xor xor_22 (o[21], a[21], b[21]);
  xor xor_23 (o[22], a[22], b[22]);
  xor xor_24 (o[23], a[23], b[23]);
  xor xor_25 (o[24], a[24], b[24]);
  xor xor_26 (o[25], a[25], b[25]);
  xor xor_27 (o[26], a[26], b[26]);
  xor xor_28 (o[27], a[27], b[27]);
  xor xor_29 (o[28], a[28], b[28]);
  xor xor_30 (o[29], a[29], b[29]);
  xor xor_31 (o[30], a[30], b[30]);
  xor xor_32 (o[31], a[31], b[31]);
endmodule

module XNORer (
  input  [31:0] a,
  input  [31:0] b,
  output [31:0] o
);

  xnor xnor_1 (o[0], a[0], b[0]);
  xnor xnor_2 (o[1], a[1], b[1]);
  xnor xnor_3 (o[2], a[2], b[2]);
  xnor xnor_4 (o[3], a[3], b[3]);
  xnor xnor_5 (o[4], a[4], b[4]);
  xnor xnor_6 (o[5], a[5], b[5]);
  xnor xnor_7 (o[6], a[6], b[6]);
  xnor xnor_8 (o[7], a[7], b[7]);
  xnor xnor_9 (o[8], a[8], b[8]);
  xnor xnor_10 (o[9], a[9], b[9]);
  xnor xnor_11 (o[10], a[10], b[10]);
  xnor xnor_12 (o[11], a[11], b[11]);
  xnor xnor_13 (o[12], a[12], b[12]);
  xnor xnor_14 (o[13], a[13], b[13]);
  xnor xnor_15 (o[14], a[14], b[14]);
  xnor xnor_16 (o[15], a[15], b[15]);
  xnor xnor_17 (o[16], a[16], b[16]);
  xnor xnor_18 (o[17], a[17], b[17]);
  xnor xnor_19 (o[18], a[18], b[18]);
  xnor xnor_20 (o[19], a[19], b[19]);
  xnor xnor_21 (o[20], a[20], b[20]);
  xnor xnor_22 (o[21], a[21], b[21]);
  xnor xnor_23 (o[22], a[22], b[22]);
  xnor xnor_24 (o[23], a[23], b[23]);
  xnor xnor_25 (o[24], a[24], b[24]);
  xnor xnor_26 (o[25], a[25], b[25]);
  xnor xnor_27 (o[26], a[26], b[26]);
  xnor xnor_28 (o[27], a[27], b[27]);
  xnor xnor_29 (o[28], a[28], b[28]);
  xnor xnor_30 (o[29], a[29], b[29]);
  xnor xnor_31 (o[30], a[30], b[30]);
  xnor xnor_32 (o[31], a[31], b[31]);
endmodule

module NORer (
  input  [31:0] a,
  input  [31:0] b,
  output [31:0] o
);

  nor nor_1 (o[0], a[0], b[0]);
  nor nor_2 (o[1], a[1], b[1]);
  nor nor_3 (o[2], a[2], b[2]);
  nor nor_4 (o[3], a[3], b[3]);
  nor nor_5 (o[4], a[4], b[4]);
  nor nor_6 (o[5], a[5], b[5]);
  nor nor_7 (o[6], a[6], b[6]);
  nor nor_8 (o[7], a[7], b[7]);
  nor nor_9 (o[8], a[8], b[8]);
  nor nor_10 (o[9], a[9], b[9]);
  nor nor_11 (o[10], a[10], b[10]);
  nor nor_12 (o[11], a[11], b[11]);
  nor nor_13 (o[12], a[12], b[12]);
  nor nor_14 (o[13], a[13], b[13]);
  nor nor_15 (o[14], a[14], b[14]);
  nor nor_16 (o[15], a[15], b[15]);
  nor nor_17 (o[16], a[16], b[16]);
  nor nor_18 (o[17], a[17], b[17]);
  nor nor_19 (o[18], a[18], b[18]);
  nor nor_20 (o[19], a[19], b[19]);
  nor nor_21 (o[20], a[20], b[20]);
  nor nor_22 (o[21], a[21], b[21]);
  nor nor_23 (o[22], a[22], b[22]);
  nor nor_24 (o[23], a[23], b[23]);
  nor nor_25 (o[24], a[24], b[24]);
  nor nor_26 (o[25], a[25], b[25]);
  nor nor_27 (o[26], a[26], b[26]);
  nor nor_28 (o[27], a[27], b[27]);
  nor nor_29 (o[28], a[28], b[28]);
  nor nor_30 (o[29], a[29], b[29]);
  nor nor_31 (o[30], a[30], b[30]);
  nor nor_32 (o[31], a[31], b[31]);
endmodule

module NANDer (
  input  [31:0] a,
  input  [31:0] b,
  output [31:0] o
);

  nand nand_1 (o[0], a[0], b[0]);
  nand nand_2 (o[1], a[1], b[1]);
  nand nand_3 (o[2], a[2], b[2]);
  nand nand_4 (o[3], a[3], b[3]);
  nand nand_5 (o[4], a[4], b[4]);
  nand nand_6 (o[5], a[5], b[5]);
  nand nand_7 (o[6], a[6], b[6]);
  nand nand_8 (o[7], a[7], b[7]);
  nand nand_9 (o[8], a[8], b[8]);
  nand nand_10 (o[9], a[9], b[9]);
  nand nand_11 (o[10], a[10], b[10]);
  nand nand_12 (o[11], a[11], b[11]);
  nand nand_13 (o[12], a[12], b[12]);
  nand nand_14 (o[13], a[13], b[13]);
  nand nand_15 (o[14], a[14], b[14]);
  nand nand_16 (o[15], a[15], b[15]);
  nand nand_17 (o[16], a[16], b[16]);
  nand nand_18 (o[17], a[17], b[17]);
  nand nand_19 (o[18], a[18], b[18]);
  nand nand_20 (o[19], a[19], b[19]);
  nand nand_21 (o[20], a[20], b[20]);
  nand nand_22 (o[21], a[21], b[21]);
  nand nand_23 (o[22], a[22], b[22]);
  nand nand_24 (o[23], a[23], b[23]);
  nand nand_25 (o[24], a[24], b[24]);
  nand nand_26 (o[25], a[25], b[25]);
  nand nand_27 (o[26], a[26], b[26]);
  nand nand_28 (o[27], a[27], b[27]);
  nand nand_29 (o[28], a[28], b[28]);
  nand nand_30 (o[29], a[29], b[29]);
  nand nand_31 (o[30], a[30], b[30]);
  nand nand_32 (o[31], a[31], b[31]);
endmodule

module ANDer (
  input  [31:0] a,
  input  [31:0] b,
  output [31:0] o
);

  and and_1 (o[0], a[0], b[0]);
  and and_2 (o[1], a[1], b[1]);
  and and_3 (o[2], a[2], b[2]);
  and and_4 (o[3], a[3], b[3]);
  and and_5 (o[4], a[4], b[4]);
  and and_6 (o[5], a[5], b[5]);
  and and_7 (o[6], a[6], b[6]);
  and and_8 (o[7], a[7], b[7]);
  and and_9 (o[8], a[8], b[8]);
  and and_10 (o[9], a[9], b[9]);
  and and_11 (o[10], a[10], b[10]);
  and and_12 (o[11], a[11], b[11]);
  and and_13 (o[12], a[12], b[12]);
  and and_14 (o[13], a[13], b[13]);
  and and_15 (o[14], a[14], b[14]);
  and and_16 (o[15], a[15], b[15]);
  and and_17 (o[16], a[16], b[16]);
  and and_18 (o[17], a[17], b[17]);
  and and_19 (o[18], a[18], b[18]);
  and and_20 (o[19], a[19], b[19]);
  and and_21 (o[20], a[20], b[20]);
  and and_22 (o[21], a[21], b[21]);
  and and_23 (o[22], a[22], b[22]);
  and and_24 (o[23], a[23], b[23]);
  and and_25 (o[24], a[24], b[24]);
  and and_26 (o[25], a[25], b[25]);
  and and_27 (o[26], a[26], b[26]);
  and and_28 (o[27], a[27], b[27]);
  and and_29 (o[28], a[28], b[28]);
  and and_30 (o[29], a[29], b[29]);
  and and_31 (o[30], a[30], b[30]);
  and and_32 (o[31], a[31], b[31]);
endmodule

module ORer (
  input  [31:0] a,
  input  [31:0] b,
  output [31:0] o
);

  or or_1 (o[0], a[0], b[0]);
  or or_2 (o[1], a[1], b[1]);
  or or_3 (o[2], a[2], b[2]);
  or or_4 (o[3], a[3], b[3]);
  or or_5 (o[4], a[4], b[4]);
  or or_6 (o[5], a[5], b[5]);
  or or_7 (o[6], a[6], b[6]);
  or or_8 (o[7], a[7], b[7]);
  or or_9 (o[8], a[8], b[8]);
  or or_10 (o[9], a[9], b[9]);
  or or_11 (o[10], a[10], b[10]);
  or or_12 (o[11], a[11], b[11]);
  or or_13 (o[12], a[12], b[12]);
  or or_14 (o[13], a[13], b[13]);
  or or_15 (o[14], a[14], b[14]);
  or or_16 (o[15], a[15], b[15]);
  or or_17 (o[16], a[16], b[16]);
  or or_18 (o[17], a[17], b[17]);
  or or_19 (o[18], a[18], b[18]);
  or or_20 (o[19], a[19], b[19]);
  or or_21 (o[20], a[20], b[20]);
  or or_22 (o[21], a[21], b[21]);
  or or_23 (o[22], a[22], b[22]);
  or or_24 (o[23], a[23], b[23]);
  or or_25 (o[24], a[24], b[24]);
  or or_26 (o[25], a[25], b[25]);
  or or_27 (o[26], a[26], b[26]);
  or or_28 (o[27], a[27], b[27]);
  or or_29 (o[28], a[28], b[28]);
  or or_30 (o[29], a[29], b[29]);
  or or_31 (o[30], a[30], b[30]);
  or or_32 (o[31], a[31], b[31]);
endmodule

module Inverter (
  input  [31:0] in_1,
  output [31:0] out_2
);

  assign out_2 = ~in_1;  // NOT_Gate not_1, 32 bits wide
endmodule

module low5_out (
  input  [4:0] i,
  output [31:0] o
);


  assign o = {{27{1'b0}}, i};
endmodule

module Negator (
  input  [31:0] in_1,
  output [31:0] out_2
);

  wire [31:0] inverter_1_out_2;

  Inverter inverter_1 (.out_2(inverter_1_out_2), .in_1(in_1));
  Adder adder_1 (.o(out_2), .a(inverter_1_out_2), .b(32'h1));  // open: co, ci
endmodule

module Subtractor (
  input  ci,
  input  [31:0] in_2,
  input  [31:0] in_3,
  output [31:0] out_4,
  output co
);

  wire [31:0] negator_1_out_2;

  Negator negator_1 (.out_2(negator_1_out_2), .in_1(in_3));
  Adder adder_1 (.co(co), .o(out_4), .a(in_2), .b(negator_1_out_2), .ci(ci));
endmodule

module low7_out (
  input  [6:0] i,
  output [31:0] o
);


  assign o = {{25{1'b0}}, i};
endmodule

module SHL (
  input  si,
  input  [31:0] i,
  output [31:0] o,
  output so
);

  wire [30:0] register_1_q;

  Register #(.trigger("high"), .width(32)) register_1 (
    .D(i), .en(1'b1), .Q({so, register_1_q}), .clk(1'b1));  // open: clr
  Register #(.trigger("high"), .width(32)) register_2 (
    .D({register_1_q, si}), .en(1'b1), .Q(o), .clk(1'b1));  // open: clr
endmodule

module SHR (
  input  [31:0] i,
  input  si,
  output so,
  output [31:0] o
);

  wire [31:1] register_1_q;

  Register #(.trigger("high"), .width(32)) register_1 (
    .D(i), .en(1'b1), .Q({register_1_q, so}), .clk(1'b1));  // open: clr
  Register #(.trigger("high"), .width(32)) register_2 (
    .D({si, register_1_q}), .en(1'b1), .Q(o), .clk(1'b1));  // open: clr
endmodule

module Arithmetic_Logic_Unit (
  input  [31:0] a,
  input  [31:0] b,
  input  ci,
  input  [4:0] op,
  output [31:0] o,
  output a_b,
  output zero,
  output a_b_2,
  output co
);

  wire adder_1_co, and_1_out, and_2_out, and_3_out, decoder_1_out0, decoder_1_out1, decoder_1_out2,
       decoder_1_out3, decoder_1_out4, decoder_1_out5, decoder_1_out6, decoder_1_out7, shl_1_so, shr_1_so;
  wire [31:0] adder_1_o, ander_1_o, inverter_1_out_2, orer_1_o, shl_1_o, shr_1_o, xorer_1_o;

  Comparator #(.width(32)) comparator_1 (.a(a), .b(b), .gt(a_b), .eq(a_b_2));  // open: lt
  XORer xorer_1 (.o(xorer_1_o), .b(b), .a(a));
  ORer orer_1 (.o(orer_1_o), .b(b), .a(a));
  ANDer ander_1 (.o(ander_1_o), .b(b), .a(a));
  Inverter inverter_1 (.out_2(inverter_1_out_2), .in_1(b));
  SHL shl_1 (.so(shl_1_so), .o(shl_1_o), .i(b), .si(ci));
  SHR shr_1 (.so(shr_1_so), .o(shr_1_o), .i(b), .si(ci));
  Adder adder_1 (.co(adder_1_co), .o(adder_1_o), .a(a), .b(b), .ci(ci));
  Decoder #(.enable("false"), .select(5)) decoder_1 (
    .out0(decoder_1_out0), .out1(decoder_1_out1), .out2(decoder_1_out2), .out3(decoder_1_out3),
    .out4(decoder_1_out4), .out5(decoder_1_out5), .out6(decoder_1_out6), .out7(decoder_1_out7), .sel(op));  // open: out8, out9, out10, out11, out12, out13, out14, out15, out16, out17, out18, out19, out20, out21, out22, out23, out24, out25, out26, out27, out28, out29, out30, out31
  and and_1 (and_1_out, shl_1_so, decoder_1_out2);
  and and_2 (and_2_out, shr_1_so, decoder_1_out1);
  and and_3 (and_3_out, adder_1_co, decoder_1_out0);
  Enabler enabler_1 (.out_3(o), .in_2(decoder_1_out6), .in_1(xorer_1_o));
  Enabler enabler_2 (.out_3(o), .in_2(decoder_1_out5), .in_1(orer_1_o));
  Enabler enabler_3 (.out_3(o), .in_2(decoder_1_out4), .in_1(ander_1_o));
  Enabler enabler_4 (.out_3(o), .in_2(decoder_1_out3), .in_1(inverter_1_out_2));
  Enabler enabler_5 (.out_3(o), .in_2(decoder_1_out2), .in_1(shl_1_o));
  Enabler enabler_6 (.out_3(o), .in_2(decoder_1_out1), .in_1(shr_1_o));
  Enabler enabler_7 (.out_3(o), .in_2(decoder_1_out0), .in_1(adder_1_o));
  assign o = decoder_1_out7 ? {32{1'b0}} : 32'bz;  // Controlled_Buffer controlled_buffer_1
  ZEROer zeroer_1 (.out(zero), .in(o));
  or or_1 (co, and_1_out, and_2_out, and_3_out);

  // Notes on the sheet:
  //   CMP
endmodule

module Register_Files (
  input  AS,
  input  AE,
  input  [31:0] i,
  input  [3:0] RA_SEL,
  input  BS,
  input  BE,
  input  [3:0] RB_SEL,
  input  CLK,
  output [31:0] o
);

  wire R00_A, R00_AE, R00_AS, R00_B, R00_BE, R00_BS, R00_E, R00_S, R01_A, R01_AE, R01_AS, R01_B, R01_BE,
       R01_BS, R01_E, R01_S, R02_A, R02_AE, R02_AS, R02_B, R02_BE, R02_BS, R02_E, R02_S, R03_A, R03_AE,
       R03_AS, R03_B, R03_BE, R03_BS, R03_E, R03_S, R04_A, R04_AE, R04_AS, R04_B, R04_BE, R04_BS, R04_E,
       R04_S, R05_A, R05_AE, R05_AS, R05_B, R05_BE, R05_BS, R05_E, R05_S, R06_A, R06_AE, R06_AS, R06_B,
       R06_BE, R06_BS, R06_E, R06_S, R07_A, R07_AE, R07_AS, R07_B, R07_BE, R07_BS, R07_E, R07_S, R08_A,
       R08_AE, R08_AS, R08_B, R08_BE, R08_BS, R08_E, R08_S, R09_A, R09_AE, R09_AS, R09_B, R09_BE, R09_BS,
       R09_E, R09_S, R10_A, R10_AE, R10_AS, R10_B, R10_BE, R10_BS, R10_E, R10_S, R11_A, R11_AE, R11_AS,
       R11_B, R11_BE, R11_BS, R11_E, R11_S, R12_A, R12_AE, R12_AS, R12_B, R12_BE, R12_BS, R12_E, R12_S,
       R13_A, R13_AE, R13_AS, R13_B, R13_BE, R13_BS, R13_E, R13_S, R14_A, R14_AE, R14_AS, R14_B, R14_BE,
       R14_BS, R14_E, R14_S, R15_A, R15_AE, R15_AS, R15_B, R15_BE, R15_BS, R15_E, R15_S;

  Decoder #(.enable("false"), .select(4)) decoder_1 (
    .out0(R00_A), .out1(R01_A), .out2(R02_A), .out3(R03_A), .out4(R04_A), .out5(R05_A), .out6(R06_A),
    .out7(R07_A), .out8(R08_A), .out9(R09_A), .out10(R10_A), .out11(R11_A), .out12(R12_A), .out13(R13_A),
    .out14(R14_A), .out15(R15_A), .sel(RA_SEL));
  Decoder #(.enable("false"), .select(4)) decoder_2 (
    .out0(R00_B), .out1(R01_B), .out2(R02_B), .out3(R03_B), .out4(R04_B), .out5(R05_B), .out6(R06_B),
    .out7(R07_B), .out8(R08_B), .out9(R09_B), .out10(R10_B), .out11(R11_B), .out12(R12_B), .out13(R13_B),
    .out14(R14_B), .out15(R15_B), .sel(RB_SEL));
  and and_1 (R00_AS, R00_A, AS);
  and and_2 (R01_AS, R01_A, AS);
  and and_3 (R02_AS, R02_A, AS);
  and and_4 (R03_AS, R03_A, AS);
  and and_5 (R04_AS, R04_A, AS);
  and and_6 (R05_AS, R05_A, AS);
  and and_7 (R06_AS, R06_A, AS);
  and and_8 (R07_AS, R07_A, AS);
  and and_9 (R08_AS, R08_A, AS);
  and and_10 (R09_AS, R09_A, AS);
  and and_11 (R10_AS, R10_A, AS);
  and and_12 (R11_AS, R11_A, AS);
  and and_13 (R12_AS, R12_A, AS);
  and and_14 (R13_AS, R13_A, AS);
  and and_15 (R14_AS, R14_A, AS);
  and and_16 (R15_AS, R15_A, AS);
  and and_17 (R00_BS, R00_B, BS);
  and and_18 (R01_BS, R01_B, BS);
  and and_19 (R02_BS, R02_B, BS);
  and and_20 (R03_BS, R03_B, BS);
  and and_21 (R04_BS, R04_B, BS);
  and and_22 (R05_BS, R05_B, BS);
  and and_23 (R06_BS, R06_B, BS);
  and and_24 (R07_BS, R07_B, BS);
  and and_25 (R08_BS, R08_B, BS);
  and and_26 (R09_BS, R09_B, BS);
  and and_27 (R10_BS, R10_B, BS);
  and and_28 (R11_BS, R11_B, BS);
  and and_29 (R12_BS, R12_B, BS);
  and and_30 (R13_BS, R13_B, BS);
  and and_31 (R14_BS, R14_B, BS);
  and and_32 (R15_BS, R15_B, BS);
  and and_33 (R00_AE, R00_A, AE);
  and and_34 (R01_AE, R01_A, AE);
  and and_35 (R02_AE, R02_A, AE);
  and and_36 (R03_AE, R03_A, AE);
  and and_37 (R04_AE, R04_A, AE);
  and and_38 (R05_AE, R05_A, AE);
  and and_39 (R06_AE, R06_A, AE);
  and and_40 (R07_AE, R07_A, AE);
  and and_41 (R08_AE, R08_A, AE);
  and and_42 (R09_AE, R09_A, AE);
  and and_43 (R10_AE, R10_A, AE);
  and and_44 (R11_AE, R11_A, AE);
  and and_45 (R12_AE, R12_A, AE);
  and and_46 (R13_AE, R13_A, AE);
  and and_47 (R14_AE, R14_A, AE);
  and and_48 (R15_AE, R15_A, AE);
  and and_49 (R00_BE, R00_B, BE);
  and and_50 (R01_BE, R01_B, BE);
  and and_51 (R02_BE, R02_B, BE);
  and and_52 (R03_BE, R03_B, BE);
  and and_53 (R04_BE, R04_B, BE);
  and and_54 (R05_BE, R05_B, BE);
  and and_55 (R06_BE, R06_B, BE);
  and and_56 (R07_BE, R07_B, BE);
  and and_57 (R08_BE, R08_B, BE);
  and and_58 (R09_BE, R09_B, BE);
  and and_59 (R10_BE, R10_B, BE);
  and and_60 (R11_BE, R11_B, BE);
  and and_61 (R12_BE, R12_B, BE);
  and and_62 (R13_BE, R13_B, BE);
  and and_63 (R14_BE, R14_B, BE);
  and and_64 (R15_BE, R15_B, BE);
  or or_1 (R00_S, R00_AS, R00_BS);
  or or_2 (R01_S, R01_AS, R01_BS);
  or or_3 (R02_S, R02_AS, R02_BS);
  or or_4 (R03_S, R03_AS, R03_BS);
  or or_5 (R04_S, R04_AS, R04_BS);
  or or_6 (R05_S, R05_AS, R05_BS);
  or or_7 (R06_S, R06_AS, R06_BS);
  or or_8 (R07_S, R07_AS, R07_BS);
  or or_9 (R08_S, R08_AS, R08_BS);
  or or_10 (R09_S, R09_AS, R09_BS);
  or or_11 (R10_S, R10_AS, R10_BS);
  or or_12 (R11_S, R11_AS, R11_BS);
  or or_13 (R12_S, R12_AS, R12_BS);
  or or_14 (R13_S, R13_AS, R13_BS);
  or or_15 (R14_S, R14_AS, R14_BS);
  or or_16 (R15_S, R15_AS, R15_BS);
  or or_17 (R00_E, R00_AE, R00_BE);
  or or_18 (R01_E, R01_AE, R01_BE);
  or or_19 (R02_E, R02_AE, R02_BE);
  or or_20 (R03_E, R03_AE, R03_BE);
  or or_21 (R04_E, R04_AE, R04_BE);
  or or_22 (R05_E, R05_AE, R05_BE);
  or or_23 (R06_E, R06_AE, R06_BE);
  or or_24 (R07_E, R07_AE, R07_BE);
  or or_25 (R08_E, R08_AE, R08_BE);
  or or_26 (R09_E, R09_AE, R09_BE);
  or or_27 (R10_E, R10_AE, R10_BE);
  or or_28 (R11_E, R11_AE, R11_BE);
  or or_29 (R12_E, R12_AE, R12_BE);
  or or_30 (R13_E, R13_AE, R13_BE);
  or or_31 (R14_E, R14_AE, R14_BE);
  or or_32 (R15_E, R15_AE, R15_BE);
  Register32 r00 (.o(o), .set(R00_S), .i(i), .CLK(CLK), .en(R00_E));
  Register32 r01 (.o(o), .set(R01_S), .i(i), .CLK(CLK), .en(R01_E));
  Register32 r02 (.o(o), .set(R02_S), .i(i), .CLK(CLK), .en(R02_E));
  Register32 r03 (.o(o), .set(R03_S), .i(i), .CLK(CLK), .en(R03_E));
  Register32 r04 (.o(o), .set(R04_S), .i(i), .CLK(CLK), .en(R04_E));
  Register32 r05 (.o(o), .set(R05_S), .i(i), .CLK(CLK), .en(R05_E));
  Register32 r06 (.o(o), .set(R06_S), .i(i), .CLK(CLK), .en(R06_E));
  Register32 r07 (.o(o), .set(R07_S), .i(i), .CLK(CLK), .en(R07_E));
  Register32 r08 (.o(o), .set(R08_S), .i(i), .CLK(CLK), .en(R08_E));
  Register32 r09 (.o(o), .set(R09_S), .i(i), .CLK(CLK), .en(R09_E));
  Register32 r10 (.o(o), .set(R10_S), .i(i), .CLK(CLK), .en(R10_E));
  Register32 r11 (.o(o), .set(R11_S), .i(i), .CLK(CLK), .en(R11_E));
  Register32 r12 (.o(o), .set(R12_S), .i(i), .CLK(CLK), .en(R12_E));
  Register32 r13 (.o(o), .set(R13_S), .i(i), .CLK(CLK), .en(R13_E));
  Register32 r14 (.o(o), .set(R14_S), .i(i), .CLK(CLK), .en(R14_E));
  Register32 r15 (.o(o), .set(R15_S), .i(i), .CLK(CLK), .en(R15_E));
endmodule

module Register32 (
  input  [31:0] i,
  input  set,
  input  en,
  input  CLK,
  output [31:0] o
);

  wire [31:0] register_1_q;

  Register #(.width(32)) register_1 (.D(i), .en(set), .Q(register_1_q), .clk(CLK));  // open: clr
  Enabler enabler_1 (.out_3(o), .in_2(en), .in_1(register_1_q));
endmodule
