// Logisim project 19_poem_print.circ as structural Verilog
module M (
  input  i,
  input  s,
  output o
);

  wire nand_1_out, nand_2_out, nand_4_out;

  nand nand_1 (nand_1_out, i, s);
  nand nand_2 (nand_2_out, nand_1_out, s);
  nand nand_3 (o, nand_1_out, nand_4_out);
  nand nand_4 (nand_4_out, o, nand_2_out);
endmodule

module M8 (
  input  in_1,
  input  [7:0] in_2,
  output [7:0] out_3
);

  M m_1 (.o(out_3[0]), .i(in_2[0]), .s(in_1));
  M m_2 (.o(out_3[1]), .i(in_2[1]), .s(in_1));
  M m_3 (.o(out_3[2]), .i(in_2[2]), .s(in_1));
  M m_4 (.o(out_3[3]), .i(in_2[3]), .s(in_1));
  M m_5 (.o(out_3[4]), .i(in_2[4]), .s(in_1));
  M m_6 (.o(out_3[5]), .i(in_2[5]), .s(in_1));
  M m_7 (.o(out_3[6]), .i(in_2[6]), .s(in_1));
  M m_8 (.o(out_3[7]), .i(in_2[7]), .s(in_1));
endmodule

module Enabler (
  input  [15:0] in_1,
  input  in_2,
  output [15:0] out_3
);

  assign out_3 = in_2 ? in_1 : 16'bz;  // Controlled_Buffer controlled_buffer_1
endmodule

module Decoder3x8 (
  input  in_1,
  input  in_2,
  input  in_3,
  output out_4,
  output out_5,
  output out_6,
  output out_7,
  output out_8,
  output out_9,
  output out_10,
  output out_11
);

  wire not_1_out, not_2_out, not_3_out;

  not not_1 (not_1_out, in_1);
  not not_2 (not_2_out, in_2);
  not not_3 (not_3_out, in_3);
  and and_1 (out_4, not_1_out, not_2_out, not_3_out);
  and and_2 (out_5, not_1_out, not_2_out, in_3);
  and and_3 (out_6, not_1_out, in_2, not_3_out);
  and and_4 (out_7, not_1_out, in_2, in_3);
  and and_5 (out_8, in_1, not_2_out, not_3_out);
  and and_6 (out_9, in_1, not_2_out, in_3);
  and and_7 (out_10, in_1, in_2, not_3_out);
  and and_8 (out_11, in_1, in_2, in_3);
endmodule

module ZEROer (
  input  [15:0] in,
  output out
);

  wire or_1_out;

  or or_1 (or_1_out, in[0], in[1], in[2], in[3], in[4], in[5], in[6], in[7], in[8], in[9], in[10], in[11], in[12], in[13], in[14], in[15]);
  not not_1 (out, or_1_out);
endmodule

module Clk (
  output clk,
  output clk_e,
  output clk_s
);

  wire clk_raw_out, j_k_ff_1_qn;

  Clock clk_raw (.out(clk_raw_out));
  J_K_Flip_Flop j_k_ff_1 (.J(1'b1), .clk(clk_raw_out), .K(1'b1), .Q(clk), .Qn(j_k_ff_1_qn));  // open: preset, reset
  nand nand_1 (clk_e, clk_raw_out, j_k_ff_1_qn);
  and and_1 (clk_s, clk_raw_out, clk);
endmodule

module Stepper (
  input  clk,
  input  reset,
  output _1,
  output _2,
  output _3,
  output _4,
  output _5,
  output _6,
  output _7
);

  wire d_ff_1_q, d_ff_2_q, d_ff_3_q, d_ff_4_q, d_ff_5_q, d_ff_6_q, d_ff_7_q, d_ff_8_q, d_ff_9_q, d_ff_10_q,
       d_ff_11_q, not_1_out, not_2_out, not_3_out, not_4_out, not_5_out, not_6_out, not_7_out, not_8_out,
       or_1_out, or_2_out;

  not not_1 (not_1_out, clk);
  not not_2 (not_2_out, _7);
  or or_1 (or_1_out, _7, clk);
  or or_2 (or_2_out, _7, not_1_out);
  D_Flip_Flop d_ff_1 (.clk(or_1_out), .D(not_2_out), .Q(d_ff_1_q), .reset(reset));  // open: Qn, preset
  or or_3 (_1, _7, not_3_out);
  not not_3 (not_3_out, d_ff_2_q);
  D_Flip_Flop d_ff_2 (.clk(or_2_out), .D(d_ff_1_q), .Q(d_ff_2_q), .reset(reset));  // open: Qn, preset
  and and_1 (_2, d_ff_2_q, not_4_out);
  not not_4 (not_4_out, d_ff_4_q);
  D_Flip_Flop d_ff_3 (.clk(or_1_out), .D(d_ff_2_q), .Q(d_ff_3_q), .reset(reset));  // open: Qn, preset
  D_Flip_Flop d_ff_4 (.clk(or_2_out), .D(d_ff_3_q), .Q(d_ff_4_q), .reset(reset));  // open: Qn, preset
  and and_2 (_3, d_ff_4_q, not_5_out);
  D_Flip_Flop d_ff_5 (.clk(or_1_out), .D(d_ff_4_q), .Q(d_ff_5_q), .reset(reset));  // open: Qn, preset
  not not_5 (not_5_out, d_ff_6_q);
  D_Flip_Flop d_ff_6 (.clk(or_2_out), .D(d_ff_5_q), .Q(d_ff_6_q), .reset(reset));  // open: Qn, preset
  and and_3 (_4, d_ff_6_q, not_6_out);
  D_Flip_Flop d_ff_7 (.clk(or_1_out), .D(d_ff_6_q), .Q(d_ff_7_q), .reset(reset));  // open: Qn, preset
  not not_6 (not_6_out, d_ff_8_q);
  D_Flip_Flop d_ff_8 (.clk(or_2_out), .D(d_ff_7_q), .Q(d_ff_8_q), .reset(reset));  // open: Qn, preset
  D_Flip_Flop d_ff_9 (.clk(or_1_out), .D(d_ff_8_q), .Q(d_ff_9_q), .reset(reset));  // open: Qn, preset
  and and_4 (_5, d_ff_8_q, not_7_out);
  not not_7 (not_7_out, d_ff_10_q);
  D_Flip_Flop d_ff_10 (.clk(or_2_out), .D(d_ff_9_q), .Q(d_ff_10_q), .reset(reset));  // open: Qn, preset
  and and_5 (_6, d_ff_10_q, not_8_out);
  not not_8 (not_8_out, _7);
  D_Flip_Flop d_ff_11 (.clk(or_1_out), .D(d_ff_10_q), .Q(d_ff_11_q), .reset(reset));  // open: Qn, preset
  D_Flip_Flop d_ff_12 (.clk(or_2_out), .D(d_ff_11_q), .Q(_7), .reset(reset));  // open: Qn, preset
endmodule

module ControlUnit (
  input  [15:0] IR_CODE,
  input  [7:0] FLAG_DATA,
  output MCLK,
  output PC_INC,
  output ACC_E,
  output PC_S,
  output RA_S,
  output MAR_S,
  output RA_E,
  output [3:0] RBbits,
  output PC_E,
  output RB_S,
  output IR_S,
  output RB_E,
  output RAM_S,
  output TMP_S,
  output RAM_E,
  output CI_E,
  output ACC_S,
  output [3:0] RAbits,
  output FLAG_S,
  output IR_E,
  output FLAG_CLR,
  output SP_INC,
  output SP_DEC,
  output SP_S,
  output SP_E,
  output TMP_C,
  output [3:0] IO,
  output [3:0] op_out
);

  wire A_2_out, A_out, and_5_out, and_6_out, and_7_out, and_8_out, and_9_out, and_10_out, and_12_out, BR_ON,
       BRN_ON, C_2_out, C_out, comparator_1_gt, comparator_2_lt, comparator_3_eq, comparator_4_gt,
       comparator_5_lt, comparator_6_gt, comparator_7_lt, E_2_out, E_out, END_INST, HLT_E, not_1_out,
       not_3_out, not_4_out, not_5_out, not_6_out, not_7_out, not_8_out, or_1_out, or_3_out, RST_MCS, TEST_A,
       TEST_C, TEST_E, TEST_Z, UPDATE_RB, Z_2_out, Z_out;
  wire [3:0] STEP;
  wire [12:0] Micro_code_ROM_p1;
  wire [30:0] Micro_code_ROM_p2;

  LED u_pc_inc (.in(PC_INC));
  LED u_pc_s (.in(PC_S));
  LED u_mar_s (.in(MAR_S));
  LED u_pc_e (.in(PC_E));
  LED u_ir_s (.in(IR_S));
  LED u_flag_s (.in(FLAG_S));
  LED u_ir_e (.in(IR_E));
  LED u_flag_clr (.in(FLAG_CLR));
  LED u_ram_s (.in(RAM_S));
  LED u_ram_e (.in(RAM_E));
  LED u_acc_s (.in(ACC_S));
  LED i_o (.in(IO[0]));
  LED d_a (.in(IO[1]));
  LED ioclk_s (.in(IO[2]));
  LED ioclk_e (.in(IO[3]));
  LED plus_sp (.in(SP_INC));
  LED minus_sp (.in(SP_DEC));
  LED u_sp_s (.in(SP_S));
  LED u_sp_e (.in(SP_E));
  // ROM #(.addrWidth(13), .dataWidth(32), .line("dual")) Micro_code_ROM: pin names not known; wires that end beside it: Micro_code_ROM_p1, {TMP_C, Micro_code_ROM_p2}, {PC_INC, PC_S, PC_E, MAR_S, IR_S, RAM_S, RAM_E, ACC_S, ACC_E, RA_S, RA_E, RB_S, RB_E, TMP_S, CI_E, IO[2], IO[3], FLAG_S, FLAG_CLR, IO[0], IO[1], TEST_C, TEST_A, TEST_E, TEST_Z, IR_E, SP_INC, SP_DEC, SP_S, SP_E, HLT_E, END_INST}
  Multiplier #(.width(13)) multiplier_1 (
    .a({1'b0, IR_CODE[15:8], STEP}), .b(13'h2), .out(Micro_code_ROM_p1));  // open: cin, cout
  Counter #(.max('hf), .width(4)) counter_1 (
    .count(not_1_out), .Q(STEP), .clk(MCLK), .clr(RST_MCS));  // open: load, D, carry
  not not_1 (not_1_out, HLT_E);
  Clock u_MCLK (.out(MCLK));
  LED u_acc_e (.in(ACC_E));
  LED u_tmp_c (.in(TMP_C));
  LED u_ra_s (.in(RA_S));
  LED u_ra_e (.in(RA_E));
  LED u_rb_s (.in(RB_S));
  LED u_rb_e (.in(RB_E));
  LED u_tmp_s (.in(TMP_S));
  LED u_ci_e (.in(CI_E));
  and and_1 (op_out[0], CI_E, and_5_out, IR_CODE[8]);
  and and_2 (op_out[1], CI_E, and_5_out, IR_CODE[9]);
  and and_3 (op_out[2], CI_E, and_5_out, IR_CODE[10]);
  and and_4 (op_out[3], CI_E, and_5_out, IR_CODE[11]);
  and and_5 (and_5_out, IR_CODE[15], IR_CODE[14]);
  and and_6 (and_6_out, IR_CODE[9], IR_CODE[10], IR_CODE[11]);
  not not_2 (UPDATE_RB, and_6_out);
  and C (C_out, TEST_C, FLAG_DATA[3]);
  and A (A_out, TEST_A, FLAG_DATA[2]);
  and E (E_out, TEST_E, FLAG_DATA[1]);
  and Z (Z_out, TEST_Z, FLAG_DATA[0]);
  Comparator comparator_1 (.a(IR_CODE[15:8]), .b(8'h40), .gt(comparator_1_gt));  // open: eq, lt
  Comparator comparator_2 (.a(IR_CODE[15:8]), .b(8'h50), .lt(comparator_2_lt));  // open: gt, eq
  and and_7 (and_7_out, comparator_1_gt, comparator_2_lt);
  Comparator #(.width(4)) comparator_3 (.a(STEP), .b(4'b0100), .eq(comparator_3_eq));  // open: gt, lt
  not not_3 (not_3_out, BR_ON);
  not not_4 (not_4_out, BRN_ON);
  Comparator comparator_4 (.a(IR_CODE[15:8]), .b(8'h40), .gt(comparator_4_gt));  // open: eq, lt
  Comparator comparator_5 (.a(IR_CODE[15:8]), .b(8'h47), .lt(comparator_5_lt));  // open: gt, eq
  or or_1 (or_1_out, C_out, A_out, E_out, Z_out);
  and and_8 (and_8_out, not_3_out, not_4_out);
  and and_9 (and_9_out, comparator_4_gt, comparator_5_lt);
  and and_10 (and_10_out, and_7_out, comparator_3_eq, and_8_out);
  and and_11 (BR_ON, and_9_out, or_1_out);
  or or_2 (RST_MCS, and_10_out, END_INST);
  not not_5 (not_5_out, FLAG_DATA[3]);
  not not_6 (not_6_out, FLAG_DATA[2]);
  not not_7 (not_7_out, FLAG_DATA[1]);
  not not_8 (not_8_out, FLAG_DATA[0]);
  and C_2 (C_2_out, TEST_C, not_5_out);
  and A_2 (A_2_out, TEST_A, not_6_out);
  and E_2 (E_2_out, TEST_E, not_7_out);
  and Z_2 (Z_2_out, TEST_Z, not_8_out);
  Comparator comparator_6 (.a(IR_CODE[15:8]), .b(8'h47), .gt(comparator_6_gt));  // open: eq, lt
  Comparator comparator_7 (.a(IR_CODE[15:8]), .b(8'h50), .lt(comparator_7_lt));  // open: gt, eq
  and and_12 (and_12_out, comparator_6_gt, comparator_7_lt);
  or or_3 (or_3_out, C_2_out, A_2_out, E_2_out, Z_2_out);
  and and_13 (BRN_ON, and_12_out, or_3_out);

  assign RAbits = IR_CODE[7:4];
  assign RBbits = IR_CODE[3:0];

  // Other names for the same wires on the sheet: DATA_ADDR = IO[1]; IN_OUT = IO[0]; IOCLK_E = IO[3]; IOCLK_S = IO[2];
  //   FZ = FLAG_DATA[0]; FE = FLAG_DATA[1]; FA = FLAG_DATA[2]; FC = FLAG_DATA[3]; OPERAND_CODE[7:0] = IR_CODE[7:0];
  //   OPRB_00 = IR_CODE[0]; RB_bits[3:0] = IR_CODE[3:0]; OPRB_01 = IR_CODE[1]; OPRB_02 = IR_CODE[2];
  //   OPRB_03 = IR_CODE[3]; OPRA_00 = IR_CODE[4]; RA_bits[3:0] = IR_CODE[7:4]; OPRA_01 = IR_CODE[5];
  //   OPRA_02 = IR_CODE[6]; OPRA_03 = IR_CODE[7]; OP_00 = IR_CODE[8]; OP_CODE[7:0] = IR_CODE[15:8];
  //   OP_01 = IR_CODE[9]; OP_02 = IR_CODE[10]; OP_03 = IR_CODE[11]; OP_04 = IR_CODE[12]; OP_05 = IR_CODE[13];
  //   OP_06 = IR_CODE[14]; OP_07 = IR_CODE[15]

  // Notes on the sheet:
  //   Control Signals
  //   contents of Micro_code_ROM (hex, n*v repeats v):
  //   compressed eJztWEtywyAM3XMK1llJCp3g42Ry/zvURiiAh98krU1asokG6+nzJAQ26CvwT4O2dy/ScoHcA1V6
  //   cAhixfAfKvo6MY6JOAUhq1sD6FIDqHSVMIJcI4hK+iqBOMlym12LrciGwayiAQuAm8mdkzxi1XNh
  //   USasX9s5CCSi56QVbsTUQrADc+RYILQv8vcQSUquAjIa2inpkJJKwGlK42+J/4vYyhbXrWscmNDH
  //   lXFwRPdWdqpbNazuRQndtDaeXyW2GUSHJtnzhR4XNAbfGNDY6XstivhmkUm3Dd8/OhmEQp2lsIsE
  //   CiSkFHaRgMF3SmGXbyYrQ+H5U3cixkJYUY6uI/6IDtuQ2y5SME8F5BkamsxfY7B8iNLOWjpUZ3NO
  //   RMchx32nakc3a9m21oIdphZsWhqTq4k4BXG7/LnXAVpXthxJ021EyidiIibipeP04XWR3N0uXAsX
  //   0ai+szxEKQ9XjZcWhLthtdhd6bPWU1+X9Y+m9m0Kzi3AB3t/pak7P0SwPQIjUfg2zcWH5e9MVWNZ
  //   rkrGhh0fsXozxe2JKqaY5UtVjaV8fUYlx+XsmDIPfM2diIk4CvENqVC/Pg==
  //   Micro state Counter
  //   ALU OP OUT Module
  //   IR Code bits
  //   OPERAND Code bits
  //   Branch If
  //   Step reset and Next Instruction
  //   OP Code bits
  //   Branch If Not
endmodule

module CPU (
  input  CAP,
  input  SH,
  input  in_3,
  input  CTR,
  input  ALT
);

  wire _0, _1, _2, _3, _4, _5, _6, _7, _8, _9, A, B, BS, C, controlunit_1_acc_e, controlunit_1_acc_s,
       controlunit_1_ci_e, controlunit_1_flag_clr, controlunit_1_flag_s, controlunit_1_ir_e,
       controlunit_1_ir_s, controlunit_1_mar_s, controlunit_1_mclk, controlunit_1_pc_e, controlunit_1_pc_inc,
       controlunit_1_pc_s, controlunit_1_ra_e, controlunit_1_ra_s, controlunit_1_ram_e, controlunit_1_ram_s,
       controlunit_1_rb_e, controlunit_1_rb_s, controlunit_1_sp_dec, controlunit_1_sp_e,
       controlunit_1_sp_inc, controlunit_1_sp_s, controlunit_1_tmp_c, controlunit_1_tmp_s, D, DL, E, EN, ES,
       F, F1, F2, F3, F4, F5, F6, F7, F8, F9, FA, FB, FC, flag_register_1_ct_o, G, H, I, J, K, L, M, N,
       not_1_out, O, P, Q, R, rgb_video_1_p3, S, SP, T, TB, tunnel, tunnel_t, tunnel_t_t, tunnel_t_t_t,
       tunnel_t_t_t_t, tunnel_t_t_t_t_t, tunnel_t_t_t_t_t_t, tunnel_t_t_t_t_t_t_t, tunnel_t_t_t_t_t_t_t_t,
       tunnel_t_t_t_t_t_t_t_t_t, tunnel_t_t_t_t_t_t_t_t_t_t, tunnel_t_t_t_t_t_t_t_t_t_t_t,
       tunnel_t_t_t_t_t_t_t_t_t_t_t_t, tunnel_t_t_t_t_t_t_t_t_t_t_t_t_t, tunnel_t_t_t_t_t_t_t_t_t_t_t_t_t_t,
       tunnel_t_t_t_t_t_t_t_t_t_t_t_t_t_t_t, tunnel_t_t_t_t_t_t_t_t_t_t_t_t_t_t_t_t,
       tunnel_t_t_t_t_t_t_t_t_t_t_t_t_t_t_t_t_t, tunnel_t_t_t_t_t_t_t_t_t_t_t_t_t_t_t_t_t_t,
       tunnel_t_t_t_t_t_t_t_t_t_t_t_t_t_t_t_t_t_t_t, tunnel_t_t_t_t_t_t_t_t_t_t_t_t_t_t_t_t_t_t_t_t,
       tunnel_t_t_t_t_t_t_t_t_t_t_t_t_t_t_t_t_t_t_t_t_t, tunnel_t_t_t_t_t_t_t_t_t_t_t_t_t_t_t_t_t_t_t_t_t_t,
       tunnel_t_t_t_t_t_t_t_t_t_t_t_t_t_t_t_t_t_t_t_t_t_t_t,
       tunnel_t_t_t_t_t_t_t_t_t_t_t_t_t_t_t_t_t_t_t_t_t_t_t_t,
       tunnel_t_t_t_t_t_t_t_t_t_t_t_t_t_t_t_t_t_t_t_t_t_t_t_t_t,
       tunnel_t_t_t_t_t_t_t_t_t_t_t_t_t_t_t_t_t_t_t_t_t_t_t_t_t_t,
       tunnel_t_t_t_t_t_t_t_t_t_t_t_t_t_t_t_t_t_t_t_t_t_t_t_t_t_t_t,
       tunnel_t_t_t_t_t_t_t_t_t_t_t_t_t_t_t_t_t_t_t_t_t_t_t_t_t_t_t_t,
       tunnel_t_t_t_t_t_t_t_t_t_t_t_t_t_t_t_t_t_t_t_t_t_t_t_t_t_t_t_t_t,
       tunnel_t_t_t_t_t_t_t_t_t_t_t_t_t_t_t_t_t_t_t_t_t_t_t_t_t_t_t_t_t_t,
       tunnel_t_t_t_t_t_t_t_t_t_t_t_t_t_t_t_t_t_t_t_t_t_t_t_t_t_t_t_t_t_t_t, U, V, W, X, Y, Z;
  wire [3:0] arithmetic_logic_unit_1_f0, controlunit_1_io, controlunit_1_op_out, controlunit_1_rabits,
       controlunit_1_rbbits;
  wire [7:0] ascii_in, controlled_buffer_21_out, controlled_buffer_29_out, flag_register_1_f_o,
       video_graphics_adaptor_1_px, video_graphics_adaptor_1_py;
  wire [15:0] arithmetic_logic_unit_1_o, instruction_register_1_o, stack_pointer_1_o, temp_register_1_o,
       video_graphics_adaptor_1_color;

  Flag_Register flag_register_1 (
    .F_O(flag_register_1_f_o), .CT_O(flag_register_1_ct_o), .F_I(arithmetic_logic_unit_1_f0),
    .CLK(controlunit_1_mclk), .DATA_S(controlunit_1_flag_s), .CLR_S(controlunit_1_flag_clr),
    .CT_S(controlunit_1_tmp_s), .CT_E(controlunit_1_ci_e));
  Arithmetic_Logic_Unit arithmetic_logic_unit_1 (
    .o(arithmetic_logic_unit_1_o), .f0(arithmetic_logic_unit_1_f0), .ci(flag_register_1_ct_o),
    .a(stack_pointer_1_o), .b(temp_register_1_o), .op(controlunit_1_op_out));
  Temp_Register temp_register_1 (
    .o(temp_register_1_o), .set(controlunit_1_tmp_s), .CLK(controlunit_1_mclk), .rst(controlunit_1_tmp_c),
    .i(stack_pointer_1_o));
  Stack_Pointer stack_pointer_1 (
    .o(stack_pointer_1_o), .sp_i(stack_pointer_1_o), .CLK(controlunit_1_mclk), .en(controlunit_1_sp_e),
    .sp_inc(controlunit_1_sp_inc), .sp_dec(controlunit_1_sp_dec), .sp_s(controlunit_1_sp_s));
  Accumulator accumulator_1 (
    .o(stack_pointer_1_o), .CLK(controlunit_1_mclk), .set(controlunit_1_acc_s),
    .i(arithmetic_logic_unit_1_o), .en(controlunit_1_acc_e));
  Program_Counter program_counter_1 (
    .o(stack_pointer_1_o), .i(stack_pointer_1_o), .set_2(controlunit_1_pc_inc), .CLK(controlunit_1_mclk),
    .set(controlunit_1_pc_s), .en(controlunit_1_pc_e));
  ControlUnit controlunit_1 (
    .IO(controlunit_1_io), .PC_INC(controlunit_1_pc_inc), .PC_S(controlunit_1_pc_s),
    .MAR_S(controlunit_1_mar_s), .PC_E(controlunit_1_pc_e), .IR_S(controlunit_1_ir_s),
    .RAM_S(controlunit_1_ram_s), .RAM_E(controlunit_1_ram_e), .ACC_S(controlunit_1_acc_s),
    .FLAG_S(controlunit_1_flag_s), .IR_E(controlunit_1_ir_e), .FLAG_CLR(controlunit_1_flag_clr),
    .SP_INC(controlunit_1_sp_inc), .SP_DEC(controlunit_1_sp_dec), .SP_S(controlunit_1_sp_s),
    .SP_E(controlunit_1_sp_e), .TMP_C(controlunit_1_tmp_c), .RBbits(controlunit_1_rbbits),
    .RAbits(controlunit_1_rabits), .MCLK(controlunit_1_mclk), .ACC_E(controlunit_1_acc_e),
    .RA_S(controlunit_1_ra_s), .RA_E(controlunit_1_ra_e), .RB_S(controlunit_1_rb_s),
    .RB_E(controlunit_1_rb_e), .TMP_S(controlunit_1_tmp_s), .CI_E(controlunit_1_ci_e),
    .op_out(controlunit_1_op_out), .IR_CODE(instruction_register_1_o), .FLAG_DATA(flag_register_1_f_o));
  Instruction_Register instruction_register_1 (
    .o(instruction_register_1_o), .o_l(stack_pointer_1_o), .i(stack_pointer_1_o), .set(controlunit_1_ir_s),
    .CLK(controlunit_1_mclk), .en(controlunit_1_ir_e));
  Register_Files register_files_1 (
    .o(stack_pointer_1_o), .RA_SEL(controlunit_1_rabits), .RB_SEL(controlunit_1_rbbits),
    .i(stack_pointer_1_o), .CLK(controlunit_1_mclk), .AS(controlunit_1_ra_s), .BS(controlunit_1_rb_s),
    .BE(controlunit_1_rb_e), .AE(controlunit_1_ra_e));
  Random_Access_Memory random_access_memory_1 (
    .o(stack_pointer_1_o), .i(stack_pointer_1_o), .CLK(controlunit_1_mclk), .sa(controlunit_1_mar_s),
    .sd(controlunit_1_ram_s), .e(controlunit_1_ram_e));
  Video_Graphics_Adaptor video_graphics_adaptor_1 (
    .px(video_graphics_adaptor_1_px), .py(video_graphics_adaptor_1_py),
    .color(video_graphics_adaptor_1_color), .fromBus(stack_pointer_1_o), .IO(controlunit_1_io));
  // RGB_Video #(.height(256), .width(256)) rgb_video_1: pin names not known; wires that end beside it: stack_pointer_1_o, in_3, rgb_video_1_p3, 1'b1, video_graphics_adaptor_1_px, video_graphics_adaptor_1_py, video_graphics_adaptor_1_color
  Clock clock_1 (.out(rgb_video_1_p3));
  Button u_ES (.out(ES));
  Button u_F1 (.out(F1));
  Button u_F2 (.out(F2));
  Button u_F3 (.out(F3));
  Button u_F4 (.out(F4));
  Button button (.out(tunnel_t_t_t_t_t_t_t_t_t_t_t_t_t_t_t_t_t_t_t_t_t_t_t_t_t_t_t_t_t_t_t));
  Button button_2 (.out(tunnel));
  Button button_3 (.out(tunnel_t_t_t_t_t_t_t_t_t_t_t_t_t_t_t_t_t_t_t_t_t_t));
  Button button_4 (.out(tunnel_t_t));
  Button button_5 (.out(tunnel_t_t_t_t_t_t_t_t_t_t_t_t_t_t_t_t_t_t_t_t_t_t_t_t_t_t_t));
  Button u__1 (.out(_1));
  Button u__2 (.out(_2));
  Button u__3 (.out(_3));
  Button u_TB (.out(TB));
  Button u_Q (.out(Q));
  Button u_W (.out(W));
  Button u_E (.out(E));
  Button u_A (.out(A));
  Button u_S (.out(S));
  Button u_Z (.out(Z));
  Button u_X (.out(X));
  assign ascii_in = BS ? 8'h8 : 8'bz;  // Controlled_Buffer controlled_buffer_1
  assign ascii_in = TB ? 8'h9 : 8'bz;  // Controlled_Buffer controlled_buffer_2
  assign ascii_in = EN ? 8'hd : 8'bz;  // Controlled_Buffer controlled_buffer_3
  assign ascii_in = ES ? 8'h1b : 8'bz;  // Controlled_Buffer controlled_buffer_4
  Button u_F5 (.out(F5));
  Button u_F6 (.out(F6));
  Button u_F7 (.out(F7));
  Button button_6 (.out(tunnel_t_t_t));
  Button button_7 (.out(tunnel_t_t_t_t));
  Button button_8 (.out(tunnel_t_t_t_t_t_t_t_t_t_t_t_t_t_t_t_t_t_t_t_t_t_t_t_t_t_t));
  Button button_9 (.out(tunnel_t_t_t_t_t));
  Button u__4 (.out(_4));
  Button u__5 (.out(_5));
  Button u__6 (.out(_6));
  Button u__7 (.out(_7));
  Button u_R (.out(R));
  Button u_T (.out(T));
  Button u_Y (.out(Y));
  Button u_U (.out(U));
  Button u_D (.out(D));
  Button u_F (.out(F));
  Button u_G (.out(G));
  Button u_H (.out(H));
  Button u_C (.out(C));
  Button u_V (.out(V));
  Button u_B (.out(B));
  Button u_N (.out(N));
  Button u_F8 (.out(F8));
  Button u_F9 (.out(F9));
  Button u_FA (.out(FA));
  Button u_FB (.out(FB));
  Button button_10 (.out(tunnel_t_t_t_t_t_t_t_t_t));
  Button button_11 (.out(tunnel_t_t_t_t_t_t_t));
  Button button_12 (.out(tunnel_t_t_t_t_t_t_t_t));
  Button button_13 (.out(tunnel_t_t_t_t_t_t_t_t_t_t_t_t_t));
  Button u__8 (.out(_8));
  Button u__9 (.out(_9));
  Button u__0 (.out(_0));
  Button button_14 (.out(tunnel_t_t_t_t_t_t_t_t_t_t_t_t));
  Button u_I (.out(I));
  Button u_O (.out(O));
  Button u_P (.out(P));
  Button button_15 (.out(tunnel_t_t_t_t_t_t_t_t_t_t_t_t_t_t_t_t_t_t_t_t_t_t_t));
  Button u_J (.out(J));
  Button u_K (.out(K));
  Button u_L (.out(L));
  Button button_16 (.out(tunnel_t_t_t_t_t_t_t_t_t_t_t_t_t_t_t_t_t));
  Button u_M (.out(M));
  Button button_17 (.out(tunnel_t_t_t_t_t_t_t_t_t_t_t));
  Button button_18 (.out(tunnel_t_t_t_t_t_t_t_t_t_t_t_t_t_t));
  Button button_19 (.out(tunnel_t_t_t_t_t_t_t_t_t_t_t_t_t_t_t));
  assign ascii_in = SP ? 8'h20 : 8'bz;  // Controlled_Buffer controlled_buffer_5
  assign ascii_in = tunnel ? 8'h21 : 8'bz;  // Controlled_Buffer controlled_buffer_6
  assign ascii_in = tunnel_t ? 8'h22 : 8'bz;  // Controlled_Buffer controlled_buffer_7
  assign ascii_in = tunnel_t_t ? 8'h23 : 8'bz;  // Controlled_Buffer controlled_buffer_8
  assign ascii_in = tunnel_t_t_t ? 8'h24 : 8'bz;  // Controlled_Buffer controlled_buffer_9
  assign ascii_in = tunnel_t_t_t_t ? 8'h25 : 8'bz;  // Controlled_Buffer controlled_buffer_10
  assign ascii_in = tunnel_t_t_t_t_t ? 8'h26 : 8'bz;  // Controlled_Buffer controlled_buffer_11
  assign ascii_in = tunnel_t_t_t_t_t_t ? 8'h27 : 8'bz;  // Controlled_Buffer controlled_buffer_12
  Button u_FC (.out(FC));
  Button button_20 ();  // open: out
  Button button_21 ();  // open: out
  Button button_22 (.out(tunnel_t_t_t_t_t_t_t_t_t_t));
  Button u_BS (.out(BS));
  Button u_DL (.out(DL));
  Button button_23 (.out(tunnel_t_t_t_t_t_t_t_t_t_t_t_t_t_t_t_t_t_t_t));
  Button button_24 (.out(tunnel_t_t_t_t_t_t_t_t_t_t_t_t_t_t_t_t_t_t_t_t_t_t_t_t_t_t_t_t));
  Button button_25 (.out(tunnel_t_t_t_t_t_t_t_t_t_t_t_t_t_t_t_t_t_t_t_t_t_t_t_t_t_t_t_t_t_t));
  Button button_26 (.out(tunnel_t_t_t_t_t_t_t_t_t_t_t_t_t_t_t_t_t_t_t_t_t_t_t_t_t_t_t_t_t));
  Button button_27 (.out(tunnel_t_t_t_t_t_t_t_t_t_t_t_t_t_t_t_t_t_t_t_t_t_t_t_t_t));
  Button button_28 (.out(tunnel_t_t_t_t_t_t_t_t_t_t_t_t_t_t_t_t_t_t_t_t_t_t_t_t));
  Button button_29 (.out(tunnel_t_t_t_t_t_t));
  Button button_30 (.out(tunnel_t_t_t_t_t_t_t_t_t_t_t_t_t_t_t_t));
  Button button_31 (.out(tunnel_t));
  Button u_EN (.out(EN));
  Button button_32 (.out(tunnel_t_t_t_t_t_t_t_t_t_t_t_t_t_t_t_t_t_t));
  Button button_33 (.out(tunnel_t_t_t_t_t_t_t_t_t_t_t_t_t_t_t_t_t_t_t_t));
  Button button_34 (.out(tunnel_t_t_t_t_t_t_t_t_t_t_t_t_t_t_t_t_t_t_t_t_t));
  assign ascii_in = tunnel_t_t_t_t_t_t_t ? 8'h28 : 8'bz;  // Controlled_Buffer controlled_buffer_13
  assign ascii_in = tunnel_t_t_t_t_t_t_t_t ? 8'h29 : 8'bz;  // Controlled_Buffer controlled_buffer_14
  assign ascii_in = tunnel_t_t_t_t_t_t_t_t_t ? 8'h2a : 8'bz;  // Controlled_Buffer controlled_buffer_15
  assign ascii_in = tunnel_t_t_t_t_t_t_t_t_t_t ? 8'h2b : 8'bz;  // Controlled_Buffer controlled_buffer_16
  assign ascii_in = tunnel_t_t_t_t_t_t_t_t_t_t_t ? 8'h2c : 8'bz;  // Controlled_Buffer controlled_buffer_17
  assign ascii_in = tunnel_t_t_t_t_t_t_t_t_t_t_t_t ? 8'h2d : 8'bz;  // Controlled_Buffer controlled_buffer_18
  assign ascii_in = tunnel_t_t_t_t_t_t_t_t_t_t_t_t_t_t ? 8'h2e : 8'bz;  // Controlled_Buffer controlled_buffer_19
  assign ascii_in = tunnel_t_t_t_t_t_t_t_t_t_t_t_t_t_t_t ? 8'h2f : 8'bz;  // Controlled_Buffer controlled_buffer_20
  Button button_35 ();  // open: out
  Button u_SP (.out(SP));
  assign controlled_buffer_21_out = A ? 8'h41 : 8'bz;  // Controlled_Buffer controlled_buffer_21
  assign controlled_buffer_21_out = B ? 8'h42 : 8'bz;  // Controlled_Buffer controlled_buffer_22
  assign controlled_buffer_21_out = C ? 8'h43 : 8'bz;  // Controlled_Buffer controlled_buffer_23
  assign controlled_buffer_21_out = D ? 8'h44 : 8'bz;  // Controlled_Buffer controlled_buffer_24
  assign controlled_buffer_21_out = E ? 8'h45 : 8'bz;  // Controlled_Buffer controlled_buffer_25
  assign controlled_buffer_21_out = F ? 8'h46 : 8'bz;  // Controlled_Buffer controlled_buffer_26
  assign controlled_buffer_21_out = G ? 8'h47 : 8'bz;  // Controlled_Buffer controlled_buffer_27
  assign controlled_buffer_21_out = H ? 8'h48 : 8'bz;  // Controlled_Buffer controlled_buffer_28
  assign controlled_buffer_29_out = A ? 8'h61 : 8'bz;  // Controlled_Buffer controlled_buffer_29
  assign controlled_buffer_29_out = B ? 8'h62 : 8'bz;  // Controlled_Buffer controlled_buffer_30
  assign controlled_buffer_29_out = C ? 8'h63 : 8'bz;  // Controlled_Buffer controlled_buffer_31
  assign controlled_buffer_29_out = D ? 8'h64 : 8'bz;  // Controlled_Buffer controlled_buffer_32
  assign controlled_buffer_29_out = E ? 8'h65 : 8'bz;  // Controlled_Buffer controlled_buffer_33
  assign controlled_buffer_29_out = F ? 8'h66 : 8'bz;  // Controlled_Buffer controlled_buffer_34
  assign controlled_buffer_29_out = G ? 8'h67 : 8'bz;  // Controlled_Buffer controlled_buffer_35
  assign controlled_buffer_29_out = H ? 8'h68 : 8'bz;  // Controlled_Buffer controlled_buffer_36
  assign ascii_in = _0 ? 8'h30 : 8'bz;  // Controlled_Buffer controlled_buffer_37
  assign ascii_in = _1 ? 8'h31 : 8'bz;  // Controlled_Buffer controlled_buffer_38
  assign ascii_in = _2 ? 8'h32 : 8'bz;  // Controlled_Buffer controlled_buffer_39
  assign ascii_in = _3 ? 8'h33 : 8'bz;  // Controlled_Buffer controlled_buffer_40
  assign ascii_in = _4 ? 8'h34 : 8'bz;  // Controlled_Buffer controlled_buffer_41
  assign ascii_in = _5 ? 8'h35 : 8'bz;  // Controlled_Buffer controlled_buffer_42
  assign ascii_in = _6 ? 8'h36 : 8'bz;  // Controlled_Buffer controlled_buffer_43
  assign ascii_in = _7 ? 8'h37 : 8'bz;  // Controlled_Buffer controlled_buffer_44
  assign controlled_buffer_21_out = I ? 8'h49 : 8'bz;  // Controlled_Buffer controlled_buffer_45
  assign controlled_buffer_21_out = J ? 8'h4a : 8'bz;  // Controlled_Buffer controlled_buffer_46
  assign controlled_buffer_21_out = K ? 8'h4b : 8'bz;  // Controlled_Buffer controlled_buffer_47
  assign controlled_buffer_21_out = L ? 8'h4c : 8'bz;  // Controlled_Buffer controlled_buffer_48
  assign controlled_buffer_21_out = M ? 8'h4d : 8'bz;  // Controlled_Buffer controlled_buffer_49
  assign controlled_buffer_21_out = N ? 8'h4e : 8'bz;  // Controlled_Buffer controlled_buffer_50
  assign controlled_buffer_21_out = O ? 8'h4f : 8'bz;  // Controlled_Buffer controlled_buffer_51
  assign controlled_buffer_21_out = P ? 8'h50 : 8'bz;  // Controlled_Buffer controlled_buffer_52
  assign controlled_buffer_29_out = I ? 8'h69 : 8'bz;  // Controlled_Buffer controlled_buffer_53
  assign controlled_buffer_29_out = J ? 8'h6a : 8'bz;  // Controlled_Buffer controlled_buffer_54
  assign controlled_buffer_29_out = K ? 8'h6b : 8'bz;  // Controlled_Buffer controlled_buffer_55
  assign controlled_buffer_29_out = L ? 8'h6c : 8'bz;  // Controlled_Buffer controlled_buffer_56
  assign controlled_buffer_29_out = M ? 8'h6d : 8'bz;  // Controlled_Buffer controlled_buffer_57
  assign controlled_buffer_29_out = N ? 8'h6e : 8'bz;  // Controlled_Buffer controlled_buffer_58
  assign controlled_buffer_29_out = O ? 8'h6f : 8'bz;  // Controlled_Buffer controlled_buffer_59
  assign controlled_buffer_29_out = P ? 8'h70 : 8'bz;  // Controlled_Buffer controlled_buffer_60
  assign ascii_in = _8 ? 8'h38 : 8'bz;  // Controlled_Buffer controlled_buffer_61
  assign ascii_in = _9 ? 8'h39 : 8'bz;  // Controlled_Buffer controlled_buffer_62
  assign ascii_in = tunnel_t_t_t_t_t_t_t_t_t_t_t_t_t_t_t_t ? 8'h3a : 8'bz;  // Controlled_Buffer controlled_buffer_63
  assign ascii_in = tunnel_t_t_t_t_t_t_t_t_t_t_t_t_t_t_t_t_t ? 8'h3b : 8'bz;  // Controlled_Buffer controlled_buffer_64
  assign ascii_in = tunnel_t_t_t_t_t_t_t_t_t_t_t_t_t_t_t_t_t_t ? 8'h3c : 8'bz;  // Controlled_Buffer controlled_buffer_65
  assign ascii_in = tunnel_t_t_t_t_t_t_t_t_t_t_t_t_t_t_t_t_t_t_t ? 8'h3d : 8'bz;  // Controlled_Buffer controlled_buffer_66
  assign ascii_in = tunnel_t_t_t_t_t_t_t_t_t_t_t_t_t_t_t_t_t_t_t_t ? 8'h3e : 8'bz;  // Controlled_Buffer controlled_buffer_67
  assign ascii_in = tunnel_t_t_t_t_t_t_t_t_t_t_t_t_t_t_t_t_t_t_t_t_t ? 8'h3f : 8'bz;  // Controlled_Buffer controlled_buffer_68
  assign controlled_buffer_29_out = Q ? 8'h71 : 8'bz;  // Controlled_Buffer controlled_buffer_69
  assign controlled_buffer_29_out = R ? 8'h72 : 8'bz;  // Controlled_Buffer controlled_buffer_70
  assign controlled_buffer_29_out = S ? 8'h73 : 8'bz;  // Controlled_Buffer controlled_buffer_71
  assign controlled_buffer_29_out = T ? 8'h74 : 8'bz;  // Controlled_Buffer controlled_buffer_72
  assign controlled_buffer_29_out = U ? 8'h75 : 8'bz;  // Controlled_Buffer controlled_buffer_73
  assign controlled_buffer_29_out = V ? 8'h76 : 8'bz;  // Controlled_Buffer controlled_buffer_74
  assign controlled_buffer_29_out = W ? 8'h77 : 8'bz;  // Controlled_Buffer controlled_buffer_75
  assign controlled_buffer_29_out = X ? 8'h78 : 8'bz;  // Controlled_Buffer controlled_buffer_76
  assign controlled_buffer_21_out = Q ? 8'h51 : 8'bz;  // Controlled_Buffer controlled_buffer_77
  assign controlled_buffer_21_out = R ? 8'h52 : 8'bz;  // Controlled_Buffer controlled_buffer_78
  assign controlled_buffer_21_out = S ? 8'h53 : 8'bz;  // Controlled_Buffer controlled_buffer_79
  assign controlled_buffer_21_out = T ? 8'h54 : 8'bz;  // Controlled_Buffer controlled_buffer_80
  assign controlled_buffer_21_out = U ? 8'h55 : 8'bz;  // Controlled_Buffer controlled_buffer_81
  assign controlled_buffer_21_out = V ? 8'h56 : 8'bz;  // Controlled_Buffer controlled_buffer_82
  assign controlled_buffer_21_out = W ? 8'h57 : 8'bz;  // Controlled_Buffer controlled_buffer_83
  assign controlled_buffer_21_out = X ? 8'h58 : 8'bz;  // Controlled_Buffer controlled_buffer_84
  assign ascii_in = tunnel_t_t_t_t_t_t_t_t_t_t_t_t_t_t_t_t_t_t_t_t_t_t ? 8'h40 : 8'bz;  // Controlled_Buffer controlled_buffer_85
  assign ascii_in = tunnel_t_t_t_t_t_t_t_t_t_t_t_t_t_t_t_t_t_t_t_t_t_t_t ? 8'h5b : 8'bz;  // Controlled_Buffer controlled_buffer_86
  assign ascii_in = tunnel_t_t_t_t_t_t_t_t_t_t_t_t_t_t_t_t_t_t_t_t_t_t_t_t ? 8'h5c : 8'bz;  // Controlled_Buffer controlled_buffer_87
  assign ascii_in = tunnel_t_t_t_t_t_t_t_t_t_t_t_t_t_t_t_t_t_t_t_t_t_t_t_t_t ? 8'h5d : 8'bz;  // Controlled_Buffer controlled_buffer_88
  assign ascii_in = tunnel_t_t_t_t_t_t_t_t_t_t_t_t_t_t_t_t_t_t_t_t_t_t_t_t_t_t ? 8'h5e : 8'bz;  // Controlled_Buffer controlled_buffer_89
  assign ascii_in = tunnel_t_t_t_t_t_t_t_t_t_t_t_t_t ? 8'h5f : 8'bz;  // Controlled_Buffer controlled_buffer_90
  assign ascii_in = tunnel_t_t_t_t_t_t_t_t_t_t_t_t_t_t_t_t_t_t_t_t_t_t_t_t_t_t_t ? 8'h60 : 8'bz;  // Controlled_Buffer controlled_buffer_91
  assign ascii_in = tunnel_t_t_t_t_t_t_t_t_t_t_t_t_t_t_t_t_t_t_t_t_t_t_t_t_t_t_t_t ? 8'h7b : 8'bz;  // Controlled_Buffer controlled_buffer_92
  assign controlled_buffer_21_out = Y ? 8'h59 : 8'bz;  // Controlled_Buffer controlled_buffer_93
  assign controlled_buffer_21_out = Z ? 8'h5a : 8'bz;  // Controlled_Buffer controlled_buffer_94
  assign controlled_buffer_29_out = Y ? 8'h79 : 8'bz;  // Controlled_Buffer controlled_buffer_95
  assign controlled_buffer_29_out = Z ? 8'h7a : 8'bz;  // Controlled_Buffer controlled_buffer_96
  assign ascii_in = tunnel_t_t_t_t_t_t_t_t_t_t_t_t_t_t_t_t_t_t_t_t_t_t_t_t_t_t_t_t_t ? 8'h7c : 8'bz;  // Controlled_Buffer controlled_buffer_97
  assign ascii_in = tunnel_t_t_t_t_t_t_t_t_t_t_t_t_t_t_t_t_t_t_t_t_t_t_t_t_t_t_t_t_t_t ? 8'h7d : 8'bz;  // Controlled_Buffer controlled_buffer_98
  assign ascii_in = tunnel_t_t_t_t_t_t_t_t_t_t_t_t_t_t_t_t_t_t_t_t_t_t_t_t_t_t_t_t_t_t_t ? 8'h7e : 8'bz;  // Controlled_Buffer controlled_buffer_99
  assign ascii_in = DL ? 8'h7f : 8'bz;  // Controlled_Buffer controlled_buffer_100
  assign ascii_in = CAP ? controlled_buffer_21_out : 8'bz;  // Controlled_Buffer controlled_buffer_101
  assign ascii_in = not_1_out ? controlled_buffer_29_out : 8'bz;  // Controlled_Buffer controlled_buffer_102
  not not_1 (not_1_out, CAP);
endmodule

module R0 (
  input  [31:0] i,
  input  set,
  input  en,
  output [31:0] o
);

  wire [31:0] register_1_q;

  Register #(.trigger("high"), .width(32)) register_1 (.D(i), .en(set), .Q(register_1_q), .clk(1'b1));  // open: clr
  // Enabler enabler_1: pin names not known; wires that end beside it: register_1_q, en, o
endmodule

module R1 (
  input  [31:0] i,
  input  set,
  input  en,
  output [31:0] o
);

  wire [31:0] register_1_q;

  Register #(.trigger("high"), .width(32)) register_1 (.D(i), .en(set), .Q(register_1_q), .clk(1'b1));  // open: clr
  // Enabler enabler_1: pin names not known; wires that end beside it: register_1_q, en, o
endmodule

module R2 (
  input  [31:0] i,
  input  set,
  input  en,
  output [31:0] o
);

  wire [31:0] register_1_q;

  Register #(.trigger("high"), .width(32)) register_1 (.D(i), .en(set), .Q(register_1_q), .clk(1'b1));  // open: clr
  // Enabler enabler_1: pin names not known; wires that end beside it: register_1_q, en, o
endmodule

module R3 (
  input  [31:0] i,
  input  set,
  input  en,
  output [31:0] o
);

  wire [31:0] register_1_q;

  Register #(.trigger("high"), .width(32)) register_1 (.D(i), .en(set), .Q(register_1_q), .clk(1'b1));  // open: clr
  // Enabler enabler_1: pin names not known; wires that end beside it: register_1_q, en, o
endmodule

module Bus1 (
  input  [15:0] in_1,
  input  bus1_e,
  output [15:0] out_3
);

  wire not_1_out;

  not not_1 (not_1_out, bus1_e);
  assign out_3 = not_1_out ? in_1 : 16'bz;  // Controlled_Buffer controlled_buffer_1
  assign out_3 = bus1_e ? 16'h1 : 16'bz;  // Controlled_Buffer controlled_buffer_2
endmodule

module Decoder_2x4 (
  input  a,
  input  b,
  output _01,
  output o2,
  output o3,
  output o4
);

  wire not_1_out, not_2_out;

  not not_1 (not_1_out, a);
  not not_2 (not_2_out, b);
  and and_1 (_01, not_1_out, not_2_out);
  and and_2 (o2, a, not_2_out);
  and and_3 (o3, not_1_out, b);
  and and_4 (o4, a, b);
endmodule

module Decoder_2x4_inverted (
  input  a,
  input  b,
  output _01,
  output o2,
  output o3,
  output o4
);

  wire not_1_out, not_2_out;

  not not_1 (not_1_out, a);
  not not_2 (not_2_out, b);
  and and_1 (_01, not_1_out, not_2_out);
  and and_2 (o2, a, not_2_out);
  and and_3 (o3, not_1_out, b);
  and and_4 (o4, a, b);
endmodule

module Flag_Register (
  input  [3:0] F_I,
  input  CT_S,
  input  CT_E,
  input  CLK,
  input  DATA_S,
  input  CLR_S,
  output [7:0] F_O,
  output CT_O
);

  wire bitselector_2_out, register_2_q;
  wire [3:0] bitselector_1_out;

  Register register_1 (.D({4'b0000, F_I}), .en(DATA_S), .Q(F_O), .clk(CLK), .clr(CLR_S));
  LED Z (.in(bitselector_1_out[0]));
  LED E (.in(bitselector_1_out[1]));
  LED A (.in(bitselector_1_out[2]));
  BitSelector #(.group(4)) bitselector_1 (.in(F_O), .out(bitselector_1_out), .sel(1'b0));
  LED C (.in(bitselector_1_out[3]));
  BitSelector bitselector_2 (.in(F_O), .out(bitselector_2_out), .sel(3'b011));
  Register #(.width(1)) register_2 (.D(bitselector_2_out), .Q(register_2_q), .clk(CLK));  // open: en, clr
  and and_1 (CT_O, register_2_q, CT_E);
endmodule

module Carry_Temp_Register (
  input  i,
  input  CLK,
  input  set,
  input  en,
  output o
);

  wire register_1_q;

  Register #(.width(1)) register_1 (.D(i), .en(set), .Q(register_1_q), .clk(CLK));  // open: clr
  and and_1 (o, register_1_q, en);
endmodule

module IN_MAR16 (
  input  [15:0] i,
  input  set,
  output [15:0] o
);

  Register #(.trigger("high"), .width(16)) register_1 (.D(i), .en(set), .Q(o), .clk(1'b1));  // open: clr
endmodule

module OUT_MAR16 (
  input  [15:0] i,
  input  set,
  output [15:0] o
);

  Register #(.trigger("high"), .width(16)) register_1 (.D(i), .en(set), .Q(o), .clk(1'b1));  // open: clr
endmodule

module Memory_Address_Register (
  input  [15:0] i,
  input  set,
  input  clk,
  output [15:0] o
);

  Register #(.width(16)) register_1 (.D(i), .en(set), .Q(o), .clk(clk));  // open: clr
endmodule

module Random_Access_Memory (
  input  [15:0] i,
  input  sa,
  input  sd,
  input  CLK,
  input  e,
  output [15:0] o
);

  wire [15:0] memory_address_register_1_o, ram_1_dout;

  Memory_Address_Register memory_address_register_1 (.o(memory_address_register_1_o), .i(i), .set(sa), .clk(CLK));
  RAM #(.addrWidth(16), .dataWidth(16), .\type ("nonvolatile")) ram_1 (
    .addr(memory_address_register_1_o), .we(sd), .clk(CLK), .din(i), .dout(ram_1_dout));
  assign o = e ? ram_1_dout : 16'bz;  // Controlled_Buffer controlled_buffer_1
  Hex_Digit_Display d3 (.value(ram_1_dout[15:12]));  // open: dp
  Hex_Digit_Display d2 (.value(ram_1_dout[11:8]));  // open: dp
  Hex_Digit_Display d1 (.value(ram_1_dout[7:4]));  // open: dp
  Hex_Digit_Display d0 (.value(ram_1_dout[3:0]));  // open: dp
endmodule

module Video_Graphics_Adaptor (
  input  [3:0] IO,
  input  [15:0] fromBus,
  output [7:0] px,
  output [7:0] py,
  output [15:0] color
);

  wire _0, _1, _2, _3, _4, _5, _6, _7, _8, _9, A, ADDR_S, B, BS, C, CAP, clk_2_out, clk_out, D, DATA_S, DL,
       E, EN, ES, F, f_co, fx_counter_carry, G, H, I, J, K, L, M, N, not_1_out, not_2_out, O, P, Q, R, S, SP,
       T, TB, tunnel, tunnel_t, tunnel_t_t, tunnel_t_t_t, tunnel_t_t_t_t, tunnel_t_t_t_t_t,
       tunnel_t_t_t_t_t_t, tunnel_t_t_t_t_t_t_t, tunnel_t_t_t_t_t_t_t_t, tunnel_t_t_t_t_t_t_t_t_t,
       tunnel_t_t_t_t_t_t_t_t_t_t, tunnel_t_t_t_t_t_t_t_t_t_t_t, tunnel_t_t_t_t_t_t_t_t_t_t_t_t,
       tunnel_t_t_t_t_t_t_t_t_t_t_t_t_t, tunnel_t_t_t_t_t_t_t_t_t_t_t_t_t_t,
       tunnel_t_t_t_t_t_t_t_t_t_t_t_t_t_t_t, tunnel_t_t_t_t_t_t_t_t_t_t_t_t_t_t_t_t,
       tunnel_t_t_t_t_t_t_t_t_t_t_t_t_t_t_t_t_t, tunnel_t_t_t_t_t_t_t_t_t_t_t_t_t_t_t_t_t_t,
       tunnel_t_t_t_t_t_t_t_t_t_t_t_t_t_t_t_t_t_t_t, tunnel_t_t_t_t_t_t_t_t_t_t_t_t_t_t_t_t_t_t_t_t,
       tunnel_t_t_t_t_t_t_t_t_t_t_t_t_t_t_t_t_t_t_t_t_t, tunnel_t_t_t_t_t_t_t_t_t_t_t_t_t_t_t_t_t_t_t_t_t_t,
       tunnel_t_t_t_t_t_t_t_t_t_t_t_t_t_t_t_t_t_t_t_t_t_t_t,
       tunnel_t_t_t_t_t_t_t_t_t_t_t_t_t_t_t_t_t_t_t_t_t_t_t_t,
       tunnel_t_t_t_t_t_t_t_t_t_t_t_t_t_t_t_t_t_t_t_t_t_t_t_t_t,
       tunnel_t_t_t_t_t_t_t_t_t_t_t_t_t_t_t_t_t_t_t_t_t_t_t_t_t_t,
       tunnel_t_t_t_t_t_t_t_t_t_t_t_t_t_t_t_t_t_t_t_t_t_t_t_t_t_t_t,
       tunnel_t_t_t_t_t_t_t_t_t_t_t_t_t_t_t_t_t_t_t_t_t_t_t_t_t_t_t_t,
       tunnel_t_t_t_t_t_t_t_t_t_t_t_t_t_t_t_t_t_t_t_t_t_t_t_t_t_t_t_t_t,
       tunnel_t_t_t_t_t_t_t_t_t_t_t_t_t_t_t_t_t_t_t_t_t_t_t_t_t_t_t_t_t_t,
       tunnel_t_t_t_t_t_t_t_t_t_t_t_t_t_t_t_t_t_t_t_t_t_t_t_t_t_t_t_t_t_t_t, U, V, W, X, Y, Z;
  wire [2:0] dx, dy;
  wire [7:0] ascii_in, controlled_buffer_22_out, controlled_buffer_30_out, px0, py0, rom_1_data;
  wire [15:0] adder_1_out, ascii_px, controlled_buffer_1_out, multiplexer_1_out, register_1_q, vin_1_o,
       zero_one_1_out_2, zero_one_2_out_2, zero_one_3_out_2, zero_one_4_out_2, zero_one_5_out_2,
       zero_one_6_out_2, zero_one_7_out_2, zero_one_8_out_2;

  assign controlled_buffer_1_out = DATA_S ? fromBus : 16'bz;  // Controlled_Buffer controlled_buffer_1
  Multiplier #(.width(16)) multiplier_1 (.a(16'h8), .b(controlled_buffer_1_out), .out(ascii_px));  // open: cin, cout
  not not_1 (not_1_out, IO[1]);
  VIN vin_1 (.o(vin_1_o), .i(fromBus), .set(ADDR_S), .clk(IO[2]));
  Register #(.trigger("falling"), .width(16)) register_1 (
    .D(ascii_px), .en(DATA_S), .Q(register_1_q), .clk(IO[2]));  // open: clr
  and and_1 (ADDR_S, IO[1], IO[0]);
  and and_2 (DATA_S, not_1_out, IO[0]);
  ROM #(.addrWidth(16)) rom_1 (.addr(adder_1_out), .data(rom_1_data));
  Adder_part #(.width(16)) adder_1 (.a({{13{1'b0}}, dy}), .b(register_1_q), .out(adder_1_out));  // open: cin, cout
  Multiplier multiplier_2 (.a(vin_1_o[7:0]), .b(8'h8), .out(px0));  // open: cin, cout
  Multiplier multiplier_3 (.a(vin_1_o[15:8]), .b(8'h8), .out(py0));  // open: cin, cout
  Adder_part adder_2 (.a(px0), .b({{5{1'b0}}, dx}), .out(px));  // open: cin, cout
  Clock #(.phaseOffset(1)) clk (.out(clk_out));
  Adder_part adder_3 (.a(py0), .b({{5{1'b0}}, dy}), .out(py));  // open: cin, cout
  zero_one zero_one_1 (.out_2(zero_one_1_out_2), .binary(rom_1_data[7]));
  zero_one zero_one_2 (.out_2(zero_one_2_out_2), .binary(rom_1_data[6]));
  zero_one zero_one_3 (.out_2(zero_one_3_out_2), .binary(rom_1_data[5]));
  zero_one zero_one_4 (.out_2(zero_one_4_out_2), .binary(rom_1_data[4]));
  zero_one zero_one_5 (.out_2(zero_one_5_out_2), .binary(rom_1_data[3]));
  zero_one zero_one_6 (.out_2(zero_one_6_out_2), .binary(rom_1_data[2]));
  zero_one zero_one_7 (.out_2(zero_one_7_out_2), .binary(rom_1_data[1]));
  zero_one zero_one_8 (.out_2(zero_one_8_out_2), .binary(rom_1_data[0]));
  Counter #(.max('h7), .width(3)) fx_counter (
    .count(1'b1), .Q(dx), .carry(fx_counter_carry), .clk(clk_out));  // open: load, D, clr
  Counter #(.max('h7), .trigger("falling"), .width(3)) fy_counter (
    .count(1'b1), .Q(dy), .carry(f_co), .clk(fx_counter_carry));  // open: load, D, clr
  Multiplexer #(.enable("false"), .select(3), .width(16)) multiplexer_1 (
    .in0(zero_one_1_out_2), .in1(zero_one_2_out_2), .in2(zero_one_3_out_2), .in3(zero_one_4_out_2),
    .in4(zero_one_5_out_2), .in5(zero_one_6_out_2), .in6(zero_one_7_out_2), .in7(zero_one_8_out_2),
    .out(multiplexer_1_out), .sel(dx));
  Clock #(.phaseOffset(1)) clk_2 (.out(clk_2_out));
  RAM #(.addrWidth(16), .dataWidth(16), .trigger("high")) Video_RAM (
    .addr({py, px}), .we(1'b1), .clk(clk_2_out), .din(multiplexer_1_out), .dout(color));
  assign ascii_in = BS ? 8'h8 : 8'bz;  // Controlled_Buffer controlled_buffer_2
  assign ascii_in = TB ? 8'h9 : 8'bz;  // Controlled_Buffer controlled_buffer_3
  assign ascii_in = EN ? 8'hd : 8'bz;  // Controlled_Buffer controlled_buffer_4
  assign ascii_in = ES ? 8'h1b : 8'bz;  // Controlled_Buffer controlled_buffer_5
  assign ascii_in = SP ? 8'h20 : 8'bz;  // Controlled_Buffer controlled_buffer_6
  assign ascii_in = tunnel ? 8'h21 : 8'bz;  // Controlled_Buffer controlled_buffer_7
  assign ascii_in = tunnel_t ? 8'h22 : 8'bz;  // Controlled_Buffer controlled_buffer_8
  assign ascii_in = tunnel_t_t ? 8'h23 : 8'bz;  // Controlled_Buffer controlled_buffer_9
  assign ascii_in = tunnel_t_t_t ? 8'h24 : 8'bz;  // Controlled_Buffer controlled_buffer_10
  assign ascii_in = tunnel_t_t_t_t ? 8'h25 : 8'bz;  // Controlled_Buffer controlled_buffer_11
  assign ascii_in = tunnel_t_t_t_t_t ? 8'h26 : 8'bz;  // Controlled_Buffer controlled_buffer_12
  assign ascii_in = tunnel_t_t_t_t_t_t ? 8'h27 : 8'bz;  // Controlled_Buffer controlled_buffer_13
  assign ascii_in = tunnel_t_t_t_t_t_t_t ? 8'h28 : 8'bz;  // Controlled_Buffer controlled_buffer_14
  assign ascii_in = tunnel_t_t_t_t_t_t_t_t ? 8'h29 : 8'bz;  // Controlled_Buffer controlled_buffer_15
  assign ascii_in = tunnel_t_t_t_t_t_t_t_t_t ? 8'h2a : 8'bz;  // Controlled_Buffer controlled_buffer_16
  assign ascii_in = tunnel_t_t_t_t_t_t_t_t_t_t ? 8'h2b : 8'bz;  // Controlled_Buffer controlled_buffer_17
  assign ascii_in = tunnel_t_t_t_t_t_t_t_t_t_t_t ? 8'h2c : 8'bz;  // Controlled_Buffer controlled_buffer_18
  assign ascii_in = tunnel_t_t_t_t_t_t_t_t_t_t_t_t ? 8'h2d : 8'bz;  // Controlled_Buffer controlled_buffer_19
  assign ascii_in = tunnel_t_t_t_t_t_t_t_t_t_t_t_t_t_t ? 8'h2e : 8'bz;  // Controlled_Buffer controlled_buffer_20
  assign ascii_in = tunnel_t_t_t_t_t_t_t_t_t_t_t_t_t_t_t ? 8'h2f : 8'bz;  // Controlled_Buffer controlled_buffer_21
  assign controlled_buffer_22_out = A ? 8'h41 : 8'bz;  // Controlled_Buffer controlled_buffer_22
  assign controlled_buffer_22_out = B ? 8'h42 : 8'bz;  // Controlled_Buffer controlled_buffer_23
  assign controlled_buffer_22_out = C ? 8'h43 : 8'bz;  // Controlled_Buffer controlled_buffer_24
  assign controlled_buffer_22_out = D ? 8'h44 : 8'bz;  // Controlled_Buffer controlled_buffer_25
  assign controlled_buffer_22_out = E ? 8'h45 : 8'bz;  // Controlled_Buffer controlled_buffer_26
  assign controlled_buffer_22_out = F ? 8'h46 : 8'bz;  // Controlled_Buffer controlled_buffer_27
  assign controlled_buffer_22_out = G ? 8'h47 : 8'bz;  // Controlled_Buffer controlled_buffer_28
  assign controlled_buffer_22_out = H ? 8'h48 : 8'bz;  // Controlled_Buffer controlled_buffer_29
  assign controlled_buffer_30_out = A ? 8'h61 : 8'bz;  // Controlled_Buffer controlled_buffer_30
  assign controlled_buffer_30_out = B ? 8'h62 : 8'bz;  // Controlled_Buffer controlled_buffer_31
  assign controlled_buffer_30_out = C ? 8'h63 : 8'bz;  // Controlled_Buffer controlled_buffer_32
  assign controlled_buffer_30_out = D ? 8'h64 : 8'bz;  // Controlled_Buffer controlled_buffer_33
  assign controlled_buffer_30_out = E ? 8'h65 : 8'bz;  // Controlled_Buffer controlled_buffer_34
  assign controlled_buffer_30_out = F ? 8'h66 : 8'bz;  // Controlled_Buffer controlled_buffer_35
  assign controlled_buffer_30_out = G ? 8'h67 : 8'bz;  // Controlled_Buffer controlled_buffer_36
  assign controlled_buffer_30_out = H ? 8'h68 : 8'bz;  // Controlled_Buffer controlled_buffer_37
  assign ascii_in = _0 ? 8'h30 : 8'bz;  // Controlled_Buffer controlled_buffer_38
  assign ascii_in = _1 ? 8'h31 : 8'bz;  // Controlled_Buffer controlled_buffer_39
  assign ascii_in = _2 ? 8'h32 : 8'bz;  // Controlled_Buffer controlled_buffer_40
  assign ascii_in = _3 ? 8'h33 : 8'bz;  // Controlled_Buffer controlled_buffer_41
  assign ascii_in = _4 ? 8'h34 : 8'bz;  // Controlled_Buffer controlled_buffer_42
  assign ascii_in = _5 ? 8'h35 : 8'bz;  // Controlled_Buffer controlled_buffer_43
  assign ascii_in = _6 ? 8'h36 : 8'bz;  // Controlled_Buffer controlled_buffer_44
  assign ascii_in = _7 ? 8'h37 : 8'bz;  // Controlled_Buffer controlled_buffer_45
  assign controlled_buffer_22_out = I ? 8'h49 : 8'bz;  // Controlled_Buffer controlled_buffer_46
  assign controlled_buffer_22_out = J ? 8'h4a : 8'bz;  // Controlled_Buffer controlled_buffer_47
  assign controlled_buffer_22_out = K ? 8'h4b : 8'bz;  // Controlled_Buffer controlled_buffer_48
  assign controlled_buffer_22_out = L ? 8'h4c : 8'bz;  // Controlled_Buffer controlled_buffer_49
  assign controlled_buffer_22_out = M ? 8'h4d : 8'bz;  // Controlled_Buffer controlled_buffer_50
  assign controlled_buffer_22_out = N ? 8'h4e : 8'bz;  // Controlled_Buffer controlled_buffer_51
  assign controlled_buffer_22_out = O ? 8'h4f : 8'bz;  // Controlled_Buffer controlled_buffer_52
  assign controlled_buffer_22_out = P ? 8'h50 : 8'bz;  // Controlled_Buffer controlled_buffer_53
  assign controlled_buffer_30_out = I ? 8'h69 : 8'bz;  // Controlled_Buffer controlled_buffer_54
  assign controlled_buffer_30_out = J ? 8'h6a : 8'bz;  // Controlled_Buffer controlled_buffer_55
  assign controlled_buffer_30_out = K ? 8'h6b : 8'bz;  // Controlled_Buffer controlled_buffer_56
  assign controlled_buffer_30_out = L ? 8'h6c : 8'bz;  // Controlled_Buffer controlled_buffer_57
  assign controlled_buffer_30_out = M ? 8'h6d : 8'bz;  // Controlled_Buffer controlled_buffer_58
  assign controlled_buffer_30_out = N ? 8'h6e : 8'bz;  // Controlled_Buffer controlled_buffer_59
  assign controlled_buffer_30_out = O ? 8'h6f : 8'bz;  // Controlled_Buffer controlled_buffer_60
  assign controlled_buffer_30_out = P ? 8'h70 : 8'bz;  // Controlled_Buffer controlled_buffer_61
  assign ascii_in = _8 ? 8'h38 : 8'bz;  // Controlled_Buffer controlled_buffer_62
  assign ascii_in = _9 ? 8'h39 : 8'bz;  // Controlled_Buffer controlled_buffer_63
  assign ascii_in = tunnel_t_t_t_t_t_t_t_t_t_t_t_t_t_t_t_t ? 8'h3a : 8'bz;  // Controlled_Buffer controlled_buffer_64
  assign ascii_in = tunnel_t_t_t_t_t_t_t_t_t_t_t_t_t_t_t_t_t ? 8'h3b : 8'bz;  // Controlled_Buffer controlled_buffer_65
  assign ascii_in = tunnel_t_t_t_t_t_t_t_t_t_t_t_t_t_t_t_t_t_t ? 8'h3c : 8'bz;  // Controlled_Buffer controlled_buffer_66
  assign ascii_in = tunnel_t_t_t_t_t_t_t_t_t_t_t_t_t_t_t_t_t_t_t ? 8'h3d : 8'bz;  // Controlled_Buffer controlled_buffer_67
  assign ascii_in = tunnel_t_t_t_t_t_t_t_t_t_t_t_t_t_t_t_t_t_t_t_t ? 8'h3e : 8'bz;  // Controlled_Buffer controlled_buffer_68
  assign ascii_in = tunnel_t_t_t_t_t_t_t_t_t_t_t_t_t_t_t_t_t_t_t_t_t ? 8'h3f : 8'bz;  // Controlled_Buffer controlled_buffer_69
  assign controlled_buffer_22_out = Q ? 8'h51 : 8'bz;  // Controlled_Buffer controlled_buffer_70
  assign controlled_buffer_22_out = R ? 8'h52 : 8'bz;  // Controlled_Buffer controlled_buffer_71
  assign controlled_buffer_22_out = S ? 8'h53 : 8'bz;  // Controlled_Buffer controlled_buffer_72
  assign controlled_buffer_22_out = T ? 8'h54 : 8'bz;  // Controlled_Buffer controlled_buffer_73
  assign controlled_buffer_22_out = U ? 8'h55 : 8'bz;  // Controlled_Buffer controlled_buffer_74
  assign controlled_buffer_22_out = V ? 8'h56 : 8'bz;  // Controlled_Buffer controlled_buffer_75
  assign controlled_buffer_22_out = W ? 8'h57 : 8'bz;  // Controlled_Buffer controlled_buffer_76
  assign controlled_buffer_22_out = X ? 8'h58 : 8'bz;  // Controlled_Buffer controlled_buffer_77
  assign controlled_buffer_30_out = Q ? 8'h71 : 8'bz;  // Controlled_Buffer controlled_buffer_78
  assign controlled_buffer_30_out = R ? 8'h72 : 8'bz;  // Controlled_Buffer controlled_buffer_79
  assign controlled_buffer_30_out = S ? 8'h73 : 8'bz;  // Controlled_Buffer controlled_buffer_80
  assign controlled_buffer_30_out = T ? 8'h74 : 8'bz;  // Controlled_Buffer controlled_buffer_81
  assign controlled_buffer_30_out = U ? 8'h75 : 8'bz;  // Controlled_Buffer controlled_buffer_82
  assign controlled_buffer_30_out = V ? 8'h76 : 8'bz;  // Controlled_Buffer controlled_buffer_83
  assign controlled_buffer_30_out = W ? 8'h77 : 8'bz;  // Controlled_Buffer controlled_buffer_84
  assign controlled_buffer_30_out = X ? 8'h78 : 8'bz;  // Controlled_Buffer controlled_buffer_85
  assign ascii_in = tunnel_t_t_t_t_t_t_t_t_t_t_t_t_t_t_t_t_t_t_t_t_t_t ? 8'h40 : 8'bz;  // Controlled_Buffer controlled_buffer_86
  assign ascii_in = tunnel_t_t_t_t_t_t_t_t_t_t_t_t_t_t_t_t_t_t_t_t_t_t_t ? 8'h5b : 8'bz;  // Controlled_Buffer controlled_buffer_87
  assign ascii_in = tunnel_t_t_t_t_t_t_t_t_t_t_t_t_t_t_t_t_t_t_t_t_t_t_t_t ? 8'h5c : 8'bz;  // Controlled_Buffer controlled_buffer_88
  assign ascii_in = tunnel_t_t_t_t_t_t_t_t_t_t_t_t_t_t_t_t_t_t_t_t_t_t_t_t_t ? 8'h5d : 8'bz;  // Controlled_Buffer controlled_buffer_89
  assign ascii_in = tunnel_t_t_t_t_t_t_t_t_t_t_t_t_t_t_t_t_t_t_t_t_t_t_t_t_t_t ? 8'h5e : 8'bz;  // Controlled_Buffer controlled_buffer_90
  assign ascii_in = tunnel_t_t_t_t_t_t_t_t_t_t_t_t_t ? 8'h5f : 8'bz;  // Controlled_Buffer controlled_buffer_91
  assign ascii_in = tunnel_t_t_t_t_t_t_t_t_t_t_t_t_t_t_t_t_t_t_t_t_t_t_t_t_t_t_t ? 8'h60 : 8'bz;  // Controlled_Buffer controlled_buffer_92
  assign ascii_in = tunnel_t_t_t_t_t_t_t_t_t_t_t_t_t_t_t_t_t_t_t_t_t_t_t_t_t_t_t_t ? 8'h7b : 8'bz;  // Controlled_Buffer controlled_buffer_93
  assign controlled_buffer_22_out = Y ? 8'h59 : 8'bz;  // Controlled_Buffer controlled_buffer_94
  assign controlled_buffer_22_out = Z ? 8'h5a : 8'bz;  // Controlled_Buffer controlled_buffer_95
  assign controlled_buffer_30_out = Y ? 8'h79 : 8'bz;  // Controlled_Buffer controlled_buffer_96
  assign controlled_buffer_30_out = Z ? 8'h7a : 8'bz;  // Controlled_Buffer controlled_buffer_97
  assign ascii_in = tunnel_t_t_t_t_t_t_t_t_t_t_t_t_t_t_t_t_t_t_t_t_t_t_t_t_t_t_t_t_t ? 8'h7c : 8'bz;  // Controlled_Buffer controlled_buffer_98
  assign ascii_in = tunnel_t_t_t_t_t_t_t_t_t_t_t_t_t_t_t_t_t_t_t_t_t_t_t_t_t_t_t_t_t_t ? 8'h7d : 8'bz;  // Controlled_Buffer controlled_buffer_99
  assign ascii_in = tunnel_t_t_t_t_t_t_t_t_t_t_t_t_t_t_t_t_t_t_t_t_t_t_t_t_t_t_t_t_t_t_t ? 8'h7e : 8'bz;  // Controlled_Buffer controlled_buffer_100
  assign ascii_in = DL ? 8'h7f : 8'bz;  // Controlled_Buffer controlled_buffer_101
  assign ascii_in = CAP ? controlled_buffer_22_out : 8'bz;  // Controlled_Buffer controlled_buffer_102
  assign ascii_in = not_2_out ? controlled_buffer_30_out : 8'bz;  // Controlled_Buffer controlled_buffer_103
  not not_2 (not_2_out, CAP);

  // Other names for the same wires on the sheet: FONT_POS[15:0] = {py, px}; font_y[2:0] = dy; IN_OUT = IO[0];
  //   DATA_ADDR = IO[1]; IOCLK_S = IO[2]; IOCLK_E = IO[3]

  // Notes on the sheet:
  //   contents of rom_1 (hex, n*v repeats v):
  //   8*0 78 84 cc 84 b4 84 78 0 78 fc b4 fc 84 cc 78 0 0 48 fc fc fc 78 30 0 0 30 78 fc 78 30 0 0 30 78
  //   30 fc fc 30 78 0 0 30 78 fc fc 30 78 0 0 0 38 7c 7c 38 0 0 ff ff c7 83 83 c7 ff ff 0 0 38 44 44 38 0
  //   0 ff ff c7 bb bb c7 ff ff fc fc cc 84 b4 fc fc 0 fc fc b4 84 cc fc fc 0 fc fc c4 8c c4 fc fc 0 fc fc
  //   8c c4 8c fc fc 0 38 bb 7c c7 c7 7c bb 38 0 80 f0 fc f0 80 0 0 0 4 3c fc 3c 4 0 0 30 78 fc 30 30 fc
  //   78 30 5*44 0 44 0 7c b4 b4 74 34 34 34 0 7c c3 78 cc cc 78 8c 78 5*0 7c 7c 0 38 7c ff 38 ff 7c 38 ff
  //   30 78 fc 4*30 0 4*30 fc 78 30 0 0 30 38 fc 38 30 0 0 0 30 70 ff 70 30 0 0 0 fc 84 b4 84 fc fc 0 0 0
  //   44 ff 44 4*0 30 30 78 78 fc 0 0 0 fc 78 78 30 30 10*0 5*30 0 30 0 34 34 48 5*0 48 48 fc 48 fc 48 48
  //   0 30 7c 80 78 4 f8 30 0 84 88 8 30 40 44 84 0 30 48 30 74 b8 88 74 0 8 8 30 5*0 c 30 40 40 40 30 c 0
  //   70 8 4 4 4 8 70 0 0 0 44 38 44 4*0 30 30 fc 30 30 7*0 30 30 30 0 0 0 fc 9*0 30 30 0 4 8 8 30 40 40
  //   80 0 78 84 8c b4 c4 84 78 0 30 70 4*30 fc 0 78 84 4 38 40 84 fc 0 78 84 4 38 4 84 78 0 c 34 44 84 fc
  //   4 4 0 fc 80 f8 4 4 84 78 0 38 40 80 f8 84 84 78 0 fc 84 4 8 30 30 30 0 78 84 84 78 84 84 78 0 78 84
  //   84 7c 4 8 70 0 0 30 30 0 0 30 30 0 0 30 30 0 0 30 30 30 8 30 40 80 40 30 8 0 0 0 fc 0 0 fc 0 0 80 40
  //   30 8 30 40 80 0 78 84 4 8 30 0 30 0 7c 83 bb bb bf 80 7c 0 78 84 fc 4*84 0 f8 84 f8 84 84 84 f8 0 78
  //   84 80 80 80 84 78 0 f8 5*84 f8 0 fc 80 f0 80 80 80 fc 0 fc 80 f0 4*80 0 7c 80 8c 84 84 84 78 0 84 84
  //   fc 4*84 0 78 5*30 78 0 5*4 84 78 0 84 88 f0 88 84 84 84 0 6*80 fc 0 84 cc b4 4*84 0 84 c4 b4 8c 84
  //   84 84 0 78 5*84 78 0 f8 84 f8 4*80 0 78 4*84 88 74 0 f8 84 f8 4*84 0 7c 80 78 4 4 84 78 0 fc 6*30 0
  //   6*84 78 0 4*84 48 48 30 0 4*84 b4 cc 84 0 84 48 30 48 84 84 84 0 84 48 5*30 0 fc 4 8 30 40 80 fc 0
  //   78 5*40 78 0 80 40 40 30 8 8 4 0 78 5*8 78 0 30 48 84 12*0 fc 30 30 8 7*0 78 4 7c 84 7c 0 80 80 b8
  //   c4 84 84 f8 0 0 0 78 84 80 84 78 0 4 4 74 8c 84 84 7c 0 0 0 78 84 fc 80 7c 0 c 30 7c 4*30 0 0 0 7c
  //   84 84 7c 4 f8 80 80 b8 c4 84 84 84 0 30 0 5*30 0 4 0 4 4 4 84 84 78 40 40 44 48 70 48 44 0 6*30 8 0
  //   0 0 c8 b4 b4 84 84 0 0 0 f8 4*84 0 0 0 78 84 84 84 78 0 0 0 b8 c4 84 f8 80 80 0 0 74 8c 84 7c 4 4 0
  //   0 b8 c4 80 80 80 0 0 0 7c 80 78 4 f8 0 30 30 78 30 30 30 8 0 0 0 4*84 7c 0 0 0 84 84 84 48 30 0 0 0
  //   84 84 b4 b4 7c 0 0 0 84 48 30 48 84 0 0 0 84 84 84 7c 4 f8 0 0 fc 8 30 40 fc 0 c 30 30 40 30 30 c 0
  //   30 30 30 0 30 30 30 0 70 8 8 4 8 8 70 0 74 b8 8*0 30 48 84 84 fc 0 0 30 78 cc 78 48 48 0 0 78 fc fc
  //   30 30 30 0 40 b0 4 b 40 b0 4 b 7*fc 0 fc fc fc 0 fc fc fc 0 fc fc fc 0 cf cf cf 0 fb 78 87 cb 3c bf
  //   4c f3 b4 b4 fc 84 fc b4 b4 0 7f 4f cb fb bb bf b7 f7 4 83 bb 3b 8 70 77 37 84 fc 84 84 84 fc 84 84 0
  //   ff 44 44 44 ff 0 0 0 f 30 48 84 f3 8c 84 0 c0 30 48 84 3c c4 84 8c f3 84 48 30 f 0 0 c4 3c 84 48 30
  //   c0 0 0 84 84 84 b4 b4 84 84 84 0 ff 0 38 0 ff 0 0 0 fc 84 fc fc 0 84 0 fc 84 f4 cc fc cc fc 0 ff 88
  //   80 b0 c0 84 88 80 0 fc 30 4*fc 0 38 44 44 4*38 0 38 7c 7c 4*38 0 0 c0 c0 30 8 fc fc 0 0 c c 30 40 fc
  //   fc 0 fc cc 84 fc 84 84 fc 0 fc b4 fc b4 fc b4 fc 0 38 44 40 f8 40 40 fc 0 0 fc b4 cc 84 b4 fc 0 0 0
  //   48 30 48 0 0 0 8 34 30 78 30 30 b0 40 0 fc 84 cc cc cc fc 0 0 fc cc 84 cc cc fc 0 0 fc cc cc 84 cc
  //   fc 0 0 fc cc cc cc 84 fc 0 30 48 84 0 30 48 84 0 84 48 30 0 84 48 30 0 33 88 44 33 44 88 33 0 88 33
  //   44 88 44 33 88 0 30 0 30 40 80 84 78 0 ff bb f ff f7 83 cf fc 0 0 0 fc 4 4 0 0 0 fc fc fc 0 30 30 0
  //   0 fc fc 0 cc fc fc 0 0 fc f4 fc 84 84 fc 0 0 34 48 b0 48 34 0 0 0 b0 48 34 48 b0 0 0 84 30 84 30 84
  //   30 84 30 b4 4b b4 4b b4 4b b4 4b bc f7 bc f7 bc f7 bc f7 11*30 f0 6*30 f0 30 f0 30 30 30 48 48 48 c8
  //   4*48 0 0 0 f8 4*48 0 0 f0 30 f0 30 30 30 48 48 c8 8 c8 11*48 0 0 f8 8 c8 5*48 c8 8 f8 0 0 0 4*48 f8
  //   0 0 0 30 30 f0 30 f0 6*0 f0 7*30 3f 4*0 30 30 30 ff 7*0 ff 7*30 3f 4*30 0 0 0 ff 4*0 30 30 30 ff
  //   6*30 3f 30 3f 30 30 30 4*48 4f 5*48 4f 40 7f 5*0 7f 40 4f 5*48 cf 0 ff 5*0 ff 0 cf 5*48 4f 40 4f 48
  //   48 48 0 0 ff 0 ff 0 0 0 48 48 cf 0 cf 48 48 48 30 30 ff 0 ff 0 0 0 48 48 48 ff 6*0 ff 0 ff 30 30 30
  //   0 0 0 ff 7*48 7f 4*0 30 30 3f 30 3f 5*0 3f 30 3f 30 30 30 0 0 0 7f 7*48 ff 4*48 30 30 ff 30 ff 6*30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
endmodule

module Accumulator (
  input  [15:0] i,
  input  set,
  input  en,
  input  CLK,
  output [15:0] o
);

  wire [15:0] register_1_q;

  Register #(.width(16)) register_1 (.D(i), .en(set), .Q(register_1_q), .clk(CLK));  // open: clr
  Enabler enabler_1 (.out_3(o), .in_2(en), .in_1(register_1_q));
endmodule

module Program_Counter (
  input  set,
  input  [15:0] i,
  input  set_2,
  input  CLK,
  input  en,
  output [15:0] o
);

  wire [15:0] counter_1_q;

  Counter #(.max('hffff), .width(16)) counter_1 (
    .load(set), .D(i), .count(set_2), .Q(counter_1_q), .clk(CLK));  // open: carry, clr
  Enabler enabler_1 (.out_3(o), .in_2(en), .in_1(counter_1_q));
endmodule

module Instruction_Register (
  input  [15:0] i,
  input  set,
  input  CLK,
  input  en,
  output [15:0] o,
  output [15:0] o_l
);

  Register #(.width(16)) register_1 (.D(i), .en(set), .Q(o), .clk(CLK));  // open: clr
  Enabler8 enabler8_1 (.out_3(o_l[7:0]), .in_2(en), .in_1(o[7:0]));
  assign o_l[15:8] = en ? {8{1'b0}} : 8'bz;  // Controlled_Buffer controlled_buffer_1
endmodule

module Temp_Register (
  input  [15:0] i,
  input  set,
  input  CLK,
  input  rst,
  output [15:0] o
);

  Register #(.width(16)) register_1 (.D(i), .en(set), .Q(o), .clk(CLK), .clr(rst));
endmodule

module Adder1 (
  input  a,
  input  b,
  input  ci,
  output sum,
  output co
);

  wire co1_out, co2_out, sum1_out;

  xor sum1 (sum1_out, a, b);
  xor sum2 (sum, sum1_out, ci);
  and co2 (co2_out, sum1_out, ci);
  and co1 (co1_out, a, b);
  or or_1 (co, co2_out, co1_out);
endmodule

module Adder8 (
  input  ci,
  input  [7:0] a,
  input  [7:0] b,
  output [7:0] o,
  output co
);

  wire adder1_1_co, adder1_2_co, adder1_3_co, adder1_4_co, adder1_5_co, adder1_6_co, adder1_7_co;

  Adder1 adder1_1 (.co(adder1_1_co), .sum(o[0]), .ci(ci), .a(a[0]), .b(b[0]));
  Adder1 adder1_2 (.co(adder1_2_co), .sum(o[1]), .ci(adder1_1_co), .a(a[1]), .b(b[1]));
  Adder1 adder1_3 (.co(adder1_3_co), .sum(o[2]), .ci(adder1_2_co), .a(a[2]), .b(b[2]));
  Adder1 adder1_4 (.co(adder1_4_co), .sum(o[3]), .ci(adder1_3_co), .a(a[3]), .b(b[3]));
  Adder1 adder1_5 (.co(adder1_5_co), .sum(o[4]), .ci(adder1_4_co), .a(a[4]), .b(b[4]));
  Adder1 adder1_6 (.co(adder1_6_co), .sum(o[5]), .ci(adder1_5_co), .a(a[5]), .b(b[5]));
  Adder1 adder1_7 (.co(adder1_7_co), .sum(o[6]), .ci(adder1_6_co), .a(a[6]), .b(b[6]));
  Adder1 adder1_8 (.co(co), .sum(o[7]), .ci(adder1_7_co), .a(a[7]), .b(b[7]));
endmodule

module Adder (
  input  ci,
  input  [15:0] a,
  input  [15:0] b,
  output [15:0] o,
  output co
);

  wire adder8_1_co;

  Adder8 adder8_1 (.co(adder8_1_co), .o(o[7:0]), .a(a[7:0]), .b(b[7:0]), .ci(ci));
  Adder8 adder8_2 (.co(co), .o(o[15:8]), .a(a[15:8]), .b(b[15:8]), .ci(adder8_1_co));
endmodule

module Adder32 (
  input  ci,
  input  [31:0] a,
  input  [31:0] b,
  output [31:0] o,
  output co
);

  wire adder_1_co;

  Adder adder_1 (.co(adder_1_co), .o(o[15:0]), .b(b[15:0]), .a(a[15:0]), .ci(ci));
  Adder adder_2 (.co(co), .o(o[31:16]), .b(b[31:16]), .a(a[31:16]), .ci(adder_1_co));
endmodule

module XORer (
  input  [15:0] a,
  input  [15:0] b,
  output [15:0] o
);

  assign o = a ^ b;  // XOR_Gate xor_1, 16 bits wide
endmodule

module XNORer (
  input  [15:0] a,
  input  [15:0] b,
  output [15:0] o
);

  assign o = ~(a ^ b);  // XNOR_Gate xnor_1, 16 bits wide
endmodule

module NORer (
  input  [15:0] a,
  input  [15:0] b,
  output [15:0] o
);

  assign o = ~(a | b);  // NOR_Gate nor_1, 16 bits wide
endmodule

module NANDer (
  input  [15:0] a,
  input  [15:0] b,
  output [15:0] o
);

  assign o = ~(a & b);  // NAND_Gate nand_1, 16 bits wide
endmodule

module ANDer (
  input  [15:0] a,
  input  [15:0] b,
  output [15:0] o
);

  assign o = a & b;  // AND_Gate and_1, 16 bits wide
endmodule

module ORer (
  input  [15:0] a,
  input  [15:0] b,
  output [15:0] o
);

  assign o = a | b;  // OR_Gate or_1, 16 bits wide
endmodule

module Inverter (
  input  [15:0] in_1,
  output [15:0] out_2
);

  assign out_2 = ~in_1;  // NOT_Gate not_1, 16 bits wide
endmodule

module low5_out (
  input  [4:0] i,
  output [31:0] o
);


  assign o = {{27{1'b0}}, i};
endmodule

module Negator (
  input  [15:0] in_1,
  output [15:0] out_2
);

  wire [15:0] inverter_1_out_2;

  Inverter inverter_1 (.out_2(inverter_1_out_2), .in_1(in_1));
  Adder adder_1 (.o(out_2), .b(16'h1), .a(inverter_1_out_2));  // open: co, ci
endmodule

module Subtractor (
  input  bi,
  input  [15:0] a,
  input  [15:0] b,
  output [15:0] o,
  output bo
);

  wire sub8_1_co;

  Sub8 sub8_1 (.co(sub8_1_co), .o(o[7:0]), .a(a[7:0]), .b(b[7:0]), .bi(bi));
  Sub8 sub8_2 (.co(bo), .o(o[15:8]), .a(a[15:8]), .b(b[15:8]), .bi(sub8_1_co));
endmodule

module low7_out (
  input  [6:0] i,
  output [31:0] o
);


  assign o = {{25{1'b0}}, i};
endmodule

module SHL (
  input  si,
  input  [15:0] i,
  output [15:0] o,
  output so
);

  wire [14:0] register_1_q;

  Register #(.trigger("high"), .width(16)) register_1 (
    .D(i), .en(1'b1), .Q({so, register_1_q}), .clk(1'b1));  // open: clr
  Register #(.trigger("high"), .width(16)) register_2 (
    .D({register_1_q, si}), .en(1'b1), .Q(o), .clk(1'b1));  // open: clr
endmodule

module SHR (
  input  [15:0] i,
  input  si,
  output so,
  output [15:0] o
);

  wire [15:1] register_1_q;

  Register #(.trigger("high"), .width(16)) register_1 (
    .D(i), .en(1'b1), .Q({register_1_q, so}), .clk(1'b1));  // open: clr
  Register #(.trigger("high"), .width(16)) register_2 (
    .D({si, register_1_q}), .en(1'b1), .Q(o), .clk(1'b1));  // open: clr
endmodule

module Arithmetic_Logic_Unit (
  input  [15:0] a,
  input  [15:0] b,
  input  ci,
  input  [3:0] op,
  output [3:0] f0,
  output [15:0] o
);

  wire adder_1_co, and_1_out, and_2_out, and_3_out, and_4_out, decoder_1_out0, decoder_1_out1,
       decoder_1_out2, decoder_1_out3, decoder_1_out8, decoder_1_out9, decoder_1_out10, decoder_1_out11,
       decoder_1_out12, decoder_1_out13, decoder_1_out15, shl_1_so, shr_1_so, subtractor_1_bo;
  wire [15:0] adder_1_o, ander_1_o, dec_1_o, inc_1_o, inverter_1_out_2, orer_1_o, shl_1_o, shr_1_o,
       subtractor_1_o, xorer_1_o;

  Comparator #(.width(16)) comparator_1 (.a(a), .b(b), .gt(f0[2]), .eq(f0[1]));  // open: lt
  XORer xorer_1 (.o(xorer_1_o), .a(a), .b(b));
  ORer orer_1 (.o(orer_1_o), .a(a), .b(b));
  ANDer ander_1 (.o(ander_1_o), .a(a), .b(b));
  Inverter inverter_1 (.out_2(inverter_1_out_2), .in_1(b));
  SHL shl_1 (.so(shl_1_so), .o(shl_1_o), .i(b), .si(ci));
  SHR shr_1 (.so(shr_1_so), .o(shr_1_o), .i(b), .si(ci));
  DEC dec_1 (.o(dec_1_o), .b(b));
  INC inc_1 (.o(inc_1_o), .b(b));
  Subtractor subtractor_1 (.bo(subtractor_1_bo), .o(subtractor_1_o), .b(b), .a(a), .bi(ci));
  Adder adder_1 (.co(adder_1_co), .o(adder_1_o), .b(b), .a(a), .ci(ci));
  Decoder #(.enable("false"), .select(4)) decoder_1 (
    .out0(decoder_1_out0), .out1(decoder_1_out1), .out2(decoder_1_out2), .out3(decoder_1_out3),
    .out8(decoder_1_out8), .out9(decoder_1_out9), .out10(decoder_1_out10), .out11(decoder_1_out11),
    .out12(decoder_1_out12), .out13(decoder_1_out13), .out15(decoder_1_out15), .sel(op));  // open: out4, out5, out6, out7, out14
  and and_1 (and_1_out, shl_1_so, decoder_1_out9);
  and and_2 (and_2_out, shr_1_so, decoder_1_out8);
  and and_3 (and_3_out, subtractor_1_bo, decoder_1_out1);
  and and_4 (and_4_out, adder_1_co, decoder_1_out0);
  Enabler enabler_1 (.out_3(o), .in_2(decoder_1_out13), .in_1(xorer_1_o));
  Enabler enabler_2 (.out_3(o), .in_2(decoder_1_out12), .in_1(orer_1_o));
  Enabler enabler_3 (.out_3(o), .in_2(decoder_1_out11), .in_1(ander_1_o));
  Enabler enabler_4 (.out_3(o), .in_2(decoder_1_out10), .in_1(inverter_1_out_2));
  Enabler enabler_5 (.out_3(o), .in_2(decoder_1_out9), .in_1(shl_1_o));
  Enabler enabler_6 (.out_3(o), .in_2(decoder_1_out8), .in_1(shr_1_o));
  Enabler enabler_7 (.out_3(o), .in_2(decoder_1_out3), .in_1(dec_1_o));
  Enabler enabler_8 (.out_3(o), .in_2(decoder_1_out2), .in_1(inc_1_o));
  Enabler enabler_9 (.out_3(o), .in_2(decoder_1_out1), .in_1(subtractor_1_o));
  Enabler enabler_10 (.out_3(o), .in_2(decoder_1_out0), .in_1(adder_1_o));
  assign o = decoder_1_out15 ? 16'h1 : 16'bz;  // Controlled_Buffer controlled_buffer_1
  ZEROer zeroer_1 (.out(f0[0]), .in(o));
  or or_1 (f0[3], and_1_out, and_2_out, and_3_out, and_4_out);

  // Other names for the same wires on the sheet: ZERO = f0[0]; EQ = f0[1]; AL = f0[2]; CO = f0[3]

  // Notes on the sheet:
  //   CMP
endmodule

module Register_Files (
  input  AS,
  input  AE,
  input  [15:0] i,
  input  [3:0] RA_SEL,
  input  BS,
  input  BE,
  input  [3:0] RB_SEL,
  input  CLK,
  output [15:0] o
);

  wire R00_A, R00_AE, R00_AS, R00_B, R00_BE, R00_BS, R00_E, R00_S, R01_A, R01_AE, R01_AS, R01_B, R01_BE,
       R01_BS, R01_E, R01_S, R02_A, R02_AE, R02_AS, R02_B, R02_BE, R02_BS, R02_E, R02_S, R03_A, R03_AE,
       R03_AS, R03_B, R03_BE, R03_BS, R03_E, R03_S, R04_A, R04_AE, R04_AS, R04_B, R04_BE, R04_BS, R04_E,
       R04_S, R05_A, R05_AE, R05_AS, R05_B, R05_BE, R05_BS, R05_E, R05_S, R06_A, R06_AE, R06_AS, R06_B,
       R06_BE, R06_BS, R06_E, R06_S, R07_A, R07_AE, R07_AS, R07_B, R07_BE, R07_BS, R07_E, R07_S, R08_A,
       R08_AE, R08_AS, R08_B, R08_BE, R08_BS, R08_E, R08_S, R09_A, R09_AE, R09_AS, R09_B, R09_BE, R09_BS,
       R09_E, R09_S, R10_A, R10_AE, R10_AS, R10_B, R10_BE, R10_BS, R10_E, R10_S, R11_A, R11_AE, R11_AS,
       R11_B, R11_BE, R11_BS, R11_E, R11_S, R12_A, R12_AE, R12_AS, R12_B, R12_BE, R12_BS, R12_E, R12_S,
       R13_A, R13_AE, R13_AS, R13_B, R13_BE, R13_BS, R13_E, R13_S, R14_A, R14_AE, R14_AS, R14_B, R14_BE,
       R14_BS, R14_E, R14_S, R15_A, R15_AE, R15_AS, R15_B, R15_BE, R15_BS, R15_E, R15_S;

  Decoder #(.enable("false"), .select(4)) decoder_1 (
    .out0(R00_A), .out1(R01_A), .out2(R02_A), .out3(R03_A), .out4(R04_A), .out5(R05_A), .out6(R06_A),
    .out7(R07_A), .out8(R08_A), .out9(R09_A), .out10(R10_A), .out11(R11_A), .out12(R12_A), .out13(R13_A),
    .out14(R14_A), .out15(R15_A), .sel(RA_SEL));
  Decoder #(.enable("false"), .select(4)) decoder_2 (
    .out0(R00_B), .out1(R01_B), .out2(R02_B), .out3(R03_B), .out4(R04_B), .out5(R05_B), .out6(R06_B),
    .out7(R07_B), .out8(R08_B), .out9(R09_B), .out10(R10_B), .out11(R11_B), .out12(R12_B), .out13(R13_B),
    .out14(R14_B), .out15(R15_B), .sel(RB_SEL));
  and and_1 (R00_AS, R00_A, AS);
  and and_2 (R01_AS, R01_A, AS);
  and and_3 (R02_AS, R02_A, AS);
  and and_4 (R03_AS, R03_A, AS);
  and and_5 (R04_AS, R04_A, AS);
  and and_6 (R05_AS, R05_A, AS);
  and and_7 (R06_AS, R06_A, AS);
  and and_8 (R07_AS, R07_A, AS);
  and and_9 (R08_AS, R08_A, AS);
  and and_10 (R09_AS, R09_A, AS);
  and and_11 (R10_AS, R10_A, AS);
  and and_12 (R11_AS, R11_A, AS);
  and and_13 (R12_AS, R12_A, AS);
  and and_14 (R13_AS, R13_A, AS);
  and and_15 (R14_AS, R14_A, AS);
  and and_16 (R15_AS, R15_A, AS);
  and and_17 (R00_BS, R00_B, BS);
  and and_18 (R01_BS, R01_B, BS);
  and and_19 (R02_BS, R02_B, BS);
  and and_20 (R03_BS, R03_B, BS);
  and and_21 (R04_BS, R04_B, BS);
  and and_22 (R05_BS, R05_B, BS);
  and and_23 (R06_BS, R06_B, BS);
  and and_24 (R07_BS, R07_B, BS);
  and and_25 (R08_BS, R08_B, BS);
  and and_26 (R09_BS, R09_B, BS);
  and and_27 (R10_BS, R10_B, BS);
  and and_28 (R11_BS, R11_B, BS);
  and and_29 (R12_BS, R12_B, BS);
  and and_30 (R13_BS, R13_B, BS);
  and and_31 (R14_BS, R14_B, BS);
  and and_32 (R15_BS, R15_B, BS);
  and and_33 (R00_AE, R00_A, AE);
  and and_34 (R01_AE, R01_A, AE);
  and and_35 (R02_AE, R02_A, AE);
  and and_36 (R03_AE, R03_A, AE);
  and and_37 (R04_AE, R04_A, AE);
  and and_38 (R05_AE, R05_A, AE);
  and and_39 (R06_AE, R06_A, AE);
  and and_40 (R07_AE, R07_A, AE);
  and and_41 (R08_AE, R08_A, AE);
  and and_42 (R09_AE, R09_A, AE);
  and and_43 (R10_AE, R10_A, AE);
  and and_44 (R11_AE, R11_A, AE);
  and and_45 (R12_AE, R12_A, AE);
  and and_46 (R13_AE, R13_A, AE);
  and and_47 (R14_AE, R14_A, AE);
  and and_48 (R15_AE, R15_A, AE);
  and and_49 (R00_BE, R00_B, BE);
  and and_50 (R01_BE, R01_B, BE);
  and and_51 (R02_BE, R02_B, BE);
  and and_52 (R03_BE, R03_B, BE);
  and and_53 (R04_BE, R04_B, BE);
  and and_54 (R05_BE, R05_B, BE);
  and and_55 (R06_BE, R06_B, BE);
  and and_56 (R07_BE, R07_B, BE);
  and and_57 (R08_BE, R08_B, BE);
  and and_58 (R09_BE, R09_B, BE);
  and and_59 (R10_BE, R10_B, BE);
  and and_60 (R11_BE, R11_B, BE);
  and and_61 (R12_BE, R12_B, BE);
  and and_62 (R13_BE, R13_B, BE);
  and and_63 (R14_BE, R14_B, BE);
  and and_64 (R15_BE, R15_B, BE);
  or or_1 (R00_S, R00_AS, R00_BS);
  or or_2 (R01_S, R01_AS, R01_BS);
  or or_3 (R02_S, R02_AS, R02_BS);
  or or_4 (R03_S, R03_AS, R03_BS);
  or or_5 (R04_S, R04_AS, R04_BS);
  or or_6 (R05_S, R05_AS, R05_BS);
  or or_7 (R06_S, R06_AS, R06_BS);
  or or_8 (R07_S, R07_AS, R07_BS);
  or or_9 (R08_S, R08_AS, R08_BS);
  or or_10 (R09_S, R09_AS, R09_BS);
  or or_11 (R10_S, R10_AS, R10_BS);
  or or_12 (R11_S, R11_AS, R11_BS);
  or or_13 (R12_S, R12_AS, R12_BS);
  or or_14 (R13_S, R13_AS, R13_BS);
  or or_15 (R14_S, R14_AS, R14_BS);
  or or_16 (R15_S, R15_AS, R15_BS);
  or or_17 (R00_E, R00_AE, R00_BE);
  or or_18 (R01_E, R01_AE, R01_BE);
  or or_19 (R02_E, R02_AE, R02_BE);
  or or_20 (R03_E, R03_AE, R03_BE);
  or or_21 (R04_E, R04_AE, R04_BE);
  or or_22 (R05_E, R05_AE, R05_BE);
  or or_23 (R06_E, R06_AE, R06_BE);
  or or_24 (R07_E, R07_AE, R07_BE);
  or or_25 (R08_E, R08_AE, R08_BE);
  or or_26 (R09_E, R09_AE, R09_BE);
  or or_27 (R10_E, R10_AE, R10_BE);
  or or_28 (R11_E, R11_AE, R11_BE);
  or or_29 (R12_E, R12_AE, R12_BE);
  or or_30 (R13_E, R13_AE, R13_BE);
  or or_31 (R14_E, R14_AE, R14_BE);
  or or_32 (R15_E, R15_AE, R15_BE);
  Register32 r00 (.o(o), .set(R00_S), .i(i), .CLK(CLK), .en(R00_E));
  Register32 r01 (.o(o), .set(R01_S), .i(i), .CLK(CLK), .en(R01_E));
  Register32 r02 (.o(o), .set(R02_S), .i(i), .CLK(CLK), .en(R02_E));
  Register32 r03 (.o(o), .set(R03_S), .i(i), .CLK(CLK), .en(R03_E));
  Register32 r04 (.o(o), .set(R04_S), .i(i), .CLK(CLK), .en(R04_E));
  Register32 r05 (.o(o), .set(R05_S), .i(i), .CLK(CLK), .en(R05_E));
  Register32 r06 (.o(o), .set(R06_S), .i(i), .CLK(CLK), .en(R06_E));
  Register32 r07 (.o(o), .set(R07_S), .i(i), .CLK(CLK), .en(R07_E));
  Register32 r08 (.o(o), .set(R08_S), .i(i), .CLK(CLK), .en(R08_E));
  Register32 r09 (.o(o), .set(R09_S), .i(i), .CLK(CLK), .en(R09_E));
  Register32 r10 (.o(o), .set(R10_S), .i(i), .CLK(CLK), .en(R10_E));
  Register32 r11 (.o(o), .set(R11_S), .i(i), .CLK(CLK), .en(R11_E));
  Register32 r12 (.o(o), .set(R12_S), .i(i), .CLK(CLK), .en(R12_E));
  Register32 r13 (.o(o), .set(R13_S), .i(i), .CLK(CLK), .en(R13_E));
  Register32 r14 (.o(o), .set(R14_S), .i(i), .CLK(CLK), .en(R14_E));
  Register32 r15 (.o(o), .set(R15_S), .i(i), .CLK(CLK), .en(R15_E));
endmodule

module Register32 (
  input  [15:0] i,
  input  set,
  input  en,
  input  CLK,
  output [15:0] o
);

  wire [15:0] register_1_q;

  Register #(.width(16)) register_1 (.D(i), .en(set), .Q(register_1_q), .clk(CLK));  // open: clr
  Enabler enabler_1 (.out_3(o), .in_2(en), .in_1(register_1_q));
endmodule

module Data_Register (
  input  [15:0] i,
  input  set,
  input  en,
  input  CLK,
  output [15:0] o
);

  wire [15:0] register_1_q;

  Register #(.width(16)) register_1 (.D(i), .en(set), .Q(register_1_q), .clk(CLK));  // open: clr
  Enabler enabler_1 (.out_3(o), .in_2(en), .in_1(register_1_q));
endmodule

module Enabler8 (
  input  [7:0] in_1,
  input  in_2,
  output [7:0] out_3
);

  assign out_3 = in_2 ? in_1 : 8'bz;  // Controlled_Buffer controlled_buffer_1
endmodule

module INC (
  input  [15:0] b,
  output [15:0] o
);

  Adder adder_1 (.o(o), .b(b), .a(16'h1));  // open: co, ci
endmodule

module DEC (
  input  [15:0] b,
  output [15:0] o
);

  Subtractor subtractor_1 (.o(o), .b(b), .a(16'h1));  // open: bo, bi
endmodule

module Stack_Pointer (
  input  sp_inc,
  input  sp_dec,
  input  sp_s,
  input  [15:0] sp_i,
  input  CLK,
  input  en,
  output [15:0] o
);

  wire or_1_out;
  wire [15:0] counter_1_q;

  or or_1 (or_1_out, sp_inc, sp_dec);
  Counter #(.max('hffff), .width(16)) counter_1 (
    .load(sp_s), .D(sp_i), .count(or_1_out), .Q(counter_1_q), .up(sp_inc), .clk(CLK));  // open: carry, clr
  Enabler enabler_1 (.out_3(o), .in_2(en), .in_1(counter_1_q));
endmodule

module BIOS (
  input  [15:0] i,
  input  sa,
  input  sd,
  input  clk,
  input  e,
  output [15:0] o
);

  wire [15:0] memory_address_register_1_o, rom_1_data;

  Memory_Address_Register memory_address_register_1 (.o(memory_address_register_1_o), .i(i), .set(sa), .clk(clk));
  ROM #(.addrWidth(16), .dataWidth(16)) rom_1 (.addr(memory_address_register_1_o), .data(rom_1_data));
  assign o = e ? rom_1_data : 16'bz;  // Controlled_Buffer controlled_buffer_1
  Hex_Digit_Display d3 (.value(rom_1_data[15:12]));  // open: dp
  Hex_Digit_Display d2 (.value(rom_1_data[11:8]));  // open: dp
  Hex_Digit_Display d1 (.value(rom_1_data[7:4]));  // open: dp
  Hex_Digit_Display d0 (.value(rom_1_data[3:0]));  // open: dp
endmodule

module zero_one (
  input  binary,
  output [15:0] out_2
);

  wire not_1_out;

  not not_1 (not_1_out, binary);
  assign out_2 = not_1_out ? {16{1'b0}} : 16'bz;  // Controlled_Buffer controlled_buffer_1
  assign out_2 = binary ? {16{1'b1}} : 16'bz;  // Controlled_Buffer controlled_buffer_2
endmodule

module framebuffer256x256 (
  input  [7:0] text_x,
  input  reset,
  input  [7:0] text_y,
  input  wrt,
  input  [7:0] in_5,
  input  r_s,
  output [15:0] out_7
);

  wire clk_2_out, f_co, fx_counter_carry, rgb_video_1_p2;
  wire [2:0] dx, dy;
  wire [7:0] px, px0, py, py0, rom_1_data;
  wire [15:0] adder_3_out, rgb_video_1_p6, zero_one_1_out_2, zero_one_2_out_2, zero_one_3_out_2,
       zero_one_4_out_2, zero_one_5_out_2, zero_one_6_out_2, zero_one_7_out_2, zero_one_8_out_2;

  Multiplier multiplier_1 (.a(text_x), .b(8'h8), .out(px0));  // open: cin, cout
  Multiplier multiplier_2 (.a(text_y), .b(8'h8), .out(py0));  // open: cin, cout
  Multiplier #(.width(16)) multiplier_3 (.a(16'h8), .b({{8{1'b0}}, in_5}), .out(out_7));  // open: cin, cout
  Adder_part adder_1 (.a(px0), .b({{5{1'b0}}, dx}), .out(px));  // open: cin, cout
  Adder_part adder_2 (.a(py0), .b({{5{1'b0}}, dy}), .out(py));  // open: cin, cout
  Adder_part #(.width(16)) adder_3 (.a({{13{1'b0}}, dy}), .b(out_7), .out(adder_3_out));  // open: cin, cout
  ROM #(.addrWidth(16)) rom_1 (.addr(adder_3_out), .data(rom_1_data));
  // RGB_Video #(.height(256), .width(256)) rgb_video_1: pin names not known; wires that end beside it: reset, rgb_video_1_p2, wrt, px, py, rgb_video_1_p6
  Clock #(.phaseOffset(1)) clk (.out(rgb_video_1_p2));
  Clock #(.phaseOffset(1)) clk_2 (.out(clk_2_out));
  zero_one zero_one_1 (.out_2(zero_one_1_out_2), .binary(rom_1_data[7]));
  zero_one zero_one_2 (.out_2(zero_one_2_out_2), .binary(rom_1_data[6]));
  zero_one zero_one_3 (.out_2(zero_one_3_out_2), .binary(rom_1_data[5]));
  zero_one zero_one_4 (.out_2(zero_one_4_out_2), .binary(rom_1_data[4]));
  zero_one zero_one_5 (.out_2(zero_one_5_out_2), .binary(rom_1_data[3]));
  zero_one zero_one_6 (.out_2(zero_one_6_out_2), .binary(rom_1_data[2]));
  zero_one zero_one_7 (.out_2(zero_one_7_out_2), .binary(rom_1_data[1]));
  zero_one zero_one_8 (.out_2(zero_one_8_out_2), .binary(rom_1_data[0]));
  Counter #(.max('h7), .width(3)) fx_counter (
    .count(r_s), .Q(dx), .carry(fx_counter_carry), .clk(clk_2_out));  // open: load, D, clr
  Counter #(.max('h7), .trigger("falling"), .width(3)) fy_counter (
    .count(r_s), .Q(dy), .carry(f_co), .clk(fx_counter_carry));  // open: load, D, clr
  Multiplexer #(.enable("false"), .select(3), .width(16)) multiplexer_1 (
    .in0(zero_one_1_out_2), .in1(zero_one_2_out_2), .in2(zero_one_3_out_2), .in3(zero_one_4_out_2),
    .in4(zero_one_5_out_2), .in5(zero_one_6_out_2), .in6(zero_one_7_out_2), .in7(zero_one_8_out_2),
    .out(rgb_video_1_p6), .sel(dx));

  // Other names for the same wires on the sheet: ascii_px[15:0] = out_7; font_y[2:0] = dy

  // Notes on the sheet:
  //   contents of rom_1 (hex, n*v repeats v):
  //   8*0 78 84 cc 84 b4 84 78 0 78 fc b4 fc 84 cc 78 0 0 48 fc fc fc 78 30 0 0 30 78 fc 78 30 0 0 30 78
  //   30 fc fc 30 78 0 0 30 78 fc fc 30 78 0 0 0 38 7c 7c 38 0 0 ff ff c7 83 83 c7 ff ff 0 0 38 44 44 38 0
  //   0 ff ff c7 bb bb c7 ff ff fc fc cc 84 b4 fc fc 0 fc fc b4 84 cc fc fc 0 fc fc c4 8c c4 fc fc 0 fc fc
  //   8c c4 8c fc fc 0 38 bb 7c c7 c7 7c bb 38 0 80 f0 fc f0 80 0 0 0 4 3c fc 3c 4 0 0 30 78 fc 30 30 fc
  //   78 30 5*44 0 44 0 7c b4 b4 74 34 34 34 0 7c c3 78 cc cc 78 8c 78 5*0 7c 7c 0 38 7c ff 38 ff 7c 38 ff
  //   30 78 fc 4*30 0 4*30 fc 78 30 0 0 30 38 fc 38 30 0 0 0 30 70 ff 70 30 0 0 0 fc 84 b4 84 fc fc 0 0 0
  //   44 ff 44 4*0 30 30 78 78 fc 0 0 0 fc 78 78 30 30 10*0 5*30 0 30 0 34 34 48 5*0 48 48 fc 48 fc 48 48
  //   0 30 7c 80 78 4 f8 30 0 84 88 8 30 40 44 84 0 30 48 30 74 b8 88 74 0 8 8 30 5*0 c 30 40 40 40 30 c 0
  //   70 8 4 4 4 8 70 0 0 0 44 38 44 4*0 30 30 fc 30 30 7*0 30 30 30 0 0 0 fc 9*0 30 30 0 4 8 8 30 40 40
  //   80 0 78 84 8c b4 c4 84 78 0 30 70 4*30 fc 0 78 84 4 38 40 84 fc 0 78 84 4 38 4 84 78 0 c 34 44 84 fc
  //   4 4 0 fc 80 f8 4 4 84 78 0 38 40 80 f8 84 84 78 0 fc 84 4 8 30 30 30 0 78 84 84 78 84 84 78 0 78 84
  //   84 7c 4 8 70 0 0 30 30 0 0 30 30 0 0 30 30 0 0 30 30 30 8 30 40 80 40 30 8 0 0 0 fc 0 0 fc 0 0 80 40
  //   30 8 30 40 80 0 78 84 4 8 30 0 30 0 7c 83 bb bb bf 80 7c 0 78 84 fc 4*84 0 f8 84 f8 84 84 84 f8 0 78
  //   84 80 80 80 84 78 0 f8 5*84 f8 0 fc 80 f0 80 80 80 fc 0 fc 80 f0 4*80 0 7c 80 8c 84 84 84 78 0 84 84
  //   fc 4*84 0 78 5*30 78 0 5*4 84 78 0 84 88 f0 88 84 84 84 0 6*80 fc 0 84 cc b4 4*84 0 84 c4 b4 8c 84
  //   84 84 0 78 5*84 78 0 f8 84 f8 4*80 0 78 4*84 88 74 0 f8 84 f8 4*84 0 7c 80 78 4 4 84 78 0 fc 6*30 0
  //   6*84 78 0 4*84 48 48 30 0 4*84 b4 cc 84 0 84 48 30 48 84 84 84 0 84 48 5*30 0 fc 4 8 30 40 80 fc 0
  //   78 5*40 78 0 80 40 40 30 8 8 4 0 78 5*8 78 0 30 48 84 12*0 fc 30 30 8 7*0 78 4 7c 84 7c 0 80 80 b8
  //   c4 84 84 f8 0 0 0 78 84 80 84 78 0 4 4 74 8c 84 84 7c 0 0 0 78 84 fc 80 7c 0 c 30 7c 4*30 0 0 0 7c
  //   84 84 7c 4 f8 80 80 b8 c4 84 84 84 0 30 0 5*30 0 4 0 4 4 4 84 84 78 40 40 44 48 70 48 44 0 6*30 8 0
  //   0 0 c8 b4 b4 84 84 0 0 0 f8 4*84 0 0 0 78 84 84 84 78 0 0 0 b8 c4 84 f8 80 80 0 0 74 8c 84 7c 4 4 0
  //   0 b8 c4 80 80 80 0 0 0 7c 80 78 4 f8 0 30 30 78 30 30 30 8 0 0 0 4*84 7c 0 0 0 84 84 84 48 30 0 0 0
  //   84 84 b4 b4 7c 0 0 0 84 48 30 48 84 0 0 0 84 84 84 7c 4 f8 0 0 fc 8 30 40 fc 0 c 30 30 40 30 30 c 0
  //   30 30 30 0 30 30 30 0 70 8 8 4 8 8 70 0 74 b8 8*0 30 48 84 84 fc 0 0 30 78 cc 78 48 48 0 0 78 fc fc
  //   30 30 30 0 40 b0 4 b 40 b0 4 b 7*fc 0 fc fc fc 0 fc fc fc 0 fc fc fc 0 cf cf cf 0 fb 78 87 cb 3c bf
  //   4c f3 b4 b4 fc 84 fc b4 b4 0 7f 4f cb fb bb bf b7 f7 4 83 bb 3b 8 70 77 37 84 fc 84 84 84 fc 84 84 0
  //   ff 44 44 44 ff 0 0 0 f 30 48 84 f3 8c 84 0 c0 30 48 84 3c c4 84 8c f3 84 48 30 f 0 0 c4 3c 84 48 30
  //   c0 0 0 84 84 84 b4 b4 84 84 84 0 ff 0 38 0 ff 0 0 0 fc 84 fc fc 0 84 0 fc 84 f4 cc fc cc fc 0 ff 88
  //   80 b0 c0 84 88 80 0 fc 30 4*fc 0 38 44 44 4*38 0 38 7c 7c 4*38 0 0 c0 c0 30 8 fc fc 0 0 c c 30 40 fc
  //   fc 0 fc cc 84 fc 84 84 fc 0 fc b4 fc b4 fc b4 fc 0 38 44 40 f8 40 40 fc 0 0 fc b4 cc 84 b4 fc 0 0 0
  //   48 30 48 0 0 0 8 34 30 78 30 30 b0 40 0 fc 84 cc cc cc fc 0 0 fc cc 84 cc cc fc 0 0 fc cc cc 84 cc
  //   fc 0 0 fc cc cc cc 84 fc 0 30 48 84 0 30 48 84 0 84 48 30 0 84 48 30 0 33 88 44 33 44 88 33 0 88 33
  //   44 88 44 33 88 0 30 0 30 40 80 84 78 0 ff bb f ff f7 83 cf fc 0 0 0 fc 4 4 0 0 0 fc fc fc 0 30 30 0
  //   0 fc fc 0 cc fc fc 0 0 fc f4 fc 84 84 fc 0 0 34 48 b0 48 34 0 0 0 b0 48 34 48 b0 0 0 84 30 84 30 84
  //   30 84 30 b4 4b b4 4b b4 4b b4 4b bc f7 bc f7 bc f7 bc f7 11*30 f0 6*30 f0 30 f0 30 30 30 48 48 48 c8
  //   4*48 0 0 0 f8 4*48 0 0 f0 30 f0 30 30 30 48 48 c8 8 c8 11*48 0 0 f8 8 c8 5*48 c8 8 f8 0 0 0 4*48 f8
  //   0 0 0 30 30 f0 30 f0 6*0 f0 7*30 3f 4*0 30 30 30 ff 7*0 ff 7*30 3f 4*30 0 0 0 ff 4*0 30 30 30 ff
  //   6*30 3f 30 3f 30 30 30 4*48 4f 5*48 4f 40 7f 5*0 7f 40 4f 5*48 cf 0 ff 5*0 ff 0 cf 5*48 4f 40 4f 48
  //   48 48 0 0 ff 0 ff 0 0 0 48 48 cf 0 cf 48 48 48 30 30 ff 0 ff 0 0 0 48 48 48 ff 6*0 ff 0 ff 30 30 30
  //   0 0 0 ff 7*48 7f 4*0 30 30 3f 30 3f 5*0 3f 30 3f 30 30 30 0 0 0 7f 7*48 ff 4*48 30 30 ff 30 ff 6*30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
endmodule

module VIN (
  input  [15:0] i,
  input  set,
  input  clk,
  output [15:0] o
);

  Register #(.trigger("falling"), .width(16)) register_1 (.D(i), .en(set), .Q(o), .clk(clk));  // open: clr
endmodule

module VOUT (
  input  [15:0] i,
  input  set,
  input  clk,
  output [15:0] o
);

  Register #(.trigger("falling"), .width(16)) register_1 (.D(i), .en(set), .Q(o), .clk(clk));  // open: clr
endmodule

module Sub1 (
  input  a,
  input  b,
  input  bi,
  output diff,
  output bo
);

  wire co1_out, co2_out, not_1_out, not_2_out, sum1_out;

  xor sum1 (sum1_out, a, b);
  not not_1 (not_1_out, a);
  not not_2 (not_2_out, sum1_out);
  and co2 (co2_out, not_2_out, bi);
  and co1 (co1_out, not_1_out, b);
  xor sum2 (diff, sum1_out, bi);
  or or_1 (bo, co2_out, co1_out);
endmodule

module Sub8 (
  input  bi,
  input  [7:0] a,
  input  [7:0] b,
  output [7:0] o,
  output co
);

  wire sub1_1_bo, sub1_2_bo, sub1_3_bo, sub1_4_bo, sub1_5_bo, sub1_6_bo, sub1_7_bo;

  Sub1 sub1_1 (.bo(sub1_1_bo), .diff(o[0]), .bi(bi), .a(a[0]), .b(b[0]));
  Sub1 sub1_2 (.bo(sub1_2_bo), .diff(o[1]), .bi(sub1_1_bo), .a(a[1]), .b(b[1]));
  Sub1 sub1_3 (.bo(sub1_3_bo), .diff(o[2]), .bi(sub1_2_bo), .a(a[2]), .b(b[2]));
  Sub1 sub1_4 (.bo(sub1_4_bo), .diff(o[3]), .bi(sub1_3_bo), .a(a[3]), .b(b[3]));
  Sub1 sub1_5 (.bo(sub1_5_bo), .diff(o[4]), .bi(sub1_4_bo), .a(a[4]), .b(b[4]));
  Sub1 sub1_6 (.bo(sub1_6_bo), .diff(o[5]), .bi(sub1_5_bo), .a(a[5]), .b(b[5]));
  Sub1 sub1_7 (.bo(sub1_7_bo), .diff(o[6]), .bi(sub1_6_bo), .a(a[6]), .b(b[6]));
  Sub1 sub1_8 (.bo(co), .diff(o[7]), .bi(sub1_7_bo), .a(a[7]), .b(b[7]));
endmodule
