// Logisim project 22_bigram_test.circ as structural Verilog
module M (
  input  i,
  input  s,
  output o
);

  wire nand_1_out, nand_2_out, nand_4_out;

  nand nand_1 (nand_1_out, i, s);
  nand nand_2 (nand_2_out, nand_1_out, s);
  nand nand_3 (o, nand_1_out, nand_4_out);
  nand nand_4 (nand_4_out, o, nand_2_out);
endmodule

module M8 (
  input  in_1,
  input  [7:0] in_2,
  output [7:0] out_3
);

  M m_1 (.o(out_3[0]), .i(in_2[0]), .s(in_1));
  M m_2 (.o(out_3[1]), .i(in_2[1]), .s(in_1));
  M m_3 (.o(out_3[2]), .i(in_2[2]), .s(in_1));
  M m_4 (.o(out_3[3]), .i(in_2[3]), .s(in_1));
  M m_5 (.o(out_3[4]), .i(in_2[4]), .s(in_1));
  M m_6 (.o(out_3[5]), .i(in_2[5]), .s(in_1));
  M m_7 (.o(out_3[6]), .i(in_2[6]), .s(in_1));
  M m_8 (.o(out_3[7]), .i(in_2[7]), .s(in_1));
endmodule

module Enabler (
  input  [15:0] in_1,
  input  in_2,
  output [15:0] out_3
);

  assign out_3 = in_2 ? in_1 : 16'bz;  // Controlled_Buffer controlled_buffer_1
endmodule

module Decoder3x8 (
  input  in_1,
  input  in_2,
  input  in_3,
  output out_4,
  output out_5,
  output out_6,
  output out_7,
  output out_8,
  output out_9,
  output out_10,
  output out_11
);

  wire not_1_out, not_2_out, not_3_out;

  not not_1 (not_1_out, in_1);
  not not_2 (not_2_out, in_2);
  not not_3 (not_3_out, in_3);
  and and_1 (out_4, not_1_out, not_2_out, not_3_out);
  and and_2 (out_5, not_1_out, not_2_out, in_3);
  and and_3 (out_6, not_1_out, in_2, not_3_out);
  and and_4 (out_7, not_1_out, in_2, in_3);
  and and_5 (out_8, in_1, not_2_out, not_3_out);
  and and_6 (out_9, in_1, not_2_out, in_3);
  and and_7 (out_10, in_1, in_2, not_3_out);
  and and_8 (out_11, in_1, in_2, in_3);
endmodule

module ZEROer (
  input  [15:0] in,
  output out
);

  wire or_1_out;

  or or_1 (or_1_out, in[0], in[1], in[2], in[3], in[4], in[5], in[6], in[7], in[8], in[9], in[10], in[11], in[12], in[13], in[14], in[15]);
  not not_1 (out, or_1_out);
endmodule

module Clk (
  output clk,
  output clk_e,
  output clk_s
);

  wire clk_raw_out, j_k_ff_1_qn;

  Clock clk_raw (.out(clk_raw_out));
  J_K_Flip_Flop j_k_ff_1 (.J(1'b1), .clk(clk_raw_out), .K(1'b1), .Q(clk), .Qn(j_k_ff_1_qn));  // open: preset, reset
  nand nand_1 (clk_e, clk_raw_out, j_k_ff_1_qn);
  and and_1 (clk_s, clk_raw_out, clk);
endmodule

module Stepper (
  input  clk,
  input  reset,
  output _1,
  output _2,
  output _3,
  output _4,
  output _5,
  output _6,
  output _7
);

  wire d_ff_1_q, d_ff_2_q, d_ff_3_q, d_ff_4_q, d_ff_5_q, d_ff_6_q, d_ff_7_q, d_ff_8_q, d_ff_9_q, d_ff_10_q,
       d_ff_11_q, not_1_out, not_2_out, not_3_out, not_4_out, not_5_out, not_6_out, not_7_out, not_8_out,
       or_1_out, or_2_out;

  not not_1 (not_1_out, clk);
  not not_2 (not_2_out, _7);
  or or_1 (or_1_out, _7, clk);
  or or_2 (or_2_out, _7, not_1_out);
  D_Flip_Flop d_ff_1 (.clk(or_1_out), .D(not_2_out), .Q(d_ff_1_q), .reset(reset));  // open: Qn, preset
  or or_3 (_1, _7, not_3_out);
  not not_3 (not_3_out, d_ff_2_q);
  D_Flip_Flop d_ff_2 (.clk(or_2_out), .D(d_ff_1_q), .Q(d_ff_2_q), .reset(reset));  // open: Qn, preset
  and and_1 (_2, d_ff_2_q, not_4_out);
  not not_4 (not_4_out, d_ff_4_q);
  D_Flip_Flop d_ff_3 (.clk(or_1_out), .D(d_ff_2_q), .Q(d_ff_3_q), .reset(reset));  // open: Qn, preset
  D_Flip_Flop d_ff_4 (.clk(or_2_out), .D(d_ff_3_q), .Q(d_ff_4_q), .reset(reset));  // open: Qn, preset
  and and_2 (_3, d_ff_4_q, not_5_out);
  D_Flip_Flop d_ff_5 (.clk(or_1_out), .D(d_ff_4_q), .Q(d_ff_5_q), .reset(reset));  // open: Qn, preset
  not not_5 (not_5_out, d_ff_6_q);
  D_Flip_Flop d_ff_6 (.clk(or_2_out), .D(d_ff_5_q), .Q(d_ff_6_q), .reset(reset));  // open: Qn, preset
  and and_3 (_4, d_ff_6_q, not_6_out);
  D_Flip_Flop d_ff_7 (.clk(or_1_out), .D(d_ff_6_q), .Q(d_ff_7_q), .reset(reset));  // open: Qn, preset
  not not_6 (not_6_out, d_ff_8_q);
  D_Flip_Flop d_ff_8 (.clk(or_2_out), .D(d_ff_7_q), .Q(d_ff_8_q), .reset(reset));  // open: Qn, preset
  D_Flip_Flop d_ff_9 (.clk(or_1_out), .D(d_ff_8_q), .Q(d_ff_9_q), .reset(reset));  // open: Qn, preset
  and and_4 (_5, d_ff_8_q, not_7_out);
  not not_7 (not_7_out, d_ff_10_q);
  D_Flip_Flop d_ff_10 (.clk(or_2_out), .D(d_ff_9_q), .Q(d_ff_10_q), .reset(reset));  // open: Qn, preset
  and and_5 (_6, d_ff_10_q, not_8_out);
  not not_8 (not_8_out, _7);
  D_Flip_Flop d_ff_11 (.clk(or_1_out), .D(d_ff_10_q), .Q(d_ff_11_q), .reset(reset));  // open: Qn, preset
  D_Flip_Flop d_ff_12 (.clk(or_2_out), .D(d_ff_11_q), .Q(_7), .reset(reset));  // open: Qn, preset
endmodule

module ControlUnit (
  input  [15:0] IR_CODE,
  input  CLK,
  input  [15:0] FLAG_DATA,
  input  INTR,
  output PC_INC,
  output ACC_E,
  output PC_S,
  output RA_S,
  output MAR_S,
  output RA_E,
  output [3:0] RBbits,
  output PC_E,
  output RB_S,
  output IR_S,
  output RB_E,
  output RAM_S,
  output TMP_S,
  output RAM_E,
  output CI_E,
  output ACC_S,
  output [3:0] RAbits,
  output FLAG_S,
  output IR_E,
  output FLAG_CLR,
  output SP_INC,
  output SP_DEC,
  output SP_S,
  output SP_E,
  output TMP_C,
  output FLAG_E,
  output [3:0] IO_MODE_OUT,
  output [3:0] OP_OUT,
  output G_CLK_S,
  output INT_CLR,
  output [15:0] INT_SVC_OUT
);

  wire A_2_out, A_out, and_5_out, and_6_out, and_7_out, and_8_out, and_10_out, and_12_out, BR_ON, BRN_ON,
       C_2_out, C_out, comparator_1_gt, comparator_2_lt, comparator_3_gt, comparator_4_lt, comparator_5_gt,
       comparator_6_lt, comparator_7_eq, E_2_out, E_out, END_INST, HLT_E, INT_CHK, INT_E, INT_ON, LOAD_STEP,
       not_1_out, not_3_out, not_4_out, not_5_out, not_6_out, or_1_out, or_3_out, or_4_out, RST_MCS, TEST_A,
       TEST_C, TEST_E, TEST_Z, UPDATE_RB, Z_2_out, Z_out;
  wire [4:0] STEP;
  wire [5:0] interupt_ROM_p1;
  wire [12:0] Micro_code_ROM_p1;
  wire [25:0] multiplexer_1_out;
  wire [31:0] INT_OUT0, INT_OUT1, MC_OUT0, MC_OUT1;

  LED u_pc_inc (.in(PC_INC));
  LED u_pc_s (.in(PC_S));
  LED u_mar_s (.in(MAR_S));
  LED u_pc_e (.in(PC_E));
  LED u_ir_s (.in(IR_S));
  LED u_flag_s (.in(FLAG_S));
  LED u_ir_e (.in(IR_E));
  LED u_flag_clr (.in(FLAG_CLR));
  LED u_ram_s (.in(RAM_S));
  LED u_ram_e (.in(RAM_E));
  LED u_acc_s (.in(ACC_S));
  LED i_o (.in(IO_MODE_OUT[0]));
  LED d_a (.in(IO_MODE_OUT[1]));
  LED ioclk_s (.in(IO_MODE_OUT[2]));
  LED ioclk_e (.in(IO_MODE_OUT[3]));
  LED plus_sp (.in(SP_INC));
  LED minus_sp (.in(SP_DEC));
  LED u_sp_s (.in(SP_S));
  LED u_sp_e (.in(SP_E));
  // ROM #(.addrWidth(6), .dataWidth(32), .line("dual")) interupt_ROM: pin names not known; wires that end beside it: interupt_ROM_p1, INT_OUT0, INT_OUT1
  Multiplier #(.width(6)) multiplier_1 (.a({1'b0, STEP}), .b(6'b000010), .out(interupt_ROM_p1));  // open: cin, cout
  // ROM #(.addrWidth(13), .dataWidth(32), .line("dual")) Micro_code_ROM: pin names not known; wires that end beside it: Micro_code_ROM_p1, MC_OUT0, MC_OUT1
  Multiplier #(.width(13)) multiplier_2 (
    .a({1'b0, IR_CODE[15:8], STEP[3:0]}), .b(13'h2), .out(Micro_code_ROM_p1));  // open: cin, cout
  LED u_acc_e (.in(ACC_E));
  LED u_tmp_c (.in(TMP_C));
  LED u_ra_s (.in(RA_S));
  LED u_ra_e (.in(RA_E));
  LED u_rb_s (.in(RB_S));
  LED u_rb_e (.in(RB_E));
  LED u_tmp_s (.in(TMP_S));
  LED u_ci_e (.in(CI_E));
  and and_1 (OP_OUT[0], CI_E, and_5_out, IR_CODE[8]);
  and and_2 (OP_OUT[1], CI_E, and_5_out, IR_CODE[9]);
  and and_3 (OP_OUT[2], CI_E, and_5_out, IR_CODE[10]);
  and and_4 (OP_OUT[3], CI_E, and_5_out, IR_CODE[11]);
  Multiplexer #(.enable("false"), .width(32)) multiplexer_1 (
    .in0(MC_OUT0), .in1(INT_OUT0),
    .out({END_INST, TMP_C, INT_CHK, INT_E, INT_CLR, G_CLK_S, multiplexer_1_out}), .sel(INT_ON));
  Multiplexer #(.enable("false"), .width(32)) multiplexer_2 (
    .in0(MC_OUT1), .in1(INT_OUT1),
    .out({PC_INC, PC_S, PC_E, MAR_S, IR_S, RAM_S, RAM_E, ACC_S, ACC_E, RA_S, RA_E, RB_S, RB_E, TMP_S, CI_E, IO_MODE_OUT[2], IO_MODE_OUT[3], FLAG_S, FLAG_E, FLAG_CLR, IO_MODE_OUT[0], IO_MODE_OUT[1], TEST_C, TEST_A, TEST_E, TEST_Z, IR_E, SP_INC, SP_DEC, SP_S, SP_E, HLT_E}),
    .sel(INT_ON));
  not not_1 (not_1_out, HLT_E);
  Counter #(.max('h1f), .width(5)) counter_1 (
    .load(LOAD_STEP), .D(5'b00111), .count(not_1_out), .Q(STEP), .clk(CLK), .clr(RST_MCS));  // open: carry
  and and_5 (and_5_out, IR_CODE[15], IR_CODE[14]);
  and and_6 (and_6_out, IR_CODE[9], IR_CODE[10], IR_CODE[11]);
  not not_2 (UPDATE_RB, and_6_out);
  Enabler enabler_1 (.out_3(INT_SVC_OUT), .in_2(INT_E), .in_1(16'hffdf));
  and C (C_out, TEST_C, FLAG_DATA[3]);
  and A (A_out, TEST_A, FLAG_DATA[2]);
  and E (E_out, TEST_E, FLAG_DATA[1]);
  and Z (Z_out, TEST_Z, FLAG_DATA[0]);
  and and_7 (and_7_out, INTR, INT_CHK);
  Comparator #(.mode("unsigned")) comparator_1 (.a(IR_CODE[15:8]), .b(8'h40), .gt(comparator_1_gt));  // open: eq, lt
  Comparator #(.mode("unsigned")) comparator_2 (.a(IR_CODE[15:8]), .b(8'h47), .lt(comparator_2_lt));  // open: gt, eq
  or or_1 (or_1_out, C_out, A_out, E_out, Z_out);
  and and_8 (and_8_out, comparator_1_gt, comparator_2_lt);
  LED u_int_CHK (.in(INT_CHK));
  LED int_10 (.in(INTR));
  LED EVAC (.in(INT_CLR));
  and and_9 (BR_ON, and_8_out, or_1_out);
  LED u_int_on (.in(INT_ON));
  Register #(.width(1)) INTF (.D(INTR), .Q(INT_ON), .clk(INT_CHK), .clr(INT_CLR));  // open: en
  or or_2 (RST_MCS, and_7_out, END_INST, INT_CLR);
  not not_3 (not_3_out, FLAG_DATA[3]);
  not not_4 (not_4_out, FLAG_DATA[2]);
  not not_5 (not_5_out, FLAG_DATA[1]);
  not not_6 (not_6_out, FLAG_DATA[0]);
  and C_2 (C_2_out, TEST_C, not_3_out);
  and A_2 (A_2_out, TEST_A, not_4_out);
  and E_2 (E_2_out, TEST_E, not_5_out);
  and Z_2 (Z_2_out, TEST_Z, not_6_out);
  Comparator #(.mode("unsigned")) comparator_3 (.a(IR_CODE[15:8]), .b(8'h47), .gt(comparator_3_gt));  // open: eq, lt
  Comparator #(.mode("unsigned")) comparator_4 (.a(IR_CODE[15:8]), .b(8'h50), .lt(comparator_4_lt));  // open: gt, eq
  and and_10 (and_10_out, comparator_3_gt, comparator_4_lt);
  or or_3 (or_3_out, C_2_out, A_2_out, E_2_out, Z_2_out);
  and and_11 (BRN_ON, and_10_out, or_3_out);
  Comparator #(.mode("unsigned")) comparator_5 (.a(IR_CODE[15:8]), .b(8'h40), .gt(comparator_5_gt));  // open: eq, lt
  Comparator #(.mode("unsigned")) comparator_6 (.a(IR_CODE[15:8]), .b(8'h50), .lt(comparator_6_lt));  // open: gt, eq
  and and_12 (and_12_out, comparator_5_gt, comparator_6_lt);
  Comparator #(.width(5)) comparator_7 (.a(STEP), .b(5'b00011), .eq(comparator_7_eq));  // open: gt, lt
  or or_4 (or_4_out, BR_ON, BRN_ON);
  and and_13 (LOAD_STEP, and_12_out, comparator_7_eq, or_4_out);

  assign RAbits = IR_CODE[7:4];
  assign RBbits = IR_CODE[3:0];

  // Other names for the same wires on the sheet: DATA_ADDR = IO_MODE_OUT[1]; IN_OUT = IO_MODE_OUT[0];
  //   IOCLK_E = IO_MODE_OUT[3]; IOCLK_S = IO_MODE_OUT[2]; GMODE_CLK_S = G_CLK_S; EVAC_END = INT_CLR;
  //   FZ = FLAG_DATA[0]; FE = FLAG_DATA[1]; FA = FLAG_DATA[2]; FC = FLAG_DATA[3]; INT10 = INTR;
  //   OPERAND_CODE[7:0] = IR_CODE[7:0]; OPRB_00 = IR_CODE[0]; RB_bits[3:0] = IR_CODE[3:0]; OPRB_01 = IR_CODE[1];
  //   OPRB_02 = IR_CODE[2]; OPRB_03 = IR_CODE[3]; OPRA_00 = IR_CODE[4]; RA_bits[3:0] = IR_CODE[7:4];
  //   OPRA_01 = IR_CODE[5]; OPRA_02 = IR_CODE[6]; OPRA_03 = IR_CODE[7]; OP_00 = IR_CODE[8];
  //   OP_CODE[7:0] = IR_CODE[15:8]; OP_01 = IR_CODE[9]; OP_02 = IR_CODE[10]; OP_03 = IR_CODE[11]; OP_04 = IR_CODE[12];
  //   OP_05 = IR_CODE[13]; OP_06 = IR_CODE[14]; OP_07 = IR_CODE[15]

  // Notes on the sheet:
  //   Control Signals
  //   contents of interupt_ROM (hex, n*v repeats v):
  //   0 1000000a 0 24000000 0 1000000a 0 4002000 10000000 40000000 8000000 0 80000000
  //   contents of Micro_code_ROM (hex, n*v repeats v):
  //   compressed eJztWUFywyAMvOsVOuckKNOS52Ty/z/UxuAIgkBMJ7Hbkks8wEpaSWDJEH7Q9kNCf4uP9nqh2gRI
  //   E29BEJoA3KfAp0frdFqgq/6kiI378rPL8sUDjsw2mM2gi87B5Bkw/sCInRORRscyKQ+YNaUIfIiw
  //   gkX56AZ1ogjo5QE6WgF+lwAKI5iEZXmgYVQ0XpbWNi3/uU+vdn98FsZiTAfv5J3yFkHOs59+kPFM
  //   EqpOIyGLmnQm4u2INYxyHEF1Ju1nP4zsn6N5s1FbbtJnFpxm9dQzqu1jym1S0QQVTShrgjonX1UE
  //   PUo8+ApKIX+gx6iXIqKiGfCKphnwifhLCBfHgNWXsYYqsoo3Io6N+vQYk87Xs7tVl+bFaXM7FjXc
  //   Sdq0/4tgozEpwDfjJxX0h39i8LnJqtZwQTnhvG+grquuerkmguBKd8mlAui39ecT8UrE50VoMpRN
  //   8UlotBEGt/rHoP1i60D77pyIiZiIEyII7/Hf2FB97oXr8jYNixXFIn+ddsSNHZVrIXBzFF/usjli
  //   DQwlvl87zQhgyzpQiJObiS7ZesnXsQ6GyMqfcWXrQE9WVRWLTh32J5dvySW5Me019ks3WqAV3srT
  //   5nXZ+br2fHmXcv0TmkQ53/964bxnUggP12kDwhV3m9VMgCHhwfL+N8yH5TAqXDhdmwFVnWaFW8aa
  //   93YwBuNwfCMwERNxOOIbg6aADQ==
  //   ALU OP OUT Module
  //   Micro state Counter
  //   IR Code bits
  //   OPERAND Code bits
  //   Branch If
  //   Step reset and Next Instruction
  //   OP Code bits
  //   Branch If Not
  //   Branch PC Step
endmodule

module CPU (
  input  in_1,
  input  in_2
);

  wire clock_1_out, clock_2_out, controlunit_1_acc_e, controlunit_1_acc_s, controlunit_1_ci_e,
       controlunit_1_flag_clr, controlunit_1_flag_e, controlunit_1_flag_s, controlunit_1_g_clk_s,
       controlunit_1_int_clr, controlunit_1_ir_e, controlunit_1_ir_s, controlunit_1_mar_s,
       controlunit_1_pc_e, controlunit_1_pc_inc, controlunit_1_pc_s, controlunit_1_ra_e, controlunit_1_ra_s,
       controlunit_1_ram_e, controlunit_1_ram_s, controlunit_1_rb_e, controlunit_1_rb_s,
       controlunit_1_sp_dec, controlunit_1_sp_e, controlunit_1_sp_inc, controlunit_1_sp_s,
       controlunit_1_tmp_c, controlunit_1_tmp_s, flag_register_1_ct_o, keyboard_1_avail;
  wire [3:0] controlunit_1_io_mode_out, controlunit_1_op_out, controlunit_1_rabits, controlunit_1_rbbits;
  wire [7:0] keyboard_1_data, vga_1_px, vga_1_py;
  wire [15:0] alu_1_flag_out, alu_1_out, flag_register_1_out, instruction_register_1_out, mar_1_out,
       ram_1_dout, register_files_1_out, temp_register_1_out, vga_1_out;

  Register_Files register_files_1 (
    .OUT(register_files_1_out), .RA_SEL(controlunit_1_rabits), .RB_SEL(controlunit_1_rbbits),
    .IN(register_files_1_out), .CLK(clock_1_out), .SET_RA(controlunit_1_ra_s), .SET_RB(controlunit_1_rb_s),
    .EN_RB(controlunit_1_rb_e), .EN_RA(controlunit_1_ra_e));
  ALU alu_1 (
    .OUT(alu_1_out), .FLAG_OUT(alu_1_flag_out), .CI(flag_register_1_ct_o), .IN_A(register_files_1_out),
    .IN_B(temp_register_1_out), .OP_IN(controlunit_1_op_out));
  Flag_Register flag_register_1 (
    .OUT(flag_register_1_out), .OUT2(register_files_1_out), .CT_O(flag_register_1_ct_o), .IN(alu_1_flag_out),
    .CLK(clock_1_out), .SET(controlunit_1_flag_s), .CLR(controlunit_1_flag_clr), .EN(controlunit_1_flag_e),
    .CT_S(controlunit_1_tmp_s), .CT_E(controlunit_1_ci_e));
  Temp_Register temp_register_1 (
    .OUT(temp_register_1_out), .SET(controlunit_1_tmp_s), .CLK(clock_1_out), .RESET(controlunit_1_tmp_c),
    .IN(register_files_1_out));
  Accumulator accumulator_1 (
    .OUT(register_files_1_out), .CLK(clock_1_out), .SET(controlunit_1_acc_s), .IN(alu_1_out),
    .EN(controlunit_1_acc_e));
  Keyboard #(.asciiwidth(8)) keyboard_1 (
    .clk(clock_1_out), .re(in_1), .clr(controlunit_1_int_clr), .avail(keyboard_1_avail),
    .data(keyboard_1_data[6:0]));
  ControlUnit controlunit_1 (
    .IO_MODE_OUT(controlunit_1_io_mode_out), .PC_INC(controlunit_1_pc_inc), .PC_S(controlunit_1_pc_s),
    .MAR_S(controlunit_1_mar_s), .PC_E(controlunit_1_pc_e), .IR_S(controlunit_1_ir_s),
    .RAM_S(controlunit_1_ram_s), .RAM_E(controlunit_1_ram_e), .ACC_S(controlunit_1_acc_s),
    .FLAG_S(controlunit_1_flag_s), .IR_E(controlunit_1_ir_e), .FLAG_CLR(controlunit_1_flag_clr),
    .SP_INC(controlunit_1_sp_inc), .SP_DEC(controlunit_1_sp_dec), .SP_S(controlunit_1_sp_s),
    .SP_E(controlunit_1_sp_e), .TMP_C(controlunit_1_tmp_c), .FLAG_E(controlunit_1_flag_e),
    .INT_SVC_OUT(register_files_1_out), .RBbits(controlunit_1_rbbits), .RAbits(controlunit_1_rabits),
    .INT_CLR(controlunit_1_int_clr), .ACC_E(controlunit_1_acc_e), .RA_S(controlunit_1_ra_s),
    .RA_E(controlunit_1_ra_e), .RB_S(controlunit_1_rb_s), .RB_E(controlunit_1_rb_e),
    .TMP_S(controlunit_1_tmp_s), .CI_E(controlunit_1_ci_e), .OP_OUT(controlunit_1_op_out),
    .G_CLK_S(controlunit_1_g_clk_s), .INTR(keyboard_1_avail), .IR_CODE(instruction_register_1_out),
    .FLAG_DATA(flag_register_1_out), .CLK(clock_1_out));
  KBD_CTRL kbd_ctrl_1 (
    .OUT(register_files_1_out), .IN(keyboard_1_data), .CLR(keyboard_1_avail),
    .IO_MODE(controlunit_1_io_mode_out));
  VGA vga_1 (
    .PX(vga_1_px), .PY(vga_1_py), .OUT(vga_1_out), .IO_MODE(controlunit_1_io_mode_out),
    .IN(register_files_1_out), .G_MODE(controlunit_1_g_clk_s));
  Clock clock_1 (.out(clock_1_out));
  Stack_Pointer stack_pointer_1 (
    .OUT(register_files_1_out), .IN(register_files_1_out), .CLK(clock_1_out), .EN(controlunit_1_sp_e),
    .INC_IN(controlunit_1_sp_inc), .DEC_IN(controlunit_1_sp_dec), .SET(controlunit_1_sp_s));
  MAR mar_1 (.OUT(mar_1_out), .IN(register_files_1_out), .SET(controlunit_1_mar_s), .CLK(clock_1_out));
  RAM_part #(.addrWidth(16), .dataWidth(16), .\type ("nonvolatile")) ram_1 (
    .addr(mar_1_out), .we(controlunit_1_ram_s), .clk(clock_1_out), .din(register_files_1_out),
    .dout(ram_1_dout));
  Instruction_Register instruction_register_1 (
    .OUT(instruction_register_1_out), .OUTL(register_files_1_out), .IN(register_files_1_out),
    .SET(controlunit_1_ir_s), .CLK(clock_1_out), .EN(controlunit_1_ir_e));
  Program_Counter program_counter_1 (
    .OUT(register_files_1_out), .IN(register_files_1_out), .plus_1(controlunit_1_pc_inc), .CLK(clock_1_out),
    .SET(controlunit_1_pc_s), .EN(controlunit_1_pc_e));
  assign register_files_1_out = controlunit_1_ram_e ? ram_1_dout : 16'bz;  // Controlled_Buffer controlled_buffer_1
  Clock clock_2 (.out(clock_2_out));
  // RGB_Video #(.height(256), .width(256)) rgb_video_1: pin names not known; wires that end beside it: in_2, clock_2_out, 1'b1, vga_1_px, vga_1_py, vga_1_out
  // Pins of 7 and 8 bits meet at keyboard_1_data
endmodule

module R0 (
  input  [31:0] i,
  input  set,
  input  en,
  output [31:0] o
);

  wire [31:0] register_1_q;

  Register #(.trigger("high"), .width(32)) register_1 (.D(i), .en(set), .Q(register_1_q), .clk(1'b1));  // open: clr
  // Enabler enabler_1: pin names not known; wires that end beside it: register_1_q, en, o
endmodule

module R1 (
  input  [31:0] i,
  input  set,
  input  en,
  output [31:0] o
);

  wire [31:0] register_1_q;

  Register #(.trigger("high"), .width(32)) register_1 (.D(i), .en(set), .Q(register_1_q), .clk(1'b1));  // open: clr
  // Enabler enabler_1: pin names not known; wires that end beside it: register_1_q, en, o
endmodule

module R2 (
  input  [31:0] i,
  input  set,
  input  en,
  output [31:0] o
);

  wire [31:0] register_1_q;

  Register #(.trigger("high"), .width(32)) register_1 (.D(i), .en(set), .Q(register_1_q), .clk(1'b1));  // open: clr
  // Enabler enabler_1: pin names not known; wires that end beside it: register_1_q, en, o
endmodule

module R3 (
  input  [31:0] i,
  input  set,
  input  en,
  output [31:0] o
);

  wire [31:0] register_1_q;

  Register #(.trigger("high"), .width(32)) register_1 (.D(i), .en(set), .Q(register_1_q), .clk(1'b1));  // open: clr
  // Enabler enabler_1: pin names not known; wires that end beside it: register_1_q, en, o
endmodule

module Bus1 (
  input  [15:0] in_1,
  input  bus1_e,
  output [15:0] out_3
);

  wire not_1_out;

  not not_1 (not_1_out, bus1_e);
  assign out_3 = not_1_out ? in_1 : 16'bz;  // Controlled_Buffer controlled_buffer_1
  assign out_3 = bus1_e ? 16'h1 : 16'bz;  // Controlled_Buffer controlled_buffer_2
endmodule

module Decoder_2x4 (
  input  a,
  input  b,
  output _01,
  output o2,
  output o3,
  output o4
);

  wire not_1_out, not_2_out;

  not not_1 (not_1_out, a);
  not not_2 (not_2_out, b);
  and and_1 (_01, not_1_out, not_2_out);
  and and_2 (o2, a, not_2_out);
  and and_3 (o3, not_1_out, b);
  and and_4 (o4, a, b);
endmodule

module Decoder_2x4_inverted (
  input  a,
  input  b,
  output _01,
  output o2,
  output o3,
  output o4
);

  wire not_1_out, not_2_out;

  not not_1 (not_1_out, a);
  not not_2 (not_2_out, b);
  and and_1 (_01, not_1_out, not_2_out);
  and and_2 (o2, a, not_2_out);
  and and_3 (o3, not_1_out, b);
  and and_4 (o4, a, b);
endmodule

module Flag_Register (
  input  EN,
  input  [15:0] IN,
  input  CT_E,
  input  CT_S,
  input  CLK,
  input  SET,
  input  CLR,
  output [15:0] OUT,
  output [15:0] OUT2,
  output CT_O
);

  wire bitselector_1_out, register_2_q;
  wire [3:0] bitselector_2_out;

  Register #(.width(16)) register_1 (.D(IN), .en(SET), .Q(OUT), .clk(CLK), .clr(CLR));
  Enabler enabler_1 (.out_3(OUT2), .in_2(EN), .in_1(OUT));
  BitSelector #(.width(16)) bitselector_1 (.in(OUT), .out(bitselector_1_out), .sel(4'b0011));
  BitSelector #(.group(4), .width(16)) bitselector_2 (.in(OUT), .out(bitselector_2_out), .sel(2'b00));
  Register #(.width(1)) register_2 (.D(bitselector_1_out), .en(CT_S), .Q(register_2_q), .clk(CLK));  // open: clr
  LED Z (.in(bitselector_2_out[0]));
  LED E (.in(bitselector_2_out[1]));
  LED A (.in(bitselector_2_out[2]));
  LED C (.in(bitselector_2_out[3]));
  and and_1 (CT_O, register_2_q, CT_E);
endmodule

module IN_MAR16 (
  input  [15:0] i,
  input  set,
  output [15:0] o
);

  Register #(.trigger("high"), .width(16)) register_1 (.D(i), .en(set), .Q(o), .clk(1'b1));  // open: clr
endmodule

module OUT_MAR16 (
  input  [15:0] i,
  input  set,
  output [15:0] o
);

  Register #(.trigger("high"), .width(16)) register_1 (.D(i), .en(set), .Q(o), .clk(1'b1));  // open: clr
endmodule

module MAR (
  input  [15:0] IN,
  input  SET,
  input  CLK,
  output [15:0] OUT
);

  Register #(.width(16)) register_1 (.D(IN), .en(SET), .Q(OUT), .clk(CLK));  // open: clr
endmodule

module VGA (
  input  [3:0] IO_MODE,
  input  G_MODE,
  input  [15:0] IN,
  output [7:0] PX,
  output [7:0] PY,
  output [15:0] OUT
);

  wire ADDR_S, clk_2_out, clk_out, DATA_S, f_co, fx_counter_carry, MODE, multiplexer_2_out, not_1_out;
  wire [2:0] dx, dy;
  wire [7:0] px0, py0, rom_1_data;
  wire [15:0] adder_3_out, ascii_px, controlled_buffer_1_out, FONT_DATA, GRAPHIC_POS, multiplexer_1_out,
       multiplexer_3_out, register_1_q, zero_one_1_out_2, zero_one_2_out_2, zero_one_3_out_2,
       zero_one_4_out_2, zero_one_5_out_2, zero_one_6_out_2, zero_one_7_out_2, zero_one_8_out_2;

  assign controlled_buffer_1_out = DATA_S ? IN : 16'bz;  // Controlled_Buffer controlled_buffer_1
  Adder_part adder_1 (.a(px0), .b({{5{1'b0}}, dx}), .out(PX));  // open: cin, cout
  Multiplier #(.mode("unsigned"), .width(16)) multiplier_1 (
    .a(16'h8), .b(controlled_buffer_1_out), .out(ascii_px));  // open: cin, cout
  not not_1 (not_1_out, IO_MODE[1]);
  Adder_part adder_2 (.a(py0), .b({{5{1'b0}}, dy}), .out(PY));  // open: cin, cout
  VIN vin_1 (.o(GRAPHIC_POS), .i(IN), .set(ADDR_S), .clk(IO_MODE[2]));
  Register #(.trigger("falling"), .width(16)) register_1 (
    .D(ascii_px), .en(DATA_S), .Q(register_1_q), .clk(IO_MODE[2]));  // open: clr
  and and_1 (ADDR_S, IO_MODE[1], IO_MODE[0]);
  and and_2 (DATA_S, not_1_out, IO_MODE[0]);
  Adder_part #(.width(16)) adder_3 (.a({{13{1'b0}}, dy}), .b(register_1_q), .out(adder_3_out));  // open: cin, cout
  ROM #(.addrWidth(16)) rom_1 (.addr(adder_3_out), .data(rom_1_data));
  Multiplier #(.mode("unsigned")) multiplier_2 (.a(GRAPHIC_POS[7:0]), .b(8'h8), .out(px0));  // open: cin, cout
  Multiplier #(.mode("unsigned")) multiplier_3 (.a(GRAPHIC_POS[15:8]), .b(8'h8), .out(py0));  // open: cin, cout
  Register #(.trigger("falling"), .width(1)) INTF (.D(IN[0]), .Q(MODE), .clk(G_MODE));  // open: en, clr
  Clock #(.phaseOffset(1)) clk (.out(clk_out));
  zero_one zero_one_1 (.out_2(zero_one_1_out_2), .binary(rom_1_data[7]));
  zero_one zero_one_2 (.out_2(zero_one_2_out_2), .binary(rom_1_data[6]));
  zero_one zero_one_3 (.out_2(zero_one_3_out_2), .binary(rom_1_data[5]));
  zero_one zero_one_4 (.out_2(zero_one_4_out_2), .binary(rom_1_data[4]));
  zero_one zero_one_5 (.out_2(zero_one_5_out_2), .binary(rom_1_data[3]));
  zero_one zero_one_6 (.out_2(zero_one_6_out_2), .binary(rom_1_data[2]));
  zero_one zero_one_7 (.out_2(zero_one_7_out_2), .binary(rom_1_data[1]));
  zero_one zero_one_8 (.out_2(zero_one_8_out_2), .binary(rom_1_data[0]));
  Counter #(.max('h7), .width(3)) fx_counter (
    .count(1'b1), .Q(dx), .carry(fx_counter_carry), .clk(clk_out));  // open: load, D, clr
  Multiplexer #(.enable("false"), .width(16)) multiplexer_1 (
    .in0({PY, PX}), .in1(GRAPHIC_POS), .out(multiplexer_1_out), .sel(MODE));
  Multiplexer #(.enable("false")) multiplexer_2 (.in0(1'b1), .in1(DATA_S), .out(multiplexer_2_out), .sel(MODE));
  Multiplexer #(.enable("false"), .width(16)) multiplexer_3 (
    .in0(FONT_DATA), .in1(IN), .out(multiplexer_3_out), .sel(MODE));
  Counter #(.max('h7), .trigger("falling"), .width(3)) fy_counter (
    .count(1'b1), .Q(dy), .carry(f_co), .clk(fx_counter_carry));  // open: load, D, clr
  RAM_part #(.addrWidth(16), .dataWidth(16), .trigger("high")) Video_RAM (
    .addr(multiplexer_1_out), .we(multiplexer_2_out), .clk(clk_2_out), .din(multiplexer_3_out), .dout(OUT));
  Clock #(.phaseOffset(1)) clk_2 (.out(clk_2_out));
  Multiplexer #(.enable("false"), .select(3), .width(16)) multiplexer_4 (
    .in0(zero_one_1_out_2), .in1(zero_one_2_out_2), .in2(zero_one_3_out_2), .in3(zero_one_4_out_2),
    .in4(zero_one_5_out_2), .in5(zero_one_6_out_2), .in6(zero_one_7_out_2), .in7(zero_one_8_out_2),
    .out(FONT_DATA), .sel(dx));

  // Other names for the same wires on the sheet: font_y[2:0] = dy; FONT_POS[15:0] = {PY, PX}; IN_DATA[15:0] = IN;
  //   IN_OUT = IO_MODE[0]; DATA_ADDR = IO_MODE[1]; IOCLK_S = IO_MODE[2]; IOCLK_E = IO_MODE[3]

  // Notes on the sheet:
  //   contents of rom_1 (hex, n*v repeats v):
  //   8*0 78 84 cc 84 b4 84 78 0 78 fc b4 fc 84 cc 78 0 0 48 fc fc fc 78 30 0 0 30 78 fc 78 30 0 0 30 78
  //   30 fc fc 30 78 0 0 30 78 fc fc 30 78 0 0 0 38 7c 7c 38 0 0 ff ff c7 83 83 c7 ff ff 0 0 38 44 44 38 0
  //   0 ff ff c7 bb bb c7 ff ff fc fc cc 84 b4 fc fc 0 fc fc b4 84 cc fc fc 0 fc fc c4 8c c4 fc fc 0 fc fc
  //   8c c4 8c fc fc 0 38 bb 7c c7 c7 7c bb 38 0 80 f0 fc f0 80 0 0 0 4 3c fc 3c 4 0 0 30 78 fc 30 30 fc
  //   78 30 5*44 0 44 0 7c b4 b4 74 34 34 34 0 7c c3 78 cc cc 78 8c 78 5*0 7c 7c 0 38 7c ff 38 ff 7c 38 ff
  //   30 78 fc 4*30 0 4*30 fc 78 30 0 0 30 38 fc 38 30 0 0 0 30 70 ff 70 30 0 0 0 fc 84 b4 84 fc fc 0 0 0
  //   44 ff 44 4*0 30 30 78 78 fc 0 0 0 fc 78 78 30 30 10*0 5*30 0 30 0 34 34 48 5*0 48 48 fc 48 fc 48 48
  //   0 30 7c 80 78 4 f8 30 0 84 88 8 30 40 44 84 0 30 48 30 74 b8 88 74 0 8 8 30 5*0 c 30 40 40 40 30 c 0
  //   70 8 4 4 4 8 70 0 0 0 44 38 44 4*0 30 30 fc 30 30 7*0 30 30 30 0 0 0 fc 9*0 30 30 0 4 8 8 30 40 40
  //   80 0 78 84 8c b4 c4 84 78 0 30 70 4*30 fc 0 78 84 4 38 40 84 fc 0 78 84 4 38 4 84 78 0 c 34 44 84 fc
  //   4 4 0 fc 80 f8 4 4 84 78 0 38 40 80 f8 84 84 78 0 fc 84 4 8 30 30 30 0 78 84 84 78 84 84 78 0 78 84
  //   84 7c 4 8 70 0 0 30 30 0 0 30 30 0 0 30 30 0 0 30 30 30 8 30 40 80 40 30 8 0 0 0 fc 0 0 fc 0 0 80 40
  //   30 8 30 40 80 0 78 84 4 8 30 0 30 0 7c 83 bb bb bf 80 7c 0 78 84 fc 4*84 0 f8 84 f8 84 84 84 f8 0 78
  //   84 80 80 80 84 78 0 f8 5*84 f8 0 fc 80 f0 80 80 80 fc 0 fc 80 f0 4*80 0 7c 80 8c 84 84 84 78 0 84 84
  //   fc 4*84 0 78 5*30 78 0 5*4 84 78 0 84 88 f0 88 84 84 84 0 6*80 fc 0 84 cc b4 4*84 0 84 c4 b4 8c 84
  //   84 84 0 78 5*84 78 0 f8 84 f8 4*80 0 78 4*84 88 74 0 f8 84 f8 4*84 0 7c 80 78 4 4 84 78 0 fc 6*30 0
  //   6*84 78 0 4*84 48 48 30 0 4*84 b4 cc 84 0 84 48 30 48 84 84 84 0 84 48 5*30 0 fc 4 8 30 40 80 fc 0
  //   78 5*40 78 0 80 40 40 30 8 8 4 0 78 5*8 78 0 30 48 84 12*0 fc 30 30 8 7*0 78 4 7c 84 7c 0 80 80 b8
  //   c4 84 84 f8 0 0 0 78 84 80 84 78 0 4 4 74 8c 84 84 7c 0 0 0 78 84 fc 80 7c 0 c 30 7c 4*30 0 0 0 7c
  //   84 84 7c 4 f8 80 80 b8 c4 84 84 84 0 30 0 5*30 0 4 0 4 4 4 84 84 78 40 40 44 48 70 48 44 0 6*30 8 0
  //   0 0 c8 b4 b4 84 84 0 0 0 f8 4*84 0 0 0 78 84 84 84 78 0 0 0 b8 c4 84 f8 80 80 0 0 74 8c 84 7c 4 4 0
  //   0 b8 c4 80 80 80 0 0 0 7c 80 78 4 f8 0 30 30 78 30 30 30 8 0 0 0 4*84 7c 0 0 0 84 84 84 48 30 0 0 0
  //   84 84 b4 b4 7c 0 0 0 84 48 30 48 84 0 0 0 84 84 84 7c 4 f8 0 0 fc 8 30 40 fc 0 c 30 30 40 30 30 c 0
  //   30 30 30 0 30 30 30 0 70 8 8 4 8 8 70 0 74 b8 8*0 30 48 84 84 fc 0 0 30 78 cc 78 48 48 0 0 78 fc fc
  //   30 30 30 0 40 b0 4 b 40 b0 4 b 7*fc 0 fc fc fc 0 fc fc fc 0 fc fc fc 0 cf cf cf 0 fb 78 87 cb 3c bf
  //   4c f3 b4 b4 fc 84 fc b4 b4 0 7f 4f cb fb bb bf b7 f7 4 83 bb 3b 8 70 77 37 84 fc 84 84 84 fc 84 84 0
  //   ff 44 44 44 ff 0 0 0 f 30 48 84 f3 8c 84 0 c0 30 48 84 3c c4 84 8c f3 84 48 30 f 0 0 c4 3c 84 48 30
  //   c0 0 0 84 84 84 b4 b4 84 84 84 0 ff 0 38 0 ff 0 0 0 fc 84 fc fc 0 84 0 fc 84 f4 cc fc cc fc 0 ff 88
  //   80 b0 c0 84 88 80 0 fc 30 4*fc 0 38 44 44 4*38 0 38 7c 7c 4*38 0 0 c0 c0 30 8 fc fc 0 0 c c 30 40 fc
  //   fc 0 fc cc 84 fc 84 84 fc 0 fc b4 fc b4 fc b4 fc 0 38 44 40 f8 40 40 fc 0 0 fc b4 cc 84 b4 fc 0 0 0
  //   48 30 48 0 0 0 8 34 30 78 30 30 b0 40 0 fc 84 cc cc cc fc 0 0 fc cc 84 cc cc fc 0 0 fc cc cc 84 cc
  //   fc 0 0 fc cc cc cc 84 fc 0 30 48 84 0 30 48 84 0 84 48 30 0 84 48 30 0 33 88 44 33 44 88 33 0 88 33
  //   44 88 44 33 88 0 30 0 30 40 80 84 78 0 ff bb f ff f7 83 cf fc 0 0 0 fc 4 4 0 0 0 fc fc fc 0 30 30 0
  //   0 fc fc 0 cc fc fc 0 0 fc f4 fc 84 84 fc 0 0 34 48 b0 48 34 0 0 0 b0 48 34 48 b0 0 0 84 30 84 30 84
  //   30 84 30 b4 4b b4 4b b4 4b b4 4b bc f7 bc f7 bc f7 bc f7 11*30 f0 6*30 f0 30 f0 30 30 30 48 48 48 c8
  //   4*48 0 0 0 f8 4*48 0 0 f0 30 f0 30 30 30 48 48 c8 8 c8 11*48 0 0 f8 8 c8 5*48 c8 8 f8 0 0 0 4*48 f8
  //   0 0 0 30 30 f0 30 f0 6*0 f0 7*30 3f 4*0 30 30 30 ff 7*0 ff 7*30 3f 4*30 0 0 0 ff 4*0 30 30 30 ff
  //   6*30 3f 30 3f 30 30 30 4*48 4f 5*48 4f 40 7f 5*0 7f 40 4f 5*48 cf 0 ff 5*0 ff 0 cf 5*48 4f 40 4f 48
  //   48 48 0 0 ff 0 ff 0 0 0 48 48 cf 0 cf 48 48 48 30 30 ff 0 ff 0 0 0 48 48 48 ff 6*0 ff 0 ff 30 30 30
  //   0 0 0 ff 7*48 7f 4*0 30 30 3f 30 3f 5*0 3f 30 3f 30 30 30 0 0 0 7f 7*48 ff 4*48 30 30 ff 30 ff 6*30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
endmodule

module Accumulator (
  input  [15:0] IN,
  input  SET,
  input  EN,
  input  CLK,
  output [15:0] OUT
);

  wire [15:0] register_1_q;

  Register #(.width(16)) register_1 (.D(IN), .en(SET), .Q(register_1_q), .clk(CLK));  // open: clr
  Enabler enabler_1 (.out_3(OUT), .in_2(EN), .in_1(register_1_q));
endmodule

module Program_Counter (
  input  SET,
  input  [15:0] IN,
  input  plus_1,
  input  CLK,
  input  EN,
  output [15:0] OUT
);

  wire [15:0] counter_1_q;

  Counter #(.max('hffff), .width(16)) counter_1 (
    .load(SET), .D(IN), .count(plus_1), .Q(counter_1_q), .clk(CLK));  // open: carry, clr
  Enabler enabler_1 (.out_3(OUT), .in_2(EN), .in_1(counter_1_q));
endmodule

module Instruction_Register (
  input  [15:0] IN,
  input  SET,
  input  CLK,
  input  EN,
  output [15:0] OUT,
  output [15:0] OUTL
);

  Register #(.width(16)) register_1 (.D(IN), .en(SET), .Q(OUT), .clk(CLK));  // open: clr
  Enabler8 enabler8_1 (.out_3(OUTL[7:0]), .in_2(EN), .in_1(OUT[7:0]));
  assign OUTL[15:8] = EN ? {8{1'b0}} : 8'bz;  // Controlled_Buffer controlled_buffer_1
endmodule

module Temp_Register (
  input  [15:0] IN,
  input  SET,
  input  CLK,
  input  RESET,
  output [15:0] OUT
);

  Register #(.width(16)) register_1 (.D(IN), .en(SET), .Q(OUT), .clk(CLK), .clr(RESET));
endmodule

module Adder1 (
  input  a,
  input  b,
  input  ci,
  output sum,
  output co
);

  wire co1_out, co2_out, sum1_out;

  xor sum1 (sum1_out, a, b);
  xor sum2 (sum, sum1_out, ci);
  and co2 (co2_out, sum1_out, ci);
  and co1 (co1_out, a, b);
  or or_1 (co, co2_out, co1_out);
endmodule

module Adder8 (
  input  ci,
  input  [7:0] a,
  input  [7:0] b,
  output [7:0] o,
  output co
);

  wire adder1_1_co, adder1_2_co, adder1_3_co, adder1_4_co, adder1_5_co, adder1_6_co, adder1_7_co;

  Adder1 adder1_1 (.co(adder1_1_co), .sum(o[0]), .ci(ci), .a(a[0]), .b(b[0]));
  Adder1 adder1_2 (.co(adder1_2_co), .sum(o[1]), .ci(adder1_1_co), .a(a[1]), .b(b[1]));
  Adder1 adder1_3 (.co(adder1_3_co), .sum(o[2]), .ci(adder1_2_co), .a(a[2]), .b(b[2]));
  Adder1 adder1_4 (.co(adder1_4_co), .sum(o[3]), .ci(adder1_3_co), .a(a[3]), .b(b[3]));
  Adder1 adder1_5 (.co(adder1_5_co), .sum(o[4]), .ci(adder1_4_co), .a(a[4]), .b(b[4]));
  Adder1 adder1_6 (.co(adder1_6_co), .sum(o[5]), .ci(adder1_5_co), .a(a[5]), .b(b[5]));
  Adder1 adder1_7 (.co(adder1_7_co), .sum(o[6]), .ci(adder1_6_co), .a(a[6]), .b(b[6]));
  Adder1 adder1_8 (.co(co), .sum(o[7]), .ci(adder1_7_co), .a(a[7]), .b(b[7]));
endmodule

module Adder (
  input  ci,
  input  [15:0] a,
  input  [15:0] b,
  output [15:0] o,
  output co
);

  wire adder8_1_co;

  Adder8 adder8_1 (.co(adder8_1_co), .o(o[7:0]), .a(a[7:0]), .b(b[7:0]), .ci(ci));
  Adder8 adder8_2 (.co(co), .o(o[15:8]), .a(a[15:8]), .b(b[15:8]), .ci(adder8_1_co));
endmodule

module Adder32 (
  input  ci,
  input  [31:0] a,
  input  [31:0] b,
  output [31:0] o,
  output co
);

  wire adder_1_co;

  Adder adder_1 (.co(adder_1_co), .o(o[15:0]), .b(b[15:0]), .a(a[15:0]), .ci(ci));
  Adder adder_2 (.co(co), .o(o[31:16]), .b(b[31:16]), .a(a[31:16]), .ci(adder_1_co));
endmodule

module XORer (
  input  [15:0] a,
  input  [15:0] b,
  output [15:0] o
);

  assign o = a ^ b;  // XOR_Gate xor_1, 16 bits wide
endmodule

module XNORer (
  input  [15:0] a,
  input  [15:0] b,
  output [15:0] o
);

  assign o = ~(a ^ b);  // XNOR_Gate xnor_1, 16 bits wide
endmodule

module NORer (
  input  [15:0] a,
  input  [15:0] b,
  output [15:0] o
);

  assign o = ~(a | b);  // NOR_Gate nor_1, 16 bits wide
endmodule

module NANDer (
  input  [15:0] a,
  input  [15:0] b,
  output [15:0] o
);

  assign o = ~(a & b);  // NAND_Gate nand_1, 16 bits wide
endmodule

module ANDer (
  input  [15:0] a,
  input  [15:0] b,
  output [15:0] o
);

  assign o = a & b;  // AND_Gate and_1, 16 bits wide
endmodule

module ORer (
  input  [15:0] a,
  input  [15:0] b,
  output [15:0] o
);

  assign o = a | b;  // OR_Gate or_1, 16 bits wide
endmodule

module Inverter (
  input  [15:0] in_1,
  output [15:0] out_2
);

  assign out_2 = ~in_1;  // NOT_Gate not_1, 16 bits wide
endmodule

module low5_out (
  input  [4:0] i,
  output [31:0] o
);


  assign o = {{27{1'b0}}, i};
endmodule

module Negator (
  input  [15:0] in_1,
  output [15:0] out_2
);

  wire [15:0] inverter_1_out_2;

  Inverter inverter_1 (.out_2(inverter_1_out_2), .in_1(in_1));
  Adder adder_1 (.o(out_2), .b(16'h1), .a(inverter_1_out_2));  // open: co, ci
endmodule

module Subtractor (
  input  bi,
  input  [15:0] a,
  input  [15:0] b,
  output [15:0] o,
  output bo
);

  wire sub8_1_co;

  Sub8 sub8_1 (.co(sub8_1_co), .o(o[7:0]), .a(a[7:0]), .b(b[7:0]), .bi(bi));
  Sub8 sub8_2 (.co(bo), .o(o[15:8]), .a(a[15:8]), .b(b[15:8]), .bi(sub8_1_co));
endmodule

module low7_out (
  input  [6:0] i,
  output [31:0] o
);


  assign o = {{25{1'b0}}, i};
endmodule

module SHL (
  input  si,
  input  [15:0] i,
  output [15:0] o,
  output so
);

  wire [14:0] register_1_q;

  Register #(.trigger("high"), .width(16)) register_1 (
    .D(i), .en(1'b1), .Q({so, register_1_q}), .clk(1'b1));  // open: clr
  Register #(.trigger("high"), .width(16)) register_2 (
    .D({register_1_q, si}), .en(1'b1), .Q(o), .clk(1'b1));  // open: clr
endmodule

module SHR (
  input  [15:0] i,
  input  si,
  output so,
  output [15:0] o
);

  wire [15:1] register_1_q;

  Register #(.trigger("high"), .width(16)) register_1 (
    .D(i), .en(1'b1), .Q({register_1_q, so}), .clk(1'b1));  // open: clr
  Register #(.trigger("high"), .width(16)) register_2 (
    .D({si, register_1_q}), .en(1'b1), .Q(o), .clk(1'b1));  // open: clr
endmodule

module ALU (
  input  [15:0] IN_A,
  input  [15:0] IN_B,
  input  CI,
  input  [3:0] OP_IN,
  output [15:0] FLAG_OUT,
  output [15:0] OUT
);

  wire adder_1_co, and_1_out, and_2_out, and_3_out, and_4_out, decoder_1_out0, decoder_1_out1,
       decoder_1_out2, decoder_1_out3, decoder_1_out8, decoder_1_out9, decoder_1_out10, decoder_1_out11,
       decoder_1_out12, decoder_1_out13, decoder_1_out15, shl_1_so, shr_1_so, subtractor_1_bo;
  wire [15:0] adder_1_o, ander_1_o, dec_1_o, inc_1_o, inverter_1_out_2, orer_1_o, shl_1_o, shr_1_o,
       subtractor_1_o, xorer_1_o;

  Comparator #(.width(16)) comparator_1 (.a(IN_A), .b(IN_B), .gt(FLAG_OUT[2]), .eq(FLAG_OUT[1]));  // open: lt
  XORer xorer_1 (.o(xorer_1_o), .a(IN_A), .b(IN_B));
  ORer orer_1 (.o(orer_1_o), .a(IN_A), .b(IN_B));
  ANDer ander_1 (.o(ander_1_o), .a(IN_A), .b(IN_B));
  Inverter inverter_1 (.out_2(inverter_1_out_2), .in_1(IN_B));
  SHL shl_1 (.so(shl_1_so), .o(shl_1_o), .i(IN_B), .si(CI));
  SHR shr_1 (.so(shr_1_so), .o(shr_1_o), .i(IN_B), .si(CI));
  DEC dec_1 (.o(dec_1_o), .b(IN_B));
  INC inc_1 (.o(inc_1_o), .b(IN_B));
  Subtractor subtractor_1 (.bo(subtractor_1_bo), .o(subtractor_1_o), .b(IN_B), .a(IN_A), .bi(CI));
  Adder adder_1 (.co(adder_1_co), .o(adder_1_o), .b(IN_B), .a(IN_A), .ci(CI));
  Decoder #(.enable("false"), .select(4)) decoder_1 (
    .out0(decoder_1_out0), .out1(decoder_1_out1), .out2(decoder_1_out2), .out3(decoder_1_out3),
    .out8(decoder_1_out8), .out9(decoder_1_out9), .out10(decoder_1_out10), .out11(decoder_1_out11),
    .out12(decoder_1_out12), .out13(decoder_1_out13), .out15(decoder_1_out15), .sel(OP_IN));  // open: out4, out5, out6, out7, out14
  and and_1 (and_1_out, shl_1_so, decoder_1_out9);
  and and_2 (and_2_out, shr_1_so, decoder_1_out8);
  and and_3 (and_3_out, subtractor_1_bo, decoder_1_out1);
  and and_4 (and_4_out, adder_1_co, decoder_1_out0);
  Enabler enabler_1 (.out_3(OUT), .in_2(decoder_1_out13), .in_1(xorer_1_o));
  Enabler enabler_2 (.out_3(OUT), .in_2(decoder_1_out12), .in_1(orer_1_o));
  Enabler enabler_3 (.out_3(OUT), .in_2(decoder_1_out11), .in_1(ander_1_o));
  Enabler enabler_4 (.out_3(OUT), .in_2(decoder_1_out10), .in_1(inverter_1_out_2));
  Enabler enabler_5 (.out_3(OUT), .in_2(decoder_1_out9), .in_1(shl_1_o));
  Enabler enabler_6 (.out_3(OUT), .in_2(decoder_1_out8), .in_1(shr_1_o));
  Enabler enabler_7 (.out_3(OUT), .in_2(decoder_1_out3), .in_1(dec_1_o));
  Enabler enabler_8 (.out_3(OUT), .in_2(decoder_1_out2), .in_1(inc_1_o));
  Enabler enabler_9 (.out_3(OUT), .in_2(decoder_1_out1), .in_1(subtractor_1_o));
  Enabler enabler_10 (.out_3(OUT), .in_2(decoder_1_out0), .in_1(adder_1_o));
  assign OUT = decoder_1_out15 ? 16'h1 : 16'bz;  // Controlled_Buffer controlled_buffer_1
  ZEROer zeroer_1 (.out(FLAG_OUT[0]), .in(OUT));
  or or_1 (FLAG_OUT[3], and_1_out, and_2_out, and_3_out, and_4_out);

  assign FLAG_OUT[15:4] = {12{1'b0}};

  // Other names for the same wires on the sheet: ZERO = FLAG_OUT[0]; EQ = FLAG_OUT[1]; AL = FLAG_OUT[2];
  //   CO = FLAG_OUT[3]

  // Notes on the sheet:
  //   CMP
endmodule

module Register_Files (
  input  SET_RA,
  input  EN_RA,
  input  [15:0] IN,
  input  [3:0] RA_SEL,
  input  SET_RB,
  input  EN_RB,
  input  [3:0] RB_SEL,
  input  CLK,
  output [15:0] OUT
);

  wire R00_A, R00_AE, R00_AS, R00_B, R00_BE, R00_BS, R00_E, R00_S, R01_A, R01_AE, R01_AS, R01_B, R01_BE,
       R01_BS, R01_E, R01_S, R02_A, R02_AE, R02_AS, R02_B, R02_BE, R02_BS, R02_E, R02_S, R03_A, R03_AE,
       R03_AS, R03_B, R03_BE, R03_BS, R03_E, R03_S, R04_A, R04_AE, R04_AS, R04_B, R04_BE, R04_BS, R04_E,
       R04_S, R05_A, R05_AE, R05_AS, R05_B, R05_BE, R05_BS, R05_E, R05_S, R06_A, R06_AE, R06_AS, R06_B,
       R06_BE, R06_BS, R06_E, R06_S, R07_A, R07_AE, R07_AS, R07_B, R07_BE, R07_BS, R07_E, R07_S, R08_A,
       R08_AE, R08_AS, R08_B, R08_BE, R08_BS, R08_E, R08_S, R09_A, R09_AE, R09_AS, R09_B, R09_BE, R09_BS,
       R09_E, R09_S, R10_A, R10_AE, R10_AS, R10_B, R10_BE, R10_BS, R10_E, R10_S, R11_A, R11_AE, R11_AS,
       R11_B, R11_BE, R11_BS, R11_E, R11_S, R12_A, R12_AE, R12_AS, R12_B, R12_BE, R12_BS, R12_E, R12_S,
       R13_A, R13_AE, R13_AS, R13_B, R13_BE, R13_BS, R13_E, R13_S, R14_A, R14_AE, R14_AS, R14_B, R14_BE,
       R14_BS, R14_E, R14_S, R15_A, R15_AE, R15_AS, R15_B, R15_BE, R15_BS, R15_E, R15_S;

  Decoder #(.enable("false"), .select(4)) decoder_1 (
    .out0(R00_A), .out1(R01_A), .out2(R02_A), .out3(R03_A), .out4(R04_A), .out5(R05_A), .out6(R06_A),
    .out7(R07_A), .out8(R08_A), .out9(R09_A), .out10(R10_A), .out11(R11_A), .out12(R12_A), .out13(R13_A),
    .out14(R14_A), .out15(R15_A), .sel(RA_SEL));
  Decoder #(.enable("false"), .select(4)) decoder_2 (
    .out0(R00_B), .out1(R01_B), .out2(R02_B), .out3(R03_B), .out4(R04_B), .out5(R05_B), .out6(R06_B),
    .out7(R07_B), .out8(R08_B), .out9(R09_B), .out10(R10_B), .out11(R11_B), .out12(R12_B), .out13(R13_B),
    .out14(R14_B), .out15(R15_B), .sel(RB_SEL));
  and and_1 (R00_AS, R00_A, SET_RA);
  and and_2 (R01_AS, R01_A, SET_RA);
  and and_3 (R02_AS, R02_A, SET_RA);
  and and_4 (R03_AS, R03_A, SET_RA);
  and and_5 (R04_AS, R04_A, SET_RA);
  and and_6 (R05_AS, R05_A, SET_RA);
  and and_7 (R06_AS, R06_A, SET_RA);
  and and_8 (R07_AS, R07_A, SET_RA);
  and and_9 (R08_AS, R08_A, SET_RA);
  and and_10 (R09_AS, R09_A, SET_RA);
  and and_11 (R10_AS, R10_A, SET_RA);
  and and_12 (R11_AS, R11_A, SET_RA);
  and and_13 (R12_AS, R12_A, SET_RA);
  and and_14 (R13_AS, R13_A, SET_RA);
  and and_15 (R14_AS, R14_A, SET_RA);
  and and_16 (R15_AS, R15_A, SET_RA);
  and and_17 (R00_BS, R00_B, SET_RB);
  and and_18 (R01_BS, R01_B, SET_RB);
  and and_19 (R02_BS, R02_B, SET_RB);
  and and_20 (R03_BS, R03_B, SET_RB);
  and and_21 (R04_BS, R04_B, SET_RB);
  and and_22 (R05_BS, R05_B, SET_RB);
  and and_23 (R06_BS, R06_B, SET_RB);
  and and_24 (R07_BS, R07_B, SET_RB);
  and and_25 (R08_BS, R08_B, SET_RB);
  and and_26 (R09_BS, R09_B, SET_RB);
  and and_27 (R10_BS, R10_B, SET_RB);
  and and_28 (R11_BS, R11_B, SET_RB);
  and and_29 (R12_BS, R12_B, SET_RB);
  and and_30 (R13_BS, R13_B, SET_RB);
  and and_31 (R14_BS, R14_B, SET_RB);
  and and_32 (R15_BS, R15_B, SET_RB);
  and and_33 (R00_AE, R00_A, EN_RA);
  and and_34 (R01_AE, R01_A, EN_RA);
  and and_35 (R02_AE, R02_A, EN_RA);
  and and_36 (R03_AE, R03_A, EN_RA);
  and and_37 (R04_AE, R04_A, EN_RA);
  and and_38 (R05_AE, R05_A, EN_RA);
  and and_39 (R06_AE, R06_A, EN_RA);
  and and_40 (R07_AE, R07_A, EN_RA);
  and and_41 (R08_AE, R08_A, EN_RA);
  and and_42 (R09_AE, R09_A, EN_RA);
  and and_43 (R10_AE, R10_A, EN_RA);
  and and_44 (R11_AE, R11_A, EN_RA);
  and and_45 (R12_AE, R12_A, EN_RA);
  and and_46 (R13_AE, R13_A, EN_RA);
  and and_47 (R14_AE, R14_A, EN_RA);
  and and_48 (R15_AE, R15_A, EN_RA);
  and and_49 (R00_BE, R00_B, EN_RB);
  and and_50 (R01_BE, R01_B, EN_RB);
  and and_51 (R02_BE, R02_B, EN_RB);
  and and_52 (R03_BE, R03_B, EN_RB);
  and and_53 (R04_BE, R04_B, EN_RB);
  and and_54 (R05_BE, R05_B, EN_RB);
  and and_55 (R06_BE, R06_B, EN_RB);
  and and_56 (R07_BE, R07_B, EN_RB);
  and and_57 (R08_BE, R08_B, EN_RB);
  and and_58 (R09_BE, R09_B, EN_RB);
  and and_59 (R10_BE, R10_B, EN_RB);
  and and_60 (R11_BE, R11_B, EN_RB);
  and and_61 (R12_BE, R12_B, EN_RB);
  and and_62 (R13_BE, R13_B, EN_RB);
  and and_63 (R14_BE, R14_B, EN_RB);
  and and_64 (R15_BE, R15_B, EN_RB);
  or or_1 (R00_S, R00_AS, R00_BS);
  or or_2 (R01_S, R01_AS, R01_BS);
  or or_3 (R02_S, R02_AS, R02_BS);
  or or_4 (R03_S, R03_AS, R03_BS);
  or or_5 (R04_S, R04_AS, R04_BS);
  or or_6 (R05_S, R05_AS, R05_BS);
  or or_7 (R06_S, R06_AS, R06_BS);
  or or_8 (R07_S, R07_AS, R07_BS);
  or or_9 (R08_S, R08_AS, R08_BS);
  or or_10 (R09_S, R09_AS, R09_BS);
  or or_11 (R10_S, R10_AS, R10_BS);
  or or_12 (R11_S, R11_AS, R11_BS);
  or or_13 (R12_S, R12_AS, R12_BS);
  or or_14 (R13_S, R13_AS, R13_BS);
  or or_15 (R14_S, R14_AS, R14_BS);
  or or_16 (R15_S, R15_AS, R15_BS);
  or or_17 (R00_E, R00_AE, R00_BE);
  or or_18 (R01_E, R01_AE, R01_BE);
  or or_19 (R02_E, R02_AE, R02_BE);
  or or_20 (R03_E, R03_AE, R03_BE);
  or or_21 (R04_E, R04_AE, R04_BE);
  or or_22 (R05_E, R05_AE, R05_BE);
  or or_23 (R06_E, R06_AE, R06_BE);
  or or_24 (R07_E, R07_AE, R07_BE);
  or or_25 (R08_E, R08_AE, R08_BE);
  or or_26 (R09_E, R09_AE, R09_BE);
  or or_27 (R10_E, R10_AE, R10_BE);
  or or_28 (R11_E, R11_AE, R11_BE);
  or or_29 (R12_E, R12_AE, R12_BE);
  or or_30 (R13_E, R13_AE, R13_BE);
  or or_31 (R14_E, R14_AE, R14_BE);
  or or_32 (R15_E, R15_AE, R15_BE);
  Register32 r00 (.o(OUT), .set(R00_S), .i(IN), .CLK(CLK), .en(R00_E));
  Register32 r01 (.o(OUT), .set(R01_S), .i(IN), .CLK(CLK), .en(R01_E));
  Register32 r02 (.o(OUT), .set(R02_S), .i(IN), .CLK(CLK), .en(R02_E));
  Register32 r03 (.o(OUT), .set(R03_S), .i(IN), .CLK(CLK), .en(R03_E));
  Register32 r04 (.o(OUT), .set(R04_S), .i(IN), .CLK(CLK), .en(R04_E));
  Register32 r05 (.o(OUT), .set(R05_S), .i(IN), .CLK(CLK), .en(R05_E));
  Register32 r06 (.o(OUT), .set(R06_S), .i(IN), .CLK(CLK), .en(R06_E));
  Register32 r07 (.o(OUT), .set(R07_S), .i(IN), .CLK(CLK), .en(R07_E));
  Register32 r08 (.o(OUT), .set(R08_S), .i(IN), .CLK(CLK), .en(R08_E));
  Register32 r09 (.o(OUT), .set(R09_S), .i(IN), .CLK(CLK), .en(R09_E));
  Register32 r10 (.o(OUT), .set(R10_S), .i(IN), .CLK(CLK), .en(R10_E));
  Register32 r11 (.o(OUT), .set(R11_S), .i(IN), .CLK(CLK), .en(R11_E));
  Register32 r12 (.o(OUT), .set(R12_S), .i(IN), .CLK(CLK), .en(R12_E));
  Register32 r13 (.o(OUT), .set(R13_S), .i(IN), .CLK(CLK), .en(R13_E));
  Register32 r14 (.o(OUT), .set(R14_S), .i(IN), .CLK(CLK), .en(R14_E));
  Register32 r15 (.o(OUT), .set(R15_S), .i(IN), .CLK(CLK), .en(R15_E));
endmodule

module Register32 (
  input  [15:0] i,
  input  set,
  input  en,
  input  CLK,
  output [15:0] o
);

  wire [15:0] register_1_q;

  Register #(.width(16)) register_1 (.D(i), .en(set), .Q(register_1_q), .clk(CLK));  // open: clr
  Enabler enabler_1 (.out_3(o), .in_2(en), .in_1(register_1_q));
endmodule

module Data_Register (
  input  [15:0] i,
  input  set,
  input  en,
  input  CLK,
  output [15:0] o
);

  wire [15:0] register_1_q;

  Register #(.width(16)) register_1 (.D(i), .en(set), .Q(register_1_q), .clk(CLK));  // open: clr
  Enabler enabler_1 (.out_3(o), .in_2(en), .in_1(register_1_q));
endmodule

module Enabler8 (
  input  [7:0] in_1,
  input  in_2,
  output [7:0] out_3
);

  assign out_3 = in_2 ? in_1 : 8'bz;  // Controlled_Buffer controlled_buffer_1
endmodule

module INC (
  input  [15:0] b,
  output [15:0] o
);

  Adder adder_1 (.o(o), .b(b), .a(16'h1));  // open: co, ci
endmodule

module DEC (
  input  [15:0] b,
  output [15:0] o
);

  Subtractor subtractor_1 (.o(o), .b(b), .a(16'h1));  // open: bo, bi
endmodule

module Stack_Pointer (
  input  INC_IN,
  input  DEC_IN,
  input  SET,
  input  [15:0] IN,
  input  CLK,
  input  EN,
  output [15:0] OUT
);

  wire or_1_out;
  wire [15:0] counter_1_q;

  or or_1 (or_1_out, INC_IN, DEC_IN);
  Counter #(.max('hffff), .width(16)) counter_1 (
    .load(SET), .D(IN), .count(or_1_out), .Q(counter_1_q), .up(INC_IN), .clk(CLK));  // open: carry, clr
  Enabler enabler_1 (.out_3(OUT), .in_2(EN), .in_1(counter_1_q));
endmodule

module BIOS (
  input  [15:0] i,
  input  sa,
  input  sd,
  input  clk,
  input  e,
  output [15:0] o
);

  wire [15:0] mar_1_out, rom_1_data;

  MAR mar_1 (.OUT(mar_1_out));  // open: IN, SET, CLK
  ROM #(.addrWidth(16), .dataWidth(16)) rom_1 (.addr(mar_1_out), .data(rom_1_data));
  assign o = e ? rom_1_data : 16'bz;  // Controlled_Buffer controlled_buffer_1
  Hex_Digit_Display d3 (.value(rom_1_data[15:12]));  // open: dp
  Hex_Digit_Display d2 (.value(rom_1_data[11:8]));  // open: dp
  Hex_Digit_Display d1 (.value(rom_1_data[7:4]));  // open: dp
  Hex_Digit_Display d0 (.value(rom_1_data[3:0]));  // open: dp
endmodule

module zero_one (
  input  binary,
  output [15:0] out_2
);

  wire not_1_out;

  not not_1 (not_1_out, binary);
  assign out_2 = not_1_out ? {16{1'b0}} : 16'bz;  // Controlled_Buffer controlled_buffer_1
  assign out_2 = binary ? {16{1'b1}} : 16'bz;  // Controlled_Buffer controlled_buffer_2
endmodule

module framebuffer256x256 (
  input  [7:0] text_x,
  input  reset,
  input  [7:0] text_y,
  input  wrt,
  input  [7:0] in_5,
  input  r_s,
  output [15:0] out_7
);

  wire clk_2_out, f_co, fx_counter_carry, rgb_video_1_p2;
  wire [2:0] dx, dy;
  wire [7:0] px, px0, py, py0, rom_1_data;
  wire [15:0] adder_3_out, rgb_video_1_p6, zero_one_1_out_2, zero_one_2_out_2, zero_one_3_out_2,
       zero_one_4_out_2, zero_one_5_out_2, zero_one_6_out_2, zero_one_7_out_2, zero_one_8_out_2;

  Multiplier multiplier_1 (.a(text_x), .b(8'h8), .out(px0));  // open: cin, cout
  Multiplier multiplier_2 (.a(text_y), .b(8'h8), .out(py0));  // open: cin, cout
  Multiplier #(.width(16)) multiplier_3 (.a(16'h8), .b({{8{1'b0}}, in_5}), .out(out_7));  // open: cin, cout
  Adder_part adder_1 (.a(px0), .b({{5{1'b0}}, dx}), .out(px));  // open: cin, cout
  Adder_part adder_2 (.a(py0), .b({{5{1'b0}}, dy}), .out(py));  // open: cin, cout
  Adder_part #(.width(16)) adder_3 (.a({{13{1'b0}}, dy}), .b(out_7), .out(adder_3_out));  // open: cin, cout
  ROM #(.addrWidth(16)) rom_1 (.addr(adder_3_out), .data(rom_1_data));
  // RGB_Video #(.height(256), .width(256)) rgb_video_1: pin names not known; wires that end beside it: reset, rgb_video_1_p2, wrt, px, py, rgb_video_1_p6
  Clock #(.phaseOffset(1)) clk (.out(rgb_video_1_p2));
  Clock #(.phaseOffset(1)) clk_2 (.out(clk_2_out));
  zero_one zero_one_1 (.out_2(zero_one_1_out_2), .binary(rom_1_data[7]));
  zero_one zero_one_2 (.out_2(zero_one_2_out_2), .binary(rom_1_data[6]));
  zero_one zero_one_3 (.out_2(zero_one_3_out_2), .binary(rom_1_data[5]));
  zero_one zero_one_4 (.out_2(zero_one_4_out_2), .binary(rom_1_data[4]));
  zero_one zero_one_5 (.out_2(zero_one_5_out_2), .binary(rom_1_data[3]));
  zero_one zero_one_6 (.out_2(zero_one_6_out_2), .binary(rom_1_data[2]));
  zero_one zero_one_7 (.out_2(zero_one_7_out_2), .binary(rom_1_data[1]));
  zero_one zero_one_8 (.out_2(zero_one_8_out_2), .binary(rom_1_data[0]));
  Counter #(.max('h7), .width(3)) fx_counter (
    .count(r_s), .Q(dx), .carry(fx_counter_carry), .clk(clk_2_out));  // open: load, D, clr
  Counter #(.max('h7), .trigger("falling"), .width(3)) fy_counter (
    .count(r_s), .Q(dy), .carry(f_co), .clk(fx_counter_carry));  // open: load, D, clr
  Multiplexer #(.enable("false"), .select(3), .width(16)) multiplexer_1 (
    .in0(zero_one_1_out_2), .in1(zero_one_2_out_2), .in2(zero_one_3_out_2), .in3(zero_one_4_out_2),
    .in4(zero_one_5_out_2), .in5(zero_one_6_out_2), .in6(zero_one_7_out_2), .in7(zero_one_8_out_2),
    .out(rgb_video_1_p6), .sel(dx));

  // Other names for the same wires on the sheet: ascii_px[15:0] = out_7; font_y[2:0] = dy

  // Notes on the sheet:
  //   contents of rom_1 (hex, n*v repeats v):
  //   8*0 78 84 cc 84 b4 84 78 0 78 fc b4 fc 84 cc 78 0 0 48 fc fc fc 78 30 0 0 30 78 fc 78 30 0 0 30 78
  //   30 fc fc 30 78 0 0 30 78 fc fc 30 78 0 0 0 38 7c 7c 38 0 0 ff ff c7 83 83 c7 ff ff 0 0 38 44 44 38 0
  //   0 ff ff c7 bb bb c7 ff ff fc fc cc 84 b4 fc fc 0 fc fc b4 84 cc fc fc 0 fc fc c4 8c c4 fc fc 0 fc fc
  //   8c c4 8c fc fc 0 38 bb 7c c7 c7 7c bb 38 0 80 f0 fc f0 80 0 0 0 4 3c fc 3c 4 0 0 30 78 fc 30 30 fc
  //   78 30 5*44 0 44 0 7c b4 b4 74 34 34 34 0 7c c3 78 cc cc 78 8c 78 5*0 7c 7c 0 38 7c ff 38 ff 7c 38 ff
  //   30 78 fc 4*30 0 4*30 fc 78 30 0 0 30 38 fc 38 30 0 0 0 30 70 ff 70 30 0 0 0 fc 84 b4 84 fc fc 0 0 0
  //   44 ff 44 4*0 30 30 78 78 fc 0 0 0 fc 78 78 30 30 10*0 5*30 0 30 0 34 34 48 5*0 48 48 fc 48 fc 48 48
  //   0 30 7c 80 78 4 f8 30 0 84 88 8 30 40 44 84 0 30 48 30 74 b8 88 74 0 8 8 30 5*0 c 30 40 40 40 30 c 0
  //   70 8 4 4 4 8 70 0 0 0 44 38 44 4*0 30 30 fc 30 30 7*0 30 30 30 0 0 0 fc 9*0 30 30 0 4 8 8 30 40 40
  //   80 0 78 84 8c b4 c4 84 78 0 30 70 4*30 fc 0 78 84 4 38 40 84 fc 0 78 84 4 38 4 84 78 0 c 34 44 84 fc
  //   4 4 0 fc 80 f8 4 4 84 78 0 38 40 80 f8 84 84 78 0 fc 84 4 8 30 30 30 0 78 84 84 78 84 84 78 0 78 84
  //   84 7c 4 8 70 0 0 30 30 0 0 30 30 0 0 30 30 0 0 30 30 30 8 30 40 80 40 30 8 0 0 0 fc 0 0 fc 0 0 80 40
  //   30 8 30 40 80 0 78 84 4 8 30 0 30 0 7c 83 bb bb bf 80 7c 0 78 84 fc 4*84 0 f8 84 f8 84 84 84 f8 0 78
  //   84 80 80 80 84 78 0 f8 5*84 f8 0 fc 80 f0 80 80 80 fc 0 fc 80 f0 4*80 0 7c 80 8c 84 84 84 78 0 84 84
  //   fc 4*84 0 78 5*30 78 0 5*4 84 78 0 84 88 f0 88 84 84 84 0 6*80 fc 0 84 cc b4 4*84 0 84 c4 b4 8c 84
  //   84 84 0 78 5*84 78 0 f8 84 f8 4*80 0 78 4*84 88 74 0 f8 84 f8 4*84 0 7c 80 78 4 4 84 78 0 fc 6*30 0
  //   6*84 78 0 4*84 48 48 30 0 4*84 b4 cc 84 0 84 48 30 48 84 84 84 0 84 48 5*30 0 fc 4 8 30 40 80 fc 0
  //   78 5*40 78 0 80 40 40 30 8 8 4 0 78 5*8 78 0 30 48 84 12*0 fc 30 30 8 7*0 78 4 7c 84 7c 0 80 80 b8
  //   c4 84 84 f8 0 0 0 78 84 80 84 78 0 4 4 74 8c 84 84 7c 0 0 0 78 84 fc 80 7c 0 c 30 7c 4*30 0 0 0 7c
  //   84 84 7c 4 f8 80 80 b8 c4 84 84 84 0 30 0 5*30 0 4 0 4 4 4 84 84 78 40 40 44 48 70 48 44 0 6*30 8 0
  //   0 0 c8 b4 b4 84 84 0 0 0 f8 4*84 0 0 0 78 84 84 84 78 0 0 0 b8 c4 84 f8 80 80 0 0 74 8c 84 7c 4 4 0
  //   0 b8 c4 80 80 80 0 0 0 7c 80 78 4 f8 0 30 30 78 30 30 30 8 0 0 0 4*84 7c 0 0 0 84 84 84 48 30 0 0 0
  //   84 84 b4 b4 7c 0 0 0 84 48 30 48 84 0 0 0 84 84 84 7c 4 f8 0 0 fc 8 30 40 fc 0 c 30 30 40 30 30 c 0
  //   30 30 30 0 30 30 30 0 70 8 8 4 8 8 70 0 74 b8 8*0 30 48 84 84 fc 0 0 30 78 cc 78 48 48 0 0 78 fc fc
  //   30 30 30 0 40 b0 4 b 40 b0 4 b 7*fc 0 fc fc fc 0 fc fc fc 0 fc fc fc 0 cf cf cf 0 fb 78 87 cb 3c bf
  //   4c f3 b4 b4 fc 84 fc b4 b4 0 7f 4f cb fb bb bf b7 f7 4 83 bb 3b 8 70 77 37 84 fc 84 84 84 fc 84 84 0
  //   ff 44 44 44 ff 0 0 0 f 30 48 84 f3 8c 84 0 c0 30 48 84 3c c4 84 8c f3 84 48 30 f 0 0 c4 3c 84 48 30
  //   c0 0 0 84 84 84 b4 b4 84 84 84 0 ff 0 38 0 ff 0 0 0 fc 84 fc fc 0 84 0 fc 84 f4 cc fc cc fc 0 ff 88
  //   80 b0 c0 84 88 80 0 fc 30 4*fc 0 38 44 44 4*38 0 38 7c 7c 4*38 0 0 c0 c0 30 8 fc fc 0 0 c c 30 40 fc
  //   fc 0 fc cc 84 fc 84 84 fc 0 fc b4 fc b4 fc b4 fc 0 38 44 40 f8 40 40 fc 0 0 fc b4 cc 84 b4 fc 0 0 0
  //   48 30 48 0 0 0 8 34 30 78 30 30 b0 40 0 fc 84 cc cc cc fc 0 0 fc cc 84 cc cc fc 0 0 fc cc cc 84 cc
  //   fc 0 0 fc cc cc cc 84 fc 0 30 48 84 0 30 48 84 0 84 48 30 0 84 48 30 0 33 88 44 33 44 88 33 0 88 33
  //   44 88 44 33 88 0 30 0 30 40 80 84 78 0 ff bb f ff f7 83 cf fc 0 0 0 fc 4 4 0 0 0 fc fc fc 0 30 30 0
  //   0 fc fc 0 cc fc fc 0 0 fc f4 fc 84 84 fc 0 0 34 48 b0 48 34 0 0 0 b0 48 34 48 b0 0 0 84 30 84 30 84
  //   30 84 30 b4 4b b4 4b b4 4b b4 4b bc f7 bc f7 bc f7 bc f7 11*30 f0 6*30 f0 30 f0 30 30 30 48 48 48 c8
  //   4*48 0 0 0 f8 4*48 0 0 f0 30 f0 30 30 30 48 48 c8 8 c8 11*48 0 0 f8 8 c8 5*48 c8 8 f8 0 0 0 4*48 f8
  //   0 0 0 30 30 f0 30 f0 6*0 f0 7*30 3f 4*0 30 30 30 ff 7*0 ff 7*30 3f 4*30 0 0 0 ff 4*0 30 30 30 ff
  //   6*30 3f 30 3f 30 30 30 4*48 4f 5*48 4f 40 7f 5*0 7f 40 4f 5*48 cf 0 ff 5*0 ff 0 cf 5*48 4f 40 4f 48
  //   48 48 0 0 ff 0 ff 0 0 0 48 48 cf 0 cf 48 48 48 30 30 ff 0 ff 0 0 0 48 48 48 ff 6*0 ff 0 ff 30 30 30
  //   0 0 0 ff 7*48 7f 4*0 30 30 3f 30 3f 5*0 3f 30 3f 30 30 30 0 0 0 7f 7*48 ff 4*48 30 30 ff 30 ff 6*30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
endmodule

module VIN (
  input  [15:0] i,
  input  set,
  input  clk,
  output [15:0] o
);

  Register #(.trigger("falling"), .width(16)) register_1 (.D(i), .en(set), .Q(o), .clk(clk));  // open: clr
endmodule

module VOUT (
  input  [15:0] i,
  input  set,
  input  clk,
  output [15:0] o
);

  Register #(.trigger("falling"), .width(16)) register_1 (.D(i), .en(set), .Q(o), .clk(clk));  // open: clr
endmodule

module Sub1 (
  input  a,
  input  b,
  input  bi,
  output diff,
  output bo
);

  wire co1_out, co2_out, not_1_out, not_2_out, sum1_out;

  xor sum1 (sum1_out, a, b);
  not not_1 (not_1_out, a);
  not not_2 (not_2_out, sum1_out);
  and co2 (co2_out, not_2_out, bi);
  and co1 (co1_out, not_1_out, b);
  xor sum2 (diff, sum1_out, bi);
  or or_1 (bo, co2_out, co1_out);
endmodule

module Sub8 (
  input  bi,
  input  [7:0] a,
  input  [7:0] b,
  output [7:0] o,
  output co
);

  wire sub1_1_bo, sub1_2_bo, sub1_3_bo, sub1_4_bo, sub1_5_bo, sub1_6_bo, sub1_7_bo;

  Sub1 sub1_1 (.bo(sub1_1_bo), .diff(o[0]), .bi(bi), .a(a[0]), .b(b[0]));
  Sub1 sub1_2 (.bo(sub1_2_bo), .diff(o[1]), .bi(sub1_1_bo), .a(a[1]), .b(b[1]));
  Sub1 sub1_3 (.bo(sub1_3_bo), .diff(o[2]), .bi(sub1_2_bo), .a(a[2]), .b(b[2]));
  Sub1 sub1_4 (.bo(sub1_4_bo), .diff(o[3]), .bi(sub1_3_bo), .a(a[3]), .b(b[3]));
  Sub1 sub1_5 (.bo(sub1_5_bo), .diff(o[4]), .bi(sub1_4_bo), .a(a[4]), .b(b[4]));
  Sub1 sub1_6 (.bo(sub1_6_bo), .diff(o[5]), .bi(sub1_5_bo), .a(a[5]), .b(b[5]));
  Sub1 sub1_7 (.bo(sub1_7_bo), .diff(o[6]), .bi(sub1_6_bo), .a(a[6]), .b(b[6]));
  Sub1 sub1_8 (.bo(co), .diff(o[7]), .bi(sub1_7_bo), .a(a[7]), .b(b[7]));
endmodule

module keyboard (
  input  CAP,
  input  SH,
  input  CTR,
  input  ALT
);

  wire _0, _1, _2, _3, _4, _5, _6, _7, _8, _9, A, B, BS, C, D, DL, E, EN, ES, F, F1, F2, F3, F4, F5, F6, F7,
       F8, F9, FA, FB, FC, G, H, I, J, K, L, M, N, not_1_out, O, P, Q, R, S, SP, T, TB, tunnel, tunnel_t,
       tunnel_t_t, tunnel_t_t_t, tunnel_t_t_t_t, tunnel_t_t_t_t_t, tunnel_t_t_t_t_t_t, tunnel_t_t_t_t_t_t_t,
       tunnel_t_t_t_t_t_t_t_t, tunnel_t_t_t_t_t_t_t_t_t, tunnel_t_t_t_t_t_t_t_t_t_t,
       tunnel_t_t_t_t_t_t_t_t_t_t_t, tunnel_t_t_t_t_t_t_t_t_t_t_t_t, tunnel_t_t_t_t_t_t_t_t_t_t_t_t_t,
       tunnel_t_t_t_t_t_t_t_t_t_t_t_t_t_t, tunnel_t_t_t_t_t_t_t_t_t_t_t_t_t_t_t,
       tunnel_t_t_t_t_t_t_t_t_t_t_t_t_t_t_t_t, tunnel_t_t_t_t_t_t_t_t_t_t_t_t_t_t_t_t_t,
       tunnel_t_t_t_t_t_t_t_t_t_t_t_t_t_t_t_t_t_t, tunnel_t_t_t_t_t_t_t_t_t_t_t_t_t_t_t_t_t_t_t,
       tunnel_t_t_t_t_t_t_t_t_t_t_t_t_t_t_t_t_t_t_t_t, tunnel_t_t_t_t_t_t_t_t_t_t_t_t_t_t_t_t_t_t_t_t_t,
       tunnel_t_t_t_t_t_t_t_t_t_t_t_t_t_t_t_t_t_t_t_t_t_t,
       tunnel_t_t_t_t_t_t_t_t_t_t_t_t_t_t_t_t_t_t_t_t_t_t_t,
       tunnel_t_t_t_t_t_t_t_t_t_t_t_t_t_t_t_t_t_t_t_t_t_t_t_t,
       tunnel_t_t_t_t_t_t_t_t_t_t_t_t_t_t_t_t_t_t_t_t_t_t_t_t_t,
       tunnel_t_t_t_t_t_t_t_t_t_t_t_t_t_t_t_t_t_t_t_t_t_t_t_t_t_t,
       tunnel_t_t_t_t_t_t_t_t_t_t_t_t_t_t_t_t_t_t_t_t_t_t_t_t_t_t_t,
       tunnel_t_t_t_t_t_t_t_t_t_t_t_t_t_t_t_t_t_t_t_t_t_t_t_t_t_t_t_t,
       tunnel_t_t_t_t_t_t_t_t_t_t_t_t_t_t_t_t_t_t_t_t_t_t_t_t_t_t_t_t_t,
       tunnel_t_t_t_t_t_t_t_t_t_t_t_t_t_t_t_t_t_t_t_t_t_t_t_t_t_t_t_t_t_t,
       tunnel_t_t_t_t_t_t_t_t_t_t_t_t_t_t_t_t_t_t_t_t_t_t_t_t_t_t_t_t_t_t_t, U, V, W, X, Y, Z;
  wire [7:0] ascii_in, controlled_buffer_21_out, controlled_buffer_29_out;

  Button u_ES (.out(ES));
  Button u_F1 (.out(F1));
  Button button (.out(tunnel_t_t_t_t_t_t_t_t_t_t_t_t_t_t_t_t_t_t_t_t_t_t_t_t_t_t_t_t_t_t_t));
  Button button_2 (.out(tunnel));
  Button button_3 (.out(tunnel_t_t_t_t_t_t_t_t_t_t_t_t_t_t_t_t_t_t_t_t_t_t_t_t_t_t_t));
  Button u__1 (.out(_1));
  Button u_TB (.out(TB));
  assign ascii_in = BS ? 8'h8 : 8'bz;  // Controlled_Buffer controlled_buffer_1
  assign ascii_in = TB ? 8'h9 : 8'bz;  // Controlled_Buffer controlled_buffer_2
  assign ascii_in = EN ? 8'hd : 8'bz;  // Controlled_Buffer controlled_buffer_3
  assign ascii_in = ES ? 8'h1b : 8'bz;  // Controlled_Buffer controlled_buffer_4
  Button u_F2 (.out(F2));
  Button u_F3 (.out(F3));
  Button u_F4 (.out(F4));
  Button u_F5 (.out(F5));
  Button button_4 (.out(tunnel_t_t_t_t_t_t_t_t_t_t_t_t_t_t_t_t_t_t_t_t_t_t));
  Button button_5 (.out(tunnel_t_t));
  Button button_6 (.out(tunnel_t_t_t));
  Button button_7 (.out(tunnel_t_t_t_t));
  Button u__2 (.out(_2));
  Button u__3 (.out(_3));
  Button u__4 (.out(_4));
  Button u__5 (.out(_5));
  Button u_Q (.out(Q));
  Button u_W (.out(W));
  Button u_E (.out(E));
  Button u_R (.out(R));
  Button u_A (.out(A));
  Button u_S (.out(S));
  Button u_D (.out(D));
  Button u_F (.out(F));
  Button u_Z (.out(Z));
  Button u_X (.out(X));
  Button u_C (.out(C));
  Button u_F6 (.out(F6));
  Button u_F7 (.out(F7));
  Button u_F8 (.out(F8));
  Button button_8 (.out(tunnel_t_t_t_t_t_t_t_t_t_t_t_t_t_t_t_t_t_t_t_t_t_t_t_t_t_t));
  Button button_9 (.out(tunnel_t_t_t_t_t));
  Button button_10 (.out(tunnel_t_t_t_t_t_t_t_t_t));
  Button button_11 (.out(tunnel_t_t_t_t_t_t_t));
  Button u__6 (.out(_6));
  Button u__7 (.out(_7));
  Button u__8 (.out(_8));
  Button u__9 (.out(_9));
  Button u_T (.out(T));
  Button u_Y (.out(Y));
  Button u_U (.out(U));
  Button u_I (.out(I));
  Button u_G (.out(G));
  Button u_H (.out(H));
  Button u_J (.out(J));
  Button u_K (.out(K));
  Button u_V (.out(V));
  Button u_B (.out(B));
  Button u_N (.out(N));
  Button u_M (.out(M));
  assign ascii_in = SP ? 8'h20 : 8'bz;  // Controlled_Buffer controlled_buffer_5
  assign ascii_in = tunnel ? 8'h21 : 8'bz;  // Controlled_Buffer controlled_buffer_6
  assign ascii_in = tunnel_t ? 8'h22 : 8'bz;  // Controlled_Buffer controlled_buffer_7
  assign ascii_in = tunnel_t_t ? 8'h23 : 8'bz;  // Controlled_Buffer controlled_buffer_8
  assign ascii_in = tunnel_t_t_t ? 8'h24 : 8'bz;  // Controlled_Buffer controlled_buffer_9
  assign ascii_in = tunnel_t_t_t_t ? 8'h25 : 8'bz;  // Controlled_Buffer controlled_buffer_10
  assign ascii_in = tunnel_t_t_t_t_t ? 8'h26 : 8'bz;  // Controlled_Buffer controlled_buffer_11
  assign ascii_in = tunnel_t_t_t_t_t_t ? 8'h27 : 8'bz;  // Controlled_Buffer controlled_buffer_12
  Button u_F9 (.out(F9));
  Button u_FA (.out(FA));
  Button u_FB (.out(FB));
  Button u_FC (.out(FC));
  Button button_12 (.out(tunnel_t_t_t_t_t_t_t_t));
  Button button_13 (.out(tunnel_t_t_t_t_t_t_t_t_t_t_t_t_t));
  Button button_14 (.out(tunnel_t_t_t_t_t_t_t_t_t_t));
  Button u_BS (.out(BS));
  Button u__0 (.out(_0));
  Button button_15 (.out(tunnel_t_t_t_t_t_t_t_t_t_t_t_t));
  Button button_16 (.out(tunnel_t_t_t_t_t_t_t_t_t_t_t_t_t_t_t_t_t_t_t));
  Button button_17 (.out(tunnel_t_t_t_t_t_t_t_t_t_t_t_t_t_t_t_t_t_t_t_t_t_t_t_t_t_t_t_t));
  Button u_O (.out(O));
  Button u_P (.out(P));
  Button button_18 (.out(tunnel_t_t_t_t_t_t_t_t_t_t_t_t_t_t_t_t_t_t_t_t_t_t_t));
  Button button_19 (.out(tunnel_t_t_t_t_t_t_t_t_t_t_t_t_t_t_t_t_t_t_t_t_t_t_t_t_t));
  Button u_L (.out(L));
  Button button_20 (.out(tunnel_t_t_t_t_t_t_t_t_t_t_t_t_t_t_t_t_t));
  Button n_1 (.out(tunnel_t_t_t_t_t_t));
  Button button_21 (.out(tunnel_t_t_t_t_t_t_t_t_t_t_t_t_t_t_t_t));
  Button button_22 (.out(tunnel_t_t_t_t_t_t_t_t_t_t_t));
  Button button_23 (.out(tunnel_t_t_t_t_t_t_t_t_t_t_t_t_t_t));
  Button button_24 (.out(tunnel_t_t_t_t_t_t_t_t_t_t_t_t_t_t_t));
  Button button_25 (.out(tunnel_t_t_t_t_t_t_t_t_t_t_t_t_t_t_t_t_t_t));
  Button button_26 ();  // open: out
  Button button_27 ();  // open: out
  Button button_28 ();  // open: out
  Button u_DL (.out(DL));
  Button button_29 (.out(tunnel_t_t_t_t_t_t_t_t_t_t_t_t_t_t_t_t_t_t_t_t_t_t_t_t_t_t_t_t_t_t));
  Button button_30 (.out(tunnel_t_t_t_t_t_t_t_t_t_t_t_t_t_t_t_t_t_t_t_t_t_t_t_t_t_t_t_t_t));
  Button button_31 (.out(tunnel_t_t_t_t_t_t_t_t_t_t_t_t_t_t_t_t_t_t_t_t_t_t_t_t));
  Button button_32 (.out(tunnel_t));
  Button u_EN (.out(EN));
  Button button_33 (.out(tunnel_t_t_t_t_t_t_t_t_t_t_t_t_t_t_t_t_t_t_t_t));
  Button button_34 (.out(tunnel_t_t_t_t_t_t_t_t_t_t_t_t_t_t_t_t_t_t_t_t_t));
  Button u_SP (.out(SP));
  assign ascii_in = tunnel_t_t_t_t_t_t_t ? 8'h28 : 8'bz;  // Controlled_Buffer controlled_buffer_13
  assign ascii_in = tunnel_t_t_t_t_t_t_t_t ? 8'h29 : 8'bz;  // Controlled_Buffer controlled_buffer_14
  assign ascii_in = tunnel_t_t_t_t_t_t_t_t_t ? 8'h2a : 8'bz;  // Controlled_Buffer controlled_buffer_15
  assign ascii_in = tunnel_t_t_t_t_t_t_t_t_t_t ? 8'h2b : 8'bz;  // Controlled_Buffer controlled_buffer_16
  assign ascii_in = tunnel_t_t_t_t_t_t_t_t_t_t_t ? 8'h2c : 8'bz;  // Controlled_Buffer controlled_buffer_17
  assign ascii_in = tunnel_t_t_t_t_t_t_t_t_t_t_t_t ? 8'h2d : 8'bz;  // Controlled_Buffer controlled_buffer_18
  assign ascii_in = tunnel_t_t_t_t_t_t_t_t_t_t_t_t_t_t ? 8'h2e : 8'bz;  // Controlled_Buffer controlled_buffer_19
  assign ascii_in = tunnel_t_t_t_t_t_t_t_t_t_t_t_t_t_t_t ? 8'h2f : 8'bz;  // Controlled_Buffer controlled_buffer_20
  assign controlled_buffer_21_out = A ? 8'h41 : 8'bz;  // Controlled_Buffer controlled_buffer_21
  assign controlled_buffer_21_out = B ? 8'h42 : 8'bz;  // Controlled_Buffer controlled_buffer_22
  assign controlled_buffer_21_out = C ? 8'h43 : 8'bz;  // Controlled_Buffer controlled_buffer_23
  assign controlled_buffer_21_out = D ? 8'h44 : 8'bz;  // Controlled_Buffer controlled_buffer_24
  assign controlled_buffer_21_out = E ? 8'h45 : 8'bz;  // Controlled_Buffer controlled_buffer_25
  assign controlled_buffer_21_out = F ? 8'h46 : 8'bz;  // Controlled_Buffer controlled_buffer_26
  assign controlled_buffer_21_out = G ? 8'h47 : 8'bz;  // Controlled_Buffer controlled_buffer_27
  assign controlled_buffer_21_out = H ? 8'h48 : 8'bz;  // Controlled_Buffer controlled_buffer_28
  assign controlled_buffer_29_out = A ? 8'h61 : 8'bz;  // Controlled_Buffer controlled_buffer_29
  assign controlled_buffer_29_out = B ? 8'h62 : 8'bz;  // Controlled_Buffer controlled_buffer_30
  assign controlled_buffer_29_out = C ? 8'h63 : 8'bz;  // Controlled_Buffer controlled_buffer_31
  assign controlled_buffer_29_out = D ? 8'h64 : 8'bz;  // Controlled_Buffer controlled_buffer_32
  assign controlled_buffer_29_out = E ? 8'h65 : 8'bz;  // Controlled_Buffer controlled_buffer_33
  assign controlled_buffer_29_out = F ? 8'h66 : 8'bz;  // Controlled_Buffer controlled_buffer_34
  assign controlled_buffer_29_out = G ? 8'h67 : 8'bz;  // Controlled_Buffer controlled_buffer_35
  assign controlled_buffer_29_out = H ? 8'h68 : 8'bz;  // Controlled_Buffer controlled_buffer_36
  assign ascii_in = _0 ? 8'h30 : 8'bz;  // Controlled_Buffer controlled_buffer_37
  assign ascii_in = _1 ? 8'h31 : 8'bz;  // Controlled_Buffer controlled_buffer_38
  assign ascii_in = _2 ? 8'h32 : 8'bz;  // Controlled_Buffer controlled_buffer_39
  assign ascii_in = _3 ? 8'h33 : 8'bz;  // Controlled_Buffer controlled_buffer_40
  assign ascii_in = _4 ? 8'h34 : 8'bz;  // Controlled_Buffer controlled_buffer_41
  assign ascii_in = _5 ? 8'h35 : 8'bz;  // Controlled_Buffer controlled_buffer_42
  assign ascii_in = _6 ? 8'h36 : 8'bz;  // Controlled_Buffer controlled_buffer_43
  assign ascii_in = _7 ? 8'h37 : 8'bz;  // Controlled_Buffer controlled_buffer_44
  assign controlled_buffer_21_out = I ? 8'h49 : 8'bz;  // Controlled_Buffer controlled_buffer_45
  assign controlled_buffer_21_out = J ? 8'h4a : 8'bz;  // Controlled_Buffer controlled_buffer_46
  assign controlled_buffer_21_out = K ? 8'h4b : 8'bz;  // Controlled_Buffer controlled_buffer_47
  assign controlled_buffer_21_out = L ? 8'h4c : 8'bz;  // Controlled_Buffer controlled_buffer_48
  assign controlled_buffer_21_out = M ? 8'h4d : 8'bz;  // Controlled_Buffer controlled_buffer_49
  assign controlled_buffer_21_out = N ? 8'h4e : 8'bz;  // Controlled_Buffer controlled_buffer_50
  assign controlled_buffer_21_out = O ? 8'h4f : 8'bz;  // Controlled_Buffer controlled_buffer_51
  assign controlled_buffer_21_out = P ? 8'h50 : 8'bz;  // Controlled_Buffer controlled_buffer_52
  assign controlled_buffer_29_out = I ? 8'h69 : 8'bz;  // Controlled_Buffer controlled_buffer_53
  assign controlled_buffer_29_out = J ? 8'h6a : 8'bz;  // Controlled_Buffer controlled_buffer_54
  assign controlled_buffer_29_out = K ? 8'h6b : 8'bz;  // Controlled_Buffer controlled_buffer_55
  assign controlled_buffer_29_out = L ? 8'h6c : 8'bz;  // Controlled_Buffer controlled_buffer_56
  assign controlled_buffer_29_out = M ? 8'h6d : 8'bz;  // Controlled_Buffer controlled_buffer_57
  assign controlled_buffer_29_out = N ? 8'h6e : 8'bz;  // Controlled_Buffer controlled_buffer_58
  assign controlled_buffer_29_out = O ? 8'h6f : 8'bz;  // Controlled_Buffer controlled_buffer_59
  assign controlled_buffer_29_out = P ? 8'h70 : 8'bz;  // Controlled_Buffer controlled_buffer_60
  assign ascii_in = _8 ? 8'h38 : 8'bz;  // Controlled_Buffer controlled_buffer_61
  assign ascii_in = _9 ? 8'h39 : 8'bz;  // Controlled_Buffer controlled_buffer_62
  assign ascii_in = tunnel_t_t_t_t_t_t_t_t_t_t_t_t_t_t_t_t ? 8'h3a : 8'bz;  // Controlled_Buffer controlled_buffer_63
  assign ascii_in = tunnel_t_t_t_t_t_t_t_t_t_t_t_t_t_t_t_t_t ? 8'h3b : 8'bz;  // Controlled_Buffer controlled_buffer_64
  assign ascii_in = tunnel_t_t_t_t_t_t_t_t_t_t_t_t_t_t_t_t_t_t ? 8'h3c : 8'bz;  // Controlled_Buffer controlled_buffer_65
  assign ascii_in = tunnel_t_t_t_t_t_t_t_t_t_t_t_t_t_t_t_t_t_t_t ? 8'h3d : 8'bz;  // Controlled_Buffer controlled_buffer_66
  assign ascii_in = tunnel_t_t_t_t_t_t_t_t_t_t_t_t_t_t_t_t_t_t_t_t ? 8'h3e : 8'bz;  // Controlled_Buffer controlled_buffer_67
  assign ascii_in = tunnel_t_t_t_t_t_t_t_t_t_t_t_t_t_t_t_t_t_t_t_t_t ? 8'h3f : 8'bz;  // Controlled_Buffer controlled_buffer_68
  assign controlled_buffer_21_out = Q ? 8'h51 : 8'bz;  // Controlled_Buffer controlled_buffer_69
  assign controlled_buffer_21_out = R ? 8'h52 : 8'bz;  // Controlled_Buffer controlled_buffer_70
  assign controlled_buffer_21_out = S ? 8'h53 : 8'bz;  // Controlled_Buffer controlled_buffer_71
  assign controlled_buffer_21_out = T ? 8'h54 : 8'bz;  // Controlled_Buffer controlled_buffer_72
  assign controlled_buffer_21_out = U ? 8'h55 : 8'bz;  // Controlled_Buffer controlled_buffer_73
  assign controlled_buffer_21_out = V ? 8'h56 : 8'bz;  // Controlled_Buffer controlled_buffer_74
  assign controlled_buffer_21_out = W ? 8'h57 : 8'bz;  // Controlled_Buffer controlled_buffer_75
  assign controlled_buffer_21_out = X ? 8'h58 : 8'bz;  // Controlled_Buffer controlled_buffer_76
  assign controlled_buffer_29_out = Q ? 8'h71 : 8'bz;  // Controlled_Buffer controlled_buffer_77
  assign controlled_buffer_29_out = R ? 8'h72 : 8'bz;  // Controlled_Buffer controlled_buffer_78
  assign controlled_buffer_29_out = S ? 8'h73 : 8'bz;  // Controlled_Buffer controlled_buffer_79
  assign controlled_buffer_29_out = T ? 8'h74 : 8'bz;  // Controlled_Buffer controlled_buffer_80
  assign controlled_buffer_29_out = U ? 8'h75 : 8'bz;  // Controlled_Buffer controlled_buffer_81
  assign controlled_buffer_29_out = V ? 8'h76 : 8'bz;  // Controlled_Buffer controlled_buffer_82
  assign controlled_buffer_29_out = W ? 8'h77 : 8'bz;  // Controlled_Buffer controlled_buffer_83
  assign controlled_buffer_29_out = X ? 8'h78 : 8'bz;  // Controlled_Buffer controlled_buffer_84
  assign ascii_in = tunnel_t_t_t_t_t_t_t_t_t_t_t_t_t_t_t_t_t_t_t_t_t_t ? 8'h40 : 8'bz;  // Controlled_Buffer controlled_buffer_85
  assign ascii_in = tunnel_t_t_t_t_t_t_t_t_t_t_t_t_t_t_t_t_t_t_t_t_t_t_t ? 8'h5b : 8'bz;  // Controlled_Buffer controlled_buffer_86
  assign ascii_in = tunnel_t_t_t_t_t_t_t_t_t_t_t_t_t_t_t_t_t_t_t_t_t_t_t_t ? 8'h5c : 8'bz;  // Controlled_Buffer controlled_buffer_87
  assign ascii_in = tunnel_t_t_t_t_t_t_t_t_t_t_t_t_t_t_t_t_t_t_t_t_t_t_t_t_t ? 8'h5d : 8'bz;  // Controlled_Buffer controlled_buffer_88
  assign ascii_in = tunnel_t_t_t_t_t_t_t_t_t_t_t_t_t_t_t_t_t_t_t_t_t_t_t_t_t_t ? 8'h5e : 8'bz;  // Controlled_Buffer controlled_buffer_89
  assign ascii_in = tunnel_t_t_t_t_t_t_t_t_t_t_t_t_t ? 8'h5f : 8'bz;  // Controlled_Buffer controlled_buffer_90
  assign ascii_in = tunnel_t_t_t_t_t_t_t_t_t_t_t_t_t_t_t_t_t_t_t_t_t_t_t_t_t_t_t ? 8'h60 : 8'bz;  // Controlled_Buffer controlled_buffer_91
  assign ascii_in = tunnel_t_t_t_t_t_t_t_t_t_t_t_t_t_t_t_t_t_t_t_t_t_t_t_t_t_t_t_t ? 8'h7b : 8'bz;  // Controlled_Buffer controlled_buffer_92
  assign controlled_buffer_21_out = Y ? 8'h59 : 8'bz;  // Controlled_Buffer controlled_buffer_93
  assign controlled_buffer_21_out = Z ? 8'h5a : 8'bz;  // Controlled_Buffer controlled_buffer_94
  assign controlled_buffer_29_out = Y ? 8'h79 : 8'bz;  // Controlled_Buffer controlled_buffer_95
  assign controlled_buffer_29_out = Z ? 8'h7a : 8'bz;  // Controlled_Buffer controlled_buffer_96
  assign ascii_in = tunnel_t_t_t_t_t_t_t_t_t_t_t_t_t_t_t_t_t_t_t_t_t_t_t_t_t_t_t_t_t ? 8'h7c : 8'bz;  // Controlled_Buffer controlled_buffer_97
  assign ascii_in = tunnel_t_t_t_t_t_t_t_t_t_t_t_t_t_t_t_t_t_t_t_t_t_t_t_t_t_t_t_t_t_t ? 8'h7d : 8'bz;  // Controlled_Buffer controlled_buffer_98
  assign ascii_in = tunnel_t_t_t_t_t_t_t_t_t_t_t_t_t_t_t_t_t_t_t_t_t_t_t_t_t_t_t_t_t_t_t ? 8'h7e : 8'bz;  // Controlled_Buffer controlled_buffer_99
  assign ascii_in = DL ? 8'h7f : 8'bz;  // Controlled_Buffer controlled_buffer_100
  assign ascii_in = CAP ? controlled_buffer_21_out : 8'bz;  // Controlled_Buffer controlled_buffer_101
  not not_1 (not_1_out, CAP);
  assign ascii_in = not_1_out ? controlled_buffer_29_out : 8'bz;  // Controlled_Buffer controlled_buffer_102
endmodule

module KBD_CTRL (
  input  [7:0] IN,
  input  CLR,
  input  [3:0] IO_MODE,
  output [15:0] OUT
);

  wire and_1_out, not_1_out, not_2_out;
  wire [15:0] register_1_q;

  Register #(.width(16)) register_1 (.D({{8{1'b0}}, IN}), .Q(register_1_q), .clk(CLR));  // open: en, clr
  Enabler enabler_1 (.out_3(OUT), .in_2(and_1_out), .in_1(register_1_q));
  not not_1 (not_1_out, IO_MODE[0]);
  and and_1 (and_1_out, not_1_out, not_2_out, IO_MODE[3]);
  not not_2 (not_2_out, IO_MODE[1]);

  // Other names for the same wires on the sheet: IN_OUT = IO_MODE[0]; DATA_ADDR = IO_MODE[1]; IOCLK_S = IO_MODE[2];
  //   IOCLK_E = IO_MODE[3]
endmodule

// 22
module framebufferAnime128x128 (
  input  reset,
  input  wrt
);

  wire clk_out, xcnt_carry, ycnt_carry;
  wire [15:0] rgb_video_1_p6;
  wire [21:0] xcnt_q;

  Counter zcnt (.Q(xcnt_q[21:14]), .clk(ycnt_carry));  // open: load, D, count, carry, clr
  Counter #(.max('h7f), .trigger("falling"), .width(7)) ycnt (
    .Q(xcnt_q[13:7]), .carry(ycnt_carry), .clk(xcnt_carry));  // open: load, D, count, clr
  Counter #(.max('h7f), .width(7)) xcnt (
    .Q(xcnt_q[6:0]), .carry(xcnt_carry), .clk(clk_out));  // open: load, D, count, clr
  Clock clk (.out(clk_out));
  // RGB_Video rgb_video_1: pin names not known; wires that end beside it: reset, clk_out, wrt, xcnt_q[6:0], xcnt_q[13:7], rgb_video_1_p6
  ROM #(.addrWidth(12), .dataWidth(16)) rom_1 (.addr(xcnt_q[11:0]), .data(rgb_video_1_p6));
  // Pins of 12 and 22 bits meet at xcnt_q

  // Notes on the sheet:
  //   contents of rom_1 (hex, n*v repeats v):
  //   compressed eJyNnEuao7gShedahcc1Ar2QliMJvP8l3DgnQgIyq/q7g47GmU6X+TnxlCB5f3xSi1VMqZ/sR/vk
  //   Nvond39+jhAvMeVyR2jfz9HPTcx3+8Q/8r/dfhD6MuXrci9f+etyiYk05ycHD7OJ8deQf+oaLuFf
  //   Sb4tI/988pGmfGLzalxs23oZl8n1U8axf85c6+f87s3BfHrq+TOuo75NkfeJwZHjy3ElmHDA5HUE
  //   k/TI6cssv+3nmeSTjyhH3yzfT76LIcvVZd8Wsm0AGbhlcLuRnZsQnPDWz178SC2DX77RXXodJr/x
  //   i19rNO3Fj6w2NW6RfPGT95UYNpzgk0u/drCqDcCMH4+e/NKb356nAcm8q3F2RIh7ftBN7eZXJj8/
  //   hp1qf/Ob4nIGjC/Pt5GfTdXd/M75ecv85HcBnej9P/j5f/Iror+0fc7r23Fa1Yk2yKUpv/THuKWi
  //   ZmlMlRX/GJbjwB+Uh0n4dGpLAIGNXGN+7xsQT5KaUTYPF/zhkWRjgMDm+3kK7GbzBAQ2oDT+Aig/
  //   KLknlkXJ+6eXnrmLb4KSyap2/mzKqt4Cq26+NFpnVlB6LD8F1LrY5MWG4tnWxeapZbCp0M2C0fsO
  //   QDA84i8q2Mj7JpvvYrOcb3sEL7cUNAG1vwJyM5ZVw/JngqkfSuW8TmUCz2ufaR44Hp4HBQmddDxC
  //   lUnr4EfVWz9Oj65ezcjpARm+awGtJrTadTpDNmnRhR7S6WbcX2iJOWCi/BlyhOjncsLoAqNzGQNl
  //   Ryqn7h7IoG9czYewlpxMXX6bmvK+qqnjG5UfqDk6naGrf0H34nc75JPQ/b7FTz+q45Mr+I3xPDc5
  //   VYeTxumDAZAoHGEl2REqy52m724ik5ch4Z3++7G/3m5ap+PR1NYtsP6m1ZzRmuYRmPyNTGJ/QBQT
  //   A270RQ3sS23qkO3hdxNPfSUA/FY05oxWLTNP0uB9+LOeRNZNMrCrZ80LlNJSk1Qxh9ISglUJgZWH
  //   b3o9MnQ8Aj++T83klzo/byMwNZPfT3SsLtpt3Ett9Rm3Fr9QL+EnRvkFvK+dKUEx/UHS4paGepiw
  //   +JEaIt0UmrzvND0Jq+NTzyNJGv6GT0l7/BRQq+SX6qECSf3WWF7olB+4dBK6qcF83y9Pj/ctfvK3
  //   8qGTX7tghvEzkuQnUeJVnS1+iL2mur9JTyL2fv2Fnzf9Xcc+oKbGtPng94yAKrg26wz+tkqOlXMQ
  //   QsB0ngWsDqEmGfRIe/rkccbPEb/RHWdIL2p0z06zLwMuP6jJpXjxC4ufV36pk1/alv6uqb8BfoPU
  //   /o2OSdExMz75+Re/W3/w32OkHYVUVXTXNwwcdTFBc6nUWkKStVu/UM8Bp748RWbUWktHdjnuch4x
  //   yWmNLqxOqdhKEicWkhNnStkdCLDZaof9LS787a7G8eiIe5j+S3QVcPLXnL2rn2/2AWEGQUH3nfqb
  //   /ps8lOjHza/9n/yOzyNb7Neh/OQllLMDyT5TruZdViDiySKpIvEK3ojwRV3FP/WkskRFR5Tin8ii
  //   dDwuBWl7Es/zgVEKuXIKwUULZOQtIwBPgCpxNPAXSKs8HVxw52uOn30r+8fvW9Tvz6ojoZmISNgI
  //   AU5TrUZP5bbi3sNbpXLz5Ue0W4mi3Nmizsptu7OFIvtQcmyjmBmu/DVkA07Z0omw1UGrwhzAVA9X
  //   zgQGKZt7QkoVSASt/FnexW+vvTq8GT4Kbw07VAScHYYRX8BCT47AJj/52RDDMwp7TGJ8/Pjt8m4v
  //   go4XnIb5QDMr6pqjF2bWhlqna2/Gws7yhqLrnxLkfaW308kRejjftR/W8te3xY89MruWMgt1tqvm
  //   t8ej8kWV4hjy6JRVo/thmAp9Tx1wTw5h60O3EzUl/kxMyMb5pDS7KDXNuJf79ZWf7fizHaWZdJYE
  //   BiOfl/ALMbmP70dklgXY8HK0BTsCP1+FZKgjw3+qVmoHCsESmvBrl5z03sTTWxO6fpO03oRGDSK4
  //   HuWTz1T9Z0T5Ln3k4XoUdG0I7Bbko2qQS1YCopiXDzh8yTCHk5cidL+JDnzEJ3v7+MlUSxZXoqid
  //   cixRovs0cKYDDpZ2GjeP6Jf4xSEgYgUNMSvQuQKcFGGJ8sU5QziCnEcZ1ZuvjiAZhDEOIMLeJrqt
  //   wRT/2UvexBTht/ukbnV0BYbz9U0YiBPX4MEve8mEXiLIXhLaX4nGUUTYx7iEn8TCEaXV7TEO0Z9o
  //   qEfx/dbloxr4Ha2JGLzIOzf513IrxZFk9vjHGy9KZGPNl2L2gaOMGjq2TwW1CoVRNFREQheY4BAS
  //   +i+JawVeAR9UfqBGTUKJasRr3TxiSNu1GS1grySpOomOTn21KjoIru0f+uq+ZXlz5H9OQt72iVW+
  //   7NFjB70CKqcAEdesPYsU6hUmvSExamsb6OEtBSabAS6X6pB/v40qziyR/2jC+/AxKji5EIFidDXg
  //   gjVRfd6vqDrkP06V5ilGnT2xze6IatSIjbbgbV1dbnMqPJiDAj3p5VWzqfoxkomoTzIKwyfDu0gr
  //   2SwrwoWVXvs6xjeJdJEig9xATxDioHilqDFIPEzA+QGfFIQC7oKcoJ9GDIe8z4vXdXFMub6bAG5k
  //   NsREGC9vDqjq9hYFUoHYhnhn26IaYhUBSiAPozl8KLCCWbEjBVwvfIB8SqwlylWTE7jFwXxdYw+a
  //   4TNmPIlTCVQlBzKpRjyk4JYkbbDc6yyXpQR0Q7sUKQsbCuca2TzIKTCFaXZtV3e+jF1lJ8yCKk4R
  //   bpFmoxOKrwmw0iXgtyjpoAepNsZoQ9XXxyb/UB/FiZsKUxh5JRBHhNn6hCg4RapV/l3Rd0YSyAAh
  //   SLKiS1WQIOzp+0j38BluC+F5vwRKdKLSWFuCCoLWQJyHmSsLP1/BXqc/4mtWdTB1Stir0Bx7sRPJ
  //   m1UiDCakqHw4K+hz4ITehFU2LxRzm/CzYMfChEZFJ/hCzRpzXO2E4Umu4gj44LzjOlV+1V/ZiWYq
  //   XopWO4MbRSfvE5pDQSLMOY+Pp/OKorJCiyiPRJJRUcnnIfRFSE2+nkCLylox71ei8uRLbkFO4wo6
  //   02KxUxGvGiKXMEQSSYFlhaTKnUWH1591lDhUWT/PrGxQbrvrm8akierbKiPr7+jBDM0z1sFvyXAq
  //   T76QVx9pAsxJvhR+Im8wqHDGDvmdkhKkqRDlNXqf46keLcMtJehXJALJEM2EKB4pBoOp/crwyIK3
  //   VOOyZ8IxnPgAJ2/J6tdFczJzihCPiI8RfwHj7pzHnFy6fN0axAtqlPaxIIkIzuDYFVdULQ1xjy2H
  //   1teqNxst6PDgAlhpYboa7Y/xljJY1oquiOlWHiHyu/D71Y4BWpBgT8GJ6eqqyi+KpAhRCHWcVkLy
  //   gGw3iEvOl/yEbjWIqk7Rn+VaocFIUFG1ZM2mxURY2pCw4VtWp6UxD4f0gI5OK193X/x2pOOMmHog
  //   iIKkfHJhupH6yrUhntvPDqeF4HQ2BXFhRUO01qg1N7UGM/tjKlHe3LTUVX6o8Hb48B35gtR6cI3A
  //   CMTTN36oMmhufijk1E2RHeV6NITTsql2S4cz9VjsfVBxk0ztGn8WCi7P6CrgoyE37MM8GSHRyZkf
  //   6rrmtVSdUGOWZ9aD6hy/OPUXmSchYFY3uWUKXZk6hox2SuU7J+ploksz/OWvtDLmtU1FeEuPJEuQ
  //   ygh1k5vNxcwcbM6ovyo+zaJE9CL86Lrkd+tvSU/9V/kxHbFPyeSneVQRz2wieg74KIRSfDwipolw
  //   Bjx1Z8SDADkiS0QzCHiCjqU9Yw6LK159iBAeFfhmSplVJNweScgxiUtZ1HQZ504LFyF+E5XYnY1h
  //   tHG2Mdbso5tVMFKHaNpi8J38Ns3Gqr8gxVVn/Lv5KUTfZ0VSWM/Rf7OjdvlRTLCsqbtl3mv9WXd3  KDCfBskQUSK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
endmodule

// 22
module framebuffer128x128 (
  input  reset
);

  wire clk_out, xcnt_carry;
  wire [11:0] xcnt_q;
  wire [15:0] rgb_video_1_p6;

  Counter #(.max('h3f), .trigger("falling"), .width(6)) ycnt (
    .Q(xcnt_q[11:6]), .clk(xcnt_carry));  // open: load, D, count, carry, clr
  Counter #(.max('h3f), .width(6)) xcnt (
    .Q(xcnt_q[5:0]), .carry(xcnt_carry), .clk(clk_out));  // open: load, D, count, clr
  Clock clk (.out(clk_out));
  // RGB_Video #(.height(64), .scale(4), .width(64)) rgb_video_1: pin names not known; wires that end beside it: reset, clk_out, 1'b1, xcnt_q[5:0], xcnt_q[11:6], rgb_video_1_p6
  ROM #(.addrWidth(12), .dataWidth(16)) rom_1 (.addr(xcnt_q), .data(rgb_video_1_p6));

  // Notes on the sheet:
  //   contents of rom_1 (hex, n*v repeats v):
  //   compressed eJx1nEmio7oSROdaBeM7AnVIy5EE3v8SfkZkSmDX+5Ms3FwbDpGt5Eren1vyvmyp0USYXGG6mDG2
  //   7O/L5eDvLYf4EdP3Lfd+iPn4LY8QtjOGKCZFB7OdI4WtjHRsJR67HO2f7ezl2kq4P3zOlfDZtxp7
  //   EFPD11GN8hdmXBldjmJP0+AFvK/EROPl24J35zjkqF/HdgYaOUl5uOtz8m1q5Hv5UM2u5uxNzi+U
  //   e5mPsw+QP+MnlxjWV564NpzVuKITYGD1GEXXxJROdAJsv1zq5Jc/E90lpxuPYPwG+IWPXEeQc8nt
  //   xt+WKkcF92PPZo6RttOP6k5/y6t+NHkLzd3kA/yQKyLnIZyHcK7x9BtNGec8ezW8GH75Id+Le6n8
  //   zHzzM2DOqPVlGm8t+OUFMYMfn7veEM/xDVFuo/ArixqPilyMb7j8Nha/25n06q7oMj+PZ6+CE5LJ
  //   l+bC4ePm5dJh/Ob3hqNbjuoeNr4qJrhQc5S/ELXH2pLSPcMO4o2+cOIGFEe6cpX3ZEpRJyrCT/0p
  //   v0WtLzMhGivy+w90nejyrSb3hx8+hRAp6jdJ071KwLfHAB28thm6yS8v173Ma016wi/jNEJtWfhF
  //   4bePAHR+O0oRs5dDjojzDsAZnDKF4V8QZ6gRd8ELSS9ylKMT9yMI4jtvse3nFo+R5dv2AXWCZKB5
  //   +B0THeH0t9biH5C5N7J4T6Pc7iVDEKzgVic8hAC4GBymmxFQQvAeOKXLDAJd6lTbuQMZA11wFuME
  //   fO6ihHC0rKCUUWmBoJwcTWR7fhsCXcbJ3y6CIs14lGjh1xNUSUSLOxJUvYRHJxcGcqk4DeGmGtPI
  //   QW5UVqGAvh+KuRe/+0ty/lJDnCDpsqlScS4tHvPN++CRe/4297hyBNEtfuKeTr0VwvU1E52551Ee
  //   TODHI0Is9hzMjrfs23wVnBX7YR9F/67UYozT03NST+er9hbhHA/xeRFkeYRmHtcfp3yMPBf/ZpQD
  //   mXhPWtPIc5cqcBlHr8qdClSlrvfFSQu+rmHNzAFkDHBB8yjCGi/RTY9UAIqneNCJBkE8fQpLlUlY
  //   ef3VAi143YuxoqSrT/jq6qJM5xVqM4rJS7C2QN8Wsccxp+LWCyu/PvgMAYk8+L4ALcx5peX8dnTK
  //   E4TdL7lwGb6M+CHuk3jiwmVeoHKIkxx8MB4ZcaoEJ8bzSJ4Tzwu75pJlEPfUzxfSQmEWhDKJVX7n
  //   v/KE3AuEP1+Rk4wngi08mJf0Ysej8TZMOPbQALoZ4wRWj9/Se8yXU+pNehneBmpSRG/FiBr/Kkuo
  //   Ok2mkB4vUQq3qbcdEV/SZr3jVrsUPrXn6sSUrQbJnTXspx6Vdp/b2eTNucmdyN4nR7qheoY+C4LE
  //   SUgrgDqCY2RVehBiRIhk9DH5DdAjJCbaz0q5TwWzKL9qvJf8ht4SM7ukBAa3gO946iCNfyu3B4aM
  //   y0o5Mx87iiio5ZzpRl5DVYnmfCwuWHC00OrWg+TK1qWma73gIZ8by/DVBsIecPfiipfUk5tISfgn
  //   TbsU9yM0qN4cV2KgmCIJ+JA7oUdIxSuHOOYQI/d5M7TkQoP3mVsvX3wUaOQArTuYjWl1Zac3vsnQ
  //   WV5+4QuaoT1CtgpCrghOlFR0KMnk/GIXGlJe95FhfKNxvUtNPE3bXg+VqZgGmcJshE1dihDDq+RR
  //   wxpHRbdHM3goOfjUECgX2JWLNjnxVc8c8+HxAmsyDe0JaEuDcfIz+fX58SxavjUIb334vZVHUy0W
  //   6e2uIzuebqzSOtQg1EovA8AugzN8JzA3qQHnTtPtyOTIo+5gth5RxHVJoeLDVh7ylsU/yx8juCeT
  //   aLjwEh8kNn4UT/qbqHZlqHJRQL+U1D+NzQ8gVdm7Vkb/dsxy5ctJE/IG4zAAudh8NU13kRV6q61F
  //   qQNVM2OnmWwI4wcQH05AwkbOakS5qT0izLd2TgdlQhZKCmjVL16fZRnNuoQl/ZSTd9ptDJpzHr11
  //   trOtnkFQua1k6h9hKbJ3pxJejmk986LlJrKg1XCUCCNHqJDp2Ww4211chTsKLXVCuTq5+v6oynTz
  //   6CssM+TkxI/RtUjPwCbBawFz+5kKxmL0FCta3sj74JUs7yKiKR3NaK1+V4z7v9zOfs8MK3pzP175
  //   wPtG5t6xrK5ZSP9OBXW3JIx+gqVRCQxU4xJ9jHsbQxrcIQ+dHOE58Uo1+jAOg2hG+KkvAl2Uuyk5
  //   Q3Ti76K9Az2MhY6l7VXErXpQDboNvKD8pKphVEuqncmPMw6YSn7BmGrnm77EpyQ1PzwjlDfEdxZ9
  //   +BHdMla/rSJO+CUVbry1AW8IWYIOmICOR+O+3JX2W6lJQhgKR0g+D2d+wJG80PU5Zl8WJVL86ViA
  //   ucCxH3uGBua5zfKr6g/v85o45AWKkMopOmqpi18HvxrsOb6qJvykC+SHtxz18+Tyx0/ydKxrDd1J
  //   c0x+y8CDI0ZQnLuJo1aUY6zTitYTVBOOHIVEah2q48PW7678qElkWtFf7FOnE+zZ0KdWyQDWe5Gf
  //   D4rTZjC3XyKcmuT7MHmx6lsErBNC5dcXv4szwPD1XA1LicuEwzFmrnJl1bvXRFdmw6B9GfsHNqtp
  //   n0Zwpq6962EzO44yDqlB0yGNlFRcAWnvBCapx/ydHUsxrW4PqYfVtJgB59Qc2Rj/FKcGgIu+j/hn
  //   ImSjwQaORfEU4VTiw8+6WOlsKVuIkIMset6/+ouuRptWbi8l6jTwxQ+ZhlOlB+KTjR9g2oTMh5wW
  //   BP9RI8BgDKdTukw8mgbNwTTei+uKT0vidKnShTy6q2Z9FkBoA8Ya90TbUNqQmnnQuyWACn9m2c7m
  //   Q74jZyjx4edNf2tU5TXRYiIlidYBokqPA1e58v2ZTD4Qhd+1+PUviC93TsbvBTEoP6X2NRfgkaK7
  //   58Rp/zEf5ccomvyedSTE+vPsctHKr7firIrd0T+Vnd2pdho6cpMSUCCO5E4vtb/IMZuza565AREV
  //   dcD89RjRWTqJJj3eiseow6Ku5PsYOzVp6lCSNAinRszsoMD5RHhozdlpeqaZhzNuF4JamYxewxK/
  //   pplSh7AYSe2eyHAkL3zsfU0iG1utsLd9k7Jmh2IgFoFSgILFG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
endmodule
