// Logisim project 51강_나눗셈 나머지 연산 하드웨어.circ as structural Verilog: 13 circuits, main circuit main
module main (
  input  [7:0] in_1,
  input  [7:0] in_2,
  input  [7:0] \나눠질_수 ,
  input  [7:0] \나눌_수 ,
  output [7:0] out_5,
  output [7:0] out_6,
  output [7:0] \몫 ,
  output [7:0] \몫_2 ,
  output [7:0] \나머지 ,
  output [7:0] \몫_3 
);

  wire [7:0] adder8_2_o, inverter_1_out_2;

  Inverter inverter_1 (.out_2(inverter_1_out_2), .in_1(in_2));
  Adder8 adder8_1 (.o(out_5), .a(in_1), .b(adder8_2_o));  // open: co, ci
  Adder8 adder8_2 (.o(adder8_2_o), .a(inverter_1_out_2), .b(8'h1));  // open: co, ci
  Subtractor8 subtractor8_1 (.o(out_6), .a(in_1), .b(in_2));  // open: bo, bi
  HW_DIV hw_div_1 (.\몫 (\몫_2 ), .\나머지 (\나머지 ), .\나눌_수 (\나눌_수 ), .\나눠질_수 (\나눠질_수 ));
  Divider #(.mode("unsigned")) divider_1 (.a(\나눠질_수 ), .b(\나눌_수 ), .out(\몫 ), .rem(\몫_3 ));  // open: upper

  // Notes on the sheet:
  //   8비트 전감산기
  //   8비트 나눗셈/ 나머지 연산장치
endmodule

module Adder1 (
  input  a,
  input  b,
  input  ci,
  output sum,
  output co
);

  wire co1_out, co2_out, sum1_out;

  xor sum1 (sum1_out, a, b);
  xor sum2 (sum, sum1_out, ci);
  and co2 (co2_out, sum1_out, ci);
  and co1 (co1_out, a, b);
  or or_1 (co, co2_out, co1_out);
endmodule

module Adder8 (
  input  ci,
  input  [7:0] a,
  input  [7:0] b,
  output [7:0] o,
  output co
);

  wire adder1_1_co, adder1_2_co, adder1_3_co, adder1_4_co, adder1_5_co, adder1_6_co, adder1_7_co;

  Adder1 adder1_1 (.co(adder1_1_co), .sum(o[0]), .ci(ci), .a(a[0]), .b(b[0]));
  Adder1 adder1_2 (.co(adder1_2_co), .sum(o[1]), .ci(adder1_1_co), .a(a[1]), .b(b[1]));
  Adder1 adder1_3 (.co(adder1_3_co), .sum(o[2]), .ci(adder1_2_co), .a(a[2]), .b(b[2]));
  Adder1 adder1_4 (.co(adder1_4_co), .sum(o[3]), .ci(adder1_3_co), .a(a[3]), .b(b[3]));
  Adder1 adder1_5 (.co(adder1_5_co), .sum(o[4]), .ci(adder1_4_co), .a(a[4]), .b(b[4]));
  Adder1 adder1_6 (.co(adder1_6_co), .sum(o[5]), .ci(adder1_5_co), .a(a[5]), .b(b[5]));
  Adder1 adder1_7 (.co(adder1_7_co), .sum(o[6]), .ci(adder1_6_co), .a(a[6]), .b(b[6]));
  Adder1 adder1_8 (.co(co), .sum(o[7]), .ci(adder1_7_co), .a(a[7]), .b(b[7]));
endmodule

module Left_Barrel_Shifter (
  input  [7:0] A,
  input  [2:0] n,
  output [7:0] OUT,
  output [7:0] C_OUT
);

  wire multiplexer_1_out, multiplexer_2_out, multiplexer_3_out, multiplexer_4_out, multiplexer_5_out,
       multiplexer_6_out, multiplexer_7_out, multiplexer_8_out, multiplexer_9_out, multiplexer_10_out,
       multiplexer_11_out, multiplexer_12_out, multiplexer_13_out, multiplexer_14_out, multiplexer_15_out,
       multiplexer_16_out, multiplexer_17_out, multiplexer_18_out, multiplexer_19_out, multiplexer_20_out,
       multiplexer_21_out, multiplexer_22_out, multiplexer_23_out, multiplexer_24_out, multiplexer_25_out,
       multiplexer_26_out, multiplexer_27_out, multiplexer_28_out, multiplexer_29_out, multiplexer_30_out,
       multiplexer_31_out, multiplexer_32_out;

  Multiplexer #(.enable("false")) multiplexer_1 (.in0(A[0]), .in1(1'b0), .out(multiplexer_1_out), .sel(n[0]));
  Multiplexer #(.enable("false")) multiplexer_2 (.in0(A[1]), .in1(A[0]), .out(multiplexer_2_out), .sel(n[0]));
  Multiplexer #(.enable("false")) multiplexer_3 (.in0(A[2]), .in1(A[1]), .out(multiplexer_3_out), .sel(n[0]));
  Multiplexer #(.enable("false")) multiplexer_4 (.in0(A[3]), .in1(A[2]), .out(multiplexer_4_out), .sel(n[0]));
  Multiplexer #(.enable("false")) multiplexer_5 (.in0(A[4]), .in1(A[3]), .out(multiplexer_5_out), .sel(n[0]));
  Multiplexer #(.enable("false")) multiplexer_6 (.in0(A[5]), .in1(A[4]), .out(multiplexer_6_out), .sel(n[0]));
  Multiplexer #(.enable("false")) multiplexer_7 (.in0(A[6]), .in1(A[5]), .out(multiplexer_7_out), .sel(n[0]));
  Multiplexer #(.enable("false")) multiplexer_8 (.in0(A[7]), .in1(A[6]), .out(multiplexer_8_out), .sel(n[0]));
  Multiplexer #(.enable("false")) multiplexer_9 (.in0(1'b0), .in1(A[7]), .out(multiplexer_9_out), .sel(n[0]));
  Multiplexer #(.enable("false")) multiplexer_10 (.in0(1'b0), .in1(1'b0), .out(multiplexer_10_out), .sel(n[0]));
  Multiplexer #(.enable("false")) multiplexer_11 (.in0(1'b0), .in1(1'b0), .out(multiplexer_11_out), .sel(n[0]));
  Multiplexer #(.enable("false")) multiplexer_12 (.in0(1'b0), .in1(1'b0), .out(multiplexer_12_out), .sel(n[0]));
  Multiplexer #(.enable("false")) multiplexer_13 (.in0(1'b0), .in1(1'b0), .out(multiplexer_13_out), .sel(n[0]));
  Multiplexer #(.enable("false")) multiplexer_14 (.in0(1'b0), .in1(1'b0), .out(multiplexer_14_out), .sel(n[0]));
  Multiplexer #(.enable("false")) multiplexer_15 (.in0(1'b0), .in1(1'b0), .out(multiplexer_15_out), .sel(n[0]));
  Multiplexer #(.enable("false")) multiplexer_16 (.in0(1'b0), .in1(1'b0), .out(multiplexer_16_out), .sel(n[0]));
  Multiplexer #(.enable("false")) multiplexer_17 (
    .in0(multiplexer_1_out), .in1(1'b0), .out(multiplexer_17_out), .sel(n[1]));
  Multiplexer #(.enable("false")) multiplexer_18 (
    .in0(multiplexer_2_out), .in1(1'b0), .out(multiplexer_18_out), .sel(n[1]));
  Multiplexer #(.enable("false")) multiplexer_19 (
    .in0(multiplexer_3_out), .in1(multiplexer_1_out), .out(multiplexer_19_out), .sel(n[1]));
  Multiplexer #(.enable("false")) multiplexer_20 (
    .in0(multiplexer_4_out), .in1(multiplexer_2_out), .out(multiplexer_20_out), .sel(n[1]));
  Multiplexer #(.enable("false")) multiplexer_21 (
    .in0(multiplexer_5_out), .in1(multiplexer_3_out), .out(multiplexer_21_out), .sel(n[1]));
  Multiplexer #(.enable("false")) multiplexer_22 (
    .in0(multiplexer_6_out), .in1(multiplexer_4_out), .out(multiplexer_22_out), .sel(n[1]));
  Multiplexer #(.enable("false")) multiplexer_23 (
    .in0(multiplexer_7_out), .in1(multiplexer_5_out), .out(multiplexer_23_out), .sel(n[1]));
  Multiplexer #(.enable("false")) multiplexer_24 (
    .in0(multiplexer_8_out), .in1(multiplexer_6_out), .out(multiplexer_24_out), .sel(n[1]));
  Multiplexer #(.enable("false")) multiplexer_25 (
    .in0(multiplexer_9_out), .in1(multiplexer_7_out), .out(multiplexer_25_out), .sel(n[1]));
  Multiplexer #(.enable("false")) multiplexer_26 (
    .in0(multiplexer_10_out), .in1(multiplexer_8_out), .out(multiplexer_26_out), .sel(n[1]));
  Multiplexer #(.enable("false")) multiplexer_27 (
    .in0(multiplexer_11_out), .in1(multiplexer_9_out), .out(multiplexer_27_out), .sel(n[1]));
  Multiplexer #(.enable("false")) multiplexer_28 (
    .in0(multiplexer_12_out), .in1(multiplexer_10_out), .out(multiplexer_28_out), .sel(n[1]));
  Multiplexer #(.enable("false")) multiplexer_29 (
    .in0(multiplexer_13_out), .in1(multiplexer_11_out), .out(multiplexer_29_out), .sel(n[1]));
  Multiplexer #(.enable("false")) multiplexer_30 (
    .in0(multiplexer_14_out), .in1(multiplexer_12_out), .out(multiplexer_30_out), .sel(n[1]));
  Multiplexer #(.enable("false")) multiplexer_31 (
    .in0(multiplexer_15_out), .in1(multiplexer_13_out), .out(multiplexer_31_out), .sel(n[1]));
  Multiplexer #(.enable("false")) multiplexer_32 (
    .in0(multiplexer_16_out), .in1(multiplexer_14_out), .out(multiplexer_32_out), .sel(n[1]));
  Multiplexer #(.enable("false")) multiplexer_33 (.in0(multiplexer_17_out), .in1(1'b0), .out(OUT[0]), .sel(n[2]));
  Multiplexer #(.enable("false")) multiplexer_34 (.in0(multiplexer_18_out), .in1(1'b0), .out(OUT[1]), .sel(n[2]));
  Multiplexer #(.enable("false")) multiplexer_35 (.in0(multiplexer_19_out), .in1(1'b0), .out(OUT[2]), .sel(n[2]));
  Multiplexer #(.enable("false")) multiplexer_36 (.in0(multiplexer_20_out), .in1(1'b0), .out(OUT[3]), .sel(n[2]));
  Multiplexer #(.enable("false")) multiplexer_37 (
    .in0(multiplexer_21_out), .in1(multiplexer_17_out), .out(OUT[4]), .sel(n[2]));
  Multiplexer #(.enable("false")) multiplexer_38 (
    .in0(multiplexer_22_out), .in1(multiplexer_18_out), .out(OUT[5]), .sel(n[2]));
  Multiplexer #(.enable("false")) multiplexer_39 (
    .in0(multiplexer_23_out), .in1(multiplexer_19_out), .out(OUT[6]), .sel(n[2]));
  Multiplexer #(.enable("false")) multiplexer_40 (
    .in0(multiplexer_24_out), .in1(multiplexer_20_out), .out(OUT[7]), .sel(n[2]));
  Multiplexer #(.enable("false")) multiplexer_41 (
    .in0(multiplexer_25_out), .in1(multiplexer_21_out), .out(C_OUT[0]), .sel(n[2]));
  Multiplexer #(.enable("false")) multiplexer_42 (
    .in0(multiplexer_26_out), .in1(multiplexer_22_out), .out(C_OUT[1]), .sel(n[2]));
  Multiplexer #(.enable("false")) multiplexer_43 (
    .in0(multiplexer_27_out), .in1(multiplexer_23_out), .out(C_OUT[2]), .sel(n[2]));
  Multiplexer #(.enable("false")) multiplexer_44 (
    .in0(multiplexer_28_out), .in1(multiplexer_24_out), .out(C_OUT[3]), .sel(n[2]));
  Multiplexer #(.enable("false")) multiplexer_45 (
    .in0(multiplexer_29_out), .in1(multiplexer_25_out), .out(C_OUT[4]), .sel(n[2]));
  Multiplexer #(.enable("false")) multiplexer_46 (
    .in0(multiplexer_30_out), .in1(multiplexer_26_out), .out(C_OUT[5]), .sel(n[2]));
  Multiplexer #(.enable("false")) multiplexer_47 (
    .in0(multiplexer_31_out), .in1(multiplexer_27_out), .out(C_OUT[6]), .sel(n[2]));
  Multiplexer #(.enable("false")) multiplexer_48 (
    .in0(multiplexer_32_out), .in1(multiplexer_28_out), .out(C_OUT[7]), .sel(n[2]));

  // Notes on the sheet:
  //   비트 1회 시프트
  //   비트 2회 시프트
  //   비트 4회 시프트
endmodule

module HW_MUL (
  input  [7:0] A,
  input  [7:0] B,
  output [7:0] OUT,
  output [7:0] C_OUT
);

  wire adder8_1_co, adder8_3_co, adder8_5_co, adder8_7_co, adder8_9_co, adder8_11_co, adder8_13_co;
  wire [7:0] adder8_1_o, adder8_2_o, adder8_3_o, adder8_4_o, adder8_5_o, adder8_6_o, adder8_7_o, adder8_8_o,
       adder8_9_o, adder8_10_o, adder8_11_o, adder8_12_o, chk_1_o, chk_2_o, chk_3_o, chk_4_o, chk_5_o,
       chk_6_o, chk_7_o, chk_8_o, chk_9_o, chk_10_o, chk_11_o, chk_12_o, chk_13_o, chk_14_o, chk_15_o,
       chk_16_o, left_barrel_shifter_1_c_out, left_barrel_shifter_1_out, left_barrel_shifter_2_c_out,
       left_barrel_shifter_2_out, left_barrel_shifter_3_c_out, left_barrel_shifter_3_out,
       left_barrel_shifter_4_c_out, left_barrel_shifter_4_out, left_barrel_shifter_5_c_out,
       left_barrel_shifter_5_out, left_barrel_shifter_6_c_out, left_barrel_shifter_6_out,
       left_barrel_shifter_7_c_out, left_barrel_shifter_7_out, left_barrel_shifter_8_c_out,
       left_barrel_shifter_8_out;

  Left_Barrel_Shifter left_barrel_shifter_1 (
    .C_OUT(left_barrel_shifter_1_c_out), .OUT(left_barrel_shifter_1_out), .n(3'b000), .A(A));
  Left_Barrel_Shifter left_barrel_shifter_2 (
    .C_OUT(left_barrel_shifter_2_c_out), .OUT(left_barrel_shifter_2_out), .n(3'b001), .A(A));
  Left_Barrel_Shifter left_barrel_shifter_3 (
    .C_OUT(left_barrel_shifter_3_c_out), .OUT(left_barrel_shifter_3_out), .n(3'b010), .A(A));
  Left_Barrel_Shifter left_barrel_shifter_4 (
    .C_OUT(left_barrel_shifter_4_c_out), .OUT(left_barrel_shifter_4_out), .n(3'b011), .A(A));
  Left_Barrel_Shifter left_barrel_shifter_5 (
    .C_OUT(left_barrel_shifter_5_c_out), .OUT(left_barrel_shifter_5_out), .n(3'b100), .A(A));
  Left_Barrel_Shifter left_barrel_shifter_6 (
    .C_OUT(left_barrel_shifter_6_c_out), .OUT(left_barrel_shifter_6_out), .n(3'b101), .A(A));
  Left_Barrel_Shifter left_barrel_shifter_7 (
    .C_OUT(left_barrel_shifter_7_c_out), .OUT(left_barrel_shifter_7_out), .n(3'b110), .A(A));
  Left_Barrel_Shifter left_barrel_shifter_8 (
    .C_OUT(left_barrel_shifter_8_c_out), .OUT(left_barrel_shifter_8_out), .n(3'b111), .A(A));
  Adder8 adder8_1 (.co(adder8_1_co), .o(adder8_1_o), .a(chk_1_o), .b(chk_2_o));  // open: ci
  CHK chk_1 (.o(chk_1_o), .i(left_barrel_shifter_1_out), .in_2(B[0]));
  CHK chk_2 (.o(chk_2_o), .i(left_barrel_shifter_2_out), .in_2(B[1]));
  CHK chk_3 (.o(chk_3_o), .i(left_barrel_shifter_3_out), .in_2(B[2]));
  CHK chk_4 (.o(chk_4_o), .i(left_barrel_shifter_4_out), .in_2(B[3]));
  CHK chk_5 (.o(chk_5_o), .i(left_barrel_shifter_5_out), .in_2(B[4]));
  CHK chk_6 (.o(chk_6_o), .i(left_barrel_shifter_6_out), .in_2(B[5]));
  CHK chk_7 (.o(chk_7_o), .i(left_barrel_shifter_7_out), .in_2(B[6]));
  CHK chk_8 (.o(chk_8_o), .i(left_barrel_shifter_8_out), .in_2(B[7]));
  Adder8 adder8_2 (.o(adder8_2_o), .a(chk_9_o), .b(chk_10_o), .ci(adder8_1_co));  // open: co
  CHK chk_9 (.o(chk_9_o), .i(left_barrel_shifter_1_c_out), .in_2(B[0]));
  CHK chk_10 (.o(chk_10_o), .i(left_barrel_shifter_2_c_out), .in_2(B[1]));
  CHK chk_11 (.o(chk_11_o), .i(left_barrel_shifter_3_c_out), .in_2(B[2]));
  CHK chk_12 (.o(chk_12_o), .i(left_barrel_shifter_4_c_out), .in_2(B[3]));
  CHK chk_13 (.o(chk_13_o), .i(left_barrel_shifter_5_c_out), .in_2(B[4]));
  CHK chk_14 (.o(chk_14_o), .i(left_barrel_shifter_6_c_out), .in_2(B[5]));
  CHK chk_15 (.o(chk_15_o), .i(left_barrel_shifter_7_c_out), .in_2(B[6]));
  CHK chk_16 (.o(chk_16_o), .i(left_barrel_shifter_8_c_out), .in_2(B[7]));
  Adder8 adder8_3 (.co(adder8_3_co), .o(adder8_3_o), .a(adder8_1_o), .b(chk_3_o));  // open: ci
  Adder8 adder8_4 (.o(adder8_4_o), .a(adder8_2_o), .b(chk_11_o), .ci(adder8_3_co));  // open: co
  Adder8 adder8_5 (.co(adder8_5_co), .o(adder8_5_o), .a(adder8_3_o), .b(chk_4_o));  // open: ci
  Adder8 adder8_6 (.o(adder8_6_o), .a(adder8_4_o), .b(chk_12_o), .ci(adder8_5_co));  // open: co
  Adder8 adder8_7 (.co(adder8_7_co), .o(adder8_7_o), .a(adder8_5_o), .b(chk_5_o));  // open: ci
  Adder8 adder8_8 (.o(adder8_8_o), .a(adder8_6_o), .b(chk_13_o), .ci(adder8_7_co));  // open: co
  Adder8 adder8_9 (.co(adder8_9_co), .o(adder8_9_o), .a(adder8_7_o), .b(chk_6_o));  // open: ci
  Adder8 adder8_10 (.o(adder8_10_o), .a(adder8_8_o), .b(chk_14_o), .ci(adder8_9_co));  // open: co
  Adder8 adder8_11 (.co(adder8_11_co), .o(adder8_11_o), .a(adder8_9_o), .b(chk_7_o));  // open: ci
  Adder8 adder8_12 (.o(adder8_12_o), .a(adder8_10_o), .b(chk_15_o), .ci(adder8_11_co));  // open: co
  Adder8 adder8_13 (.co(adder8_13_co), .o(OUT), .a(adder8_11_o), .b(chk_8_o));  // open: ci
  Adder8 adder8_14 (.o(C_OUT), .a(adder8_12_o), .b(chk_16_o), .ci(adder8_13_co));  // open: co
endmodule

module CHK (
  input  [7:0] i,
  input  in_2,
  output [7:0] o
);

  Multiplexer #(.enable("false"), .width(8)) multiplexer_1 (.in0({8{1'b0}}), .in1(i), .out(o), .sel(in_2));
endmodule

module SHL (
  input  si,
  input  [7:0] i,
  output [7:0] o,
  output so
);

  wire [6:0] register_1_q;

  Register #(.trigger("high")) register_1 (.D(i), .en(1'b1), .Q({so, register_1_q}), .clk(1'b1));  // open: clr
  Register #(.trigger("high")) register_2 (.D({register_1_q, si}), .en(1'b1), .Q(o), .clk(1'b1));  // open: clr
endmodule

module SHR (
  input  [7:0] i,
  input  si,
  output so,
  output [7:0] o
);

  wire [7:1] register_1_q;

  Register #(.trigger("high")) register_1 (.D(i), .en(1'b1), .Q({register_1_q, so}), .clk(1'b1));  // open: clr
  Register #(.trigger("high")) register_2 (.D({si, register_1_q}), .en(1'b1), .Q(o), .clk(1'b1));  // open: clr
endmodule

module ZEROer8 (
  input  [7:0] in,
  output out
);

  wire or_1_out;

  or or_1 (or_1_out, in[0], in[1], in[2], in[3], in[4], in[5], in[6], in[7]);
  not not_1 (out, or_1_out);
endmodule

module Inverter (
  input  [7:0] in_1,
  output [7:0] out_2
);

  assign out_2 = ~in_1;  // NOT_Gate not_1, 8 bits wide
endmodule

module Subtractor1 (
  input  a,
  input  b,
  input  bi,
  output difference,
  output bo
);

  wire bo1_out, bo2_out, not_1_out, not_2_out, sum1_out;

  xor sum1 (sum1_out, a, b);
  not not_1 (not_1_out, a);
  xor sum2 (difference, sum1_out, bi);
  not not_2 (not_2_out, sum1_out);
  and bo2 (bo2_out, not_2_out, bi);
  and bo1 (bo1_out, not_1_out, b);
  or or_1 (bo, bo2_out, bo1_out);
endmodule

module Subtractor8 (
  input  bi,
  input  [7:0] a,
  input  [7:0] b,
  output [7:0] o,
  output bo
);

  wire subtractor1_1_bo, subtractor1_2_bo, subtractor1_3_bo, subtractor1_4_bo, subtractor1_5_bo,
       subtractor1_6_bo, subtractor1_7_bo;

  Subtractor1 subtractor1_1 (.bo(subtractor1_1_bo), .difference(o[0]), .bi(bi), .a(a[0]), .b(b[0]));
  Subtractor1 subtractor1_2 (.bo(subtractor1_2_bo), .difference(o[1]), .bi(subtractor1_1_bo), .a(a[1]), .b(b[1]));
  Subtractor1 subtractor1_3 (.bo(subtractor1_3_bo), .difference(o[2]), .bi(subtractor1_2_bo), .a(a[2]), .b(b[2]));
  Subtractor1 subtractor1_4 (.bo(subtractor1_4_bo), .difference(o[3]), .bi(subtractor1_3_bo), .a(a[3]), .b(b[3]));
  Subtractor1 subtractor1_5 (.bo(subtractor1_5_bo), .difference(o[4]), .bi(subtractor1_4_bo), .a(a[4]), .b(b[4]));
  Subtractor1 subtractor1_6 (.bo(subtractor1_6_bo), .difference(o[5]), .bi(subtractor1_5_bo), .a(a[5]), .b(b[5]));
  Subtractor1 subtractor1_7 (.bo(subtractor1_7_bo), .difference(o[6]), .bi(subtractor1_6_bo), .a(a[6]), .b(b[6]));
  Subtractor1 subtractor1_8 (.bo(bo), .difference(o[7]), .bi(subtractor1_7_bo), .a(a[7]), .b(b[7]));
endmodule

module HW_DIV (
  input  [7:0] \나눠질_수 ,
  input  [7:0] \나눌_수 ,
  output [7:0] \나머지 ,
  output [7:0] \몫 
);

  wire clock_1_out, clock_2_out, clock_3_out, clock_4_out, EN, not_2_out, shl_1_so, subtractor8_2_bo,
       zeroer8_1_out, zeroer8_2_out;
  wire [7:0] counter_1_q, multiplexer_1_out, register_1_q, register_2_q, register_3_q, shl_1_o, shl_2_o,
       subtractor8_1_o, subtractor8_2_o;

  Counter #(.max('h9)) counter_1 (.count(EN), .Q(counter_1_q), .clk(clock_1_out));  // open: load, D, carry, clr
  Clock clock_1 (.out(clock_1_out));
  Multiplexer #(.enable("false"), .width(8)) multiplexer_1 (
    .in0(shl_1_o), .in1(\나눠질_수 ), .out(multiplexer_1_out), .sel(zeroer8_1_out));
  Clock clock_2 (.out(clock_2_out));
  ZEROer8 zeroer8_1 (.out(zeroer8_1_out), .in(counter_1_q));
  Subtractor8 subtractor8_1 (.o(subtractor8_1_o), .a(counter_1_q), .b(8'h9));  // open: bo, bi
  Register register_1 (.D(multiplexer_1_out), .en(EN), .Q(register_1_q), .clk(clock_2_out));  // open: clr
  Subtractor8 subtractor8_2 (.bo(subtractor8_2_bo), .o(subtractor8_2_o), .a(register_2_q), .b(\나눌_수 ));  // open: bi
  not not_1 (EN, zeroer8_2_out);
  ZEROer8 zeroer8_2 (.out(zeroer8_2_out), .in(subtractor8_1_o));
  SHL shl_1 (.so(shl_1_so), .o(shl_1_o), .i(register_1_q));  // open: si
  Multiplexer #(.enable("false"), .width(8)) multiplexer_2 (
    .in0(register_2_q), .in1(subtractor8_2_o), .out(\나머지 ), .sel(not_2_out));
  not not_2 (not_2_out, subtractor8_2_bo);
  SHL shl_2 (.o(shl_2_o), .i(\나머지 ), .si(shl_1_so));  // open: so
  SHL shl_3 (.o(\몫 ), .i(register_3_q), .si(not_2_out));  // open: so
  Register register_2 (.D(shl_2_o), .en(EN), .Q(register_2_q), .clk(clock_3_out));  // open: clr
  Clock clock_3 (.out(clock_3_out));
  Register register_3 (.D(\몫 ), .en(EN), .Q(register_3_q), .clk(clock_4_out));  // open: clr
  Clock clock_4 (.out(clock_4_out));
endmodule
